// Logisim project cpu21-riscv-su-9-8.circ as structural Verilog: 25 circuits, main circuit ◇单周期RISC-V
module \单周期RISC_V  (
  input  IR1,
  input  IR2,
  input  IR3,
  output RegWrite,
  output MemWrite,
  output [31:0] PC,
  output [31:0] IR,
  output [31:0] RDin,
  output [31:0] MDin,
  output [31:0] LedData
);

  wire alu_1_equal, and_1_out, and_2_out, and_3_out, and_5_out, and_6_out, B, bltu, clearI, CLK, clock_1_out,
       comparator_1_gt, comparator_1_lt, comparator_3_eq, comparator_3_lt, d_ff_1_q, ec_eq, ecall, Go, halt,
       I, IR1_t, IR2_t, IR3_t, IRA, IRB, IRC, J, JAL, JALR, lessthen, nand_1_out, not_1_out, not_2_out,
       or_1_out, or_2_out, PCSrc, RST, S_type, sb, setI, sll, URET, W1, W2, W3, \单周期硬布线控制器_1_beq ,
       \单周期硬布线控制器_1_bne , \单周期硬布线控制器_1_memtoreg ;
  wire [0:0] \单周期硬布线控制器_1_alu_src ;
  wire [1:1] alu_1_result;
  wire [3:0] \单周期硬布线控制器_1_alu_op ;
  wire [4:0] multiplexer_4_out, multiplexer_5_out;
  wire [12:0] CNT_num;
  wire [15:0] \总周期数 ;
  wire [31:0] adder_1_out, adder_2_out, and_4_out, bit_extender_1_out, bit_extender_2_out,
       bit_extender_3_out, bit_extender_4_out, ec_out, multiplexer_1_out, multiplexer_2_out,
       multiplexer_3_out, multiplexer_7_out, multiplexer_9_out, R1, ram_1_data, \sb分线_1_output ,
       shifter_1_out;
  wire [31:2] alu_1_result_2;

  Button \u_继续运行  (.out(Go));
  Button _1 (.out(IRA));
  Button _2 (.out(IRB));
  Button _3 (.out(IRC));
  LED #(.active("true")) led_1 (.in(W1));
  LED #(.active("true")) led_2 (.in(W2));
  LED #(.active("true")) led_3 (.in(W3));
  Hex_Digit_Display hex_digit_display_1 (.value(LedData[31:28]));  // open: dp
  and and_1 (and_1_out, lessthen, bltu);
  or or_1 (or_1_out, J, PCSrc, and_1_out);
  Multiplexer #(.select(1), .width(32), .disabled("Z"), .enable("false")) multiplexer_1 (
    .in0(adder_1_out), .in1(multiplexer_2_out), .out(multiplexer_1_out), .sel(or_1_out));
  Multiplexer #(.select(1), .width(32), .disabled("Z"), .enable("false")) multiplexer_2 (
    .in0(adder_2_out), .in1(and_4_out), .out(multiplexer_2_out), .sel(JALR));
  Hex_Digit_Display hex_digit_display_2 (.value(LedData[23:20]));  // open: dp
  Hex_Digit_Display hex_digit_display_3 (.value(LedData[27:24]));  // open: dp
  not not_1 (not_1_out, halt);
  Hex_Digit_Display hex_digit_display_4 (.value(LedData[15:12]));  // open: dp
  Hex_Digit_Display hex_digit_display_5 (.value(LedData[19:16]));  // open: dp
  not not_2 (not_2_out, halt);
  Counter #(.width(16), .max('hffff), .ongoal("wrap"), .trigger("rising"), .behavior("new")) counter_1 (
    .D(16'h1), .count(not_2_out), .Q(\总周期数 ), .clk(or_2_out), .clr(Go));  // open: load, carry, preset, down
  or or_2 (or_2_out, comparator_1_gt, comparator_1_lt);
  Comparator #(.width(32), .mode("unsigned")) comparator_1 (
    .a({{20{1'b0}}, multiplexer_1_out[11:0]}), .b(PC), .gt(comparator_1_gt), .lt(comparator_1_lt));  // open: eq
  Register #(.width(32), .trigger("rising"), .Select("low")) u_PC (
    .D({{20{1'b0}}, multiplexer_1_out[11:0]}), .en(not_1_out), .Q(PC), .clk(CLK), .clr(RST));
  Hex_Digit_Display hex_digit_display_6 (.value(LedData[11:8]));  // open: dp
  Hex_Digit_Display hex_digit_display_7 (.value(LedData[7:4]));  // open: dp
  // Probe on \总周期数 
  // Probe on PC
  Hex_Digit_Display hex_digit_display_8 (.value(LedData[3:0]));  // open: dp
  or or_3 (J, JAL, JALR);
  Adder #(.width(32)) adder_1 (.a(PC), .b(32'h4), .out(adder_1_out));  // open: cin, cout
  Adder #(.width(32)) adder_2 (.a(PC), .b(shifter_1_out), .out(adder_2_out));  // open: cin, cout
  // RiscV_Probe riscv_probe_1: pin names not known; wires that end beside it: IR
  ROM #(.addrWidth(10), .dataWidth(32), .Select("high")) rom_1 (.addr(PC[11:2]), .data(IR));
  or or_4 (IR1_t, IR1, IRA);
  or or_5 (IR2_t, IR2, IRB);
  \单周期硬布线控制器  \u_单周期硬布线控制器_1  (
    .Funct({IR[30], IR[25], IR[14:12]}), .OP(IR[6:2]), .ALU_OP(\单周期硬布线控制器_1_alu_op ),
    .MemToReg(\单周期硬布线控制器_1_memtoreg ), .MemWrite(MemWrite), .ALU_SRC(\单周期硬布线控制器_1_alu_src [0]),
    .RegWrite(RegWrite), .ecall(ecall), .S_type(S_type), .Jalr(JALR), .Beq(\单周期硬布线控制器_1_beq ), .JAL(JAL),
    .Bne(\单周期硬布线控制器_1_bne ), .in_3(IR[21]), .uret(URET), .I(I), .B(B), .clearI(clearI), .sb(sb), .sll(sll),
    .setI(setI), .bltu(bltu));
  assign bit_extender_1_out = {{20{IR[31]}}, IR[31:20]};  // Bit_Extender bit_extender_1
  assign bit_extender_2_out = {{20{IR[31]}}, {IR[31:25], IR[11:7]}};  // Bit_Extender bit_extender_2
  assign bit_extender_3_out = {{20{IR[31]}}, {IR[31], IR[7], IR[30:25], IR[11:8]}};  // Bit_Extender bit_extender_3
  assign bit_extender_4_out = {{12{IR[31]}}, {IR[31], IR[19:12], IR[20], IR[30:21]}};  // Bit_Extender bit_extender_4
  or or_6 (IR3_t, IR3, IRC);
  Multiplexer #(.select(4), .width(32), .disabled("Z"), .enable("false")) multiplexer_3 (
    .in1(bit_extender_1_out), .in2(bit_extender_2_out), .in4(bit_extender_3_out), .in8(bit_extender_4_out),
    .out(multiplexer_3_out), .sel({JAL, B, S_type, I}));  // open: in0, in3, in5, in6, in7, in9, in10, in11, in12, in13, in14, in15
  Multiplexer #(.select(1), .width(5), .disabled("Z"), .enable("false")) multiplexer_4 (
    .in0(IR[19:15]), .in1(5'b10001), .out(multiplexer_4_out), .sel(ecall));
  Multiplexer #(.select(1), .width(5), .disabled("Z"), .enable("false")) multiplexer_5 (
    .in0(IR[24:20]), .in1(5'b01010), .out(multiplexer_5_out), .sel(ecall));
  Multiplexer #(.select(1), .width(32), .disabled("Z"), .enable("false")) multiplexer_6 (
    .in0(multiplexer_9_out), .in1(adder_1_out), .out(RDin), .sel(J));
  Regifile regifile_1 (
    .Din(RDin), .Clk(CLK), .R1(R1), .R2(ec_out), .WE(RegWrite), .W_num(IR[11:7]), .R1_num(multiplexer_4_out),
    .R2_num(multiplexer_5_out));
  Comparator #(.width(32), .mode("unsigned")) comparator_2 (.a(32'h22), .b(R1), .eq(ec_eq));  // open: gt, lt
  Multiplexer #(.select(2), .width(32), .disabled("Z"), .enable("false")) multiplexer_7 (
    .in0(ec_out), .in1(multiplexer_3_out), .in2({{27{1'b0}}, ec_out[4:0]}), .out(multiplexer_7_out),
    .sel({sll, \单周期硬布线控制器_1_alu_src [0]}));  // open: in3
  \sb分线  \sb分线_1  (
    .\new (ec_out[7:0]), .Address({alu_1_result[1], lessthen}), .\output (\sb分线_1_output ),
    .origin(ram_1_data));
  Shifter #(.width(32), .shift("ll")) shifter_1 (.in(multiplexer_3_out), .\dist (5'b00001), .out(shifter_1_out));
  ALU alu_1 (
    .X(R1), .Y(multiplexer_7_out), .AluOP(\单周期硬布线控制器_1_alu_op ), .Equal(alu_1_equal),
    .Result({alu_1_result_2, alu_1_result[1], lessthen}));  // open: Result_2, out_4, out_6
  Multiplexer #(.select(1), .width(32), .disabled("Z"), .enable("false")) multiplexer_8 (
    .in0(ec_out), .in1(\sb分线_1_output ), .out(MDin), .sel(sb));
  D_Flip_Flop #(.trigger("high"), .Pre_Clr_Positions("LEGACY"), .NegatePresetClear("false"), .enable("true"), .NewFFLayout("false")) d_ff_1 (.Q(d_ff_1_q));  // open: clk, D, Qn, preset, en, reset
  // Probe on 13'h159
  and and_2 (and_2_out, ecall, ~ec_eq);  // AND_Gate
  and and_3 (and_3_out, ec_eq, ecall);
  assign and_4_out = multiplexer_9_out & 32'hfffffffe;  // AND_Gate and_4, 32 bits wide
  Comparator #(.width(13), .mode("twosComplement")) comparator_3 (
    .a(CNT_num), .b(13'h159), .eq(comparator_3_eq), .lt(comparator_3_lt));  // open: gt
  Clock #(.highDuration(1), .lowDuration(1)) clock_1 (.out(clock_1_out));
  and and_5 (and_5_out, alu_1_equal, \单周期硬布线控制器_1_beq );
  and and_6 (and_6_out, ~alu_1_equal, \单周期硬布线控制器_1_bne );  // AND_Gate
  D_Flip_Flop #(.trigger("high"), .Pre_Clr_Positions("LEGACY"), .NegatePresetClear("false"), .enable("true"), .NewFFLayout("false")) d_ff_2 (
    .clk(CLK), .D(and_2_out), .Q(halt), .reset(Go));  // open: Qn, preset, en
  Register #(.width(32), .trigger("rising"), .Select("low")) register_1 (
    .D(ec_out), .en(and_3_out), .Q(LedData), .clk(CLK));  // open: clr
  Counter #(.width(13), .max('h1fff), .ongoal("wrap"), .trigger("rising"), .behavior("new")) counter_2 (
    .Q(CNT_num), .clk(clock_1_out), .down(comparator_3_lt));  // open: load, D, count, carry, clr, preset
  or or_7 (PCSrc, and_5_out, and_6_out);
  RAM #(.addrWidth(10), .dataWidth(32), .bus("separate"), .Select("high")) ram_1 (
    .addr(alu_1_result_2[11:2]), .din(MDin), .data(ram_1_data), .str(MemWrite), .clk(CLK), .ld(1'b1));  // open: sel, clr
  nand nand_1 (nand_1_out, d_ff_1_q, comparator_3_eq);
  Multiplexer #(.select(1), .width(32), .disabled("Z"), .enable("false")) multiplexer_9 (
    .in0({alu_1_result_2, alu_1_result[1], lessthen}), .in1(ram_1_data), .out(multiplexer_9_out),
    .sel(\单周期硬布线控制器_1_memtoreg ));
  assign CLK = nand_1_out ? clock_1_out : 1'bz;  // Controlled_Buffer controlled_buffer_1
  Pull_Resistor #(.pull(1)) pull_resistor_1 (.node(CLK));

  // Other names for the same wires on the sheet: R2[31:0] = ec_out

  // Notes on the sheet:
  //   中断源
  //   中断等待指示
  //   数码管输出应该用寄存器锁存，否则显示数据只能一闪而过
  //   数码管输出
  //   指令探针
  //   指令存储器
  //   contents of rom_1 (hex, n*v repeats v):
  //   100493 100006f 100493 200913 300993 100006f 100493 200913 300993 100006f 100493 200913 300993
  //   100006f 100493 200913 300993 3b4000ef 100413 100493 1f49493 900533 2200893 73 24d493 48463 fedff06f
  //   900533 2200893 73 100493 249493 900533 2200893 73 48463 fedff06f 100493 1f49493 900533 2200893 73
  //   4034d493 900533 2200893 73 4044d493 900533 2200893 73 4044d493 900533 2200893 73 4044d493 900533
  //   2200893 73 4044d493 900533 2200893 73 4044d493 900533 2200893 73 4044d493 900533 2200893 73 4044d493
  //   900533 2200893 73 100413 1f41993 41f9d993 433 c00913 300b13 140413 f47413 800293 100313 499993
  //   89e9b3 1300533 2200893 73 406282b3 fe0294e3 140413 f00f93 1f47433 1c41413 800293 100313 49d993
  //   89e9b3 1300533 2200893 73 406282b3 fe0294e3 1c45413 406b0b33 b0463 f95ff06f 2b3 fff2c293 829293
  //   ff2e293 500533 2200893 73 fff00413 493 84a023 140413 448493 84a023 140413 448493 84a023 140413
  //   448493 84a023 140413 448493 84a023 140413 448493 84a023 140413 448493 84a023 140413 448493 84a023
  //   140413 448493 84a023 140413 448493 84a023 140413 448493 84a023 140413 448493 84a023 140413 448493
  //   84a023 140413 448493 84a023 140413 448493 84a023 140413 448493 84a023 140413 448493 140413 433
  //   3c00493 42983 4aa03 149a2b3 28663 134a023 1442023 ffc48493 fe9412e3 800533 2200893 73 440413 3c00493
  //   fc9416e3 3200893 73 100293 300313 800493 849493 7648493 900533 2200893 73 800e13 5494b3 6494b3
  //   900533 2200893 73 fffe0e13 fe0e14e3 a00893 73 fff00293 7700493 849493 7748493 900533 2200893 73
  //   1000e13 54c4b3 900533 2200893 73 fffe0e13 fe0e16e3 a00893 73 313 2000e13 493 100913 930023 900533
  //   2200893 73 12484b3 130313 fffe0e13 fe0e12e3 800e13 313 32483 900533 2200893 73 430313 fffe0e13
  //   fe0e14e3 a00893 73 ff100493 900533 2200893 73 148493 fe9068e3 900533 2200893 73 a00893 73 a00893 73
  //   413 140413 800533 2200893 73 240413 800533 2200893 73 340413 800533 2200893 73 440413 800533 2200893
  //   73 540413 800533 2200893 73 640413 800533 2200893 73 740413 800533 2200893 73 840413 800533 2200893
  //   2200893 73 8067
  //   指令字
  //   JAL
  //   JALR
  //   URET
  //   I
  //   B
  //   Beq
  //   Bne
  //   MemToReg
  //   MemWrite
  //   AluOP
  //   AluSrcB
  //   RegWrite
  //   为方便自动评测，需要输出PC，IR，寄存器堆写如数据RDin
  //   RAM写使能MemWrite、RAM写入数据MDin等信号
  //   控制位
  //   暂停节拍，不能为0
  //   数据存储器
  //   戳工具置1进入计数暂停模式，ctrl+k时钟自动运行到对应节拍暂停
  //   ctrl+k关闭时钟连续运行，将控制位置零，进入单步调试模式调试
  //   用这个时钟源需要去掉电路中的其他时钟源
  //   可计数暂停的时钟源
endmodule

// 单周期硬布线控制器
module \单周期硬布线控制器  (
  input  [4:0] OP,
  input  [4:0] Funct,
  input  in_3,
  output [3:0] ALU_OP,
  output MemToReg,
  output uret,
  output MemWrite,
  output bltu,
  output setI,
  output clearI,
  output sb,
  output ecall,
  output sll,
  output ALU_SRC,
  output RegWrite,
  output S_type,
  output Beq,
  output Bne,
  output Jalr,
  output JAL,
  output I,
  output B
);

  wire \控制信号自动生成_1_ecall ;

  \运算控制器自动生成  \u_运算控制器自动生成_1  (
    .OP2(OP[0]), .OP3(OP[1]), .OP4(OP[2]), .OP5(OP[3]), .OP6(OP[4]), .F12(Funct[0]), .F13(Funct[1]),
    .F14(Funct[2]), .F25(Funct[3]), .F30(Funct[4]), .S0(ALU_OP[0]), .S1(ALU_OP[1]), .S2(ALU_OP[2]),
    .S3(ALU_OP[3]));
  \控制信号自动生成  \u_控制信号自动生成_1  (
    .OP2(OP[0]), .OP3(OP[1]), .MemToReg(MemToReg), .OP4(OP[2]), .OP5(OP[3]), .OP6(OP[4]), .F12(Funct[0]),
    .F13(Funct[1]), .F14(Funct[2]), .MemWrite(MemWrite), .F25(Funct[3]), .F30(Funct[4]), .bltu(bltu),
    .setI(setI), .clearI(clearI), .sb(sb), .sll(sll), .ALU_SRC(ALU_SRC), .RegWrite(RegWrite),
    .ecall(\控制信号自动生成_1_ecall ), .S_Type(S_type), .BEQ(Beq), .BNE(Bne), .JALR(Jalr), .JAL(JAL), .I(I), .B(B));
  and and_1 (uret, in_3, \控制信号自动生成_1_ecall );
  and and_2 (ecall, ~in_3, \控制信号自动生成_1_ecall );  // AND_Gate

  // Other names for the same wires on the sheet: IR21 = in_3; OP_CODE[4:0] = OP

  // Notes on the sheet:
  //   运算器控制器，根据指令生成运算器功能选择信号
  //   控制信号生成，产生数据通路需要的其他控制信号
endmodule

// 运算器控制器
module \运算控制器自动生成  (
  input  OP2,
  input  OP3,
  input  OP4,
  input  OP5,
  input  OP6,
  input  F12,
  input  F13,
  input  F14,
  input  F25,
  input  F30,
  output S0,
  output S1,
  output S2,
  output S3
);

  wire and_1_out, and_2_out, and_3_out, and_4_out, and_5_out, and_6_out, and_7_out, and_8_out, and_9_out,
       and_10_out, and_11_out, and_12_out, and_13_out, and_14_out, and_15_out, and_16_out, and_17_out,
       and_18_out, and_19_out, and_20_out, and_21_out, and_22_out, and_23_out, and_24_out, and_25_out,
       and_26_out, and_27_out, and_28_out, and_29_out, and_30_out, and_31_out, and_32_out, and_33_out,
       and_34_out, and_35_out, and_36_out, and_37_out, and_38_out, and_39_out, and_40_out, and_41_out,
       and_42_out, not_1_out, not_2_out, not_3_out, not_4_out, not_5_out, not_6_out, not_7_out, not_8_out,
       not_9_out, not_10_out, not_11_out, not_12_out, not_13_out, not_14_out, not_15_out, not_16_out,
       not_17_out, not_18_out, not_19_out, not_20_out, not_21_out, not_22_out, not_23_out, not_24_out,
       not_25_out, not_26_out, not_27_out, not_28_out, not_29_out, not_30_out, not_31_out, not_32_out,
       not_33_out, not_34_out, not_35_out, not_36_out, not_37_out, not_38_out, not_39_out, not_40_out,
       not_41_out, not_42_out, not_43_out, not_44_out, not_45_out, not_46_out, not_47_out, not_48_out,
       not_49_out, not_50_out, not_51_out, not_52_out, not_53_out, not_54_out, not_55_out, not_56_out,
       not_57_out, not_58_out, not_59_out, not_60_out, not_61_out, not_62_out, not_63_out, not_64_out,
       not_65_out, not_66_out, not_67_out, not_68_out, not_69_out, not_70_out, not_71_out, not_72_out,
       not_73_out, not_74_out, not_75_out, not_76_out, not_77_out, not_78_out, not_79_out, not_80_out,
       not_81_out, not_82_out, not_83_out, not_84_out, not_85_out, not_86_out, not_87_out, not_88_out,
       not_89_out, not_90_out, not_91_out, not_92_out, not_93_out, not_94_out, not_95_out, not_96_out,
       not_97_out, not_98_out, not_99_out, not_100_out, not_101_out, not_102_out, not_103_out, not_104_out,
       not_105_out, not_106_out, not_107_out, not_108_out, not_109_out, not_110_out, not_111_out,
       not_112_out, not_113_out, not_114_out, not_115_out, not_116_out, not_117_out, not_118_out,
       not_119_out, not_120_out, not_121_out, not_122_out, not_123_out, not_124_out, not_125_out,
       not_126_out, not_127_out, not_128_out, not_129_out, not_130_out, not_131_out, not_132_out,
       not_133_out, not_134_out, not_135_out, not_136_out, not_137_out, not_138_out, not_139_out,
       not_140_out, not_141_out, not_142_out, not_143_out, not_144_out, not_145_out, not_146_out,
       not_147_out, not_148_out, not_149_out, not_150_out, not_151_out, not_152_out, not_153_out,
       not_154_out, not_155_out, not_156_out, not_157_out, not_158_out, not_159_out, not_160_out,
       not_161_out, not_162_out, not_163_out, not_164_out, not_165_out, not_166_out, not_167_out,
       not_168_out, not_169_out, not_170_out, not_171_out, not_172_out, not_173_out, not_174_out,
       not_175_out, not_176_out, not_177_out, not_178_out, not_179_out, not_180_out, not_181_out,
       not_182_out, not_183_out, not_184_out, not_185_out, not_186_out, not_187_out, not_188_out,
       not_189_out, not_190_out, not_191_out, not_192_out, not_193_out, not_194_out, not_195_out,
       not_196_out, not_197_out, not_198_out, not_199_out, not_200_out, not_201_out, not_202_out,
       not_203_out, not_204_out, not_205_out, not_206_out, not_207_out, not_208_out, not_209_out,
       not_210_out, not_211_out, not_212_out, not_213_out, not_214_out, not_215_out, not_216_out,
       not_217_out, not_218_out, not_219_out, not_220_out, not_221_out, not_222_out, not_223_out,
       not_224_out, not_225_out, not_226_out, not_227_out, not_228_out, not_229_out, not_230_out,
       not_231_out, not_232_out, not_233_out, not_234_out, not_235_out, not_236_out, not_237_out,
       not_238_out, not_239_out, not_240_out, not_241_out, not_242_out, not_243_out, not_244_out,
       not_245_out, not_246_out, not_247_out, not_248_out;

  not not_1 (not_1_out, F30);
  not not_2 (not_2_out, F25);
  not not_3 (not_3_out, F14);
  not not_4 (not_4_out, F13);
  not not_5 (not_5_out, F12);
  not not_6 (not_6_out, OP6);
  not not_7 (not_7_out, OP3);
  not not_8 (not_8_out, OP2);
  not not_9 (not_9_out, F30);
  not not_10 (not_10_out, F25);
  not not_11 (not_11_out, OP6);
  not not_12 (not_12_out, OP3);
  not not_13 (not_13_out, OP2);
  not not_14 (not_14_out, F30);
  not not_15 (not_15_out, F25);
  not not_16 (not_16_out, F14);
  not not_17 (not_17_out, F12);
  not not_18 (not_18_out, OP6);
  not not_19 (not_19_out, OP3);
  not not_20 (not_20_out, OP2);
  not not_21 (not_21_out, F14);
  not not_22 (not_22_out, F13);
  not not_23 (not_23_out, F12);
  not not_24 (not_24_out, OP6);
  not not_25 (not_25_out, OP5);
  not not_26 (not_26_out, OP3);
  not not_27 (not_27_out, OP2);
  not not_28 (not_28_out, OP6);
  not not_29 (not_29_out, OP5);
  not not_30 (not_30_out, OP3);
  not not_31 (not_31_out, OP2);
  not not_32 (not_32_out, F13);
  not not_33 (not_33_out, F12);
  not not_34 (not_34_out, OP6);
  not not_35 (not_35_out, OP5);
  not not_36 (not_36_out, OP3);
  not not_37 (not_37_out, OP2);
  not not_38 (not_38_out, F14);
  not not_39 (not_39_out, F12);
  not not_40 (not_40_out, OP6);
  not not_41 (not_41_out, OP5);
  not not_42 (not_42_out, OP3);
  not not_43 (not_43_out, OP2);
  not not_44 (not_44_out, F25);
  not not_45 (not_45_out, F13);
  not not_46 (not_46_out, OP6);
  not not_47 (not_47_out, OP5);
  not not_48 (not_48_out, OP3);
  not not_49 (not_49_out, OP2);
  not not_50 (not_50_out, F14);
  not not_51 (not_51_out, F12);
  not not_52 (not_52_out, OP6);
  not not_53 (not_53_out, OP5);
  not not_54 (not_54_out, OP4);
  not not_55 (not_55_out, OP3);
  not not_56 (not_56_out, OP2);
  not not_57 (not_57_out, F14);
  not not_58 (not_58_out, F12);
  not not_59 (not_59_out, OP6);
  not not_60 (not_60_out, OP4);
  not not_61 (not_61_out, OP3);
  not not_62 (not_62_out, OP2);
  not not_63 (not_63_out, F14);
  not not_64 (not_64_out, F13);
  not not_65 (not_65_out, F12);
  not not_66 (not_66_out, OP4);
  not not_67 (not_67_out, OP3);
  not not_68 (not_68_out, F13);
  not not_69 (not_69_out, F12);
  not not_70 (not_70_out, OP6);
  not not_71 (not_71_out, OP3);
  not not_72 (not_72_out, OP2);
  not not_73 (not_73_out, F14);
  not not_74 (not_74_out, F13);
  not not_75 (not_75_out, F12);
  not not_76 (not_76_out, OP6);
  not not_77 (not_77_out, OP4);
  not not_78 (not_78_out, OP3);
  not not_79 (not_79_out, OP2);
  not not_80 (not_80_out, F25);
  not not_81 (not_81_out, F14);
  not not_82 (not_82_out, F13);
  not not_83 (not_83_out, F12);
  not not_84 (not_84_out, OP6);
  not not_85 (not_85_out, OP3);
  not not_86 (not_86_out, OP2);
  not not_87 (not_87_out, F30);
  not not_88 (not_88_out, F25);
  not not_89 (not_89_out, OP6);
  not not_90 (not_90_out, OP3);
  not not_91 (not_91_out, OP2);
  not not_92 (not_92_out, F30);
  not not_93 (not_93_out, F25);
  not not_94 (not_94_out, F14);
  not not_95 (not_95_out, F12);
  not not_96 (not_96_out, OP6);
  not not_97 (not_97_out, OP3);
  not not_98 (not_98_out, OP2);
  not not_99 (not_99_out, OP6);
  not not_100 (not_100_out, OP5);
  not not_101 (not_101_out, OP3);
  not not_102 (not_102_out, OP2);
  not not_103 (not_103_out, F14);
  not not_104 (not_104_out, F12);
  not not_105 (not_105_out, OP6);
  not not_106 (not_106_out, OP5);
  not not_107 (not_107_out, OP3);
  not not_108 (not_108_out, OP2);
  not not_109 (not_109_out, F30);
  not not_110 (not_110_out, F25);
  not not_111 (not_111_out, F13);
  not not_112 (not_112_out, OP6);
  not not_113 (not_113_out, OP5);
  not not_114 (not_114_out, OP3);
  not not_115 (not_115_out, OP2);
  not not_116 (not_116_out, F14);
  not not_117 (not_117_out, F13);
  not not_118 (not_118_out, F12);
  not not_119 (not_119_out, OP4);
  not not_120 (not_120_out, OP3);
  not not_121 (not_121_out, OP2);
  not not_122 (not_122_out, F14);
  not not_123 (not_123_out, F13);
  not not_124 (not_124_out, OP4);
  not not_125 (not_125_out, OP3);
  not not_126 (not_126_out, OP2);
  not not_127 (not_127_out, F30);
  not not_128 (not_128_out, F25);
  not not_129 (not_129_out, F14);
  not not_130 (not_130_out, F13);
  not not_131 (not_131_out, F12);
  not not_132 (not_132_out, OP6);
  not not_133 (not_133_out, OP3);
  not not_134 (not_134_out, OP2);
  not not_135 (not_135_out, F25);
  not not_136 (not_136_out, F14);
  not not_137 (not_137_out, F13);
  not not_138 (not_138_out, F12);
  not not_139 (not_139_out, OP6);
  not not_140 (not_140_out, OP3);
  not not_141 (not_141_out, OP2);
  not not_142 (not_142_out, F30);
  not not_143 (not_143_out, F25);
  not not_144 (not_144_out, OP6);
  not not_145 (not_145_out, OP3);
  not not_146 (not_146_out, OP2);
  not not_147 (not_147_out, F30);
  not not_148 (not_148_out, F25);
  not not_149 (not_149_out, F14);
  not not_150 (not_150_out, OP6);
  not not_151 (not_151_out, OP3);
  not not_152 (not_152_out, OP2);
  not not_153 (not_153_out, F14);
  not not_154 (not_154_out, F13);
  not not_155 (not_155_out, F12);
  not not_156 (not_156_out, OP6);
  not not_157 (not_157_out, OP5);
  not not_158 (not_158_out, OP3);
  not not_159 (not_159_out, OP2);
  not not_160 (not_160_out, OP6);
  not not_161 (not_161_out, OP5);
  not not_162 (not_162_out, OP3);
  not not_163 (not_163_out, OP2);
  not not_164 (not_164_out, F14);
  not not_165 (not_165_out, F12);
  not not_166 (not_166_out, OP6);
  not not_167 (not_167_out, OP5);
  not not_168 (not_168_out, OP4);
  not not_169 (not_169_out, OP3);
  not not_170 (not_170_out, OP2);
  not not_171 (not_171_out, F14);
  not not_172 (not_172_out, F12);
  not not_173 (not_173_out, OP6);
  not not_174 (not_174_out, OP4);
  not not_175 (not_175_out, OP3);
  not not_176 (not_176_out, OP2);
  not not_177 (not_177_out, F14);
  not not_178 (not_178_out, F13);
  not not_179 (not_179_out, F12);
  not not_180 (not_180_out, OP4);
  not not_181 (not_181_out, OP3);
  not not_182 (not_182_out, OP2);
  not not_183 (not_183_out, F14);
  not not_184 (not_184_out, F13);
  not not_185 (not_185_out, OP4);
  not not_186 (not_186_out, OP3);
  not not_187 (not_187_out, OP2);
  not not_188 (not_188_out, F14);
  not not_189 (not_189_out, F13);
  not not_190 (not_190_out, F12);
  not not_191 (not_191_out, OP4);
  not not_192 (not_192_out, OP3);
  not not_193 (not_193_out, F14);
  not not_194 (not_194_out, F13);
  not not_195 (not_195_out, F12);
  not not_196 (not_196_out, OP6);
  not not_197 (not_197_out, OP4);
  not not_198 (not_198_out, OP3);
  not not_199 (not_199_out, OP2);
  not not_200 (not_200_out, F12);
  not not_201 (not_201_out, OP4);
  not not_202 (not_202_out, OP3);
  not not_203 (not_203_out, OP2);
  not not_204 (not_204_out, F30);
  not not_205 (not_205_out, F25);
  not not_206 (not_206_out, F12);
  not not_207 (not_207_out, OP6);
  not not_208 (not_208_out, OP3);
  not not_209 (not_209_out, OP2);
  not not_210 (not_210_out, F30);
  not not_211 (not_211_out, F25);
  not not_212 (not_212_out, F14);
  not not_213 (not_213_out, F12);
  not not_214 (not_214_out, OP6);
  not not_215 (not_215_out, OP3);
  not not_216 (not_216_out, OP2);
  not not_217 (not_217_out, F30);
  not not_218 (not_218_out, F25);
  not not_219 (not_219_out, F14);
  not not_220 (not_220_out, OP6);
  not not_221 (not_221_out, OP3);
  not not_222 (not_222_out, OP2);
  not not_223 (not_223_out, F12);
  not not_224 (not_224_out, OP6);
  not not_225 (not_225_out, OP5);
  not not_226 (not_226_out, OP3);
  not not_227 (not_227_out, OP2);
  not not_228 (not_228_out, F13);
  not not_229 (not_229_out, F12);
  not not_230 (not_230_out, OP6);
  not not_231 (not_231_out, OP5);
  not not_232 (not_232_out, OP3);
  not not_233 (not_233_out, OP2);
  not not_234 (not_234_out, F14);
  not not_235 (not_235_out, F12);
  not not_236 (not_236_out, OP6);
  not not_237 (not_237_out, OP5);
  not not_238 (not_238_out, OP3);
  not not_239 (not_239_out, OP2);
  not not_240 (not_240_out, F13);
  not not_241 (not_241_out, F12);
  not not_242 (not_242_out, OP6);
  not not_243 (not_243_out, OP3);
  not not_244 (not_244_out, OP2);
  not not_245 (not_245_out, F12);
  not not_246 (not_246_out, OP4);
  not not_247 (not_247_out, OP3);
  not not_248 (not_248_out, OP2);
  and and_1 (and_1_out, not_1_out, not_2_out, not_3_out, not_4_out, not_5_out, not_6_out, OP5, OP4, not_7_out, not_8_out);
  and and_2 (and_2_out, not_9_out, not_10_out, F14, F13, F12, not_11_out, OP5, OP4, not_12_out, not_13_out);
  and and_3 (and_3_out, not_14_out, not_15_out, not_16_out, F13, not_17_out, not_18_out, OP5, OP4, not_19_out, not_20_out);
  and and_4 (and_4_out, not_21_out, not_22_out, not_23_out, not_24_out, not_25_out, OP4, not_26_out, not_27_out);
  and and_5 (and_5_out, F14, F13, F12, not_28_out, not_29_out, OP4, not_30_out, not_31_out);
  and and_6 (and_6_out, F14, not_32_out, not_33_out, not_34_out, not_35_out, OP4, not_36_out, not_37_out);
  and and_7 (and_7_out, not_38_out, F13, not_39_out, not_40_out, not_41_out, OP4, not_42_out, not_43_out);
  and and_8 (and_8_out, F30, not_44_out, F14, not_45_out, F12, not_46_out, not_47_out, OP4, not_48_out, not_49_out);
  and and_9 (and_9_out, not_50_out, F13, not_51_out, not_52_out, not_53_out, not_54_out, not_55_out, not_56_out);
  and and_10 (and_10_out, not_57_out, F13, not_58_out, not_59_out, OP5, not_60_out, not_61_out, not_62_out);
  and and_11 (and_11_out, not_63_out, not_64_out, not_65_out, OP6, OP5, not_66_out, not_67_out, OP2);
  and and_12 (and_12_out, F14, not_68_out, not_69_out, not_70_out, OP5, OP4, not_71_out, not_72_out);
  and and_13 (and_13_out, not_73_out, not_74_out, not_75_out, not_76_out, OP5, not_77_out, not_78_out, not_79_out);
  and and_14 (and_14_out, F30, not_80_out, not_81_out, not_82_out, not_83_out, not_84_out, OP5, OP4, not_85_out, not_86_out);
  and and_15 (and_15_out, not_87_out, not_88_out, F14, F13, F12, not_89_out, OP5, OP4, not_90_out, not_91_out);
  and and_16 (and_16_out, not_92_out, not_93_out, not_94_out, F13, not_95_out, not_96_out, OP5, OP4, not_97_out, not_98_out);
  and and_17 (and_17_out, F14, F13, F12, not_99_out, not_100_out, OP4, not_101_out, not_102_out);
  and and_18 (and_18_out, not_103_out, F13, not_104_out, not_105_out, not_106_out, OP4, not_107_out, not_108_out);
  and and_19 (and_19_out, not_109_out, not_110_out, F14, not_111_out, F12, not_112_out, not_113_out, OP4, not_114_out, not_115_out);
  and and_20 (and_20_out, not_116_out, not_117_out, not_118_out, OP6, OP5, not_119_out, not_120_out, not_121_out);
  and and_21 (and_21_out, not_122_out, not_123_out, F12, OP6, OP5, not_124_out, not_125_out, not_126_out);
  and and_22 (and_22_out, not_127_out, not_128_out, not_129_out, not_130_out, not_131_out, not_132_out, OP5, OP4, not_133_out, not_134_out);
  and and_23 (and_23_out, F30, not_135_out, not_136_out, not_137_out, not_138_out, not_139_out, OP5, OP4, not_140_out, not_141_out);
  and and_24 (and_24_out, not_142_out, not_143_out, F14, F13, F12, not_144_out, OP5, OP4, not_145_out, not_146_out);
  and and_25 (and_25_out, not_147_out, not_148_out, not_149_out, F13, F12, not_150_out, OP5, OP4, not_151_out, not_152_out);
  and and_26 (and_26_out, not_153_out, not_154_out, not_155_out, not_156_out, not_157_out, OP4, not_158_out, not_159_out);
  and and_27 (and_27_out, F14, F13, F12, not_160_out, not_161_out, OP4, not_162_out, not_163_out);
  and and_28 (and_28_out, not_164_out, F13, not_165_out, not_166_out, not_167_out, not_168_out, not_169_out, not_170_out);
  and and_29 (and_29_out, not_171_out, F13, not_172_out, not_173_out, OP5, not_174_out, not_175_out, not_176_out);
  and and_30 (and_30_out, not_177_out, not_178_out, not_179_out, OP6, OP5, not_180_out, not_181_out, not_182_out);
  and and_31 (and_31_out, not_183_out, not_184_out, F12, OP6, OP5, not_185_out, not_186_out, not_187_out);
  and and_32 (and_32_out, not_188_out, not_189_out, not_190_out, OP6, OP5, not_191_out, not_192_out, OP2);
  and and_33 (and_33_out, not_193_out, not_194_out, not_195_out, not_196_out, OP5, not_197_out, not_198_out, not_199_out);
  and and_34 (and_34_out, F14, F13, not_200_out, OP6, OP5, not_201_out, not_202_out, not_203_out);
  and and_35 (and_35_out, not_204_out, not_205_out, F14, F13, not_206_out, not_207_out, OP5, OP4, not_208_out, not_209_out);
  and and_36 (and_36_out, not_210_out, not_211_out, not_212_out, F13, not_213_out, not_214_out, OP5, OP4, not_215_out, not_216_out);
  and and_37 (and_37_out, not_217_out, not_218_out, not_219_out, F13, F12, not_220_out, OP5, OP4, not_221_out, not_222_out);
  and and_38 (and_38_out, F14, F13, not_223_out, not_224_out, not_225_out, OP4, not_226_out, not_227_out);
  and and_39 (and_39_out, F14, not_228_out, not_229_out, not_230_out, not_231_out, OP4, not_232_out, not_233_out);
  and and_40 (and_40_out, not_234_out, F13, not_235_out, not_236_out, not_237_out, OP4, not_238_out, not_239_out);
  and and_41 (and_41_out, F14, not_240_out, not_241_out, not_242_out, OP5, OP4, not_243_out, not_244_out);
  and and_42 (and_42_out, F14, F13, not_245_out, OP6, OP5, not_246_out, not_247_out, not_248_out);
  or or_1 (S0, and_1_out, and_2_out, and_3_out, and_4_out, and_5_out, and_6_out, and_7_out, and_8_out, and_9_out, and_10_out, and_11_out, and_12_out, and_13_out);
  or or_2 (S1, and_14_out, and_15_out, and_16_out, and_17_out, and_18_out, and_19_out, and_20_out, and_21_out);
  or or_3 (S2, and_22_out, and_23_out, and_24_out, and_25_out, and_26_out, and_27_out, and_28_out, and_29_out, and_30_out, and_31_out, and_32_out, and_33_out, and_34_out);
  or or_4 (S3, and_35_out, and_36_out, and_37_out, and_38_out, and_39_out, and_40_out, and_41_out, and_42_out);
endmodule

// 控制信号生成
module \控制信号自动生成  (
  input  OP2,
  input  OP3,
  input  OP4,
  input  OP5,
  input  OP6,
  input  F12,
  input  F13,
  input  F14,
  input  F25,
  input  F30,
  output MemToReg,
  output MemWrite,
  output bltu,
  output setI,
  output clearI,
  output sb,
  output sll,
  output ALU_SRC,
  output RegWrite,
  output ecall,
  output S_Type,
  output BEQ,
  output BNE,
  output JALR,
  output JAL,
  output I,
  output B
);

  wire and_2_out, and_3_out, and_9_out, and_10_out, and_11_out, and_12_out, and_13_out, and_14_out,
       and_15_out, and_16_out, and_17_out, and_18_out, and_19_out, and_20_out, and_21_out, and_22_out,
       and_23_out, and_24_out, and_25_out, and_26_out, and_27_out, and_28_out, and_29_out, and_30_out,
       and_31_out, and_32_out, and_33_out, and_34_out, and_35_out, and_36_out, and_37_out, and_38_out,
       and_39_out, and_40_out, and_41_out, and_42_out, and_43_out, and_48_out, and_49_out, and_50_out,
       and_51_out, and_52_out, and_53_out, and_54_out, and_55_out, and_56_out, and_57_out, and_58_out,
       and_59_out, and_60_out, not_1_out, not_2_out, not_3_out, not_4_out, not_5_out, not_6_out, not_7_out,
       not_8_out, not_9_out, not_10_out, not_11_out, not_12_out, not_13_out, not_14_out, not_15_out,
       not_16_out, not_17_out, not_18_out, not_19_out, not_20_out, not_21_out, not_22_out, not_23_out,
       not_24_out, not_25_out, not_26_out, not_27_out, not_28_out, not_29_out, not_30_out, not_31_out,
       not_32_out, not_33_out, not_34_out, not_35_out, not_36_out, not_37_out, not_38_out, not_39_out,
       not_40_out, not_41_out, not_42_out, not_43_out, not_44_out, not_45_out, not_46_out, not_47_out,
       not_48_out, not_49_out, not_50_out, not_51_out, not_52_out, not_53_out, not_54_out, not_55_out,
       not_56_out, not_57_out, not_58_out, not_59_out, not_60_out, not_61_out, not_62_out, not_63_out,
       not_64_out, not_65_out, not_66_out, not_67_out, not_68_out, not_69_out, not_70_out, not_71_out,
       not_72_out, not_73_out, not_74_out, not_75_out, not_76_out, not_77_out, not_78_out, not_79_out,
       not_80_out, not_81_out, not_82_out, not_83_out, not_84_out, not_85_out, not_86_out, not_87_out,
       not_88_out, not_89_out, not_90_out, not_91_out, not_92_out, not_93_out, not_94_out, not_95_out,
       not_96_out, not_97_out, not_98_out, not_99_out, not_100_out, not_101_out, not_102_out, not_103_out,
       not_104_out, not_105_out, not_106_out, not_107_out, not_108_out, not_109_out, not_110_out,
       not_111_out, not_112_out, not_113_out, not_114_out, not_115_out, not_116_out, not_117_out,
       not_118_out, not_119_out, not_120_out, not_121_out, not_122_out, not_123_out, not_124_out,
       not_125_out, not_126_out, not_127_out, not_128_out, not_129_out, not_130_out, not_131_out,
       not_132_out, not_133_out, not_134_out, not_135_out, not_136_out, not_137_out, not_138_out,
       not_139_out, not_140_out, not_141_out, not_142_out, not_143_out, not_144_out, not_145_out,
       not_146_out, not_147_out, not_148_out, not_149_out, not_150_out, not_151_out, not_152_out,
       not_153_out, not_154_out, not_155_out, not_156_out, not_157_out, not_158_out, not_159_out,
       not_160_out, not_161_out, not_162_out, not_163_out, not_164_out, not_165_out, not_166_out,
       not_167_out, not_168_out, not_169_out, not_170_out, not_171_out, not_172_out, not_173_out,
       not_174_out, not_175_out, not_176_out, not_177_out, not_178_out, not_179_out, not_180_out,
       not_181_out, not_182_out, not_183_out, not_184_out, not_185_out, not_186_out, not_187_out,
       not_188_out, not_189_out, not_190_out, not_191_out, not_192_out, not_193_out, not_194_out,
       not_195_out, not_196_out, not_197_out, not_198_out, not_199_out, not_200_out, not_201_out,
       not_202_out, not_203_out, not_204_out, not_205_out, not_206_out, not_207_out, not_208_out,
       not_209_out, not_210_out, not_211_out, not_212_out, not_213_out, not_214_out, not_215_out,
       not_216_out, not_217_out, not_218_out, not_219_out, not_220_out, not_221_out, not_222_out,
       not_223_out, not_224_out, not_225_out, not_226_out, not_227_out, not_228_out, not_229_out,
       not_230_out, not_231_out, not_232_out, not_233_out, not_234_out, not_235_out, not_236_out,
       not_237_out, not_238_out, not_239_out, not_240_out, not_241_out, not_242_out, not_243_out,
       not_244_out, not_245_out, not_246_out, not_247_out, not_248_out, not_249_out, not_250_out,
       not_251_out, not_252_out, not_253_out, not_254_out, not_255_out, not_256_out, not_257_out,
       not_258_out, not_259_out, not_260_out, not_261_out, not_262_out, not_263_out, not_264_out,
       not_265_out, not_266_out, not_267_out, not_268_out, not_269_out, not_270_out, not_271_out,
       not_272_out, not_273_out, not_274_out, not_275_out, not_276_out, not_277_out, not_278_out,
       not_279_out, not_280_out, not_281_out, not_282_out, not_283_out, not_284_out, not_285_out,
       not_286_out, not_287_out, not_288_out, not_289_out, not_290_out, not_291_out, not_292_out,
       not_293_out, not_294_out, not_295_out, not_296_out, not_297_out, not_298_out, not_299_out,
       not_300_out, not_301_out, not_302_out, not_303_out, not_304_out, not_305_out, not_306_out,
       not_307_out, not_308_out, not_309_out, not_310_out, not_311_out, not_312_out, not_313_out,
       not_314_out, not_315_out, not_316_out, not_317_out, not_318_out, not_319_out, not_320_out,
       not_321_out, not_322_out, not_323_out, not_324_out, not_325_out, not_326_out, not_327_out,
       not_328_out, not_329_out, not_330_out, not_331_out, not_332_out, not_333_out, not_334_out,
       not_335_out, not_336_out, not_337_out, not_338_out, not_339_out, not_340_out, not_341_out,
       not_342_out, not_343_out, not_344_out, not_345_out, not_346_out, not_347_out, not_348_out;

  not not_1 (not_1_out, F14);
  not not_2 (not_2_out, F12);
  not not_3 (not_3_out, OP6);
  not not_4 (not_4_out, OP5);
  not not_5 (not_5_out, OP4);
  not not_6 (not_6_out, OP3);
  not not_7 (not_7_out, OP2);
  not not_8 (not_8_out, F14);
  not not_9 (not_9_out, F12);
  not not_10 (not_10_out, OP6);
  not not_11 (not_11_out, OP4);
  not not_12 (not_12_out, OP3);
  not not_13 (not_13_out, OP2);
  not not_14 (not_14_out, F14);
  not not_15 (not_15_out, F13);
  not not_16 (not_16_out, F12);
  not not_17 (not_17_out, OP6);
  not not_18 (not_18_out, OP4);
  not not_19 (not_19_out, OP3);
  not not_20 (not_20_out, OP2);
  not not_21 (not_21_out, F12);
  not not_22 (not_22_out, OP4);
  not not_23 (not_23_out, OP3);
  not not_24 (not_24_out, OP2);
  not not_25 (not_25_out, F12);
  not not_26 (not_26_out, OP3);
  not not_27 (not_27_out, OP2);
  not not_28 (not_28_out, OP3);
  not not_29 (not_29_out, OP2);
  not not_30 (not_30_out, F14);
  not not_31 (not_31_out, F13);
  not not_32 (not_32_out, F12);
  not not_33 (not_33_out, OP6);
  not not_34 (not_34_out, OP4);
  not not_35 (not_35_out, OP3);
  not not_36 (not_36_out, OP2);
  not not_37 (not_37_out, F30);
  not not_38 (not_38_out, F25);
  not not_39 (not_39_out, F14);
  not not_40 (not_40_out, F13);
  not not_41 (not_41_out, OP6);
  not not_42 (not_42_out, OP3);
  not not_43 (not_43_out, OP2);
  not not_44 (not_44_out, F14);
  not not_45 (not_45_out, F13);
  not not_46 (not_46_out, F12);
  not not_47 (not_47_out, OP6);
  not not_48 (not_48_out, OP5);
  not not_49 (not_49_out, OP3);
  not not_50 (not_50_out, OP2);
  not not_51 (not_51_out, OP6);
  not not_52 (not_52_out, OP5);
  not not_53 (not_53_out, OP3);
  not not_54 (not_54_out, OP2);
  not not_55 (not_55_out, F12);
  not not_56 (not_56_out, OP6);
  not not_57 (not_57_out, OP5);
  not not_58 (not_58_out, OP3);
  not not_59 (not_59_out, OP2);
  not not_60 (not_60_out, F13);
  not not_61 (not_61_out, F12);
  not not_62 (not_62_out, OP6);
  not not_63 (not_63_out, OP5);
  not not_64 (not_64_out, OP3);
  not not_65 (not_65_out, OP2);
  not not_66 (not_66_out, F14);
  not not_67 (not_67_out, F12);
  not not_68 (not_68_out, OP6);
  not not_69 (not_69_out, OP5);
  not not_70 (not_70_out, OP3);
  not not_71 (not_71_out, OP2);
  not not_72 (not_72_out, F30);
  not not_73 (not_73_out, F25);
  not not_74 (not_74_out, F14);
  not not_75 (not_75_out, F13);
  not not_76 (not_76_out, OP6);
  not not_77 (not_77_out, OP5);
  not not_78 (not_78_out, OP3);
  not not_79 (not_79_out, OP2);
  not not_80 (not_80_out, F30);
  not not_81 (not_81_out, F25);
  not not_82 (not_82_out, F13);
  not not_83 (not_83_out, OP6);
  not not_84 (not_84_out, OP5);
  not not_85 (not_85_out, OP3);
  not not_86 (not_86_out, OP2);
  not not_87 (not_87_out, F25);
  not not_88 (not_88_out, F13);
  not not_89 (not_89_out, OP6);
  not not_90 (not_90_out, OP5);
  not not_91 (not_91_out, OP3);
  not not_92 (not_92_out, OP2);
  not not_93 (not_93_out, F14);
  not not_94 (not_94_out, F12);
  not not_95 (not_95_out, OP6);
  not not_96 (not_96_out, OP5);
  not not_97 (not_97_out, OP4);
  not not_98 (not_98_out, OP3);
  not not_99 (not_99_out, OP2);
  not not_100 (not_100_out, F14);
  not not_101 (not_101_out, F12);
  not not_102 (not_102_out, OP6);
  not not_103 (not_103_out, OP4);
  not not_104 (not_104_out, OP3);
  not not_105 (not_105_out, OP2);
  not not_106 (not_106_out, F14);
  not not_107 (not_107_out, F13);
  not not_108 (not_108_out, F12);
  not not_109 (not_109_out, OP4);
  not not_110 (not_110_out, OP3);
  not not_111 (not_111_out, F14);
  not not_112 (not_112_out, F13);
  not not_113 (not_113_out, F12);
  not not_114 (not_114_out, OP6);
  not not_115 (not_115_out, OP4);
  not not_116 (not_116_out, OP3);
  not not_117 (not_117_out, OP2);
  not not_118 (not_118_out, F30);
  not not_119 (not_119_out, F25);
  not not_120 (not_120_out, F14);
  not not_121 (not_121_out, F13);
  not not_122 (not_122_out, F12);
  not not_123 (not_123_out, OP6);
  not not_124 (not_124_out, OP3);
  not not_125 (not_125_out, OP2);
  not not_126 (not_126_out, F25);
  not not_127 (not_127_out, F14);
  not not_128 (not_128_out, F13);
  not not_129 (not_129_out, F12);
  not not_130 (not_130_out, OP6);
  not not_131 (not_131_out, OP3);
  not not_132 (not_132_out, OP2);
  not not_133 (not_133_out, F30);
  not not_134 (not_134_out, F25);
  not not_135 (not_135_out, OP6);
  not not_136 (not_136_out, OP3);
  not not_137 (not_137_out, OP2);
  not not_138 (not_138_out, F30);
  not not_139 (not_139_out, F25);
  not not_140 (not_140_out, F12);
  not not_141 (not_141_out, OP6);
  not not_142 (not_142_out, OP3);
  not not_143 (not_143_out, OP2);
  not not_144 (not_144_out, F30);
  not not_145 (not_145_out, F25);
  not not_146 (not_146_out, F14);
  not not_147 (not_147_out, F12);
  not not_148 (not_148_out, OP6);
  not not_149 (not_149_out, OP3);
  not not_150 (not_150_out, OP2);
  not not_151 (not_151_out, F30);
  not not_152 (not_152_out, F25);
  not not_153 (not_153_out, F14);
  not not_154 (not_154_out, OP6);
  not not_155 (not_155_out, OP3);
  not not_156 (not_156_out, OP2);
  not not_157 (not_157_out, F14);
  not not_158 (not_158_out, F13);
  not not_159 (not_159_out, F12);
  not not_160 (not_160_out, OP6);
  not not_161 (not_161_out, OP5);
  not not_162 (not_162_out, OP3);
  not not_163 (not_163_out, OP2);
  not not_164 (not_164_out, OP6);
  not not_165 (not_165_out, OP5);
  not not_166 (not_166_out, OP3);
  not not_167 (not_167_out, OP2);
  not not_168 (not_168_out, F12);
  not not_169 (not_169_out, OP6);
  not not_170 (not_170_out, OP5);
  not not_171 (not_171_out, OP3);
  not not_172 (not_172_out, OP2);
  not not_173 (not_173_out, F13);
  not not_174 (not_174_out, F12);
  not not_175 (not_175_out, OP6);
  not not_176 (not_176_out, OP5);
  not not_177 (not_177_out, OP3);
  not not_178 (not_178_out, OP2);
  not not_179 (not_179_out, F14);
  not not_180 (not_180_out, F12);
  not not_181 (not_181_out, OP6);
  not not_182 (not_182_out, OP5);
  not not_183 (not_183_out, OP3);
  not not_184 (not_184_out, OP2);
  not not_185 (not_185_out, F30);
  not not_186 (not_186_out, F25);
  not not_187 (not_187_out, F14);
  not not_188 (not_188_out, F13);
  not not_189 (not_189_out, OP6);
  not not_190 (not_190_out, OP5);
  not not_191 (not_191_out, OP3);
  not not_192 (not_192_out, OP2);
  not not_193 (not_193_out, F30);
  not not_194 (not_194_out, F25);
  not not_195 (not_195_out, F13);
  not not_196 (not_196_out, OP6);
  not not_197 (not_197_out, OP5);
  not not_198 (not_198_out, OP3);
  not not_199 (not_199_out, OP2);
  not not_200 (not_200_out, F25);
  not not_201 (not_201_out, F13);
  not not_202 (not_202_out, OP6);
  not not_203 (not_203_out, OP5);
  not not_204 (not_204_out, OP3);
  not not_205 (not_205_out, OP2);
  not not_206 (not_206_out, F14);
  not not_207 (not_207_out, F12);
  not not_208 (not_208_out, OP6);
  not not_209 (not_209_out, OP5);
  not not_210 (not_210_out, OP4);
  not not_211 (not_211_out, OP3);
  not not_212 (not_212_out, OP2);
  not not_213 (not_213_out, OP4);
  not not_214 (not_214_out, F14);
  not not_215 (not_215_out, F13);
  not not_216 (not_216_out, F12);
  not not_217 (not_217_out, OP4);
  not not_218 (not_218_out, OP3);
  not not_219 (not_219_out, F30);
  not not_220 (not_220_out, F25);
  not not_221 (not_221_out, F14);
  not not_222 (not_222_out, F13);
  not not_223 (not_223_out, OP6);
  not not_224 (not_224_out, OP3);
  not not_225 (not_225_out, OP2);
  not not_226 (not_226_out, F13);
  not not_227 (not_227_out, F12);
  not not_228 (not_228_out, OP6);
  not not_229 (not_229_out, OP3);
  not not_230 (not_230_out, OP2);
  not not_231 (not_231_out, F30);
  not not_232 (not_232_out, F25);
  not not_233 (not_233_out, F14);
  not not_234 (not_234_out, F13);
  not not_235 (not_235_out, F12);
  not not_236 (not_236_out, OP3);
  not not_237 (not_237_out, OP2);
  not not_238 (not_238_out, F14);
  not not_239 (not_239_out, F13);
  not not_240 (not_240_out, F12);
  not not_241 (not_241_out, OP3);
  not not_242 (not_242_out, OP2);
  not not_243 (not_243_out, F14);
  not not_244 (not_244_out, F12);
  not not_245 (not_245_out, OP6);
  not not_246 (not_246_out, OP4);
  not not_247 (not_247_out, OP3);
  not not_248 (not_248_out, OP2);
  not not_249 (not_249_out, F14);
  not not_250 (not_250_out, F13);
  not not_251 (not_251_out, F12);
  not not_252 (not_252_out, OP6);
  not not_253 (not_253_out, OP4);
  not not_254 (not_254_out, OP3);
  not not_255 (not_255_out, OP2);
  not not_256 (not_256_out, F14);
  not not_257 (not_257_out, F13);
  not not_258 (not_258_out, F12);
  not not_259 (not_259_out, OP4);
  not not_260 (not_260_out, OP3);
  not not_261 (not_261_out, OP2);
  not not_262 (not_262_out, F14);
  not not_263 (not_263_out, F13);
  not not_264 (not_264_out, OP4);
  not not_265 (not_265_out, OP3);
  not not_266 (not_266_out, OP2);
  not not_267 (not_267_out, F14);
  not not_268 (not_268_out, F13);
  not not_269 (not_269_out, F12);
  not not_270 (not_270_out, OP4);
  not not_271 (not_271_out, OP3);
  not not_272 (not_272_out, OP4);
  not not_273 (not_273_out, F14);
  not not_274 (not_274_out, F13);
  not not_275 (not_275_out, F12);
  not not_276 (not_276_out, OP6);
  not not_277 (not_277_out, OP5);
  not not_278 (not_278_out, OP3);
  not not_279 (not_279_out, OP2);
  not not_280 (not_280_out, OP6);
  not not_281 (not_281_out, OP5);
  not not_282 (not_282_out, OP3);
  not not_283 (not_283_out, OP2);
  not not_284 (not_284_out, F12);
  not not_285 (not_285_out, OP6);
  not not_286 (not_286_out, OP5);
  not not_287 (not_287_out, OP3);
  not not_288 (not_288_out, OP2);
  not not_289 (not_289_out, F13);
  not not_290 (not_290_out, F12);
  not not_291 (not_291_out, OP6);
  not not_292 (not_292_out, OP5);
  not not_293 (not_293_out, OP3);
  not not_294 (not_294_out, OP2);
  not not_295 (not_295_out, F14);
  not not_296 (not_296_out, F12);
  not not_297 (not_297_out, OP6);
  not not_298 (not_298_out, OP5);
  not not_299 (not_299_out, OP3);
  not not_300 (not_300_out, OP2);
  not not_301 (not_301_out, F30);
  not not_302 (not_302_out, F25);
  not not_303 (not_303_out, F14);
  not not_304 (not_304_out, F13);
  not not_305 (not_305_out, OP6);
  not not_306 (not_306_out, OP5);
  not not_307 (not_307_out, OP3);
  not not_308 (not_308_out, OP2);
  not not_309 (not_309_out, F30);
  not not_310 (not_310_out, F25);
  not not_311 (not_311_out, F13);
  not not_312 (not_312_out, OP6);
  not not_313 (not_313_out, OP5);
  not not_314 (not_314_out, OP3);
  not not_315 (not_315_out, OP2);
  not not_316 (not_316_out, F25);
  not not_317 (not_317_out, F13);
  not not_318 (not_318_out, OP6);
  not not_319 (not_319_out, OP5);
  not not_320 (not_320_out, OP3);
  not not_321 (not_321_out, OP2);
  not not_322 (not_322_out, F14);
  not not_323 (not_323_out, F12);
  not not_324 (not_324_out, OP6);
  not not_325 (not_325_out, OP5);
  not not_326 (not_326_out, OP4);
  not not_327 (not_327_out, OP3);
  not not_328 (not_328_out, OP2);
  not not_329 (not_329_out, F14);
  not not_330 (not_330_out, F13);
  not not_331 (not_331_out, F12);
  not not_332 (not_332_out, OP4);
  not not_333 (not_333_out, OP3);
  not not_334 (not_334_out, F14);
  not not_335 (not_335_out, F13);
  not not_336 (not_336_out, F12);
  not not_337 (not_337_out, OP4);
  not not_338 (not_338_out, OP3);
  not not_339 (not_339_out, OP2);
  not not_340 (not_340_out, F14);
  not not_341 (not_341_out, F13);
  not not_342 (not_342_out, OP4);
  not not_343 (not_343_out, OP3);
  not not_344 (not_344_out, OP2);
  not not_345 (not_345_out, F12);
  not not_346 (not_346_out, OP4);
  not not_347 (not_347_out, OP3);
  not not_348 (not_348_out, OP2);
  and and_1 (MemToReg, not_1_out, F13, not_2_out, not_3_out, not_4_out, not_5_out, not_6_out, not_7_out);
  and and_2 (and_2_out, not_8_out, F13, not_9_out, not_10_out, OP5, not_11_out, not_12_out, not_13_out);
  and and_3 (and_3_out, not_14_out, not_15_out, not_16_out, not_17_out, OP5, not_18_out, not_19_out, not_20_out);
  and and_4 (bltu, F14, F13, not_21_out, OP6, OP5, not_22_out, not_23_out, not_24_out);
  and and_5 (setI, F14, F13, not_25_out, OP6, OP5, OP4, not_26_out, not_27_out);
  and and_6 (clearI, F14, F13, F12, OP6, OP5, OP4, not_28_out, not_29_out);
  and and_7 (sb, not_30_out, not_31_out, not_32_out, not_33_out, OP5, not_34_out, not_35_out, not_36_out);
  and and_8 (sll, not_37_out, not_38_out, not_39_out, not_40_out, F12, not_41_out, OP5, OP4, not_42_out, not_43_out);
  and and_9 (and_9_out, not_44_out, not_45_out, not_46_out, not_47_out, not_48_out, OP4, not_49_out, not_50_out);
  and and_10 (and_10_out, F14, F13, F12, not_51_out, not_52_out, OP4, not_53_out, not_54_out);
  and and_11 (and_11_out, F14, F13, not_55_out, not_56_out, not_57_out, OP4, not_58_out, not_59_out);
  and and_12 (and_12_out, F14, not_60_out, not_61_out, not_62_out, not_63_out, OP4, not_64_out, not_65_out);
  and and_13 (and_13_out, not_66_out, F13, not_67_out, not_68_out, not_69_out, OP4, not_70_out, not_71_out);
  and and_14 (and_14_out, not_72_out, not_73_out, not_74_out, not_75_out, F12, not_76_out, not_77_out, OP4, not_78_out, not_79_out);
  and and_15 (and_15_out, not_80_out, not_81_out, F14, not_82_out, F12, not_83_out, not_84_out, OP4, not_85_out, not_86_out);
  and and_16 (and_16_out, F30, not_87_out, F14, not_88_out, F12, not_89_out, not_90_out, OP4, not_91_out, not_92_out);
  and and_17 (and_17_out, not_93_out, F13, not_94_out, not_95_out, not_96_out, not_97_out, not_98_out, not_99_out);
  and and_18 (and_18_out, not_100_out, F13, not_101_out, not_102_out, OP5, not_103_out, not_104_out, not_105_out);
  and and_19 (and_19_out, not_106_out, not_107_out, not_108_out, OP6, OP5, not_109_out, not_110_out, OP2);
  and and_20 (and_20_out, not_111_out, not_112_out, not_113_out, not_114_out, OP5, not_115_out, not_116_out, not_117_out);
  and and_21 (and_21_out, not_118_out, not_119_out, not_120_out, not_121_out, not_122_out, not_123_out, OP5, OP4, not_124_out, not_125_out);
  and and_22 (and_22_out, F30, not_126_out, not_127_out, not_128_out, not_129_out, not_130_out, OP5, OP4, not_131_out, not_132_out);
  and and_23 (and_23_out, not_133_out, not_134_out, F14, F13, F12, not_135_out, OP5, OP4, not_136_out, not_137_out);
  and and_24 (and_24_out, not_138_out, not_139_out, F14, F13, not_140_out, not_141_out, OP5, OP4, not_142_out, not_143_out);
  and and_25 (and_25_out, not_144_out, not_145_out, not_146_out, F13, not_147_out, not_148_out, OP5, OP4, not_149_out, not_150_out);
  and and_26 (and_26_out, not_151_out, not_152_out, not_153_out, F13, F12, not_154_out, OP5, OP4, not_155_out, not_156_out);
  and and_27 (and_27_out, not_157_out, not_158_out, not_159_out, not_160_out, not_161_out, OP4, not_162_out, not_163_out);
  and and_28 (and_28_out, F14, F13, F12, not_164_out, not_165_out, OP4, not_166_out, not_167_out);
  and and_29 (and_29_out, F14, F13, not_168_out, not_169_out, not_170_out, OP4, not_171_out, not_172_out);
  and and_30 (and_30_out, F14, not_173_out, not_174_out, not_175_out, not_176_out, OP4, not_177_out, not_178_out);
  and and_31 (and_31_out, not_179_out, F13, not_180_out, not_181_out, not_182_out, OP4, not_183_out, not_184_out);
  and and_32 (and_32_out, not_185_out, not_186_out, not_187_out, not_188_out, F12, not_189_out, not_190_out, OP4, not_191_out, not_192_out);
  and and_33 (and_33_out, not_193_out, not_194_out, F14, not_195_out, F12, not_196_out, not_197_out, OP4, not_198_out, not_199_out);
  and and_34 (and_34_out, F30, not_200_out, F14, not_201_out, F12, not_202_out, not_203_out, OP4, not_204_out, not_205_out);
  and and_35 (and_35_out, not_206_out, F13, not_207_out, not_208_out, not_209_out, not_210_out, not_211_out, not_212_out);
  and and_36 (and_36_out, OP6, OP5, not_213_out, OP3, OP2);
  and and_37 (and_37_out, not_214_out, not_215_out, not_216_out, OP6, OP5, not_217_out, not_218_out, OP2);
  and and_38 (and_38_out, not_219_out, not_220_out, not_221_out, not_222_out, F12, not_223_out, OP5, OP4, not_224_out, not_225_out);
  and and_39 (and_39_out, F14, not_226_out, not_227_out, not_228_out, OP5, OP4, not_229_out, not_230_out);
  and and_40 (and_40_out, not_231_out, not_232_out, not_233_out, not_234_out, not_235_out, OP6, OP5, OP4, not_236_out, not_237_out);
  and and_41 (and_41_out, not_238_out, not_239_out, not_240_out, OP6, OP5, OP4, not_241_out, not_242_out);
  and and_42 (and_42_out, not_243_out, F13, not_244_out, not_245_out, OP5, not_246_out, not_247_out, not_248_out);
  and and_43 (and_43_out, not_249_out, not_250_out, not_251_out, not_252_out, OP5, not_253_out, not_254_out, not_255_out);
  and and_44 (BEQ, not_256_out, not_257_out, not_258_out, OP6, OP5, not_259_out, not_260_out, not_261_out);
  and and_45 (BNE, not_262_out, not_263_out, F12, OP6, OP5, not_264_out, not_265_out, not_266_out);
  and and_46 (JALR, not_267_out, not_268_out, not_269_out, OP6, OP5, not_270_out, not_271_out, OP2);
  and and_47 (JAL, OP6, OP5, not_272_out, OP3, OP2);
  and and_48 (and_48_out, not_273_out, not_274_out, not_275_out, not_276_out, not_277_out, OP4, not_278_out, not_279_out);
  and and_49 (and_49_out, F14, F13, F12, not_280_out, not_281_out, OP4, not_282_out, not_283_out);
  and and_50 (and_50_out, F14, F13, not_284_out, not_285_out, not_286_out, OP4, not_287_out, not_288_out);
  and and_51 (and_51_out, F14, not_289_out, not_290_out, not_291_out, not_292_out, OP4, not_293_out, not_294_out);
  and and_52 (and_52_out, not_295_out, F13, not_296_out, not_297_out, not_298_out, OP4, not_299_out, not_300_out);
  and and_53 (and_53_out, not_301_out, not_302_out, not_303_out, not_304_out, F12, not_305_out, not_306_out, OP4, not_307_out, not_308_out);
  and and_54 (and_54_out, not_309_out, not_310_out, F14, not_311_out, F12, not_312_out, not_313_out, OP4, not_314_out, not_315_out);
  and and_55 (and_55_out, F30, not_316_out, F14, not_317_out, F12, not_318_out, not_319_out, OP4, not_320_out, not_321_out);
  and and_56 (and_56_out, not_322_out, F13, not_323_out, not_324_out, not_325_out, not_326_out, not_327_out, not_328_out);
  and and_57 (and_57_out, not_329_out, not_330_out, not_331_out, OP6, OP5, not_332_out, not_333_out, OP2);
  and and_58 (and_58_out, not_334_out, not_335_out, not_336_out, OP6, OP5, not_337_out, not_338_out, not_339_out);
  and and_59 (and_59_out, not_340_out, not_341_out, F12, OP6, OP5, not_342_out, not_343_out, not_344_out);
  and and_60 (and_60_out, F14, F13, not_345_out, OP6, OP5, not_346_out, not_347_out, not_348_out);
  or or_1 (MemWrite, and_2_out, and_3_out);
  or or_2 (ecall, and_40_out, and_41_out);
  or or_3 (S_Type, and_42_out, and_43_out);
  or or_4 (B, and_58_out, and_59_out, and_60_out);
  or or_5 (ALU_SRC, and_9_out, and_10_out, and_11_out, and_12_out, and_13_out, and_14_out, and_15_out, and_16_out, and_17_out, and_18_out, and_19_out, and_20_out);
  or or_6 (RegWrite, and_21_out, and_22_out, and_23_out, and_24_out, and_25_out, and_26_out, and_27_out, and_28_out, and_29_out, and_30_out, and_31_out, and_32_out, and_33_out, and_34_out, and_35_out, and_36_out, and_37_out, and_38_out, and_39_out);
  or or_7 (I, and_48_out, and_49_out, and_50_out, and_51_out, and_52_out, and_53_out, and_54_out, and_55_out, and_56_out, and_57_out);
endmodule

// ALU
module ALU (
  input  [31:0] X,
  input  [31:0] Y,
  input  [3:0] AluOP,
  output out_4,
  output Equal,
  output out_6,
  output [31:0] Result,
  output [31:0] Result_2
);

  wire [0:0] comparator_1_lt, comparator_2_lt;
  wire [31:0] adder_1_out, AND_out, divider_1_out, divider_1_rem, multiplier_1_cout, multiplier_1_out,
       NOR_out, OR_out, shifter_1_out, shifter_2_out, shifter_3_out, subtractor_1_out, XOR_out;

  assign AND_out = X & Y;  // AND_Gate AND, 32 bits wide
  assign OR_out = X | Y;  // OR_Gate OR, 32 bits wide
  Shifter #(.width(32), .shift("ll")) shifter_1 (.in(X), .\dist (Y[4:0]), .out(shifter_1_out));
  Shifter #(.width(32), .shift("ar")) shifter_2 (.in(X), .\dist (Y[4:0]), .out(shifter_2_out));
  Shifter #(.width(32), .shift("lr")) shifter_3 (.in(X), .\dist (Y[4:0]), .out(shifter_3_out));
  Multiplier #(.width(32)) multiplier_1 (.a(X), .b(Y), .out(multiplier_1_out), .cout(multiplier_1_cout));  // open: cin
  Divider #(.width(32)) divider_1 (.a(X), .b(Y), .out(divider_1_out), .rem(divider_1_rem));  // open: upper
  Adder #(.width(32)) adder_1 (.a(X), .b(Y), .out(adder_1_out));  // open: cin, cout
  Subtractor #(.width(32)) subtractor_1 (.a(X), .b(Y), .out(subtractor_1_out));  // open: bin, bout
  assign XOR_out = X ^ Y;  // XOR_Gate XOR, 32 bits wide
  assign NOR_out = ~(X | Y);  // NOR_Gate NOR, 32 bits wide
  Comparator #(.width(32), .mode("twosComplement")) comparator_1 (
    .a(X), .b(Y), .eq(Equal), .lt(comparator_1_lt[0]));  // open: gt
  Comparator #(.width(32), .mode("unsigned")) comparator_2 (.a(X), .b(Y), .lt(comparator_2_lt[0]));  // open: gt, eq
  Multiplexer #(.select(4), .width(32), .disabled("Z"), .enable("false")) multiplexer_1 (
    .in0(shifter_1_out), .in1(shifter_2_out), .in2(shifter_3_out), .in3(multiplier_1_out),
    .in4(divider_1_out), .in5(adder_1_out), .in6(subtractor_1_out), .in7(AND_out), .in8(OR_out),
    .in9(XOR_out), .in10(NOR_out), .in11({{31{1'b0}}, comparator_1_lt[0]}),
    .in12({{31{1'b0}}, comparator_2_lt[0]}), .in13({32{1'b0}}), .in14({32{1'b0}}), .in15({32{1'b0}}),
    .out(Result), .sel(AluOP));
  Multiplexer #(.select(4), .width(32), .disabled("Z"), .enable("false")) multiplexer_2 (
    .in0({32{1'b0}}), .in1({32{1'b0}}), .in2({32{1'b0}}), .in3(multiplier_1_cout), .in4(divider_1_rem),
    .in5({32{1'b0}}), .in6({32{1'b0}}), .in7({32{1'b0}}), .in8({32{1'b0}}), .in9({32{1'b0}}),
    .in10({32{1'b0}}), .in11({32{1'b0}}), .in12({32{1'b0}}), .in13({32{1'b0}}), .in14({32{1'b0}}),
    .in15({32{1'b0}}), .out(Result_2), .sel(AluOP));
  Multiplexer #(.select(4), .width(1), .disabled("Z"), .enable("false")) multiplexer_3 (
    .in0(1'b0), .in1(1'b0), .in2(1'b0), .in3(1'b0), .in4(1'b0), .in5(1'b0), .in6(1'b0), .in7(1'b0),
    .in8(1'b0), .in9(1'b0), .in10(1'b0), .in11(comparator_1_lt[0]), .in12(comparator_2_lt[0]), .in13(1'b0),
    .in14(1'b0), .in15(1'b0), .out(out_6), .sel(AluOP));
  not not_1 (out_4, out_6);

  // Other names for the same wires on the sheet: Result2[31:0] = Result_2; S[3:0] = AluOP; tunnel = out_6;
  //   tunnel_t = out_4

  // Notes on the sheet:
  //   不要改变此引脚区域内容，也不要改变ALU封装形式
  //   输入引脚
  //   输出引脚
endmodule

module Regifile (
  input  [31:0] Din,
  input  Clk,
  input  WE,
  input  [4:0] R1_num,
  input  [4:0] W_num,
  input  [4:0] R2_num,
  output [31:0] R1,
  output [31:0] R2
);

  // RegisterFile registerfile_1: pin names not known; wires that end beside it: Din, Clk, WE, W_num, R1_num, R2_num, R1, R2
endmodule

module \理想流水线  (
  output RegWrite,
  output MemWrite,
  output [31:0] IF_PC,
  output [31:0] ID_PC,
  output [31:0] EX_PC,
  output [31:0] M_PC,
  output [31:0] WB_PC,
  output [31:0] RDin,
  output [31:0] MDin,
  output [31:0] LedData
);

  wire alu_1_equal, and_1_out, and_3_out, and_4_out, and_5_out, and_6_out, and_7_out, B, bltu, Branch, CLK,
       clock_1_out, comparator_1_eq, comparator_1_lt, d_ff_1_q, ec_eq, ecall, ecall_star, Ex_ec_eq, EX_JALR,
       \ex_mem流水寄存器_1_bltu_2 , \ex_mem流水寄存器_1_ec_eq_2 , \ex_mem流水寄存器_1_ecall_2 , \ex_mem流水寄存器_1_jal_2 ,
       \ex_mem流水寄存器_1_jalr_2 , \ex_mem流水寄存器_1_memtoreg_2 , \ex_mem流水寄存器_1_regwrite_2 , Go, halt, I,
       \id_ex流水寄存器_1_beq_2 , \id_ex流水寄存器_1_bne_2 , \id_ex流水寄存器_1_ecall_2 , \id_ex流水寄存器_1_jal_2 ,
       \id_ex流水寄存器_1_memtoreg_2 , \id_ex流水寄存器_1_memwrite_2 , \id_ex流水寄存器_1_regwrite_2 , \id_ex流水寄存器_1_sb_2 ,
       IR1, IR2, IR3, J, JAL, JAL_star, JALR, JALR_star, lessthen, \mem_wb流水寄存器_1_memtoreg_2 , nand_1_out,
       not_1_out, not_2_out, or_1_out, PC_EN, PCSrc, RST, S_type, sb_star, URET, W1, W2, W3,
       \单周期硬布线控制器_1_alu_src , \单周期硬布线控制器_1_beq , \单周期硬布线控制器_1_bltu , \单周期硬布线控制器_1_bne , \单周期硬布线控制器_1_cleari ,
       \单周期硬布线控制器_1_memtoreg , \单周期硬布线控制器_1_memwrite , \单周期硬布线控制器_1_regwrite , \单周期硬布线控制器_1_sb ,
       \单周期硬布线控制器_1_seti , \单周期硬布线控制器_1_sll ;
  wire [1:0] \id_ex流水寄存器_1_alu_src_2 ;
  wire [3:0] \id_ex流水寄存器_1_aluop_2 , \单周期硬布线控制器_1_alu_op ;
  wire [4:0] EX_W_num, ID_R1_num, ID_R2_num, MEM_W_num, \mem_wb流水寄存器_1_w_num_2 ;
  wire [9:0] \ex_mem流水寄存器_1_address_2 ;
  wire [12:0] CNT_num;
  wire [15:0] \LoadUse次数 , \总周期数 , \插入气泡数 , \无条件分支数 , \条件分支成功数 ;
  wire [31:0] adder_1_out, adder_2_out, and_2_out, bit_extender_1_out, bit_extender_2_out,
       bit_extender_3_out, bit_extender_4_out, ec_out, EX_ec_out, EX_IR, \ex_mem流水寄存器_1_ec_out_2 ,
       \ex_mem流水寄存器_1_pc_4_2 , \ex_mem流水寄存器_1_pc_offset_2 , \ex_mem流水寄存器_1_r2_2 , \ex_mem流水寄存器_1_result_2 ,
       \id_ex流水寄存器_1_pc_4_2 , \id_ex流水寄存器_1_r1_2 , \id_ex流水寄存器_1_r2__sll_2 , \id_ex流水寄存器_1_立即数_2 , ID_IR,
       \if_id流水寄存器_1_pc_4_2 , IF_IR, MEM_IR, \mem_wb流水寄存器_1_mem_3 , \mem_wb流水寄存器_1_pc_4_2 ,
       \mem_wb流水寄存器_1_result_2 , multiplexer_1_out, multiplexer_5_out, multiplexer_6_out, multiplexer_8_out,
       ram_1_data, regifile_1_r1, regifile_1_r2, \sb分线_1_output , shifter_1_out, WB_IR;
  wire [31:1] alu_1_result;

  Button \u_总复位  (.out(RST));
  Button _1 (.out(IR1));
  Button _2 (.out(IR2));
  Button _3 (.out(IR3));
  // Probe on \总周期数 
  // Probe on \总周期数 
  Button \u_继续运行  (.out(Go));
  LED #(.active("true")) led_1 (.in(W1));
  LED #(.active("true")) led_2 (.in(W2));
  LED #(.active("true")) led_3 (.in(W3));
  Hex_Digit_Display hex_digit_display_1 (.value(LedData[31:28]));  // open: dp
  // Probe on IF_PC[19:0]
  // RiscV_Probe riscv_probe_1: pin names not known; wires that end beside it: IF_IR
  Hex_Digit_Display hex_digit_display_2 (.value(LedData[27:24]));  // open: dp
  Hex_Digit_Display hex_digit_display_3 (.value(LedData[23:20]));  // open: dp
  // Probe on ID_PC[19:0]
  // RiscV_Probe riscv_probe_2: pin names not known; wires that end beside it: ID_IR
  Multiplexer #(.select(2), .width(32), .disabled("Z"), .enable("false")) multiplexer_1 (
    .in0(adder_1_out), .in1(adder_2_out), .in2(and_2_out), .out(multiplexer_1_out), .sel({EX_JALR, PCSrc}));  // open: in3
  and and_1 (and_1_out, not_1_out, PC_EN);
  not not_1 (not_1_out, halt);
  Hex_Digit_Display hex_digit_display_4 (.value(LedData[19:16]));  // open: dp
  Hex_Digit_Display hex_digit_display_5 (.value(LedData[15:12]));  // open: dp
  not not_2 (not_2_out, halt);
  Register #(.width(32), .trigger("rising"), .Select("low")) PC (
    .D({{20{1'b0}}, multiplexer_1_out[11:0]}), .en(and_1_out), .Q(IF_PC), .clk(CLK), .clr(RST));
  Hex_Digit_Display hex_digit_display_6 (.value(LedData[11:8]));  // open: dp
  Hex_Digit_Display hex_digit_display_7 (.value(LedData[7:4]));  // open: dp
  // Probe on EX_PC[19:0]
  // RiscV_Probe riscv_probe_3: pin names not known; wires that end beside it: EX_IR
  Counter #(.width(16), .max('hffff), .ongoal("wrap"), .trigger("rising"), .behavior("new")) counter_1 (
    .D(16'h1), .count(not_2_out), .Q(\总周期数 ), .clk(CLK));  // open: load, carry, clr, preset, down
  Hex_Digit_Display hex_digit_display_8 (.value(LedData[3:0]));  // open: dp
  // Probe on IF_PC
  Adder #(.width(32)) adder_1 (.a(IF_PC), .b(32'h4), .out(adder_1_out));  // open: cin, cout
  // Probe on \总周期数 
  // Probe on M_PC[19:0]
  // RiscV_Probe riscv_probe_4: pin names not known; wires that end beside it: MEM_IR
  // Probe on \总周期数 
  // Probe on \无条件分支数 
  // Probe on \条件分支成功数 
  // Probe on \插入气泡数 
  // Probe on \LoadUse次数 
  ROM #(.addrWidth(10), .dataWidth(32), .Select("high")) rom_1 (.addr(IF_PC[11:2]), .data(IF_IR));
  // Probe on IF_PC[11:0]
  // Probe on WB_PC[19:0]
  // RiscV_Probe riscv_probe_5: pin names not known; wires that end beside it: WB_IR
  buf or_1 (or_1_out, halt);  // OR_Gate
  \IF_ID流水寄存器  \if_id流水寄存器_1  (
    .IR(IF_IR), .PC(IF_PC), .PC_4(adder_1_out), .IR_2(ID_IR), .PC_2(ID_PC), .PC_4_2(\if_id流水寄存器_1_pc_4_2 ),
    .CLK(CLK), .\EN使能端 (or_1_out));  // open: 同步清零_高电平有效, PredictJump, PredictJump_2
  // Probe on EX_PC[11:0]
  // Probe on ID_PC[11:0]
  // RiscV_Probe riscv_probe_6: pin names not known; wires that end beside it: ID_IR
  // Probe on M_PC[11:0]
  D_Flip_Flop #(.trigger("high"), .Pre_Clr_Positions("LEGACY"), .NegatePresetClear("false"), .enable("true"), .NewFFLayout("false")) d_ff_1 (.Q(d_ff_1_q));  // open: clk, D, Qn, preset, en, reset
  // Probe on 13'hc
  // Probe on WB_PC[11:0]
  Comparator #(.width(13), .mode("twosComplement")) comparator_1 (
    .a(CNT_num), .b(13'hc), .eq(comparator_1_eq), .lt(comparator_1_lt));  // open: gt
  Clock #(.highDuration(1), .lowDuration(1)) clock_1 (.out(clock_1_out));
  \单周期硬布线控制器  \u_单周期硬布线控制器_1  (
    .Funct({ID_IR[30], ID_IR[25], ID_IR[14:12]}), .OP(ID_IR[6:2]), .ALU_OP(\单周期硬布线控制器_1_alu_op ),
    .MemToReg(\单周期硬布线控制器_1_memtoreg ), .MemWrite(\单周期硬布线控制器_1_memwrite ), .ALU_SRC(\单周期硬布线控制器_1_alu_src ),
    .RegWrite(\单周期硬布线控制器_1_regwrite ), .ecall(ecall), .S_type(S_type), .Jalr(JALR), .Beq(\单周期硬布线控制器_1_beq ),
    .JAL(JAL), .Bne(\单周期硬布线控制器_1_bne ), .in_3(ID_IR[21]), .uret(URET), .I(I), .B(B),
    .clearI(\单周期硬布线控制器_1_cleari ), .sb(\单周期硬布线控制器_1_sb ), .sll(\单周期硬布线控制器_1_sll ), .setI(\单周期硬布线控制器_1_seti ),
    .bltu(\单周期硬布线控制器_1_bltu ));
  assign bit_extender_1_out = {{20{ID_IR[31]}}, ID_IR[31:20]};  // Bit_Extender bit_extender_1
  assign bit_extender_2_out = {{20{ID_IR[31]}}, {ID_IR[31:25], ID_IR[11:7]}};  // Bit_Extender bit_extender_2
  assign bit_extender_3_out = {{20{ID_IR[31]}}, {ID_IR[31], ID_IR[7], ID_IR[30:25], ID_IR[11:8]}};  // Bit_Extender bit_extender_3
  assign bit_extender_4_out = {{12{ID_IR[31]}}, {ID_IR[31], ID_IR[19:12], ID_IR[20], ID_IR[30:21]}};  // Bit_Extender bit_extender_4
  nand nand_1 (nand_1_out, d_ff_1_q, comparator_1_eq);
  Counter #(.width(13), .max('h1fff), .ongoal("stay"), .trigger("rising"), .behavior("old")) counter_2 (
    .count(comparator_1_lt), .Q(CNT_num), .clk(clock_1_out));  // open: load, D, carry, clr, preset
  Multiplexer #(.select(1), .width(5), .disabled("Z"), .enable("false")) multiplexer_2 (
    .in0(ID_IR[19:15]), .in1(5'b10001), .out(ID_R1_num), .sel(ecall));
  Multiplexer #(.select(1), .width(5), .disabled("Z"), .enable("false")) multiplexer_3 (
    .in0(ID_IR[24:20]), .in1(5'b01010), .out(ID_R2_num), .sel(ecall));
  Multiplexer #(.select(1), .width(32), .disabled("Z"), .enable("false")) multiplexer_4 (
    .in0(multiplexer_8_out), .in1(\mem_wb流水寄存器_1_pc_4_2 ), .out(RDin), .sel(J));
  Multiplexer #(.select(4), .width(32), .disabled("Z"), .enable("false")) multiplexer_5 (
    .in1(bit_extender_1_out), .in2(bit_extender_2_out), .in4(bit_extender_3_out), .in8(bit_extender_4_out),
    .out(multiplexer_5_out), .sel({JAL, B, S_type, I}));  // open: in0, in3, in5, in6, in7, in9, in10, in11, in12, in13, in14, in15
  assign CLK = nand_1_out ? clock_1_out : 1'bz;  // Controlled_Buffer controlled_buffer_1
  Pull_Resistor #(.pull(1)) pull_resistor_1 (.node(CLK));
  Regifile regifile_1 (
    .Din(RDin), .Clk(CLK), .R1(regifile_1_r1), .R2(regifile_1_r2), .WE(RegWrite),
    .W_num(\mem_wb流水寄存器_1_w_num_2 ), .R1_num(ID_R1_num), .R2_num(ID_R2_num));
  \ID_EX流水寄存器  \id_ex流水寄存器_1  (
    .ecall(ecall), .jal(JAL), .jalr(JALR), .uret(URET), .Beq(\单周期硬布线控制器_1_beq ), .Bne(\单周期硬布线控制器_1_bne ),
    .MemToReg(\单周期硬布线控制器_1_memtoreg ), .MemWrite(\单周期硬布线控制器_1_memwrite ), .AluOP(\单周期硬布线控制器_1_alu_op ),
    .Alu_Src(\单周期硬布线控制器_1_alu_src ), .RegWrite(\单周期硬布线控制器_1_regwrite ), .sb(\单周期硬布线控制器_1_sb ),
    .clearI(\单周期硬布线控制器_1_cleari ), .setI(\单周期硬布线控制器_1_seti ), .sll(\单周期硬布线控制器_1_sll ), .R1(regifile_1_r1),
    .R2__sll({{27{1'b0}}, regifile_1_r2[4:0]}), .\立即数 (multiplexer_5_out), .W_num(ID_IR[11:7]), .PC(ID_PC),
    .PC_4(\if_id流水寄存器_1_pc_4_2 ), .ecall_2(\id_ex流水寄存器_1_ecall_2 ), .jal_2(\id_ex流水寄存器_1_jal_2 ),
    .jalr_2(EX_JALR), .Beq_2(\id_ex流水寄存器_1_beq_2 ), .Bne_2(\id_ex流水寄存器_1_bne_2 ),
    .MemToReg_2(\id_ex流水寄存器_1_memtoreg_2 ), .MemWrite_2(\id_ex流水寄存器_1_memwrite_2 ),
    .AluOP_2(\id_ex流水寄存器_1_aluop_2 ), .Alu_Src_2(\id_ex流水寄存器_1_alu_src_2 [0]),
    .RegWrite_2(\id_ex流水寄存器_1_regwrite_2 ), .sb_2(\id_ex流水寄存器_1_sb_2 ), .sll_2(\id_ex流水寄存器_1_alu_src_2 [1]),
    .R1_2(\id_ex流水寄存器_1_r1_2 ), .R2__sll_2(\id_ex流水寄存器_1_r2__sll_2 ), .\立即数_2 (\id_ex流水寄存器_1_立即数_2 ),
    .W_num_2(EX_W_num), .PC_2(EX_PC), .PC_4_2(\id_ex流水寄存器_1_pc_4_2 ), .CLK(CLK), .\EN使能端 (halt),
    .bltu(\单周期硬布线控制器_1_bltu ), .bltu_2(bltu), .R2(regifile_1_r2), .R2_2(EX_ec_out), .IR(ID_IR), .IR_2(EX_IR));  // open: uret_2, clearI_2, setI_2, 同步清零_高电平有效, RsForward, RsForward_2, RtForward, RtForward_2, PredictJump, PredictJump_2
  Comparator #(.width(32), .mode("unsigned")) comparator_2 (
    .a(32'h22), .b(\id_ex流水寄存器_1_r1_2 ), .eq(Ex_ec_eq));  // open: gt, lt
  Multiplexer #(.select(2), .width(32), .disabled("Z"), .enable("false")) multiplexer_6 (
    .in0(EX_ec_out), .in1(\id_ex流水寄存器_1_立即数_2 ), .in2(\id_ex流水寄存器_1_r2__sll_2 ), .out(multiplexer_6_out),
    .sel(\id_ex流水寄存器_1_alu_src_2 ));  // open: in3
  Shifter #(.width(32), .shift("ll")) shifter_1 (.in(\id_ex流水寄存器_1_立即数_2 ), .\dist (5'b00001), .out(shifter_1_out));
  assign and_2_out = {alu_1_result, lessthen} & 32'hfffffffe;  // AND_Gate and_2, 32 bits wide
  ALU alu_1 (
    .X(\id_ex流水寄存器_1_r1_2 ), .Y(multiplexer_6_out), .AluOP(\id_ex流水寄存器_1_aluop_2 ), .Equal(alu_1_equal),
    .Result({alu_1_result, lessthen}));  // open: Result_2, out_4, out_6
  and and_3 (and_3_out, bltu, lessthen);
  and and_4 (and_4_out, alu_1_equal, \id_ex流水寄存器_1_beq_2 );
  and and_5 (and_5_out, ~alu_1_equal, \id_ex流水寄存器_1_bne_2 );  // AND_Gate
  Adder #(.width(32)) adder_2 (.a(shifter_1_out), .b(EX_PC), .out(adder_2_out));  // open: cin, cout
  or or_2 (PCSrc, and_3_out, and_4_out, and_5_out, \id_ex流水寄存器_1_jal_2 );
  or or_3 (Branch, and_3_out, and_4_out, and_5_out, \id_ex流水寄存器_1_jal_2 , EX_JALR);
  \EX_MEM流水寄存器  \ex_mem流水寄存器_1  (
    .W_num(EX_W_num), .W_num_2(MEM_W_num), .PC(EX_PC), .PC_2(M_PC), .PC_4(\id_ex流水寄存器_1_pc_4_2 ),
    .PC_4_2(\ex_mem流水寄存器_1_pc_4_2 ), .CLK(CLK), .\EN使能端 (halt), .lt(lessthen), .PC_offset(adder_2_out),
    .PC_offset_2(\ex_mem流水寄存器_1_pc_offset_2 ), .result({alu_1_result, lessthen}),
    .result_2(\ex_mem流水寄存器_1_result_2 ), .address(alu_1_result[11:2]), .address_2(\ex_mem流水寄存器_1_address_2 ),
    .ecall(\id_ex流水寄存器_1_ecall_2 ), .ecall_2(\ex_mem流水寄存器_1_ecall_2 ), .jal(\id_ex流水寄存器_1_jal_2 ),
    .jal_2(\ex_mem流水寄存器_1_jal_2 ), .jalr(EX_JALR), .jalr_2(\ex_mem流水寄存器_1_jalr_2 ),
    .MemToReg(\id_ex流水寄存器_1_memtoreg_2 ), .MemToReg_2(\ex_mem流水寄存器_1_memtoreg_2 ),
    .MemWrite(\id_ex流水寄存器_1_memwrite_2 ), .MemWrite_2(MemWrite), .RegWrite(\id_ex流水寄存器_1_regwrite_2 ),
    .RegWrite_2(\ex_mem流水寄存器_1_regwrite_2 ), .sb(\id_ex流水寄存器_1_sb_2 ), .sb_2(sb_star), .R2(EX_ec_out),
    .R2_2(\ex_mem流水寄存器_1_r2_2 ), .bltu(bltu), .bltu_2(\ex_mem流水寄存器_1_bltu_2 ), .IR(EX_IR), .IR_2(MEM_IR),
    .ec_eq(Ex_ec_eq), .ec_eq_2(\ex_mem流水寄存器_1_ec_eq_2 ), .ec_out(EX_ec_out),
    .ec_out_2(\ex_mem流水寄存器_1_ec_out_2 ));  // open: 同步清零_高电平有效, lt_2, uret, uret_2, Beq, Beq_2, Bne, Bne_2, clearI, clearI_2, setI, ecall_3, sll, sll_2, halt, halt_2
  \sb分线  \sb分线_1  (
    .\new (\ex_mem流水寄存器_1_r2_2 [7:0]), .Address(\ex_mem流水寄存器_1_result_2 [1:0]), .\output (\sb分线_1_output ),
    .origin(ram_1_data));
  Multiplexer #(.select(1), .width(32), .disabled("Z"), .enable("false")) multiplexer_7 (
    .in0(\ex_mem流水寄存器_1_r2_2 ), .in1(\sb分线_1_output ), .out(MDin), .sel(sb_star));
  RAM #(.addrWidth(10), .dataWidth(32), .bus("separate"), .Select("high")) ram_1 (
    .addr(\ex_mem流水寄存器_1_address_2 ), .din(MDin), .data(ram_1_data), .str(MemWrite), .clk(CLK), .ld(1'b1));  // open: sel, clr
  \MEM_WB流水寄存器  \mem_wb流水寄存器_1  (
    .W_num(MEM_W_num), .W_num_2(\mem_wb流水寄存器_1_w_num_2 ), .PC(M_PC), .PC_2(WB_PC),
    .PC_4(\ex_mem流水寄存器_1_pc_4_2 ), .PC_4_2(\mem_wb流水寄存器_1_pc_4_2 ), .CLK(CLK), .\EN使能端 (halt),
    .RegWrite(\ex_mem流水寄存器_1_regwrite_2 ), .RegWrite_2(RegWrite), .MemToReg(\ex_mem流水寄存器_1_memtoreg_2 ),
    .MemToReg_2(\mem_wb流水寄存器_1_memtoreg_2 ), .jalr(\ex_mem流水寄存器_1_jalr_2 ), .jalr_2(JALR_star),
    .jal(\ex_mem流水寄存器_1_jal_2 ), .jal_2(JAL_star), .ecall(\ex_mem流水寄存器_1_ecall_2 ), .ecall_2(ecall_star),
    .Result(\ex_mem流水寄存器_1_result_2 ), .Result_2(\mem_wb流水寄存器_1_result_2 ), .Mem(ram_1_data),
    .Mem_3(\mem_wb流水寄存器_1_mem_3 ), .PC_offset(\ex_mem流水寄存器_1_pc_offset_2 ), .bltu(\ex_mem流水寄存器_1_bltu_2 ),
    .IR(MEM_IR), .Mem_2(WB_IR), .ec_out(\ex_mem流水寄存器_1_ec_out_2 ), .ec_out_2(ec_out),
    .ec_eq(\ex_mem流水寄存器_1_ec_eq_2 ), .ec_eq_2(ec_eq));  // open: 同步清零_高电平有效, lt, lt_2, PC_offset_2, bltu_2, uret, uret_2, Beq, Beq_2, Bne, Bne_2, clearI, clearI_2, setI, setI_2, sll, sll_2, halt, halt_2
  Multiplexer #(.select(1), .width(32), .disabled("Z"), .enable("false")) multiplexer_8 (
    .in0(\mem_wb流水寄存器_1_result_2 ), .in1(\mem_wb流水寄存器_1_mem_3 ), .out(multiplexer_8_out),
    .sel(\mem_wb流水寄存器_1_memtoreg_2 ));
  or or_4 (J, JAL_star, JALR_star);
  and and_6 (and_6_out, ecall_star, ~ec_eq);  // AND_Gate
  and and_7 (and_7_out, ec_eq, ecall_star);
  Register #(.width(32), .trigger("rising"), .Select("low")) register_1 (
    .D(ec_out), .en(and_7_out), .Q(LedData), .clk(CLK));  // open: clr
  D_Flip_Flop #(.trigger("high"), .Pre_Clr_Positions("LEGACY"), .NegatePresetClear("false"), .enable("true"), .NewFFLayout("false")) d_ff_2 (
    .clk(CLK), .D(and_6_out), .Q(halt), .reset(Go));  // open: Qn, preset, en

  // Other names for the same wires on the sheet: IR[31:0] = ID_IR; MEM_PC[31:0] = M_PC

  // Notes on the sheet:
  //   中断源
  //   时空图监测，可删除
  //   中断等待指示
  //   数码管输出
  //   指令存储器
  //   指令字
  //   contents of rom_1 (hex, n*v repeats v):
  //   413 493 913 993 46413 14e493 296913 39e993 842023 942223 1242423 1342623 a00893 493 913 993 73
  //   控制位
  //   指令探针
  //   流水调试日志用
  //   暂停节拍，不能为0
  //   JAL
  //   JALR
  //   URET
  //   I
  //   B
  //   戳工具置1进入计数暂停模式，ctrl+k时钟自动运行到对应节拍暂停
  //   ctrl+k关闭时钟连续运行，将控制位置零，进入单步调试模式调试
  //   用这个时钟源需要去掉电路中的其他时钟源
  //   可计数暂停的时钟源
  //   ecall
  //   jal
  //   jalr
  //   uret
  //   Beq
  //   Bne
  //   MemToReg
  //   MemWrite
  //   AluOP
  //   Alu_Src
  //   RegWrite
  //   sb
  //   clearI
  //   setI
  //   sll
  //   sll指令输入线
  //   立即数
  //   写入信号
  //   PC+4
  //   为方便自动评测，需要输出流水线各段保存的PC值，注意是PC不是PC+4，另外ID段寄存器写入信息，Mem段内存写入信息也要输出
  //   ecall
  //   jal
  //   jalr
  //   MemToReg
  //   MemWrite
  //   RegWrite
  //   写入信号
  //   PC+4
  //   ecall
  //   jal
  //   jalr
  //   MemToReg
  //   RegWrite
  //   数据存储器
  //   R2*
  //   Result
  //   Mem
  //   lessthen
  //   写入信号
  //   PC+4
endmodule

module \重定向流水线  (
  output RegWrite,
  output MemWrite,
  output [31:0] IF_PC,
  output [31:0] ID_PC,
  output [31:0] EX_PC,
  output [31:0] M_PC,
  output [31:0] WB_PC,
  output [31:0] RDin,
  output [31:0] MDin,
  output [31:0] LedData
);

  wire alu_1_equal, and_1_out, and_3_out, and_4_out, and_5_out, and_6_out, and_7_out, B, bltu, Branch, CLK,
       clock_1_out, comparator_1_eq, comparator_1_lt, d_ff_1_q, ec_eq, ecall, ecall_star, EX_ec_eq, EX_ecall,
       EX_JALR, \ex_mem流水寄存器_1_bltu_2 , \ex_mem流水寄存器_1_ec_eq_2 , \ex_mem流水寄存器_1_ecall_2 ,
       \ex_mem流水寄存器_1_jal_2 , \ex_mem流水寄存器_1_jalr_2 , \ex_mem流水寄存器_1_memtoreg_2 , \ex_mem流水寄存器_1_regwrite_2 ,
       Go, halt, I, \id_ex流水寄存器_1_beq_2 , \id_ex流水寄存器_1_bne_2 , \id_ex流水寄存器_1_jal_2 ,
       \id_ex流水寄存器_1_memtoreg_2 , \id_ex流水寄存器_1_memwrite_2 , \id_ex流水寄存器_1_regwrite_2 , \id_ex流水寄存器_1_sb_2 ,
       IR1, IR2, IR3, J, JAL, JAL_star, JALR, JALR_star, lessthen, \mem_wb流水寄存器_1_memtoreg_2 , nand_1_out,
       not_1_out, not_2_out, not_3_out, or_1_out, PC_EN, PCSrc, RST, S_type, sb_star, URET, W1, W2, W3,
       \单周期硬布线控制器_1_alu_src , \单周期硬布线控制器_1_beq , \单周期硬布线控制器_1_bltu , \单周期硬布线控制器_1_bne , \单周期硬布线控制器_1_cleari ,
       \单周期硬布线控制器_1_memtoreg , \单周期硬布线控制器_1_memwrite , \单周期硬布线控制器_1_regwrite , \单周期硬布线控制器_1_sb ,
       \单周期硬布线控制器_1_seti , \单周期硬布线控制器_1_sll , \重定向逻辑_1_id_ex_clr , \重定向逻辑_1_if_id_clr ;
  wire [1:0] \id_ex流水寄存器_1_alu_src_2 , \id_ex流水寄存器_1_rsforward_2 , \id_ex流水寄存器_1_rtforward_2 ,
       \重定向逻辑_1_rsforward , \重定向逻辑_1_rtforward ;
  wire [3:0] \id_ex流水寄存器_1_aluop_2 , \单周期硬布线控制器_1_alu_op ;
  wire [4:0] EX_W_num, ID_R1_num, ID_R2_num, MEM_W_num, \mem_wb流水寄存器_1_w_num_2 ;
  wire [9:0] \ex_mem流水寄存器_1_address_2 ;
  wire [12:0] CNT_num;
  wire [15:0] \LoadUse次数 , \总周期数 , \插入气泡数 , \无条件分支数 , \条件分支成功数 ;
  wire [31:0] adder_1_out, adder_2_out, and_2_out, bit_extender_1_out, bit_extender_2_out,
       bit_extender_3_out, bit_extender_4_out, ec_out, EX_ec_out, EX_IR, \ex_mem流水寄存器_1_ec_out_2 ,
       \ex_mem流水寄存器_1_pc_4_2 , \ex_mem流水寄存器_1_pc_offset_2 , \ex_mem流水寄存器_1_r2_2 , \ex_mem流水寄存器_1_result_2 ,
       \id_ex流水寄存器_1_pc_4_2 , \id_ex流水寄存器_1_r1_2 , \id_ex流水寄存器_1_r2_2 , \id_ex流水寄存器_1_r2__sll_2 ,
       \id_ex流水寄存器_1_立即数_2 , ID_IR, \if_id流水寄存器_1_pc_4_2 , IF_IR, MEM_IR, \mem_wb流水寄存器_1_mem_3 ,
       \mem_wb流水寄存器_1_pc_4_2 , \mem_wb流水寄存器_1_result_2 , multiplexer_1_out, multiplexer_5_out,
       multiplexer_6_out, multiplexer_8_out, multiplexer_10_out, ram_1_data, regifile_1_r1, regifile_1_r2,
       \sb分线_1_output , shifter_1_out, WB_IR;
  wire [31:1] alu_1_result;

  Button \u_总复位  (.out(RST));
  Button _1 (.out(IR1));
  Button _2 (.out(IR2));
  Button _3 (.out(IR3));
  // Probe on \总周期数 
  // Probe on \总周期数 
  Button \u_继续运行  (.out(Go));
  LED #(.active("true")) led_1 (.in(W1));
  LED #(.active("true")) led_2 (.in(W2));
  LED #(.active("true")) led_3 (.in(W3));
  Hex_Digit_Display hex_digit_display_1 (.value(LedData[31:28]));  // open: dp
  // Probe on IF_PC[19:0]
  // RiscV_Probe riscv_probe_1: pin names not known; wires that end beside it: IF_IR
  Hex_Digit_Display hex_digit_display_2 (.value(LedData[27:24]));  // open: dp
  Hex_Digit_Display hex_digit_display_3 (.value(LedData[23:20]));  // open: dp
  // Probe on ID_PC[19:0]
  // RiscV_Probe riscv_probe_2: pin names not known; wires that end beside it: ID_IR
  Hex_Digit_Display hex_digit_display_4 (.value(LedData[19:16]));  // open: dp
  Hex_Digit_Display hex_digit_display_5 (.value(LedData[15:12]));  // open: dp
  Hex_Digit_Display hex_digit_display_6 (.value(LedData[11:8]));  // open: dp
  Hex_Digit_Display hex_digit_display_7 (.value(LedData[7:4]));  // open: dp
  // Probe on EX_PC[19:0]
  // RiscV_Probe riscv_probe_3: pin names not known; wires that end beside it: EX_IR
  Multiplexer #(.select(2), .width(32), .disabled("Z"), .enable("false")) multiplexer_1 (
    .in0(adder_1_out), .in1(adder_2_out), .in2(and_2_out), .out(multiplexer_1_out), .sel({EX_JALR, PCSrc}));  // open: in3
  and and_1 (and_1_out, not_1_out, PC_EN);
  not not_1 (not_1_out, halt);
  Hex_Digit_Display hex_digit_display_8 (.value(LedData[3:0]));  // open: dp
  \重定向逻辑  \u_重定向逻辑_1  (
    .R1(ID_R1_num), .I(I), .B(B), .IR(ID_IR), .R2(ID_R2_num), .BranchTakens(Branch), .J(JAL),
    .EX_WriteReg_num(EX_W_num), .EX_RegWrite(\id_ex流水寄存器_1_regwrite_2 ), .S(S_type),
    .MEM_WriteReg_num(MEM_W_num), .MEM_RegWrite(\ex_mem流水寄存器_1_regwrite_2 ),
    .EX_MemRead__MemToReg(\id_ex流水寄存器_1_memtoreg_2 ), .PC_EN(PC_EN), .ID_EX_CLR(\重定向逻辑_1_id_ex_clr ),
    .IF_ID_CLR(\重定向逻辑_1_if_id_clr ), .RsForward(\重定向逻辑_1_rsforward ), .RtForward(\重定向逻辑_1_rtforward ));
  not not_2 (not_2_out, halt);
  Counter #(.width(16), .max('hffff), .ongoal("wrap"), .trigger("rising"), .behavior("new")) counter_1 (
    .D(16'h1), .count(not_2_out), .Q(\总周期数 ), .clk(CLK));  // open: load, carry, clr, preset, down
  Register #(.width(32), .trigger("rising"), .Select("low")) PC (
    .D({{20{1'b0}}, multiplexer_1_out[11:0]}), .en(and_1_out), .Q(IF_PC), .clk(CLK), .clr(RST));
  // Probe on \总周期数 
  // Probe on M_PC[19:0]
  // RiscV_Probe riscv_probe_4: pin names not known; wires that end beside it: MEM_IR
  // Probe on \总周期数 
  // Probe on \无条件分支数 
  // Probe on \条件分支成功数 
  // Probe on \插入气泡数 
  // Probe on \LoadUse次数 
  // Probe on IF_PC
  Adder #(.width(32)) adder_1 (.a(IF_PC), .b(32'h4), .out(adder_1_out));  // open: cin, cout
  // Probe on IF_PC[11:0]
  // Probe on WB_PC[19:0]
  // RiscV_Probe riscv_probe_5: pin names not known; wires that end beside it: WB_IR
  ROM #(.addrWidth(10), .dataWidth(32), .Select("high")) rom_1 (.addr(IF_PC[11:2]), .data(IF_IR));
  // Probe on EX_PC[11:0]
  // Probe on ID_PC[11:0]
  not not_3 (not_3_out, PC_EN);
  or or_1 (or_1_out, not_3_out, halt);
  \IF_ID流水寄存器  \if_id流水寄存器_1  (
    .IR(IF_IR), .PC(IF_PC), .PC_4(adder_1_out), .IR_2(ID_IR), .PC_2(ID_PC), .PC_4_2(\if_id流水寄存器_1_pc_4_2 ),
    .\同步清零_高电平有效 (\重定向逻辑_1_if_id_clr ), .CLK(CLK), .\EN使能端 (or_1_out));  // open: PredictJump, PredictJump_2
  // Probe on M_PC[11:0]
  D_Flip_Flop #(.trigger("high"), .Pre_Clr_Positions("LEGACY"), .NegatePresetClear("false"), .enable("true"), .NewFFLayout("false")) d_ff_1 (.Q(d_ff_1_q));  // open: clk, D, Qn, preset, en, reset
  // Probe on 13'h166
  // Probe on WB_PC[11:0]
  Comparator #(.width(13), .mode("twosComplement")) comparator_1 (
    .a(CNT_num), .b(13'h166), .eq(comparator_1_eq), .lt(comparator_1_lt));  // open: gt
  Clock #(.highDuration(1), .lowDuration(1)) clock_1 (.out(clock_1_out));
  // RiscV_Probe riscv_probe_6: pin names not known; wires that end beside it: ID_IR
  nand nand_1 (nand_1_out, d_ff_1_q, comparator_1_eq);
  Counter #(.width(13), .max('h1fff), .ongoal("stay"), .trigger("rising"), .behavior("old")) counter_2 (
    .count(comparator_1_lt), .Q(CNT_num), .clk(clock_1_out));  // open: load, D, carry, clr, preset
  assign CLK = nand_1_out ? clock_1_out : 1'bz;  // Controlled_Buffer controlled_buffer_1
  \单周期硬布线控制器  \u_单周期硬布线控制器_1  (
    .Funct({ID_IR[30], ID_IR[25], ID_IR[14:12]}), .OP(ID_IR[6:2]), .ALU_OP(\单周期硬布线控制器_1_alu_op ),
    .MemToReg(\单周期硬布线控制器_1_memtoreg ), .MemWrite(\单周期硬布线控制器_1_memwrite ), .ALU_SRC(\单周期硬布线控制器_1_alu_src ),
    .RegWrite(\单周期硬布线控制器_1_regwrite ), .ecall(ecall), .S_type(S_type), .Jalr(JALR), .Beq(\单周期硬布线控制器_1_beq ),
    .JAL(JAL), .Bne(\单周期硬布线控制器_1_bne ), .in_3(ID_IR[21]), .uret(URET), .I(I), .B(B),
    .clearI(\单周期硬布线控制器_1_cleari ), .sb(\单周期硬布线控制器_1_sb ), .sll(\单周期硬布线控制器_1_sll ), .setI(\单周期硬布线控制器_1_seti ),
    .bltu(\单周期硬布线控制器_1_bltu ));
  assign bit_extender_1_out = {{20{ID_IR[31]}}, ID_IR[31:20]};  // Bit_Extender bit_extender_1
  assign bit_extender_2_out = {{20{ID_IR[31]}}, {ID_IR[31:25], ID_IR[11:7]}};  // Bit_Extender bit_extender_2
  assign bit_extender_3_out = {{20{ID_IR[31]}}, {ID_IR[31], ID_IR[7], ID_IR[30:25], ID_IR[11:8]}};  // Bit_Extender bit_extender_3
  assign bit_extender_4_out = {{12{ID_IR[31]}}, {ID_IR[31], ID_IR[19:12], ID_IR[20], ID_IR[30:21]}};  // Bit_Extender bit_extender_4
  Pull_Resistor #(.pull(1)) pull_resistor_1 (.node(CLK));
  Multiplexer #(.select(1), .width(5), .disabled("Z"), .enable("false")) multiplexer_2 (
    .in0(ID_IR[19:15]), .in1(5'b10001), .out(ID_R1_num), .sel(ecall));
  Multiplexer #(.select(1), .width(5), .disabled("Z"), .enable("false")) multiplexer_3 (
    .in0(ID_IR[24:20]), .in1(5'b01010), .out(ID_R2_num), .sel(ecall));
  Multiplexer #(.select(1), .width(32), .disabled("Z"), .enable("false")) multiplexer_4 (
    .in0(multiplexer_10_out), .in1(\mem_wb流水寄存器_1_pc_4_2 ), .out(RDin), .sel(J));
  Multiplexer #(.select(4), .width(32), .disabled("Z"), .enable("false")) multiplexer_5 (
    .in1(bit_extender_1_out), .in2(bit_extender_2_out), .in4(bit_extender_3_out), .in8(bit_extender_4_out),
    .out(multiplexer_5_out), .sel({JAL, B, S_type, I}));  // open: in0, in3, in5, in6, in7, in9, in10, in11, in12, in13, in14, in15
  Hex_Digit_Display hex_digit_display_9 (.value(LedData[31:28]));  // open: dp
  Hex_Digit_Display hex_digit_display_10 (.value(LedData[23:20]));  // open: dp
  Hex_Digit_Display hex_digit_display_11 (.value(LedData[27:24]));  // open: dp
  Regifile regifile_1 (
    .Din(RDin), .Clk(CLK), .R1(regifile_1_r1), .R2(regifile_1_r2), .WE(RegWrite),
    .W_num(\mem_wb流水寄存器_1_w_num_2 ), .R1_num(ID_R1_num), .R2_num(ID_R2_num));
  Hex_Digit_Display hex_digit_display_12 (.value(LedData[19:16]));  // open: dp
  Hex_Digit_Display hex_digit_display_13 (.value(LedData[15:12]));  // open: dp
  Hex_Digit_Display hex_digit_display_14 (.value(LedData[11:8]));  // open: dp
  Hex_Digit_Display hex_digit_display_15 (.value(LedData[7:4]));  // open: dp
  Hex_Digit_Display hex_digit_display_16 (.value(LedData[3:0]));  // open: dp
  \ID_EX流水寄存器  \id_ex流水寄存器_1  (
    .ecall(ecall), .jal(JAL), .jalr(JALR), .uret(URET), .Beq(\单周期硬布线控制器_1_beq ), .Bne(\单周期硬布线控制器_1_bne ),
    .MemToReg(\单周期硬布线控制器_1_memtoreg ), .MemWrite(\单周期硬布线控制器_1_memwrite ), .AluOP(\单周期硬布线控制器_1_alu_op ),
    .Alu_Src(\单周期硬布线控制器_1_alu_src ), .RegWrite(\单周期硬布线控制器_1_regwrite ), .sb(\单周期硬布线控制器_1_sb ),
    .clearI(\单周期硬布线控制器_1_cleari ), .setI(\单周期硬布线控制器_1_seti ), .sll(\单周期硬布线控制器_1_sll ), .R1(regifile_1_r1),
    .R2__sll({{27{1'b0}}, regifile_1_r2[4:0]}), .\立即数 (multiplexer_5_out), .W_num(ID_IR[11:7]), .PC(ID_PC),
    .PC_4(\if_id流水寄存器_1_pc_4_2 ), .ecall_2(EX_ecall), .jal_2(\id_ex流水寄存器_1_jal_2 ), .jalr_2(EX_JALR),
    .Beq_2(\id_ex流水寄存器_1_beq_2 ), .Bne_2(\id_ex流水寄存器_1_bne_2 ), .MemToReg_2(\id_ex流水寄存器_1_memtoreg_2 ),
    .MemWrite_2(\id_ex流水寄存器_1_memwrite_2 ), .AluOP_2(\id_ex流水寄存器_1_aluop_2 ),
    .Alu_Src_2(\id_ex流水寄存器_1_alu_src_2 [0]), .RegWrite_2(\id_ex流水寄存器_1_regwrite_2 ),
    .sb_2(\id_ex流水寄存器_1_sb_2 ), .sll_2(\id_ex流水寄存器_1_alu_src_2 [1]), .R1_2(\id_ex流水寄存器_1_r1_2 ),
    .R2__sll_2(\id_ex流水寄存器_1_r2__sll_2 ), .\立即数_2 (\id_ex流水寄存器_1_立即数_2 ), .W_num_2(EX_W_num), .PC_2(EX_PC),
    .PC_4_2(\id_ex流水寄存器_1_pc_4_2 ), .\同步清零_高电平有效 (\重定向逻辑_1_id_ex_clr ), .CLK(CLK), .\EN使能端 (halt),
    .bltu(\单周期硬布线控制器_1_bltu ), .bltu_2(bltu), .R2(regifile_1_r2), .R2_2(\id_ex流水寄存器_1_r2_2 ), .IR(ID_IR),
    .IR_2(EX_IR), .RsForward(\重定向逻辑_1_rsforward ), .RsForward_2(\id_ex流水寄存器_1_rsforward_2 ),
    .RtForward(\重定向逻辑_1_rtforward ), .RtForward_2(\id_ex流水寄存器_1_rtforward_2 ));  // open: uret_2, clearI_2, setI_2, PredictJump, PredictJump_2
  Multiplexer #(.select(2), .width(32), .disabled("Z"), .enable("false")) multiplexer_6 (
    .in0(\id_ex流水寄存器_1_r1_2 ), .in1(multiplexer_10_out), .in2(\ex_mem流水寄存器_1_result_2 ),
    .out(multiplexer_6_out), .sel(\id_ex流水寄存器_1_rsforward_2 ));  // open: in3
  Multiplexer #(.select(2), .width(32), .disabled("Z"), .enable("false")) multiplexer_7 (
    .in0(\id_ex流水寄存器_1_r2_2 ), .in1(multiplexer_10_out), .in2(\ex_mem流水寄存器_1_result_2 ), .out(EX_ec_out),
    .sel(\id_ex流水寄存器_1_rtforward_2 ));  // open: in3
  Multiplexer #(.select(2), .width(32), .disabled("Z"), .enable("false")) multiplexer_8 (
    .in0(EX_ec_out), .in1(\id_ex流水寄存器_1_立即数_2 ), .in2(\id_ex流水寄存器_1_r2__sll_2 ), .out(multiplexer_8_out),
    .sel(\id_ex流水寄存器_1_alu_src_2 ));  // open: in3
  // Probe on EX_ec_out
  Shifter #(.width(32), .shift("ll")) shifter_1 (.in(\id_ex流水寄存器_1_立即数_2 ), .\dist (5'b00001), .out(shifter_1_out));
  assign and_2_out = {alu_1_result, lessthen} & 32'hfffffffe;  // AND_Gate and_2, 32 bits wide
  ALU alu_1 (
    .X(multiplexer_6_out), .Y(multiplexer_8_out), .AluOP(\id_ex流水寄存器_1_aluop_2 ), .Equal(alu_1_equal),
    .Result({alu_1_result, lessthen}));  // open: Result_2, out_4, out_6
  Adder #(.width(32)) adder_2 (.a(shifter_1_out), .b(EX_PC), .out(adder_2_out));  // open: cin, cout
  and and_3 (and_3_out, bltu, lessthen);
  and and_4 (and_4_out, alu_1_equal, \id_ex流水寄存器_1_beq_2 );
  and and_5 (and_5_out, ~alu_1_equal, \id_ex流水寄存器_1_bne_2 );  // AND_Gate
  Comparator #(.width(32), .mode("unsigned")) comparator_2 (
    .a(32'h22), .b(multiplexer_6_out), .eq(EX_ec_eq));  // open: gt, lt
  or or_2 (PCSrc, and_3_out, and_4_out, and_5_out, \id_ex流水寄存器_1_jal_2 );
  or or_3 (Branch, and_3_out, and_4_out, and_5_out, \id_ex流水寄存器_1_jal_2 , EX_JALR);
  \EX_MEM流水寄存器  \ex_mem流水寄存器_1  (
    .W_num(EX_W_num), .W_num_2(MEM_W_num), .PC(EX_PC), .PC_2(M_PC), .PC_4(\id_ex流水寄存器_1_pc_4_2 ),
    .PC_4_2(\ex_mem流水寄存器_1_pc_4_2 ), .CLK(CLK), .\EN使能端 (halt), .lt(lessthen), .PC_offset(adder_2_out),
    .PC_offset_2(\ex_mem流水寄存器_1_pc_offset_2 ), .result({alu_1_result, lessthen}),
    .result_2(\ex_mem流水寄存器_1_result_2 ), .address(alu_1_result[11:2]), .address_2(\ex_mem流水寄存器_1_address_2 ),
    .ecall(EX_ecall), .ecall_2(\ex_mem流水寄存器_1_ecall_2 ), .jal(\id_ex流水寄存器_1_jal_2 ),
    .jal_2(\ex_mem流水寄存器_1_jal_2 ), .jalr(EX_JALR), .jalr_2(\ex_mem流水寄存器_1_jalr_2 ),
    .MemToReg(\id_ex流水寄存器_1_memtoreg_2 ), .MemToReg_2(\ex_mem流水寄存器_1_memtoreg_2 ),
    .MemWrite(\id_ex流水寄存器_1_memwrite_2 ), .MemWrite_2(MemWrite), .RegWrite(\id_ex流水寄存器_1_regwrite_2 ),
    .RegWrite_2(\ex_mem流水寄存器_1_regwrite_2 ), .sb(\id_ex流水寄存器_1_sb_2 ), .sb_2(sb_star), .R2(EX_ec_out),
    .R2_2(\ex_mem流水寄存器_1_r2_2 ), .bltu(bltu), .bltu_2(\ex_mem流水寄存器_1_bltu_2 ), .IR(EX_IR), .IR_2(MEM_IR),
    .ec_eq(EX_ec_eq), .ec_eq_2(\ex_mem流水寄存器_1_ec_eq_2 ), .ec_out(EX_ec_out),
    .ec_out_2(\ex_mem流水寄存器_1_ec_out_2 ));  // open: 同步清零_高电平有效, lt_2, uret, uret_2, Beq, Beq_2, Bne, Bne_2, clearI, clearI_2, setI, ecall_3, sll, sll_2, halt, halt_2
  \sb分线  \sb分线_1  (
    .\new (\ex_mem流水寄存器_1_r2_2 [7:0]), .Address(\ex_mem流水寄存器_1_result_2 [1:0]), .\output (\sb分线_1_output ),
    .origin(ram_1_data));
  RAM #(.addrWidth(10), .dataWidth(32), .bus("separate"), .Select("high")) ram_1 (
    .addr(\ex_mem流水寄存器_1_address_2 ), .din(MDin), .data(ram_1_data), .str(MemWrite), .clk(CLK), .ld(1'b1));  // open: sel, clr
  Multiplexer #(.select(1), .width(32), .disabled("Z"), .enable("false")) multiplexer_9 (
    .in0(\ex_mem流水寄存器_1_r2_2 ), .in1(\sb分线_1_output ), .out(MDin), .sel(sb_star));
  \MEM_WB流水寄存器  \mem_wb流水寄存器_1  (
    .W_num(MEM_W_num), .W_num_2(\mem_wb流水寄存器_1_w_num_2 ), .PC(M_PC), .PC_2(WB_PC),
    .PC_4(\ex_mem流水寄存器_1_pc_4_2 ), .PC_4_2(\mem_wb流水寄存器_1_pc_4_2 ), .CLK(CLK), .\EN使能端 (halt),
    .RegWrite(\ex_mem流水寄存器_1_regwrite_2 ), .RegWrite_2(RegWrite), .MemToReg(\ex_mem流水寄存器_1_memtoreg_2 ),
    .MemToReg_2(\mem_wb流水寄存器_1_memtoreg_2 ), .jalr(\ex_mem流水寄存器_1_jalr_2 ), .jalr_2(JALR_star),
    .jal(\ex_mem流水寄存器_1_jal_2 ), .jal_2(JAL_star), .ecall(\ex_mem流水寄存器_1_ecall_2 ), .ecall_2(ecall_star),
    .Result(\ex_mem流水寄存器_1_result_2 ), .Result_2(\mem_wb流水寄存器_1_result_2 ), .Mem(ram_1_data),
    .Mem_3(\mem_wb流水寄存器_1_mem_3 ), .PC_offset(\ex_mem流水寄存器_1_pc_offset_2 ), .bltu(\ex_mem流水寄存器_1_bltu_2 ),
    .IR(MEM_IR), .Mem_2(WB_IR), .ec_out(\ex_mem流水寄存器_1_ec_out_2 ), .ec_out_2(ec_out),
    .ec_eq(\ex_mem流水寄存器_1_ec_eq_2 ), .ec_eq_2(ec_eq));  // open: 同步清零_高电平有效, lt, lt_2, PC_offset_2, bltu_2, uret, uret_2, Beq, Beq_2, Bne, Bne_2, clearI, clearI_2, setI, setI_2, sll, sll_2, halt, halt_2
  Multiplexer #(.select(1), .width(32), .disabled("Z"), .enable("false")) multiplexer_10 (
    .in0(\mem_wb流水寄存器_1_result_2 ), .in1(\mem_wb流水寄存器_1_mem_3 ), .out(multiplexer_10_out),
    .sel(\mem_wb流水寄存器_1_memtoreg_2 ));
  or or_4 (J, JAL_star, JALR_star);
  and and_6 (and_6_out, ecall_star, ~ec_eq);  // AND_Gate
  and and_7 (and_7_out, ec_eq, ecall_star);
  D_Flip_Flop #(.trigger("high"), .Pre_Clr_Positions("LEGACY"), .NegatePresetClear("false"), .enable("true"), .NewFFLayout("false")) d_ff_2 (
    .clk(CLK), .D(and_6_out), .Q(halt), .reset(Go));  // open: Qn, preset, en
  Register #(.width(32), .trigger("rising"), .Select("low")) register_1 (
    .D(ec_out), .en(and_7_out), .Q(LedData), .clk(CLK));  // open: clr

  // Other names for the same wires on the sheet: IR[31:0] = ID_IR; MEM_PC[31:0] = M_PC

  // Notes on the sheet:
  //   中断源
  //   时空图监测，可删除
  //   中断等待指示
  //   数码管输出
  //   指令存储器
  //   contents of rom_1 (hex, n*v repeats v):
  //   100493 100006f 100493 200913 300993 100006f 100493 200913 300993 100006f 100493 200913 300993
  //   100006f 100493 200913 300993 3b4000ef 100413 100493 1f49493 900533 2200893 73 24d493 48463 fedff06f
  //   900533 2200893 73 100493 249493 900533 2200893 73 48463 fedff06f 100493 1f49493 900533 2200893 73
  //   4034d493 900533 2200893 73 4044d493 900533 2200893 73 4044d493 900533 2200893 73 4044d493 900533
  //   2200893 73 4044d493 900533 2200893 73 4044d493 900533 2200893 73 4044d493 900533 2200893 73 4044d493
  //   900533 2200893 73 100413 1f41993 41f9d993 433 c00913 300b13 140413 f47413 800293 100313 499993
  //   89e9b3 1300533 2200893 73 406282b3 fe0294e3 140413 f00f93 1f47433 1c41413 800293 100313 49d993
  //   89e9b3 1300533 2200893 73 406282b3 fe0294e3 1c45413 406b0b33 b0463 f95ff06f 2b3 fff2c293 829293
  //   ff2e293 500533 2200893 73 fff00413 493 84a023 140413 448493 84a023 140413 448493 84a023 140413
  //   448493 84a023 140413 448493 84a023 140413 448493 84a023 140413 448493 84a023 140413 448493 84a023
  //   140413 448493 84a023 140413 448493 84a023 140413 448493 84a023 140413 448493 84a023 140413 448493
  //   84a023 140413 448493 84a023 140413 448493 84a023 140413 448493 84a023 140413 448493 140413 433
  //   3c00493 42983 4aa03 149a2b3 28663 134a023 1442023 ffc48493 fe9412e3 800533 2200893 73 440413 3c00493
  //   fc9416e3 3200893 73 100293 300313 800493 849493 7648493 900533 2200893 73 800e13 5494b3 6494b3
  //   900533 2200893 73 fffe0e13 fe0e14e3 a00893 73 fff00293 7700493 849493 7748493 900533 2200893 73
  //   1000e13 54c4b3 900533 2200893 73 fffe0e13 fe0e16e3 a00893 73 313 2000e13 493 100913 930023 900533
  //   2200893 73 12484b3 130313 fffe0e13 fe0e12e3 800e13 313 32483 900533 2200893 73 430313 fffe0e13
  //   fe0e14e3 a00893 73 ff100493 900533 2200893 73 148493 fe9068e3 900533 2200893 73 a00893 73 a00893 73
  //   413 140413 800533 2200893 73 240413 800533 2200893 73 340413 800533 2200893 73 440413 800533 2200893
  //   73 540413 800533 2200893 73 640413 800533 2200893 73 740413 800533 2200893 73 840413 800533 2200893
  //   2200893 73 8067
  //   控制位
  //   指令字
  //   流水调试日志用
  //   暂停节拍，不能为0
  //   戳工具置1进入计数暂停模式，ctrl+k时钟自动运行到对应节拍暂停
  //   ctrl+k关闭时钟连续运行，将控制位置零，进入单步调试模式调试
  //   指令探针
  //   JAL
  //   JALR
  //   URET
  //   I
  //   B
  //   可计数暂停的时钟源
  //   为方便自动评测，需要输出流水线各段保存的PC值，注意是PC不是PC+4，另外ID段寄存器写入信息，Mem段内存写入信息也要输出
  //   sll指令输入线
  //   写入信号
  //   PC+4
  //   ecall
  //   jal
  //   jalr
  //   uret
  //   Beq
  //   Bne
  //   MemToReg
  //   MemWrite
  //   AluOP
  //   Alu_Src
  //   RegWrite
  //   sb
  //   clearI
  //   setI
  //   sll
  //   立即数
  //   ecall
  //   MemToReg
  //   MemWrite
  //   RegWrite
  //   写入信号
  //   PC+4
  //   jal
  //   jalr
  //   数据存储器
  //   ecall
  //   jal
  //   jalr
  //   MemToReg
  //   RegWrite
  //   R2*
  //   Result
  //   Mem
  //   lessthen
  //   写入信号
  //   PC+4
endmodule
module \气泡流水线  (
  output RegWrite,
  output MemWrite,
  output [31:0] IF_PC,
  output [31:0] ID_PC,
  output [31:0] EX_PC,
  output [31:0] M_PC,
  output [31:0] WB_PC,
  output [31:0] RDin,
  output [31:0] MDin,
  output [31:0] LedData
);

  wire alu_1_equal, and_1_out, and_3_out, and_4_out, and_5_out, and_6_out, and_7_out, B, bltu, Branch, CLK,
       clock_1_out, comparator_1_eq, comparator_1_lt, d_ff_1_q, ec_eq, ecall, ecall_star, Ex_ec_eq, EX_JALR,
       \ex_mem流水寄存器_1_bltu_2 , \ex_mem流水寄存器_1_ec_eq_2 , \ex_mem流水寄存器_1_ecall_2 , \ex_mem流水寄存器_1_jal_2 ,
       \ex_mem流水寄存器_1_jalr_2 , \ex_mem流水寄存器_1_memtoreg_2 , \ex_mem流水寄存器_1_regwrite_2 , Go, halt, I,
       \id_ex流水寄存器_1_beq_2 , \id_ex流水寄存器_1_bne_2 , \id_ex流水寄存器_1_ecall_2 , \id_ex流水寄存器_1_jal_2 ,
       \id_ex流水寄存器_1_memtoreg_2 , \id_ex流水寄存器_1_memwrite_2 , \id_ex流水寄存器_1_regwrite_2 , \id_ex流水寄存器_1_sb_2 ,
       IR1, IR2, IR3, J, JAL, JAL_star, JALR, JALR_star, lessthen, \mem_wb流水寄存器_1_memtoreg_2 , nand_1_out,
       not_1_out, not_2_out, or_1_out, PC_EN, PCSrc, RST, S_type, sb_star, URET, W1, W2, W3,
       \单周期硬布线控制器_1_alu_src , \单周期硬布线控制器_1_beq , \单周期硬布线控制器_1_bltu , \单周期硬布线控制器_1_bne , \单周期硬布线控制器_1_cleari ,
       \单周期硬布线控制器_1_memtoreg , \单周期硬布线控制器_1_memwrite , \单周期硬布线控制器_1_regwrite , \单周期硬布线控制器_1_sb ,
       \单周期硬布线控制器_1_seti , \单周期硬布线控制器_1_sll , \气泡逻辑_1_id_ex_clr , \气泡逻辑_1_if_id_clr , \气泡逻辑_1_if_id_en ;
  wire [1:0] \id_ex流水寄存器_1_alu_src_2 ;
  wire [3:0] \id_ex流水寄存器_1_aluop_2 , \单周期硬布线控制器_1_alu_op ;
  wire [4:0] EX_W_num, ID_R1_num, ID_R2_num, MEM_W_num, \mem_wb流水寄存器_1_w_num_2 ;
  wire [9:0] \ex_mem流水寄存器_1_address_2 ;
  wire [12:0] CNT_num;
  wire [15:0] \LoadUse次数 , \总周期数 , \插入气泡数 , \无条件分支数 , \条件分支成功数 ;
  wire [31:0] adder_1_out, adder_2_out, and_2_out, bit_extender_1_out, bit_extender_2_out,
       bit_extender_3_out, bit_extender_4_out, ec_out, EX_ec_out, EX_IR, \ex_mem流水寄存器_1_ec_out_2 ,
       \ex_mem流水寄存器_1_pc_4_2 , \ex_mem流水寄存器_1_pc_offset_2 , \ex_mem流水寄存器_1_r2_2 , \ex_mem流水寄存器_1_result_2 ,
       \id_ex流水寄存器_1_pc_4_2 , \id_ex流水寄存器_1_r1_2 , \id_ex流水寄存器_1_r2__sll_2 , \id_ex流水寄存器_1_立即数_2 , ID_IR,
       \if_id流水寄存器_1_pc_4_2 , IF_IR, MEM_IR, \mem_wb流水寄存器_1_mem_3 , \mem_wb流水寄存器_1_pc_4_2 ,
       \mem_wb流水寄存器_1_result_2 , multiplexer_1_out, multiplexer_5_out, multiplexer_6_out, multiplexer_8_out,
       ram_1_data, regifile_1_r1, regifile_1_r2, \sb分线_1_output , shifter_1_out, WB_IR;
  wire [31:1] alu_1_result;

  Button \u_总复位  (.out(RST));
  Button _1 (.out(IR1));
  Button _2 (.out(IR2));
  Button _3 (.out(IR3));
  // Probe on \总周期数 
  // Probe on \总周期数 
  Button \u_继续运行  (.out(Go));
  LED #(.active("true")) led_1 (.in(W1));
  LED #(.active("true")) led_2 (.in(W2));
  LED #(.active("true")) led_3 (.in(W3));
  Hex_Digit_Display hex_digit_display_1 (.value(LedData[31:28]));  // open: dp
  // Probe on IF_PC[19:0]
  // RiscV_Probe riscv_probe_1: pin names not known; wires that end beside it: IF_IR
  Hex_Digit_Display hex_digit_display_2 (.value(LedData[27:24]));  // open: dp
  Hex_Digit_Display hex_digit_display_3 (.value(LedData[23:20]));  // open: dp
  // Probe on ID_PC[19:0]
  // RiscV_Probe riscv_probe_2: pin names not known; wires that end beside it: ID_IR
  Hex_Digit_Display hex_digit_display_4 (.value(LedData[15:12]));  // open: dp
  Hex_Digit_Display hex_digit_display_5 (.value(LedData[19:16]));  // open: dp
  Hex_Digit_Display hex_digit_display_6 (.value(LedData[7:4]));  // open: dp
  Hex_Digit_Display hex_digit_display_7 (.value(LedData[11:8]));  // open: dp
  // Probe on EX_PC[19:0]
  // RiscV_Probe riscv_probe_3: pin names not known; wires that end beside it: EX_IR
  \气泡逻辑  \u_气泡逻辑_1  (
    .I(I), .B(B), .J(JAL), .S(S_type), .IR(ID_IR), .R1(ID_R1_num), .R2(ID_R2_num),
    .EX_RegWrite(\id_ex流水寄存器_1_regwrite_2 ), .EX_WriteReg_num(EX_W_num), .MEM_WriteReg_num(MEM_W_num),
    .MEM_RegWrite(\ex_mem流水寄存器_1_regwrite_2 ), .BranchTakens(Branch), .ID_EX_CLR(\气泡逻辑_1_id_ex_clr ),
    .IF_ID_CLR(\气泡逻辑_1_if_id_clr ), .IF_ID_EN(\气泡逻辑_1_if_id_en ), .PC_EN(PC_EN));  // open: stall
  Multiplexer #(.select(2), .width(32), .disabled("Z"), .enable("false")) multiplexer_1 (
    .in0(adder_1_out), .in1(adder_2_out), .in2(and_2_out), .out(multiplexer_1_out), .sel({EX_JALR, PCSrc}));  // open: in3
  and and_1 (and_1_out, not_1_out, PC_EN);
  not not_1 (not_1_out, halt);
  Hex_Digit_Display hex_digit_display_8 (.value(LedData[3:0]));  // open: dp
  not not_2 (not_2_out, halt);
  Counter #(.width(16), .max('hffff), .ongoal("wrap"), .trigger("rising"), .behavior("new")) counter_1 (
    .D(16'h1), .count(not_2_out), .Q(\总周期数 ), .clk(CLK));  // open: load, carry, clr, preset, down
  Register #(.width(32), .trigger("rising"), .Select("low")) PC (
    .D({{20{1'b0}}, multiplexer_1_out[11:0]}), .en(and_1_out), .Q(IF_PC), .clk(CLK), .clr(RST));
  // Probe on \总周期数 
  // Probe on M_PC[19:0]
  // RiscV_Probe riscv_probe_4: pin names not known; wires that end beside it: MEM_IR
  // Probe on \总周期数 
  // Probe on \无条件分支数 
  // Probe on \条件分支成功数 
  // Probe on \插入气泡数 
  // Probe on \LoadUse次数 
  // Probe on IF_PC
  Adder #(.width(32)) adder_1 (.a(IF_PC), .b(32'h4), .out(adder_1_out));  // open: cin, cout
  // Probe on IF_PC[11:0]
  // Probe on WB_PC[19:0]
  // RiscV_Probe riscv_probe_5: pin names not known; wires that end beside it: WB_IR
  ROM #(.addrWidth(10), .dataWidth(32), .Select("high")) rom_1 (.addr(IF_PC[11:2]), .data(IF_IR));
  // Probe on EX_PC[11:0]
  // Probe on ID_PC[11:0]
  or or_1 (or_1_out, \气泡逻辑_1_if_id_en , halt);
  \IF_ID流水寄存器  \if_id流水寄存器_1  (
    .IR(IF_IR), .PC(IF_PC), .PC_4(adder_1_out), .IR_2(ID_IR), .PC_2(ID_PC), .PC_4_2(\if_id流水寄存器_1_pc_4_2 ),
    .\同步清零_高电平有效 (\气泡逻辑_1_if_id_clr ), .CLK(CLK), .\EN使能端 (or_1_out));  // open: PredictJump, PredictJump_2
  // Probe on M_PC[11:0]
  D_Flip_Flop #(.trigger("high"), .Pre_Clr_Positions("LEGACY"), .NegatePresetClear("false"), .enable("true"), .NewFFLayout("false")) d_ff_1 (.Q(d_ff_1_q));  // open: clk, D, Qn, preset, en, reset
  // Probe on 13'h55
  // Probe on WB_PC[11:0]
  Comparator #(.width(13), .mode("twosComplement")) comparator_1 (
    .a(CNT_num), .b(13'h55), .eq(comparator_1_eq), .lt(comparator_1_lt));  // open: gt
  Clock #(.highDuration(1), .lowDuration(1)) clock_1 (.out(clock_1_out));
  // RiscV_Probe riscv_probe_6: pin names not known; wires that end beside it: ID_IR
  nand nand_1 (nand_1_out, d_ff_1_q, comparator_1_eq);
  Counter #(.width(13), .max('h1fff), .ongoal("stay"), .trigger("rising"), .behavior("old")) counter_2 (
    .count(comparator_1_lt), .Q(CNT_num), .clk(clock_1_out));  // open: load, D, carry, clr, preset
  assign CLK = nand_1_out ? clock_1_out : 1'bz;  // Controlled_Buffer controlled_buffer_1
  \单周期硬布线控制器  \u_单周期硬布线控制器_1  (
    .Funct({ID_IR[30], ID_IR[25], ID_IR[14:12]}), .OP(ID_IR[6:2]), .ALU_OP(\单周期硬布线控制器_1_alu_op ),
    .MemToReg(\单周期硬布线控制器_1_memtoreg ), .MemWrite(\单周期硬布线控制器_1_memwrite ), .ALU_SRC(\单周期硬布线控制器_1_alu_src ),
    .RegWrite(\单周期硬布线控制器_1_regwrite ), .ecall(ecall), .S_type(S_type), .Jalr(JALR), .Beq(\单周期硬布线控制器_1_beq ),
    .JAL(JAL), .Bne(\单周期硬布线控制器_1_bne ), .in_3(ID_IR[21]), .uret(URET), .I(I), .B(B),
    .clearI(\单周期硬布线控制器_1_cleari ), .sb(\单周期硬布线控制器_1_sb ), .sll(\单周期硬布线控制器_1_sll ), .setI(\单周期硬布线控制器_1_seti ),
    .bltu(\单周期硬布线控制器_1_bltu ));
  assign bit_extender_1_out = {{20{ID_IR[31]}}, ID_IR[31:20]};  // Bit_Extender bit_extender_1
  assign bit_extender_2_out = {{20{ID_IR[31]}}, {ID_IR[31:25], ID_IR[11:7]}};  // Bit_Extender bit_extender_2
  assign bit_extender_3_out = {{20{ID_IR[31]}}, {ID_IR[31], ID_IR[7], ID_IR[30:25], ID_IR[11:8]}};  // Bit_Extender bit_extender_3
  assign bit_extender_4_out = {{12{ID_IR[31]}}, {ID_IR[31], ID_IR[19:12], ID_IR[20], ID_IR[30:21]}};  // Bit_Extender bit_extender_4
  Pull_Resistor #(.pull(1)) pull_resistor_1 (.node(CLK));
  Multiplexer #(.select(1), .width(5), .disabled("Z"), .enable("false")) multiplexer_2 (
    .in0(ID_IR[19:15]), .in1(5'b10001), .out(ID_R1_num), .sel(ecall));
  Multiplexer #(.select(1), .width(5), .disabled("Z"), .enable("false")) multiplexer_3 (
    .in0(ID_IR[24:20]), .in1(5'b01010), .out(ID_R2_num), .sel(ecall));
  Multiplexer #(.select(1), .width(32), .disabled("Z"), .enable("false")) multiplexer_4 (
    .in0(multiplexer_8_out), .in1(\mem_wb流水寄存器_1_pc_4_2 ), .out(RDin), .sel(J));
  Multiplexer #(.select(4), .width(32), .disabled("Z"), .enable("false")) multiplexer_5 (
    .in1(bit_extender_1_out), .in2(bit_extender_2_out), .in4(bit_extender_3_out), .in8(bit_extender_4_out),
    .out(multiplexer_5_out), .sel({JAL, B, S_type, I}));  // open: in0, in3, in5, in6, in7, in9, in10, in11, in12, in13, in14, in15
  Regifile regifile_1 (
    .Din(RDin), .Clk(CLK), .R1(regifile_1_r1), .R2(regifile_1_r2), .WE(RegWrite),
    .W_num(\mem_wb流水寄存器_1_w_num_2 ), .R1_num(ID_R1_num), .R2_num(ID_R2_num));
  \ID_EX流水寄存器  \id_ex流水寄存器_1  (
    .ecall(ecall), .jal(JAL), .jalr(JALR), .uret(URET), .Beq(\单周期硬布线控制器_1_beq ), .Bne(\单周期硬布线控制器_1_bne ),
    .MemToReg(\单周期硬布线控制器_1_memtoreg ), .MemWrite(\单周期硬布线控制器_1_memwrite ), .AluOP(\单周期硬布线控制器_1_alu_op ),
    .Alu_Src(\单周期硬布线控制器_1_alu_src ), .RegWrite(\单周期硬布线控制器_1_regwrite ), .sb(\单周期硬布线控制器_1_sb ),
    .clearI(\单周期硬布线控制器_1_cleari ), .setI(\单周期硬布线控制器_1_seti ), .sll(\单周期硬布线控制器_1_sll ), .R1(regifile_1_r1),
    .R2__sll({{27{1'b0}}, regifile_1_r2[4:0]}), .\立即数 (multiplexer_5_out), .W_num(ID_IR[11:7]), .PC(ID_PC),
    .PC_4(\if_id流水寄存器_1_pc_4_2 ), .ecall_2(\id_ex流水寄存器_1_ecall_2 ), .jal_2(\id_ex流水寄存器_1_jal_2 ),
    .jalr_2(EX_JALR), .Beq_2(\id_ex流水寄存器_1_beq_2 ), .Bne_2(\id_ex流水寄存器_1_bne_2 ),
    .MemToReg_2(\id_ex流水寄存器_1_memtoreg_2 ), .MemWrite_2(\id_ex流水寄存器_1_memwrite_2 ),
    .AluOP_2(\id_ex流水寄存器_1_aluop_2 ), .Alu_Src_2(\id_ex流水寄存器_1_alu_src_2 [0]),
    .RegWrite_2(\id_ex流水寄存器_1_regwrite_2 ), .sb_2(\id_ex流水寄存器_1_sb_2 ), .sll_2(\id_ex流水寄存器_1_alu_src_2 [1]),
    .R1_2(\id_ex流水寄存器_1_r1_2 ), .R2__sll_2(\id_ex流水寄存器_1_r2__sll_2 ), .\立即数_2 (\id_ex流水寄存器_1_立即数_2 ),
    .W_num_2(EX_W_num), .PC_2(EX_PC), .PC_4_2(\id_ex流水寄存器_1_pc_4_2 ), .\同步清零_高电平有效 (\气泡逻辑_1_id_ex_clr ),
    .CLK(CLK), .\EN使能端 (halt), .bltu(\单周期硬布线控制器_1_bltu ), .bltu_2(bltu), .R2(regifile_1_r2),
    .R2_2(EX_ec_out), .IR(ID_IR), .IR_2(EX_IR));  // open: uret_2, clearI_2, setI_2, RsForward, RsForward_2, RtForward, RtForward_2, PredictJump, PredictJump_2
  Comparator #(.width(32), .mode("unsigned")) comparator_2 (
    .a(32'h22), .b(\id_ex流水寄存器_1_r1_2 ), .eq(Ex_ec_eq));  // open: gt, lt
  Multiplexer #(.select(2), .width(32), .disabled("Z"), .enable("false")) multiplexer_6 (
    .in0(EX_ec_out), .in1(\id_ex流水寄存器_1_立即数_2 ), .in2(\id_ex流水寄存器_1_r2__sll_2 ), .out(multiplexer_6_out),
    .sel(\id_ex流水寄存器_1_alu_src_2 ));  // open: in3
  Shifter #(.width(32), .shift("ll")) shifter_1 (.in(\id_ex流水寄存器_1_立即数_2 ), .\dist (5'b00001), .out(shifter_1_out));
  assign and_2_out = {alu_1_result, lessthen} & 32'hfffffffe;  // AND_Gate and_2, 32 bits wide
  ALU alu_1 (
    .X(\id_ex流水寄存器_1_r1_2 ), .Y(multiplexer_6_out), .AluOP(\id_ex流水寄存器_1_aluop_2 ), .Equal(alu_1_equal),
    .Result({alu_1_result, lessthen}));  // open: Result_2, out_4, out_6
  Adder #(.width(32)) adder_2 (.a(shifter_1_out), .b(EX_PC), .out(adder_2_out));  // open: cin, cout
  and and_3 (and_3_out, bltu, lessthen);
  and and_4 (and_4_out, alu_1_equal, \id_ex流水寄存器_1_beq_2 );
  and and_5 (and_5_out, ~alu_1_equal, \id_ex流水寄存器_1_bne_2 );  // AND_Gate
  or or_2 (PCSrc, and_3_out, and_4_out, and_5_out, \id_ex流水寄存器_1_jal_2 );
  or or_3 (Branch, and_3_out, and_4_out, and_5_out, \id_ex流水寄存器_1_jal_2 , EX_JALR);
  \EX_MEM流水寄存器  \ex_mem流水寄存器_1  (
    .W_num(EX_W_num), .W_num_2(MEM_W_num), .PC(EX_PC), .PC_2(M_PC), .PC_4(\id_ex流水寄存器_1_pc_4_2 ),
    .PC_4_2(\ex_mem流水寄存器_1_pc_4_2 ), .CLK(CLK), .\EN使能端 (halt), .lt(lessthen), .PC_offset(adder_2_out),
    .PC_offset_2(\ex_mem流水寄存器_1_pc_offset_2 ), .result({alu_1_result, lessthen}),
    .result_2(\ex_mem流水寄存器_1_result_2 ), .address(alu_1_result[11:2]), .address_2(\ex_mem流水寄存器_1_address_2 ),
    .ecall(\id_ex流水寄存器_1_ecall_2 ), .ecall_2(\ex_mem流水寄存器_1_ecall_2 ), .jal(\id_ex流水寄存器_1_jal_2 ),
    .jal_2(\ex_mem流水寄存器_1_jal_2 ), .jalr(EX_JALR), .jalr_2(\ex_mem流水寄存器_1_jalr_2 ),
    .MemToReg(\id_ex流水寄存器_1_memtoreg_2 ), .MemToReg_2(\ex_mem流水寄存器_1_memtoreg_2 ),
    .MemWrite(\id_ex流水寄存器_1_memwrite_2 ), .MemWrite_2(MemWrite), .RegWrite(\id_ex流水寄存器_1_regwrite_2 ),
    .RegWrite_2(\ex_mem流水寄存器_1_regwrite_2 ), .sb(\id_ex流水寄存器_1_sb_2 ), .sb_2(sb_star), .R2(EX_ec_out),
    .R2_2(\ex_mem流水寄存器_1_r2_2 ), .bltu(bltu), .bltu_2(\ex_mem流水寄存器_1_bltu_2 ), .IR(EX_IR), .IR_2(MEM_IR),
    .ec_eq(Ex_ec_eq), .ec_eq_2(\ex_mem流水寄存器_1_ec_eq_2 ), .ec_out(EX_ec_out),
    .ec_out_2(\ex_mem流水寄存器_1_ec_out_2 ));  // open: 同步清零_高电平有效, lt_2, uret, uret_2, Beq, Beq_2, Bne, Bne_2, clearI, clearI_2, setI, ecall_3, sll, sll_2, halt, halt_2
  \sb分线  \sb分线_1  (
    .\new (\ex_mem流水寄存器_1_r2_2 [7:0]), .Address(\ex_mem流水寄存器_1_result_2 [1:0]), .\output (\sb分线_1_output ),
    .origin(ram_1_data));
  RAM #(.addrWidth(10), .dataWidth(32), .bus("separate"), .Select("high")) ram_1 (
    .addr(\ex_mem流水寄存器_1_address_2 ), .din(MDin), .data(ram_1_data), .str(MemWrite), .clk(CLK), .ld(1'b1));  // open: sel, clr
  Multiplexer #(.select(1), .width(32), .disabled("Z"), .enable("false")) multiplexer_7 (
    .in0(\ex_mem流水寄存器_1_r2_2 ), .in1(\sb分线_1_output ), .out(MDin), .sel(sb_star));
  \MEM_WB流水寄存器  \mem_wb流水寄存器_1  (
    .W_num(MEM_W_num), .W_num_2(\mem_wb流水寄存器_1_w_num_2 ), .PC(M_PC), .PC_2(WB_PC),
    .PC_4(\ex_mem流水寄存器_1_pc_4_2 ), .PC_4_2(\mem_wb流水寄存器_1_pc_4_2 ), .CLK(CLK), .\EN使能端 (halt),
    .RegWrite(\ex_mem流水寄存器_1_regwrite_2 ), .RegWrite_2(RegWrite), .MemToReg(\ex_mem流水寄存器_1_memtoreg_2 ),
    .MemToReg_2(\mem_wb流水寄存器_1_memtoreg_2 ), .jalr(\ex_mem流水寄存器_1_jalr_2 ), .jalr_2(JALR_star),
    .jal(\ex_mem流水寄存器_1_jal_2 ), .jal_2(JAL_star), .ecall(\ex_mem流水寄存器_1_ecall_2 ), .ecall_2(ecall_star),
    .Result(\ex_mem流水寄存器_1_result_2 ), .Result_2(\mem_wb流水寄存器_1_result_2 ), .Mem(ram_1_data),
    .Mem_3(\mem_wb流水寄存器_1_mem_3 ), .PC_offset(\ex_mem流水寄存器_1_pc_offset_2 ), .bltu(\ex_mem流水寄存器_1_bltu_2 ),
    .IR(MEM_IR), .Mem_2(WB_IR), .ec_out(\ex_mem流水寄存器_1_ec_out_2 ), .ec_out_2(ec_out),
    .ec_eq(\ex_mem流水寄存器_1_ec_eq_2 ), .ec_eq_2(ec_eq));  // open: 同步清零_高电平有效, lt, lt_2, PC_offset_2, bltu_2, uret, uret_2, Beq, Beq_2, Bne, Bne_2, clearI, clearI_2, setI, setI_2, sll, sll_2, halt, halt_2
  Multiplexer #(.select(1), .width(32), .disabled("Z"), .enable("false")) multiplexer_8 (
    .in0(\mem_wb流水寄存器_1_result_2 ), .in1(\mem_wb流水寄存器_1_mem_3 ), .out(multiplexer_8_out),
    .sel(\mem_wb流水寄存器_1_memtoreg_2 ));
  or or_4 (J, JAL_star, JALR_star);
  and and_6 (and_6_out, ecall_star, ~ec_eq);  // AND_Gate
  and and_7 (and_7_out, ec_eq, ecall_star);
  D_Flip_Flop #(.trigger("high"), .Pre_Clr_Positions("LEGACY"), .NegatePresetClear("false"), .enable("true"), .NewFFLayout("false")) d_ff_2 (
    .clk(CLK), .D(and_6_out), .Q(halt), .reset(Go));  // open: Qn, preset, en
  Register #(.width(32), .trigger("rising"), .Select("low")) register_1 (
    .D(ec_out), .en(and_7_out), .Q(LedData), .clk(CLK));  // open: clr

  // Other names for the same wires on the sheet: IR[31:0] = ID_IR; MEM_PC[31:0] = M_PC

  // Notes on the sheet:
  //   中断源
  //   时空图监测，可删除
  //   中断等待指示
  //   数码管输出
  //   指令存储器
  //   contents of rom_1 (hex, n*v repeats v):
  //   100493 100006f 100493 200913 300993 100006f 100493 200913 300993 100006f 100493 200913 300993
  //   100006f 100493 200913 300993 3b4000ef 100413 100493 1f49493 900533 2200893 73 24d493 48463 fedff06f
  //   900533 2200893 73 100493 249493 900533 2200893 73 48463 fedff06f 100493 1f49493 900533 2200893 73
  //   4034d493 900533 2200893 73 4044d493 900533 2200893 73 4044d493 900533 2200893 73 4044d493 900533
  //   2200893 73 4044d493 900533 2200893 73 4044d493 900533 2200893 73 4044d493 900533 2200893 73 4044d493
  //   900533 2200893 73 100413 1f41993 41f9d993 433 c00913 300b13 140413 f47413 800293 100313 499993
  //   89e9b3 1300533 2200893 73 406282b3 fe0294e3 140413 f00f93 1f47433 1c41413 800293 100313 49d993
  //   89e9b3 1300533 2200893 73 406282b3 fe0294e3 1c45413 406b0b33 b0463 f95ff06f 2b3 fff2c293 829293
  //   ff2e293 500533 2200893 73 fff00413 493 84a023 140413 448493 84a023 140413 448493 84a023 140413
  //   448493 84a023 140413 448493 84a023 140413 448493 84a023 140413 448493 84a023 140413 448493 84a023
  //   140413 448493 84a023 140413 448493 84a023 140413 448493 84a023 140413 448493 84a023 140413 448493
  //   84a023 140413 448493 84a023 140413 448493 84a023 140413 448493 84a023 140413 448493 140413 433
  //   3c00493 42983 4aa03 149a2b3 28663 134a023 1442023 ffc48493 fe9412e3 800533 2200893 73 440413 3c00493
  //   fc9416e3 3200893 73 100293 300313 800493 849493 7648493 900533 2200893 73 800e13 5494b3 6494b3
  //   900533 2200893 73 fffe0e13 fe0e14e3 a00893 73 fff00293 7700493 849493 7748493 900533 2200893 73
  //   1000e13 54c4b3 900533 2200893 73 fffe0e13 fe0e16e3 a00893 73 313 2000e13 493 100913 930023 900533
  //   2200893 73 12484b3 130313 fffe0e13 fe0e12e3 800e13 313 32483 900533 2200893 73 430313 fffe0e13
  //   fe0e14e3 a00893 73 ff100493 900533 2200893 73 148493 fe9068e3 900533 2200893 73 a00893 73 a00893 73
  //   413 140413 800533 2200893 73 240413 800533 2200893 73 340413 800533 2200893 73 440413 800533 2200893
  //   73 540413 800533 2200893 73 640413 800533 2200893 73 740413 800533 2200893 73 840413 800533 2200893
  //   2200893 73 8067
  //   控制位
  //   指令字
  //   流水调试日志用
  //   暂停节拍，不能为0
  //   戳工具置1进入计数暂停模式，ctrl+k时钟自动运行到对应节拍暂停
  //   ctrl+k关闭时钟连续运行，将控制位置零，进入单步调试模式调试
  //   指令探针
  //   JAL
  //   JALR
  //   URET
  //   I
  //   B
  //   可计数暂停的时钟源
  //   为方便自动评测，需要输出流水线各段保存的PC值，注意是PC不是PC+4，另外ID段寄存器写入信息，Mem段内存写入信息也要输出
  //   sll指令输入线
  //   写入信号
  //   PC+4
  //   ecall
  //   jal
  //   jalr
  //   uret
  //   Beq
  //   Bne
  //   MemToReg
  //   MemWrite
  //   AluOP
  //   Alu_Src
  //   RegWrite
  //   sb
  //   clearI
  //   setI
  //   sll
  //   立即数
  //   ecall
  //   MemToReg
  //   MemWrite
  //   RegWrite
  //   写入信号
  //   PC+4
  //   jal
  //   jalr
  //   数据存储器
  //   ecall
  //   jal
  //   jalr
  //   MemToReg
  //   RegWrite
  //   R2*
  //   Result
  //   Mem
  //   lessthen
  //   写入信号
  //   PC+4
endmodule

module \动态分支预测流水线  (
  output RegWrite,
  output MemWrite,
  output [31:0] IF_PC,
  output [31:0] ID_PC,
  output [31:0] EX_PC,
  output [31:0] M_PC,
  output [31:0] WB_PC,
  output [31:0] RDin,
  output [31:0] MDin,
  output [31:0] LedData
);

  wire alu_1_equal, and_1_out, and_3_out, and_4_out, and_5_out, and_6_out, and_7_out, B, bltu, CLK,
       clock_1_out, comparator_1_eq, comparator_1_lt, d_ff_1_q, ec_eq, ecall, ecall_star, EX_Branch,
       EX_BranchTaken, Ex_ec_eq, EX_JALR, \ex_mem流水寄存器_1_bltu_2 , \ex_mem流水寄存器_1_ec_eq_2 ,
       \ex_mem流水寄存器_1_ecall_2 , \ex_mem流水寄存器_1_jal_2 , \ex_mem流水寄存器_1_jalr_2 , \ex_mem流水寄存器_1_memtoreg_2 ,
       \ex_mem流水寄存器_1_regwrite_2 , EX_PredictErr, EX_PredictJump, Go, halt, I, \id_ex流水寄存器_1_beq_2 ,
       \id_ex流水寄存器_1_bne_2 , \id_ex流水寄存器_1_ecall_2 , \id_ex流水寄存器_1_jal_2 , \id_ex流水寄存器_1_memtoreg_2 ,
       \id_ex流水寄存器_1_memwrite_2 , \id_ex流水寄存器_1_regwrite_2 , \id_ex流水寄存器_1_sb_2 , ID_PredictJump,
       ID_PredictJump_t, IR1, IR2, IR3, J, JAL, JAL_star, JALR, JALR_star, lessthen,
       \mem_wb流水寄存器_1_memtoreg_2 , nand_1_out, not_1_out, not_2_out, not_3_out, or_1_out, PC_EN, PCSrc,
       PredictJump, RST, S_type, sb_star, URET, W1, W2, W3, \单周期硬布线控制器_1_alu_src , \单周期硬布线控制器_1_beq ,
       \单周期硬布线控制器_1_bltu , \单周期硬布线控制器_1_bne , \单周期硬布线控制器_1_cleari , \单周期硬布线控制器_1_memtoreg ,
       \单周期硬布线控制器_1_memwrite , \单周期硬布线控制器_1_regwrite , \单周期硬布线控制器_1_sb , \单周期硬布线控制器_1_seti ,
       \单周期硬布线控制器_1_sll , \重定向逻辑_1_id_ex_clr , \重定向逻辑_1_if_id_clr ;
  wire [1:0] \id_ex流水寄存器_1_alu_src_2 , \id_ex流水寄存器_1_rsforward_2 , \id_ex流水寄存器_1_rtforward_2 ,
       \重定向逻辑_1_rsforward , \重定向逻辑_1_rtforward ;
  wire [3:0] \id_ex流水寄存器_1_aluop_2 , \单周期硬布线控制器_1_alu_op ;
  wire [4:0] EX_W_num, ID_R1_num, ID_R2_num, MEM_W_num, \mem_wb流水寄存器_1_w_num_2 ;
  wire [9:0] \ex_mem流水寄存器_1_address_2 ;
  wire [12:0] CNT_num;
  wire [15:0] \LoadUse次数 , \总周期数 , \插入气泡数 , \无条件分支数 , \条件分支成功数 ;
  wire [31:0] adder_2_out, and_2_out, bit_extender_1_out, bit_extender_2_out, bit_extender_3_out,
       bit_extender_4_out, \btb表_1_jumpaddr , ec_out, EX_ec_out, EX_IR, \ex_mem流水寄存器_1_ec_out_2 ,
       \ex_mem流水寄存器_1_pc_4_2 , \ex_mem流水寄存器_1_pc_offset_2 , \ex_mem流水寄存器_1_r2_2 , \ex_mem流水寄存器_1_result_2 ,
       \id_ex流水寄存器_1_pc_4_2 , \id_ex流水寄存器_1_r1_2 , \id_ex流水寄存器_1_r2_2 , \id_ex流水寄存器_1_r2__sll_2 ,
       \id_ex流水寄存器_1_立即数_2 , ID_IR, \if_id流水寄存器_1_pc_4_2 , IF_IR, IF_PC_4, MEM_IR, \mem_wb流水寄存器_1_mem_3 ,
       \mem_wb流水寄存器_1_pc_4_2 , \mem_wb流水寄存器_1_result_2 , multiplexer_1_out, multiplexer_2_out,
       multiplexer_3_out, multiplexer_4_out, multiplexer_8_out, multiplexer_9_out, multiplexer_11_out,
       multiplexer_13_out, ram_1_data, regifile_1_r1, regifile_1_r2, \sb分线_1_output , shifter_1_out, WB_IR;
  wire [31:1] alu_1_result;

  Button \u_总复位  (.out(RST));
  Button _1 (.out(IR1));
  Button _2 (.out(IR2));
  Button _3 (.out(IR3));
  // Probe on \总周期数 
  // Probe on \总周期数 
  Button \u_继续运行  (.out(Go));
  LED #(.active("true")) led_1 (.in(W1));
  LED #(.active("true")) led_2 (.in(W2));
  LED #(.active("true")) led_3 (.in(W3));
  Hex_Digit_Display hex_digit_display_1 (.value(LedData[31:28]));  // open: dp
  // Probe on IF_PC[19:0]
  // RiscV_Probe riscv_probe_1: pin names not known; wires that end beside it: IF_IR
  Hex_Digit_Display hex_digit_display_2 (.value(LedData[27:24]));  // open: dp
  Hex_Digit_Display hex_digit_display_3 (.value(LedData[23:20]));  // open: dp
  // Probe on ID_PC[19:0]
  // RiscV_Probe riscv_probe_2: pin names not known; wires that end beside it: ID_IR
  Multiplexer #(.select(2), .width(32), .disabled("Z"), .enable("false")) multiplexer_1 (
    .in0(\id_ex流水寄存器_1_pc_4_2 ), .in1(adder_2_out), .in2(and_2_out), .out(multiplexer_1_out),
    .sel({EX_JALR, PCSrc}));  // open: in3
  Hex_Digit_Display hex_digit_display_4 (.value(LedData[19:16]));  // open: dp
  Hex_Digit_Display hex_digit_display_5 (.value(LedData[15:12]));  // open: dp
  Multiplexer #(.select(1), .width(32), .disabled("Z"), .enable("false")) multiplexer_2 (
    .in0(multiplexer_4_out), .in1(multiplexer_1_out), .out(multiplexer_2_out), .sel(EX_PredictErr));
  \BTB表  \btb表_1  (
    .PC(IF_PC), .Ex_BranchAddr(multiplexer_3_out), .CLK(CLK), .Ex_PC(EX_PC), .EX_Branch(EX_Branch),
    .EX_BranchTaken(EX_BranchTaken), .JumpAddr(\btb表_1_jumpaddr ), .PredictJump(PredictJump));
  Multiplexer #(.select(1), .width(32), .disabled("Z"), .enable("false")) multiplexer_3 (
    .in0(adder_2_out), .in1(and_2_out), .out(multiplexer_3_out), .sel(EX_JALR));
  Hex_Digit_Display hex_digit_display_6 (.value(LedData[7:4]));  // open: dp
  Hex_Digit_Display hex_digit_display_7 (.value(LedData[11:8]));  // open: dp
  // Probe on EX_PC[19:0]
  // RiscV_Probe riscv_probe_3: pin names not known; wires that end beside it: EX_IR
  not not_1 (not_1_out, halt);
  Multiplexer #(.select(1), .width(32), .disabled("Z"), .enable("false")) multiplexer_4 (
    .in0(IF_PC_4), .in1(\btb表_1_jumpaddr ), .out(multiplexer_4_out), .sel(PredictJump));
  Hex_Digit_Display hex_digit_display_8 (.value(LedData[3:0]));  // open: dp
  \重定向逻辑  \u_重定向逻辑_1  (
    .R1(ID_R1_num), .I(I), .B(B), .IR(ID_IR), .R2(ID_R2_num), .BranchTakens(EX_PredictErr), .J(JAL),
    .EX_WriteReg_num(EX_W_num), .EX_RegWrite(\id_ex流水寄存器_1_regwrite_2 ), .S(S_type),
    .MEM_WriteReg_num(MEM_W_num), .MEM_RegWrite(\ex_mem流水寄存器_1_regwrite_2 ),
    .EX_MemRead__MemToReg(\id_ex流水寄存器_1_memtoreg_2 ), .PC_EN(PC_EN), .ID_EX_CLR(\重定向逻辑_1_id_ex_clr ),
    .IF_ID_CLR(\重定向逻辑_1_if_id_clr ), .RsForward(\重定向逻辑_1_rsforward ), .RtForward(\重定向逻辑_1_rtforward ));
  not not_2 (not_2_out, halt);
  Counter #(.width(16), .max('hffff), .ongoal("wrap"), .trigger("rising"), .behavior("new")) counter_1 (
    .D(16'h1), .count(not_2_out), .Q(\总周期数 ), .clk(CLK));  // open: load, carry, clr, preset, down
  Register #(.width(32), .trigger("rising"), .Select("low")) PC (
    .D({{20{1'b0}}, multiplexer_2_out[11:0]}), .en(and_1_out), .Q(IF_PC), .clk(CLK), .clr(RST));
  and and_1 (and_1_out, not_1_out, PC_EN);
  // Probe on \总周期数 
  // Probe on M_PC[19:0]
  // RiscV_Probe riscv_probe_4: pin names not known; wires that end beside it: MEM_IR
  // Probe on \总周期数 
  // Probe on \无条件分支数 
  // Probe on \条件分支成功数 
  // Probe on \插入气泡数 
  // Probe on \LoadUse次数 
  // Probe on IF_PC
  Adder #(.width(32)) adder_1 (.a(IF_PC), .b(32'h4), .out(IF_PC_4));  // open: cin, cout
  // Probe on IF_PC[11:0]
  // Probe on WB_PC[19:0]
  // RiscV_Probe riscv_probe_5: pin names not known; wires that end beside it: WB_IR
  ROM #(.addrWidth(10), .dataWidth(32), .Select("high")) rom_1 (.addr(IF_PC[11:2]), .data(IF_IR));
  // Probe on ID_PC[11:0]
  // Probe on EX_PC[11:0]
  not not_3 (not_3_out, PC_EN);
  or or_1 (or_1_out, not_3_out, halt);
  \IF_ID流水寄存器  \if_id流水寄存器_1  (
    .IR(IF_IR), .PC(IF_PC), .PC_4(IF_PC_4), .IR_2(ID_IR), .PC_2(ID_PC), .PC_4_2(\if_id流水寄存器_1_pc_4_2 ),
    .\同步清零_高电平有效 (\重定向逻辑_1_if_id_clr ), .CLK(CLK), .\EN使能端 (or_1_out), .PredictJump(PredictJump),
    .PredictJump_2(ID_PredictJump));
  // Probe on M_PC[11:0]
  D_Flip_Flop #(.trigger("high"), .Pre_Clr_Positions("LEGACY"), .NegatePresetClear("false"), .enable("true"), .NewFFLayout("false")) d_ff_1 (.Q(d_ff_1_q));  // open: clk, D, Qn, preset, en, reset
  // Probe on 13'h156
  // Probe on WB_PC[11:0]
  Comparator #(.width(13), .mode("twosComplement")) comparator_1 (
    .a(CNT_num), .b(13'h156), .eq(comparator_1_eq), .lt(comparator_1_lt));  // open: gt
  Clock #(.highDuration(1), .lowDuration(1)) clock_1 (.out(clock_1_out));
  // RiscV_Probe riscv_probe_6: pin names not known; wires that end beside it: ID_IR
  nand nand_1 (nand_1_out, d_ff_1_q, comparator_1_eq);
  Counter #(.width(13), .max('h1fff), .ongoal("stay"), .trigger("rising"), .behavior("old")) counter_2 (
    .count(comparator_1_lt), .Q(CNT_num), .clk(clock_1_out));  // open: load, D, carry, clr, preset
  assign CLK = nand_1_out ? clock_1_out : 1'bz;  // Controlled_Buffer controlled_buffer_1
  \单周期硬布线控制器  \u_单周期硬布线控制器_1  (
    .Funct({ID_IR[30], ID_IR[25], ID_IR[14:12]}), .OP(ID_IR[6:2]), .ALU_OP(\单周期硬布线控制器_1_alu_op ),
    .MemToReg(\单周期硬布线控制器_1_memtoreg ), .MemWrite(\单周期硬布线控制器_1_memwrite ), .ALU_SRC(\单周期硬布线控制器_1_alu_src ),
    .RegWrite(\单周期硬布线控制器_1_regwrite ), .ecall(ecall), .S_type(S_type), .Jalr(JALR), .Beq(\单周期硬布线控制器_1_beq ),
    .JAL(JAL), .Bne(\单周期硬布线控制器_1_bne ), .in_3(ID_IR[21]), .uret(URET), .I(I), .B(B),
    .clearI(\单周期硬布线控制器_1_cleari ), .sb(\单周期硬布线控制器_1_sb ), .sll(\单周期硬布线控制器_1_sll ), .setI(\单周期硬布线控制器_1_seti ),
    .bltu(\单周期硬布线控制器_1_bltu ));
  assign bit_extender_1_out = {{20{ID_IR[31]}}, ID_IR[31:20]};  // Bit_Extender bit_extender_1
  assign bit_extender_2_out = {{20{ID_IR[31]}}, {ID_IR[31:25], ID_IR[11:7]}};  // Bit_Extender bit_extender_2
  assign bit_extender_3_out = {{20{ID_IR[31]}}, {ID_IR[31], ID_IR[7], ID_IR[30:25], ID_IR[11:8]}};  // Bit_Extender bit_extender_3
  assign bit_extender_4_out = {{12{ID_IR[31]}}, {ID_IR[31], ID_IR[19:12], ID_IR[20], ID_IR[30:21]}};  // Bit_Extender bit_extender_4
  Pull_Resistor #(.pull(1)) pull_resistor_1 (.node(CLK));
  Multiplexer #(.select(1), .width(5), .disabled("Z"), .enable("false")) multiplexer_5 (
    .in0(ID_IR[19:15]), .in1(5'b10001), .out(ID_R1_num), .sel(ecall));
  Multiplexer #(.select(1), .width(5), .disabled("Z"), .enable("false")) multiplexer_6 (
    .in0(ID_IR[24:20]), .in1(5'b01010), .out(ID_R2_num), .sel(ecall));
  Multiplexer #(.select(1), .width(32), .disabled("Z"), .enable("false")) multiplexer_7 (
    .in0(multiplexer_13_out), .in1(\mem_wb流水寄存器_1_pc_4_2 ), .out(RDin), .sel(J));
  Multiplexer #(.select(4), .width(32), .disabled("Z"), .enable("false")) multiplexer_8 (
    .in1(bit_extender_1_out), .in2(bit_extender_2_out), .in4(bit_extender_3_out), .in8(bit_extender_4_out),
    .out(multiplexer_8_out), .sel({JAL, B, S_type, I}));  // open: in0, in3, in5, in6, in7, in9, in10, in11, in12, in13, in14, in15
  Regifile regifile_1 (
    .Din(RDin), .Clk(CLK), .R1(regifile_1_r1), .R2(regifile_1_r2), .WE(RegWrite),
    .W_num(\mem_wb流水寄存器_1_w_num_2 ), .R1_num(ID_R1_num), .R2_num(ID_R2_num));
  or or_2 (EX_Branch, EX_PredictJump, \id_ex流水寄存器_1_beq_2 , \id_ex流水寄存器_1_bne_2 , \id_ex流水寄存器_1_jal_2 , EX_JALR, bltu);
  \ID_EX流水寄存器  \id_ex流水寄存器_1  (
    .ecall(ecall), .jal(JAL), .jalr(JALR), .uret(URET), .Beq(\单周期硬布线控制器_1_beq ), .Bne(\单周期硬布线控制器_1_bne ),
    .MemToReg(\单周期硬布线控制器_1_memtoreg ), .MemWrite(\单周期硬布线控制器_1_memwrite ), .AluOP(\单周期硬布线控制器_1_alu_op ),
    .Alu_Src(\单周期硬布线控制器_1_alu_src ), .RegWrite(\单周期硬布线控制器_1_regwrite ), .sb(\单周期硬布线控制器_1_sb ),
    .clearI(\单周期硬布线控制器_1_cleari ), .setI(\单周期硬布线控制器_1_seti ), .sll(\单周期硬布线控制器_1_sll ), .R1(regifile_1_r1),
    .R2__sll({{27{1'b0}}, regifile_1_r2[4:0]}), .\立即数 (multiplexer_8_out), .W_num(ID_IR[11:7]), .PC(ID_PC),
    .PC_4(\if_id流水寄存器_1_pc_4_2 ), .ecall_2(\id_ex流水寄存器_1_ecall_2 ), .jal_2(\id_ex流水寄存器_1_jal_2 ),
    .jalr_2(EX_JALR), .Beq_2(\id_ex流水寄存器_1_beq_2 ), .Bne_2(\id_ex流水寄存器_1_bne_2 ),
    .MemToReg_2(\id_ex流水寄存器_1_memtoreg_2 ), .MemWrite_2(\id_ex流水寄存器_1_memwrite_2 ),
    .AluOP_2(\id_ex流水寄存器_1_aluop_2 ), .Alu_Src_2(\id_ex流水寄存器_1_alu_src_2 [0]),
    .RegWrite_2(\id_ex流水寄存器_1_regwrite_2 ), .sb_2(\id_ex流水寄存器_1_sb_2 ), .sll_2(\id_ex流水寄存器_1_alu_src_2 [1]),
    .R1_2(\id_ex流水寄存器_1_r1_2 ), .R2__sll_2(\id_ex流水寄存器_1_r2__sll_2 ), .\立即数_2 (\id_ex流水寄存器_1_立即数_2 ),
    .W_num_2(EX_W_num), .PC_2(EX_PC), .PC_4_2(\id_ex流水寄存器_1_pc_4_2 ), .\同步清零_高电平有效 (\重定向逻辑_1_id_ex_clr ),
    .CLK(CLK), .\EN使能端 (halt), .bltu(\单周期硬布线控制器_1_bltu ), .bltu_2(bltu), .R2(regifile_1_r2),
    .R2_2(\id_ex流水寄存器_1_r2_2 ), .IR(ID_IR), .IR_2(EX_IR), .RsForward(\重定向逻辑_1_rsforward ),
    .RsForward_2(\id_ex流水寄存器_1_rsforward_2 ), .RtForward(\重定向逻辑_1_rtforward ),
    .RtForward_2(\id_ex流水寄存器_1_rtforward_2 ), .PredictJump(ID_PredictJump_t), .PredictJump_2(EX_PredictJump));  // open: uret_2, clearI_2, setI_2
  Multiplexer #(.select(2), .width(32), .disabled("Z"), .enable("false")) multiplexer_9 (
    .in0(\id_ex流水寄存器_1_r1_2 ), .in1(multiplexer_13_out), .in2(\ex_mem流水寄存器_1_result_2 ),
    .out(multiplexer_9_out), .sel(\id_ex流水寄存器_1_rsforward_2 ));  // open: in3
  Multiplexer #(.select(2), .width(32), .disabled("Z"), .enable("false")) multiplexer_10 (
    .in0(\id_ex流水寄存器_1_r2_2 ), .in1(multiplexer_13_out), .in2(\ex_mem流水寄存器_1_result_2 ), .out(EX_ec_out),
    .sel(\id_ex流水寄存器_1_rtforward_2 ));  // open: in3
  Multiplexer #(.select(2), .width(32), .disabled("Z"), .enable("false")) multiplexer_11 (
    .in0(EX_ec_out), .in1(\id_ex流水寄存器_1_立即数_2 ), .in2(\id_ex流水寄存器_1_r2__sll_2 ), .out(multiplexer_11_out),
    .sel(\id_ex流水寄存器_1_alu_src_2 ));  // open: in3
  Shifter #(.width(32), .shift("ll")) shifter_1 (.in(\id_ex流水寄存器_1_立即数_2 ), .\dist (5'b00001), .out(shifter_1_out));
  assign and_2_out = {alu_1_result, lessthen} & 32'hfffffffe;  // AND_Gate and_2, 32 bits wide
  ALU alu_1 (
    .X(multiplexer_9_out), .Y(multiplexer_11_out), .AluOP(\id_ex流水寄存器_1_aluop_2 ), .Equal(alu_1_equal),
    .Result({alu_1_result, lessthen}));  // open: Result_2, out_4, out_6
  Adder #(.width(32)) adder_2 (.a(shifter_1_out), .b(EX_PC), .out(adder_2_out));  // open: cin, cout
  and and_3 (and_3_out, bltu, lessthen);
  and and_4 (and_4_out, alu_1_equal, \id_ex流水寄存器_1_beq_2 );
  and and_5 (and_5_out, ~alu_1_equal, \id_ex流水寄存器_1_bne_2 );  // AND_Gate
  Comparator #(.width(32), .mode("unsigned")) comparator_2 (
    .a(32'h22), .b(multiplexer_9_out), .eq(Ex_ec_eq));  // open: gt, lt
  or or_3 (PCSrc, and_3_out, and_4_out, and_5_out, \id_ex流水寄存器_1_jal_2 );
  or or_4 (EX_BranchTaken, and_3_out, and_4_out, and_5_out, \id_ex流水寄存器_1_jal_2 , EX_JALR);
  \EX_MEM流水寄存器  \ex_mem流水寄存器_1  (
    .W_num(EX_W_num), .W_num_2(MEM_W_num), .PC(EX_PC), .PC_2(M_PC), .PC_4(\id_ex流水寄存器_1_pc_4_2 ),
    .PC_4_2(\ex_mem流水寄存器_1_pc_4_2 ), .CLK(CLK), .\EN使能端 (halt), .lt(lessthen), .PC_offset(adder_2_out),
    .PC_offset_2(\ex_mem流水寄存器_1_pc_offset_2 ), .result({alu_1_result, lessthen}),
    .result_2(\ex_mem流水寄存器_1_result_2 ), .address(alu_1_result[11:2]), .address_2(\ex_mem流水寄存器_1_address_2 ),
    .ecall(\id_ex流水寄存器_1_ecall_2 ), .ecall_2(\ex_mem流水寄存器_1_ecall_2 ), .jal(\id_ex流水寄存器_1_jal_2 ),
    .jal_2(\ex_mem流水寄存器_1_jal_2 ), .jalr(EX_JALR), .jalr_2(\ex_mem流水寄存器_1_jalr_2 ),
    .MemToReg(\id_ex流水寄存器_1_memtoreg_2 ), .MemToReg_2(\ex_mem流水寄存器_1_memtoreg_2 ),
    .MemWrite(\id_ex流水寄存器_1_memwrite_2 ), .MemWrite_2(MemWrite), .RegWrite(\id_ex流水寄存器_1_regwrite_2 ),
    .RegWrite_2(\ex_mem流水寄存器_1_regwrite_2 ), .sb(\id_ex流水寄存器_1_sb_2 ), .sb_2(sb_star), .R2(EX_ec_out),
    .R2_2(\ex_mem流水寄存器_1_r2_2 ), .bltu(bltu), .bltu_2(\ex_mem流水寄存器_1_bltu_2 ), .IR(EX_IR), .IR_2(MEM_IR),
    .ec_eq(Ex_ec_eq), .ec_eq_2(\ex_mem流水寄存器_1_ec_eq_2 ), .ec_out(EX_ec_out),
    .ec_out_2(\ex_mem流水寄存器_1_ec_out_2 ));  // open: 同步清零_高电平有效, lt_2, uret, uret_2, Beq, Beq_2, Bne, Bne_2, clearI, clearI_2, setI, ecall_3, sll, sll_2, halt, halt_2
  xor xor_1 (EX_PredictErr, EX_PredictJump, EX_BranchTaken);
  \sb分线  \sb分线_1  (
    .\new (\ex_mem流水寄存器_1_r2_2 [7:0]), .Address(\ex_mem流水寄存器_1_result_2 [1:0]), .\output (\sb分线_1_output ),
    .origin(ram_1_data));
  RAM #(.addrWidth(10), .dataWidth(32), .bus("separate"), .Select("high")) ram_1 (
    .addr(\ex_mem流水寄存器_1_address_2 ), .din(MDin), .data(ram_1_data), .str(MemWrite), .clk(CLK), .ld(1'b1));  // open: sel, clr
  Multiplexer #(.select(1), .width(32), .disabled("Z"), .enable("false")) multiplexer_12 (
    .in0(\ex_mem流水寄存器_1_r2_2 ), .in1(\sb分线_1_output ), .out(MDin), .sel(sb_star));
  \MEM_WB流水寄存器  \mem_wb流水寄存器_1  (
    .W_num(MEM_W_num), .W_num_2(\mem_wb流水寄存器_1_w_num_2 ), .PC(M_PC), .PC_2(WB_PC),
    .PC_4(\ex_mem流水寄存器_1_pc_4_2 ), .PC_4_2(\mem_wb流水寄存器_1_pc_4_2 ), .CLK(CLK), .\EN使能端 (halt),
    .RegWrite(\ex_mem流水寄存器_1_regwrite_2 ), .RegWrite_2(RegWrite), .MemToReg(\ex_mem流水寄存器_1_memtoreg_2 ),
    .MemToReg_2(\mem_wb流水寄存器_1_memtoreg_2 ), .jalr(\ex_mem流水寄存器_1_jalr_2 ), .jalr_2(JALR_star),
    .jal(\ex_mem流水寄存器_1_jal_2 ), .jal_2(JAL_star), .ecall(\ex_mem流水寄存器_1_ecall_2 ), .ecall_2(ecall_star),
    .Result(\ex_mem流水寄存器_1_result_2 ), .Result_2(\mem_wb流水寄存器_1_result_2 ), .Mem(ram_1_data),
    .Mem_3(\mem_wb流水寄存器_1_mem_3 ), .PC_offset(\ex_mem流水寄存器_1_pc_offset_2 ), .bltu(\ex_mem流水寄存器_1_bltu_2 ),
    .IR(MEM_IR), .Mem_2(WB_IR), .ec_out(\ex_mem流水寄存器_1_ec_out_2 ), .ec_out_2(ec_out),
    .ec_eq(\ex_mem流水寄存器_1_ec_eq_2 ), .ec_eq_2(ec_eq));  // open: 同步清零_高电平有效, lt, lt_2, PC_offset_2, bltu_2, uret, uret_2, Beq, Beq_2, Bne, Bne_2, clearI, clearI_2, setI, setI_2, sll, sll_2, halt, halt_2
  Multiplexer #(.select(1), .width(32), .disabled("Z"), .enable("false")) multiplexer_13 (
    .in0(\mem_wb流水寄存器_1_result_2 ), .in1(\mem_wb流水寄存器_1_mem_3 ), .out(multiplexer_13_out),
    .sel(\mem_wb流水寄存器_1_memtoreg_2 ));
  or or_5 (J, JAL_star, JALR_star);
  and and_6 (and_6_out, ecall_star, ~ec_eq);  // AND_Gate
  and and_7 (and_7_out, ec_eq, ecall_star);
  D_Flip_Flop #(.trigger("high"), .Pre_Clr_Positions("LEGACY"), .NegatePresetClear("false"), .enable("true"), .NewFFLayout("false")) d_ff_2 (
    .clk(CLK), .D(and_6_out), .Q(halt), .reset(Go));  // open: Qn, preset, en
  Register #(.width(32), .trigger("rising"), .Select("low")) register_1 (
    .D(ec_out), .en(and_7_out), .Q(LedData), .clk(CLK));  // open: clr

  // Other names for the same wires on the sheet: IR[31:0] = ID_IR; MEM_PC[31:0] = M_PC

  // Notes on the sheet:
  //   中断源
  //   时空图监测，可删除
  //   中断等待指示
  //   数码管输出
  //   EX.PC + 4
  //   指令存储器
  //   contents of rom_1 (hex, n*v repeats v):
  //   100493 100006f 100493 200913 300993 100006f 100493 200913 300993 100006f 100493 200913 300993
  //   100006f 100493 200913 300993 3b4000ef 100413 100493 1f49493 900533 2200893 73 24d493 48463 fedff06f
  //   900533 2200893 73 100493 249493 900533 2200893 73 48463 fedff06f 100493 1f49493 900533 2200893 73
  //   4034d493 900533 2200893 73 4044d493 900533 2200893 73 4044d493 900533 2200893 73 4044d493 900533
  //   2200893 73 4044d493 900533 2200893 73 4044d493 900533 2200893 73 4044d493 900533 2200893 73 4044d493
  //   900533 2200893 73 100413 1f41993 41f9d993 433 c00913 300b13 140413 f47413 800293 100313 499993
  //   89e9b3 1300533 2200893 73 406282b3 fe0294e3 140413 f00f93 1f47433 1c41413 800293 100313 49d993
  //   89e9b3 1300533 2200893 73 406282b3 fe0294e3 1c45413 406b0b33 b0463 f95ff06f 2b3 fff2c293 829293
  //   ff2e293 500533 2200893 73 fff00413 493 84a023 140413 448493 84a023 140413 448493 84a023 140413
  //   448493 84a023 140413 448493 84a023 140413 448493 84a023 140413 448493 84a023 140413 448493 84a023
  //   140413 448493 84a023 140413 448493 84a023 140413 448493 84a023 140413 448493 84a023 140413 448493
  //   84a023 140413 448493 84a023 140413 448493 84a023 140413 448493 84a023 140413 448493 140413 433
  //   3c00493 42983 4aa03 149a2b3 28663 134a023 1442023 ffc48493 fe9412e3 800533 2200893 73 440413 3c00493
  //   fc9416e3 3200893 73 100293 300313 800493 849493 7648493 900533 2200893 73 800e13 5494b3 6494b3
  //   900533 2200893 73 fffe0e13 fe0e14e3 a00893 73 fff00293 7700493 849493 7748493 900533 2200893 73
  //   1000e13 54c4b3 900533 2200893 73 fffe0e13 fe0e16e3 a00893 73 313 2000e13 493 100913 930023 900533
  //   2200893 73 12484b3 130313 fffe0e13 fe0e12e3 800e13 313 32483 900533 2200893 73 430313 fffe0e13
  //   fe0e14e3 a00893 73 ff100493 900533 2200893 73 148493 fe9068e3 900533 2200893 73 a00893 73 a00893 73
  //   413 140413 800533 2200893 73 240413 800533 2200893 73 340413 800533 2200893 73 440413 800533 2200893
  //   73 540413 800533 2200893 73 640413 800533 2200893 73 740413 800533 2200893 73 840413 800533 2200893
  //   2200893 73 8067
  //   控制位
  //   指令字
  //   流水调试日志用
  //   暂停节拍，不能为0
  //   戳工具置1进入计数暂停模式，ctrl+k时钟自动运行到对应节拍暂停
  //   ctrl+k关闭时钟连续运行，将控制位置零，进入单步调试模式调试
  //   指令探针
  //   JAL
  //   JALR
  //   URET
  //   I
  //   B
  //   可计数暂停的时钟源
  //   为方便自动评测，需要输出流水线各段保存的PC值，注意是PC不是PC+4，另外ID段寄存器写入信息，Mem段内存写入信息也要输出
  //   sll指令输入线
  //   写入信号
  //   PC+4
  //   ecall
  //   jal
  //   jalr
  //   uret
  //   Beq
  //   Bne
  //   MemToReg
  //   MemWrite
  //   AluOP
  //   Alu_Src
  //   RegWrite
  //   sb
  //   clearI
  //   setI
  //   sll
  //   立即数
  //   EX.PC + 4
  //   ecall
  //   MemToReg
  //   MemWrite
  //   RegWrite
  //   写入信号
  //   PC+4
  //   jal
  //   jalr
  //   数据存储器
  //   ecall
  //   jal
  //   jalr
  //   MemToReg
  //   RegWrite
  //   R2*
  //   Result
  //   Mem
  //   lessthen
  //   写入信号
  //   PC+4
endmodule

module \中断按键参考电路  (
  input  \同步清零信号 ,
  output \与中断屏蔽位与 
);

  wire \_1号中断_out , and_1_out, clock_1_out, d_ff_1_q, or_1_out, or_2_out;

  Clock #(.highDuration(1), .lowDuration(1)) clock_1 (.out(clock_1_out));
  Button \_1号中断  (.out(\_1号中断_out ));
  or or_1 (or_1_out, \与中断屏蔽位与 , d_ff_1_q);
  LED #(.active("true")) \_1号中断等待指示灯  (.in(or_1_out));
  D_Flip_Flop #(.trigger("rising"), .Pre_Clr_Positions("LEGACY"), .NegatePresetClear("false"), .enable("true"), .NewFFLayout("false")) d_ff_1 (
    .clk(\_1号中断_out ), .D(1'b1), .Q(d_ff_1_q), .reset(\与中断屏蔽位与 ));  // open: Qn, preset, en
  or or_2 (or_2_out, d_ff_1_q, \与中断屏蔽位与 );
  and and_1 (and_1_out, or_2_out, ~\同步清零信号 );  // AND_Gate
  D_Flip_Flop #(.trigger("rising"), .Pre_Clr_Positions("LEGACY"), .NegatePresetClear("false"), .enable("true"), .NewFFLayout("false")) IR1 (
    .clk(clock_1_out), .D(and_1_out), .Q(\与中断屏蔽位与 ));  // open: Qn, preset, en, reset

  // Notes on the sheet:
  //   中断信号采样参考电路
  //   Reset 
endmodule

module \单周期_单级中断  (
  input  IR1,
  input  IR2,
  input  IR3,
  output RegWrite,
  output MemWrite,
  output [31:0] PC,
  output [31:0] IR,
  output [31:0] RDin,
  output [31:0] MDin,
  output [31:0] LedData
);

  wire alu_1_equal, and_2_out, and_3_out, and_4_out, and_8_out, and_9_out, and_10_out, and_11_out,
       and_12_out, and_13_out, B, bltu, clear1, clear2, clear3, clearI, CLK, clock_1_out, comparator_1_eq,
       comparator_2_eq, comparator_3_eq, comparator_4_eq, comparator_5_eq, comparator_5_lt, d_ff_2_q,
       decoder_1_out1, decoder_1_out2, decoder_1_out3, ec_eq, ecall, Go, halt, I, IE, INT, IR1_t, IR2_t,
       IR3_t, IRA, IRB, IRC, J, JAL, JALR, lessthen, nand_1_out, not_1_out, not_2_out, or_4_out, or_5_out,
       or_6_out, or_7_out, or_8_out, or_9_out, or_10_out, or_12_out, PCSrc, register_1_q, register_2_q,
       register_3_q, register_6_q, register_7_q, register_8_q, RST, S_type, sb, setI, sll, URET, W1, w1_t,
       W2, w2_t, W3, w3_t, \中断信号 , \单周期硬布线控制器_1_beq , \单周期硬布线控制器_1_bne , \单周期硬布线控制器_1_memtoreg ;
  wire [0:0] \单周期硬布线控制器_1_alu_src ;
  wire [1:0] register_4_q, \中断号 ;
  wire [1:1] alu_1_result;
  wire [3:0] \单周期硬布线控制器_1_alu_op ;
  wire [4:0] multiplexer_7_out, multiplexer_8_out;
  wire [12:0] CNT_num;
  wire [15:0] \总周期数 ;
  wire [31:0] adder_1_out, adder_2_out, and_14_out, bit_extender_1_out, bit_extender_2_out,
       bit_extender_3_out, bit_extender_4_out, ec_out, INT_PC, multiplexer_2_out, multiplexer_4_out,
       multiplexer_5_out, multiplexer_6_out, multiplexer_10_out, multiplexer_12_out, R1, ram_1_data, RET_PC,
       \sb分线_1_output , shifter_1_out, \原地址 ;
  wire [31:2] alu_1_result_2;

  Button \u_继续运行  (.out(Go));
  Button _1 ();  // open: out
  Button _2 ();  // open: out
  Button _3 ();  // open: out
  or or_1 (w1_t, register_6_q, register_1_q);
  or or_2 (w2_t, register_7_q, register_2_q);
  or or_3 (w3_t, register_8_q, register_3_q);
  LED #(.active("true")) led_1 (.in(W1));
  LED #(.active("true")) led_2 (.in(W2));
  LED #(.active("true")) led_3 (.in(W3));
  Register #(.width(1), .trigger("rising"), .Select("low")) register_1 (
    .D(1'b1), .Q(register_1_q), .clk(IR1_t), .clr(or_4_out));  // open: en
  or or_4 (or_4_out, register_6_q, RST);
  Register #(.width(1), .trigger("rising"), .Select("low")) register_2 (
    .D(1'b1), .Q(register_2_q), .clk(IR2_t), .clr(or_5_out));  // open: en
  or or_5 (or_5_out, register_7_q, RST);
  Register #(.width(1), .trigger("rising"), .Select("low")) register_3 (
    .D(1'b1), .Q(register_3_q), .clk(IR3_t), .clr(or_6_out));  // open: en
  or or_6 (or_6_out, register_8_q, RST);
  Hex_Digit_Display hex_digit_display_1 (.value(LedData[31:28]));  // open: dp
  Comparator #(.width(16), .mode("twosComplement")) comparator_1 (
    .a(16'h23b), .b(\总周期数 ), .eq(comparator_1_eq));  // open: gt, lt
  Comparator #(.width(16), .mode("twosComplement")) comparator_2 (
    .a(\总周期数 ), .b(16'h1), .eq(comparator_2_eq));  // open: gt, lt
  Comparator #(.width(16), .mode("twosComplement")) comparator_3 (
    .a(\总周期数 ), .b(16'h4), .eq(comparator_3_eq));  // open: gt, lt
  Comparator #(.width(16), .mode("twosComplement")) comparator_4 (
    .a(\总周期数 ), .b(16'h7), .eq(comparator_4_eq));  // open: gt, lt
  or or_7 (or_7_out, register_1_q, register_6_q);
  or or_8 (or_8_out, register_2_q, register_7_q);
  or or_9 (or_9_out, register_3_q, register_8_q);
  and and_1 (INT, IE, \中断信号 );
  Register #(.width(2), .trigger("rising"), .Select("low")) register_4 (
    .D(\中断号 ), .en(INT), .Q(register_4_q), .clk(CLK), .clr(RST));
  Decoder #(.select(2), .tristate("false"), .disabled("Z"), .enable("false")) decoder_1 (
    .out1(decoder_1_out1), .out2(decoder_1_out2), .out3(decoder_1_out3), .sel(register_4_q));  // open: out0
  Register #(.width(32), .trigger("rising"), .Select("low")) register_5 (
    .D(\原地址 ), .en(INT), .Q(RET_PC), .clk(CLK), .clr(RST));
  Hex_Digit_Display hex_digit_display_2 (.value(LedData[27:24]));  // open: dp
  Hex_Digit_Display hex_digit_display_3 (.value(LedData[23:20]));  // open: dp
  or or_10 (or_10_out, comparator_1_eq, comparator_2_eq);
  assign IRA = or_10_out ? ~CLK : 1'bz;  // Controlled_Inverter controlled_inverter_1
  assign IRB = comparator_3_eq ? ~CLK : 1'bz;  // Controlled_Inverter controlled_inverter_2
  assign IRC = comparator_4_eq ? ~CLK : 1'bz;  // Controlled_Inverter controlled_inverter_3
  and and_2 (and_2_out, or_7_out, ~clear1);  // AND_Gate
  and and_3 (and_3_out, or_8_out, ~clear2);  // AND_Gate
  and and_4 (and_4_out, or_9_out, ~clear3);  // AND_Gate
  Hex_Digit_Display hex_digit_display_4 (.value(LedData[15:12]));  // open: dp
  Hex_Digit_Display hex_digit_display_5 (.value(LedData[19:16]));  // open: dp
  Pull_Resistor #(.pull(0)) pull_resistor_1 (.node(IRA));
  Pull_Resistor #(.pull(0)) pull_resistor_2 (.node(IRB));
  Pull_Resistor #(.pull(0)) pull_resistor_3 (.node(IRC));
  Register #(.width(1), .trigger("rising"), .Select("low")) register_6 (
    .D(and_2_out), .Q(register_6_q), .clk(CLK), .clr(RST));  // open: en
  Register #(.width(1), .trigger("rising"), .Select("low")) register_7 (
    .D(and_3_out), .Q(register_7_q), .clk(CLK), .clr(RST));  // open: en
  Register #(.width(1), .trigger("rising"), .Select("low")) register_8 (
    .D(and_4_out), .Q(register_8_q), .clk(CLK), .clr(RST));  // open: en
  and and_5 (clear1, decoder_1_out1, URET);
  and and_6 (clear2, decoder_1_out2, URET);
  and and_7 (clear3, decoder_1_out3, URET);
  Hex_Digit_Display hex_digit_display_6 (.value(LedData[11:8]));  // open: dp
  Hex_Digit_Display hex_digit_display_7 (.value(LedData[7:4]));  // open: dp
  // Probe on \总周期数 
  Priority_Encoder #(.select(2), .disabled("Z")) priority_encoder_1 (
    .in1(register_6_q), .in2(register_7_q), .in3(register_8_q), .out(\中断号 ), .gs(\中断信号 ));  // open: in0, en_out, en_in
  and and_8 (and_8_out, ~URET, \中断信号 );  // AND_Gate
  Hex_Digit_Display hex_digit_display_8 (.value(LedData[3:0]));  // open: dp
  Button button_1 (.out(RST));
  Multiplexer #(.select(2), .width(32), .disabled("Z"), .enable("false")) multiplexer_1 (
    .in1(32'h30ac), .in2(32'h3150), .in3(32'h31f4), .out(INT_PC), .sel(\中断号 ));  // open: in0
  D_Flip_Flop #(.trigger("rising"), .Pre_Clr_Positions("LEGACY"), .NegatePresetClear("false"), .enable("true"), .NewFFLayout("false")) d_ff_1 (
    .clk(CLK), .D(and_8_out), .Qn(IE));  // open: Q, preset, en, reset
  or or_11 (IR1_t, IR1, IRA);
  or or_12 (or_12_out, J, PCSrc, and_9_out);
  Multiplexer #(.select(1), .width(32), .disabled("Z"), .enable("false")) multiplexer_2 (
    .in0(adder_2_out), .in1(and_14_out), .out(multiplexer_2_out), .sel(JALR));
  or or_13 (IR2_t, IR2, IRB);
  and and_9 (and_9_out, lessthen, bltu);
  Multiplexer #(.select(1), .width(32), .disabled("Z"), .enable("false")) multiplexer_3 (
    .in0(adder_1_out), .in1(multiplexer_2_out), .out(\原地址 ), .sel(or_12_out));
  Multiplexer #(.select(1), .width(32), .disabled("Z"), .enable("false")) multiplexer_4 (
    .in0(multiplexer_5_out), .in1(INT_PC), .out(multiplexer_4_out), .sel(INT));
  Multiplexer #(.select(1), .width(32), .disabled("Z"), .enable("false")) multiplexer_5 (
    .in0(\原地址 ), .in1(RET_PC), .out(multiplexer_5_out), .sel(URET));
  or or_14 (IR3_t, IR3, IRC);
  not not_1 (not_1_out, halt);
  Counter #(.width(16), .max('hffff), .ongoal("wrap"), .trigger("rising"), .behavior("new")) counter_1 (
    .D(16'h1), .count(not_1_out), .Q(\总周期数 ), .clk(CLK), .clr(Go));  // open: load, carry, preset, down
  Register #(.width(32), .trigger("rising"), .Select("low")) u_PC (
    .D(multiplexer_4_out), .en(not_2_out), .Q(PC), .clk(CLK), .clr(RST));
  not not_2 (not_2_out, halt);
  or or_15 (J, JAL, JALR);
  // Probe on PC
  Adder #(.width(32)) adder_1 (.a(PC), .b(32'h4), .out(adder_1_out));  // open: cin, cout
  Adder #(.width(32)) adder_2 (.a(PC), .b(shifter_1_out), .out(adder_2_out));  // open: cin, cout
  // RiscV_Probe riscv_probe_1: pin names not known; wires that end beside it: IR
  ROM #(.addrWidth(10), .dataWidth(32), .Select("high")) rom_1 (.addr(PC[11:2]), .data(IR));
  \单周期硬布线控制器  \u_单周期硬布线控制器_1  (
    .Funct({IR[30], IR[25], IR[14:12]}), .OP(IR[6:2]), .ALU_OP(\单周期硬布线控制器_1_alu_op ),
    .MemToReg(\单周期硬布线控制器_1_memtoreg ), .MemWrite(MemWrite), .ALU_SRC(\单周期硬布线控制器_1_alu_src [0]),
    .RegWrite(RegWrite), .ecall(ecall), .S_type(S_type), .Jalr(JALR), .Beq(\单周期硬布线控制器_1_beq ), .JAL(JAL),
    .Bne(\单周期硬布线控制器_1_bne ), .in_3(IR[21]), .uret(URET), .I(I), .B(B), .clearI(clearI), .sb(sb), .sll(sll),
    .setI(setI), .bltu(bltu));
  assign bit_extender_1_out = {{20{IR[31]}}, IR[31:20]};  // Bit_Extender bit_extender_1
  assign bit_extender_2_out = {{20{IR[31]}}, {IR[31:25], IR[11:7]}};  // Bit_Extender bit_extender_2
  assign bit_extender_3_out = {{20{IR[31]}}, {IR[31], IR[7], IR[30:25], IR[11:8]}};  // Bit_Extender bit_extender_3
  assign bit_extender_4_out = {{12{IR[31]}}, {IR[31], IR[19:12], IR[20], IR[30:21]}};  // Bit_Extender bit_extender_4
  D_Flip_Flop #(.trigger("high"), .Pre_Clr_Positions("LEGACY"), .NegatePresetClear("false"), .enable("true"), .NewFFLayout("false")) d_ff_2 (.Q(d_ff_2_q));  // open: clk, D, Qn, preset, en, reset
  // Probe on 13'hc
  Multiplexer #(.select(4), .width(32), .disabled("Z"), .enable("false")) multiplexer_6 (
    .in1(bit_extender_1_out), .in2(bit_extender_2_out), .in4(bit_extender_3_out), .in8(bit_extender_4_out),
    .out(multiplexer_6_out), .sel({JAL, B, S_type, I}));  // open: in0, in3, in5, in6, in7, in9, in10, in11, in12, in13, in14, in15
  Comparator #(.width(13), .mode("twosComplement")) comparator_5 (
    .a(CNT_num), .b(13'hc), .eq(comparator_5_eq), .lt(comparator_5_lt));  // open: gt
  Clock #(.highDuration(1), .lowDuration(1)) clock_1 (.out(clock_1_out));
  Multiplexer #(.select(1), .width(5), .disabled("Z"), .enable("false")) multiplexer_7 (
    .in0(IR[19:15]), .in1(5'b10001), .out(multiplexer_7_out), .sel(ecall));
  Multiplexer #(.select(1), .width(5), .disabled("Z"), .enable("false")) multiplexer_8 (
    .in0(IR[24:20]), .in1(5'b01010), .out(multiplexer_8_out), .sel(ecall));
  Multiplexer #(.select(1), .width(32), .disabled("Z"), .enable("false")) multiplexer_9 (
    .in0(multiplexer_12_out), .in1(adder_1_out), .out(RDin), .sel(J));
  Counter #(.width(13), .max('h1fff), .ongoal("stay"), .trigger("rising"), .behavior("old")) counter_2 (
    .count(comparator_5_lt), .Q(CNT_num), .clk(clock_1_out));  // open: load, D, carry, clr, preset
  // Probe on RDin
  nand nand_1 (nand_1_out, d_ff_2_q, comparator_5_eq);
  Regifile regifile_1 (
    .Din(RDin), .Clk(CLK), .R1(R1), .R2(ec_out), .WE(RegWrite), .W_num(IR[11:7]), .R1_num(multiplexer_7_out),
    .R2_num(multiplexer_8_out));
  assign CLK = nand_1_out ? clock_1_out : 1'bz;  // Controlled_Buffer controlled_buffer_1
  Pull_Resistor #(.pull(1)) pull_resistor_4 (.node(CLK));
  Comparator #(.width(32), .mode("unsigned")) comparator_6 (.a(32'h22), .b(R1), .eq(ec_eq));  // open: gt, lt
  Multiplexer #(.select(2), .width(32), .disabled("Z"), .enable("false")) multiplexer_10 (
    .in0(ec_out), .in1(multiplexer_6_out), .in2({{27{1'b0}}, ec_out[4:0]}), .out(multiplexer_10_out),
    .sel({sll, \单周期硬布线控制器_1_alu_src [0]}));  // open: in3
  \sb分线  \sb分线_1  (
    .\new (ec_out[7:0]), .Address({alu_1_result[1], lessthen}), .\output (\sb分线_1_output ),
    .origin(ram_1_data));
  Shifter #(.width(32), .shift("ll")) shifter_1 (.in(multiplexer_6_out), .\dist (5'b00001), .out(shifter_1_out));
  ALU alu_1 (
    .X(R1), .Y(multiplexer_10_out), .AluOP(\单周期硬布线控制器_1_alu_op ), .Equal(alu_1_equal),
    .Result({alu_1_result_2, alu_1_result[1], lessthen}));  // open: Result_2, out_4, out_6
  Multiplexer #(.select(1), .width(32), .disabled("Z"), .enable("false")) multiplexer_11 (
    .in0(ec_out), .in1(\sb分线_1_output ), .out(MDin), .sel(sb));
  and and_10 (and_10_out, alu_1_equal, \单周期硬布线控制器_1_beq );
  and and_11 (and_11_out, ~alu_1_equal, \单周期硬布线控制器_1_bne );  // AND_Gate
  and and_12 (and_12_out, ecall, ~ec_eq);  // AND_Gate
  and and_13 (and_13_out, ec_eq, ecall);
  assign and_14_out = multiplexer_12_out & 32'hfffffffe;  // AND_Gate and_14, 32 bits wide
  or or_16 (PCSrc, and_10_out, and_11_out);
  D_Flip_Flop #(.trigger("high"), .Pre_Clr_Positions("LEGACY"), .NegatePresetClear("false"), .enable("true"), .NewFFLayout("false")) d_ff_3 (
    .clk(CLK), .D(and_12_out), .Q(halt), .reset(Go));  // open: Qn, preset, en
  Register #(.width(32), .trigger("rising"), .Select("low")) register_9 (
    .D(ec_out), .en(and_13_out), .Q(LedData), .clk(CLK));  // open: clr
  RAM #(.addrWidth(10), .dataWidth(32), .bus("separate"), .Select("high")) ram_1 (
    .addr(alu_1_result_2[11:2]), .din(MDin), .data(ram_1_data), .str(MemWrite), .clk(CLK), .ld(1'b1));  // open: sel, clr
  Multiplexer #(.select(1), .width(32), .disabled("Z"), .enable("false")) multiplexer_12 (
    .in0({alu_1_result_2, alu_1_result[1], lessthen}), .in1(ram_1_data), .out(multiplexer_12_out),
    .sel(\单周期硬布线控制器_1_memtoreg ));

  // Other names for the same wires on the sheet: R2[31:0] = ec_out

  // Notes on the sheet:
  //   中断源
  //   中断等待指示
  //   总复位信号应将除ROM以外所有存储组件全部清零
  //   单级中断测试信号模拟器
  //   数码管输出
  //   数码管输出应该用寄存器锁存，否则显示数据只能一闪而过
  //   指令探针
  //   指令存储器
  //   为方便自动评测，需要输出PC，IR，寄存器堆写如数据RDin
  //   指令字
  //   contents of rom_1 (hex, n*v repeats v):
  //   7d000113 100413 1f41993 41f9d993 433 c00913 800b13 140413 f47413 800293 100313 499993 89e9b3 1300533
  //   2200893 73 406282b3 fe0294e3 140413 f00f93 1f47433 1c41413 800293 100313 49d993 89e9b3 1300533
  //   2200893 73 406282b3 fe0294e3 1c45413 406b0b33 b0463 f95ff06f 2b3 fff2c293 1029293 fff2e293 500533
  //   2200893 73 f5dff06f 1112023 410113 a12023 410113 812023 410113 1312023 410113 1412023 410113 1512023
  //   410113 1612023 410113 100b13 300a13 100a93 1600433 441413 14469b3 1300533 2200893 73 fe0416e3
  //   415a0a33 fe0a10e3 ffc10113 12b03 ffc10113 12a83 ffc10113 12a03 ffc10113 12983 ffc10113 12403
  //   ffc10113 12503 ffc10113 12883 200073 1112023 410113 a12023 410113 812023 410113 1312023 410113
  //   1412023 410113 1512023 410113 1612023 410113 200b13 300a13 100a93 1600433 441413 14469b3 1300533
  //   2200893 73 fe0416e3 415a0a33 fe0a10e3 ffc10113 12b03 ffc10113 12a83 ffc10113 12a03 ffc10113 12983
  //   ffc10113 12403 ffc10113 12503 ffc10113 12883 200073 1112023 410113 a12023 410113 812023 410113
  //   1312023 410113 1412023 410113 1512023 410113 1612023 410113 300b13 300a13 100a93 1600433 441413
  //   14469b3 1300533 2200893 73 fe0416e3 415a0a33 fe0a10e3 ffc10113 12b03 ffc10113 12a83 ffc10113 12a03
  //   ffc10113 12983 ffc10113 12403 ffc10113 12503 ffc10113 12883 200073
  //   RAM写使能MemWrite、RAM写入数据MDin等信号
  //   JAL
  //   JALR
  //   URET
  //   I
  //   B
  //   Beq
  //   Bne
  //   AluOP
  //   AluSrcB
  //   RegWrite
  //   MemToReg
  //   MemWrite
  //   控制位
  //   暂停节拍，不能为0
  //   戳工具置1进入计数暂停模式，ctrl+k时钟自动运行到对应节拍暂停
  //   ctrl+k关闭时钟连续运行，将控制位置零，进入单步调试模式调试
  //   可计数暂停的时钟源
  //   数据存储器
endmodule

module \单周期_多级中断  (
  input  IR1,
  input  IR2,
  input  IR3,
  output RegWrite,
  output MemWrite,
  output [31:0] PC,
  output [31:0] IR,
  output [31:0] RDin,
  output [31:0] MDin,
  output [31:0] LedData
);

  wire alu_1_equal, and_1_out, and_2_out, and_3_out, and_8_out, and_9_out, and_10_out, and_12_out,
       and_13_out, B, bltu, clear1, clear2, clear3, clearI, CLK, clock_1_out, comparator_1_eq,
       comparator_2_eq, comparator_3_eq, comparator_4_eq, comparator_5_eq, comparator_6_eq, comparator_7_eq,
       comparator_8_eq, comparator_8_lt, d_ff_1_q, decoder_1_out1, decoder_1_out2, decoder_1_out3,
       decoder_2_out1, decoder_2_out2, decoder_2_out3, decoder_3_out0, decoder_3_out1, decoder_3_out2, ec_eq,
       ecall, Go, halt, Has_Run, I, IE, INT, INT_LEVEL, IR1_t, IR2_t, IR3_t, IRA, IRB, IRC, J, JAL, JALR,
       lessthen, multiplexer_5_out, multiplexer_6_out, nand_1_out, NEW_INT, not_1_out, not_3_out, not_4_out,
       not_5_out, or_1_out, or_3_out, or_5_out, or_7_out, or_8_out, or_9_out, or_10_out, or_11_out,
       or_12_out, or_13_out, or_14_out, or_16_out, or_17_out, or_19_out, or_20_out, or_21_out, or_23_out,
       or_24_out, PCSrc, priority_encoder_1_gs, register_1_q, register_2_q, register_3_q, register_4_q,
       register_5_q, register_6_q, register_7_q, register_8_q, register_9_q, register_11_q, register_12_q,
       register_14_q, register_15_q, RST, S_type, sb, setI, sll, URET, W1, w1_t, W2, w2_t, W3, w3_t,
       \单周期硬布线控制器_1_beq , \单周期硬布线控制器_1_bne , \单周期硬布线控制器_1_memtoreg ;
  wire [0:0] \单周期硬布线控制器_1_alu_src ;
  wire [1:0] counter_1_q, multiplexer_3_out, register_10_q, subtractor_1_out, \中断号 ;
  wire [1:1] alu_1_result;
  wire [3:0] \单周期硬布线控制器_1_alu_op ;
  wire [4:0] multiplexer_14_out, multiplexer_15_out;
  wire [12:0] CNT_num;
  wire [15:0] \总周期数 ;
  wire [31:0] adder_2_out, and_11_out, bit_extender_1_out, bit_extender_2_out, bit_extender_3_out,
       bit_extender_4_out, ec_out, INT_PC, KE, multiplexer_9_out, multiplexer_10_out, multiplexer_11_out,
       multiplexer_12_out, multiplexer_13_out, multiplexer_17_out, multiplexer_19_out, PC_4, R1, ram_1_data,
       register_16_q, register_17_q, register_18_q, RET_PC, \sb分线_1_output , shifter_1_out;
  wire [31:2] alu_1_result_2;

  Button \u_继续运行  (.out(Go));
  Button _1 ();  // open: out
  Button _2 ();  // open: out
  Button _3 ();  // open: out
  LED #(.active("true")) led_1 (.in(W1));
  LED #(.active("true")) led_2 (.in(W2));
  LED #(.active("true")) led_3 (.in(W3));
  Register #(.width(1), .trigger("rising"), .Select("low")) register_1 (
    .D(1'b1), .Q(register_1_q), .clk(IR1_t), .clr(or_1_out));  // open: en
  or or_1 (or_1_out, register_7_q, RST);
  or or_2 (w1_t, register_7_q, register_1_q);
  Register #(.width(1), .trigger("rising"), .Select("low")) register_2 (
    .D(1'b1), .Q(register_2_q), .clk(IR2_t), .clr(or_3_out));  // open: en
  or or_3 (or_3_out, register_8_q, RST);
  or or_4 (w2_t, register_8_q, register_2_q);
  Register #(.width(1), .trigger("rising"), .Select("low")) register_3 (
    .D(1'b1), .Q(register_3_q), .clk(IR3_t), .clr(or_5_out));  // open: en
  or or_5 (or_5_out, register_9_q, RST);
  or or_6 (w3_t, register_9_q, register_3_q);
  Decoder #(.select(2), .tristate("false"), .disabled("Z"), .enable("false")) decoder_1 (
    .out1(decoder_1_out1), .out2(decoder_1_out2), .out3(decoder_1_out3), .sel(\中断号 ));  // open: out0
  Hex_Digit_Display hex_digit_display_1 (.value(LedData[31:28]));  // open: dp
  Comparator #(.width(16), .mode("twosComplement")) comparator_1 (
    .a(\总周期数 ), .b(16'h7), .eq(comparator_1_eq));  // open: gt, lt
  Comparator #(.width(16), .mode("twosComplement")) comparator_2 (
    .a(\总周期数 ), .b(16'h241), .eq(comparator_2_eq));  // open: gt, lt
  or or_7 (or_7_out, register_1_q, register_7_q);
  or or_8 (or_8_out, register_2_q, register_8_q);
  or or_9 (or_9_out, register_3_q, register_9_q);
  Multiplexer #(.select(2), .width(32), .disabled("Z"), .enable("false")) multiplexer_1 (
    .in1(32'h30ac), .in2(32'h3158), .in3(32'h3204), .out(INT_PC), .sel(\中断号 ));  // open: in0
  Hex_Digit_Display hex_digit_display_2 (.value(LedData[27:24]));  // open: dp
  Hex_Digit_Display hex_digit_display_3 (.value(LedData[23:20]));  // open: dp
  Comparator #(.width(16), .mode("twosComplement")) comparator_3 (
    .a(16'h258), .b(\总周期数 ), .eq(comparator_3_eq));  // open: gt, lt
  or or_10 (or_10_out, comparator_3_eq, comparator_4_eq);
  Comparator #(.width(16), .mode("twosComplement")) comparator_4 (
    .a(\总周期数 ), .b(16'h1), .eq(comparator_4_eq));  // open: gt, lt
  Comparator #(.width(16), .mode("twosComplement")) comparator_5 (
    .a(\总周期数 ), .b(16'h4), .eq(comparator_5_eq));  // open: gt, lt
  or or_11 (or_11_out, comparator_1_eq, comparator_2_eq);
  and and_1 (and_1_out, or_7_out, ~clear1);  // AND_Gate
  and and_2 (and_2_out, or_8_out, ~clear2);  // AND_Gate
  and and_3 (and_3_out, or_9_out, ~clear3);  // AND_Gate
  Register #(.width(1), .trigger("rising"), .Select("low")) register_4 (
    .D(1'b1), .en(decoder_1_out1), .Q(register_4_q), .clk(INT_LEVEL), .clr(or_12_out));
  or or_12 (or_12_out, clear1, RST);
  Register #(.width(1), .trigger("rising"), .Select("low")) register_5 (
    .D(1'b1), .en(decoder_1_out2), .Q(register_5_q), .clk(INT_LEVEL), .clr(or_13_out));
  or or_13 (or_13_out, clear2, RST);
  Register #(.width(1), .trigger("rising"), .Select("low")) register_6 (
    .D(1'b1), .en(decoder_1_out3), .Q(register_6_q), .clk(INT_LEVEL), .clr(or_14_out));
  or or_14 (or_14_out, clear3, RST);
  Hex_Digit_Display hex_digit_display_4 (.value(LedData[15:12]));  // open: dp
  Hex_Digit_Display hex_digit_display_5 (.value(LedData[19:16]));  // open: dp
  Pull_Resistor #(.pull(0)) pull_resistor_1 (.node(IRA));
  assign IRA = or_10_out ? ~CLK : 1'bz;  // Controlled_Inverter controlled_inverter_1
  Pull_Resistor #(.pull(0)) pull_resistor_2 (.node(IRB));
  assign IRB = comparator_5_eq ? ~CLK : 1'bz;  // Controlled_Inverter controlled_inverter_2
  Pull_Resistor #(.pull(0)) pull_resistor_3 (.node(IRC));
  assign IRC = or_11_out ? ~CLK : 1'bz;  // Controlled_Inverter controlled_inverter_3
  Register #(.width(1), .trigger("rising"), .Select("low")) register_7 (
    .D(and_1_out), .Q(register_7_q), .clk(CLK), .clr(RST));  // open: en
  Register #(.width(1), .trigger("rising"), .Select("low")) register_8 (
    .D(and_2_out), .Q(register_8_q), .clk(CLK), .clr(RST));  // open: en
  Register #(.width(1), .trigger("rising"), .Select("low")) register_9 (
    .D(and_3_out), .Q(register_9_q), .clk(CLK), .clr(RST));  // open: en
  Multiplexer #(.select(2), .width(1), .disabled("Z"), .enable("false")) multiplexer_2 (
    .in0(1'b1), .in1(register_4_q), .in2(register_5_q), .in3(register_6_q), .out(Has_Run), .sel(\中断号 ));
  Hex_Digit_Display hex_digit_display_6 (.value(LedData[11:8]));  // open: dp
  Hex_Digit_Display hex_digit_display_7 (.value(LedData[7:4]));  // open: dp
  // Probe on \总周期数 
  Button button_1 (.out(RST));
  Priority_Encoder #(.select(2), .disabled("Z")) priority_encoder_1 (
    .in0(1'b1), .in1(register_7_q), .in2(register_8_q), .in3(register_9_q), .out(\中断号 ),
    .gs(priority_encoder_1_gs), .en_in(1'b1));  // open: en_out
  Hex_Digit_Display hex_digit_display_8 (.value(LedData[3:0]));  // open: dp
  and and_4 (INT, priority_encoder_1_gs, IE);
  Multiplexer #(.select(1), .width(2), .disabled("Z"), .enable("false")) multiplexer_3 (
    .in0(multiplexer_3_out), .in1(\中断号 ), .out(multiplexer_3_out), .sel(IE));
  or or_15 (IR1_t, IR1, IRA);
  Register #(.width(2), .trigger("rising"), .Select("low")) register_10 (
    .D(multiplexer_3_out), .Q(register_10_q), .clk(CLK), .clr(RST));  // open: en
  Decoder #(.select(2), .tristate("false"), .disabled("Z"), .enable("false")) decoder_2 (
    .out1(decoder_2_out1), .out2(decoder_2_out2), .out3(decoder_2_out3), .sel(register_10_q));  // open: out0
  or or_16 (or_16_out, clearI, INT_LEVEL);
  not not_1 (not_1_out, or_17_out);
  or or_17 (or_17_out, URET, setI);
  Decoder #(.select(2), .tristate("false"), .disabled("Z"), .enable("false")) decoder_3 (
    .out0(decoder_3_out0), .out1(decoder_3_out1), .out2(decoder_3_out2), .sel(counter_1_q));  // open: out3
  or or_18 (IR2_t, IR2, IRB);
  Register #(.width(1), .trigger("falling"), .Select("low")) register_11 (
    .D(1'b0), .Q(register_11_q), .clk(CLK), .clr(RST), .preset(URET));  // open: en, cs
  Comparator #(.width(2), .mode("unsigned")) comparator_6 (
    .a(multiplexer_3_out), .b(register_10_q), .eq(comparator_6_eq));  // open: gt, lt
  Register #(.width(1), .trigger("rising"), .Select("low")) register_12 (
    .D(1'b0), .Q(register_12_q), .clk(not_1_out), .clr(RST), .preset(or_16_out));  // open: en, cs
  not not_2 (IE, register_12_q);
  Comparator #(.width(32), .mode("unsigned")) comparator_7 (.a(32'h48), .b(KE), .eq(comparator_7_eq));  // open: gt, lt
  Multiplexer #(.select(1), .width(32), .disabled("Z"), .enable("false")) multiplexer_4 (
    .in0(KE), .in1(32'h2c), .out(RET_PC), .sel(comparator_7_eq));
  Register #(.width(1), .trigger("rising"), .Select("low")) register_13 (
    .D(1'b1), .Q(INT_LEVEL), .clk(NEW_INT), .clr(or_20_out));  // open: en
  Register #(.width(1), .trigger("rising"), .Select("low")) register_14 (
    .D(1'b1), .Q(register_14_q), .clk(multiplexer_5_out), .clr(or_21_out));  // open: en
  Multiplexer #(.select(1), .width(1), .disabled("Z"), .enable("false")) multiplexer_5 (
    .in0(1'b1), .in1(CLK), .out(multiplexer_5_out), .sel(INT_LEVEL));
  Register #(.width(1), .trigger("falling"), .Select("low")) register_15 (
    .D(register_11_q), .Q(register_15_q), .clk(CLK), .clr(RST));  // open: en
  not not_3 (not_3_out, comparator_6_eq);
  and and_5 (clear1, decoder_2_out1, URET);
  and and_6 (clear2, decoder_2_out2, URET);
  and and_7 (clear3, decoder_2_out3, URET);
  or or_19 (or_19_out, URET, INT_LEVEL);
  Counter #(.width(2), .max('h3), .ongoal("wrap"), .trigger("rising"), .behavior("new")) counter_1 (
    .count(or_19_out), .Q(counter_1_q), .clk(CLK), .clr(RST), .down(URET));  // open: load, D, carry, preset
  Register #(.width(32), .trigger("rising"), .Select("low")) register_16 (
    .D(PC_4), .en(decoder_3_out0), .Q(register_16_q), .clk(CLK), .clr(RST));
  Register #(.width(32), .trigger("rising"), .Select("low")) register_17 (
    .D(PC_4), .en(decoder_3_out1), .Q(register_17_q), .clk(CLK), .clr(RST));
  Register #(.width(32), .trigger("rising"), .Select("low")) register_18 (
    .D(PC_4), .en(decoder_3_out2), .Q(register_18_q), .clk(CLK), .clr(RST));
  or or_20 (or_20_out, RST, register_14_q);
  or or_21 (or_21_out, register_14_q, RST);
  or or_22 (IR3_t, IR3, IRC);
  or or_23 (or_23_out, register_15_q, register_11_q);
  Multiplexer #(.select(1), .width(1), .disabled("Z"), .enable("false")) multiplexer_6 (
    .in0(not_3_out), .in1(multiplexer_6_out), .out(multiplexer_6_out), .sel(or_23_out));
  Subtractor #(.width(2)) subtractor_1 (.a(counter_1_q), .b(2'b01), .out(subtractor_1_out));  // open: bin, bout
  Multiplexer #(.select(2), .width(32), .disabled("Z"), .enable("false")) multiplexer_7 (
    .in0(register_16_q), .in1(register_17_q), .in2(register_18_q), .out(KE), .sel(subtractor_1_out));  // open: in3
  Multiplexer #(.select(1), .width(1), .disabled("Z"), .enable("false")) multiplexer_8 (
    .in0(not_3_out), .in1(multiplexer_6_out), .out(NEW_INT), .sel(Has_Run));
  // Probe on subtractor_1_out
  or or_24 (or_24_out, J, PCSrc, and_8_out);
  Multiplexer #(.select(1), .width(32), .disabled("Z"), .enable("false")) multiplexer_9 (
    .in0(adder_2_out), .in1(and_11_out), .out(multiplexer_9_out), .sel(JALR));
  and and_8 (and_8_out, lessthen, bltu);
  Multiplexer #(.select(1), .width(32), .disabled("Z"), .enable("false")) multiplexer_10 (
    .in0(PC_4), .in1(multiplexer_9_out), .out(multiplexer_10_out), .sel(or_24_out));
  Multiplexer #(.select(1), .width(32), .disabled("Z"), .enable("false")) multiplexer_11 (
    .in0(multiplexer_10_out), .in1(RET_PC), .out(multiplexer_11_out), .sel(URET));
  Multiplexer #(.select(1), .width(32), .disabled("Z"), .enable("false")) multiplexer_12 (
    .in0(multiplexer_11_out), .in1(INT_PC), .out(multiplexer_12_out), .sel(INT_LEVEL));
  not not_4 (not_4_out, halt);
  D_Flip_Flop #(.trigger("high"), .Pre_Clr_Positions("LEGACY"), .NegatePresetClear("false"), .enable("true"), .NewFFLayout("false")) d_ff_1 (.Q(d_ff_1_q));  // open: clk, D, Qn, preset, en, reset
  // Probe on 13'hc
  not not_5 (not_5_out, halt);
  Counter #(.width(16), .max('hffff), .ongoal("wrap"), .trigger("rising"), .behavior("new")) counter_2 (
    .D(16'h1), .count(not_5_out), .Q(\总周期数 ), .clk(CLK), .clr(Go));  // open: load, carry, preset, down
  Register #(.width(32), .trigger("rising"), .Select("low")) u_PC (
    .D(multiplexer_12_out), .en(not_4_out), .Q(PC), .clk(CLK), .clr(RST));
  Comparator #(.width(13), .mode("twosComplement")) comparator_8 (
    .a(CNT_num), .b(13'hc), .eq(comparator_8_eq), .lt(comparator_8_lt));  // open: gt
  Clock #(.highDuration(1), .lowDuration(1)) clock_1 (.out(clock_1_out));
  // Probe on PC
  Counter #(.width(13), .max('h1fff), .ongoal("stay"), .trigger("rising"), .behavior("old")) counter_3 (
    .count(comparator_8_lt), .Q(CNT_num), .clk(clock_1_out));  // open: load, D, carry, clr, preset
  or or_25 (J, JAL, JALR);
  Adder #(.width(32)) adder_1 (.a(PC), .b(32'h4), .out(PC_4));  // open: cin, cout
  Adder #(.width(32)) adder_2 (.a(PC), .b(shifter_1_out), .out(adder_2_out));  // open: cin, cout
  nand nand_1 (nand_1_out, d_ff_1_q, comparator_8_eq);
  // RiscV_Probe riscv_probe_1: pin names not known; wires that end beside it: IR
  assign CLK = nand_1_out ? clock_1_out : 1'bz;  // Controlled_Buffer controlled_buffer_1
  Pull_Resistor #(.pull(1)) pull_resistor_4 (.node(CLK));
  ROM #(.addrWidth(10), .dataWidth(32), .Select("high")) rom_1 (.addr(PC[11:2]), .data(IR));
  \单周期硬布线控制器  \u_单周期硬布线控制器_1  (
    .Funct({IR[30], IR[25], IR[14:12]}), .OP(IR[6:2]), .ALU_OP(\单周期硬布线控制器_1_alu_op ),
    .MemToReg(\单周期硬布线控制器_1_memtoreg ), .MemWrite(MemWrite), .ALU_SRC(\单周期硬布线控制器_1_alu_src [0]),
    .RegWrite(RegWrite), .ecall(ecall), .S_type(S_type), .Jalr(JALR), .Beq(\单周期硬布线控制器_1_beq ), .JAL(JAL),
    .Bne(\单周期硬布线控制器_1_bne ), .in_3(IR[21]), .uret(URET), .I(I), .B(B), .clearI(clearI), .sb(sb), .sll(sll),
    .setI(setI), .bltu(bltu));
  assign bit_extender_1_out = {{20{IR[31]}}, IR[31:20]};  // Bit_Extender bit_extender_1
  assign bit_extender_2_out = {{20{IR[31]}}, {IR[31:25], IR[11:7]}};  // Bit_Extender bit_extender_2
  assign bit_extender_3_out = {{20{IR[31]}}, {IR[31], IR[7], IR[30:25], IR[11:8]}};  // Bit_Extender bit_extender_3
  assign bit_extender_4_out = {{12{IR[31]}}, {IR[31], IR[19:12], IR[20], IR[30:21]}};  // Bit_Extender bit_extender_4
  Multiplexer #(.select(4), .width(32), .disabled("Z"), .enable("false")) multiplexer_13 (
    .in1(bit_extender_1_out), .in2(bit_extender_2_out), .in4(bit_extender_3_out), .in8(bit_extender_4_out),
    .out(multiplexer_13_out), .sel({JAL, B, S_type, I}));  // open: in0, in3, in5, in6, in7, in9, in10, in11, in12, in13, in14, in15
  Multiplexer #(.select(1), .width(5), .disabled("Z"), .enable("false")) multiplexer_14 (
    .in0(IR[19:15]), .in1(5'b10001), .out(multiplexer_14_out), .sel(ecall));
  Multiplexer #(.select(1), .width(5), .disabled("Z"), .enable("false")) multiplexer_15 (
    .in0(IR[24:20]), .in1(5'b01010), .out(multiplexer_15_out), .sel(ecall));
  Multiplexer #(.select(1), .width(32), .disabled("Z"), .enable("false")) multiplexer_16 (
    .in0(multiplexer_19_out), .in1(PC_4), .out(RDin), .sel(J));
  Regifile regifile_1 (
    .Din(RDin), .Clk(CLK), .R1(R1), .R2(ec_out), .WE(RegWrite), .W_num(IR[11:7]),
    .R1_num(multiplexer_14_out), .R2_num(multiplexer_15_out));
  Comparator #(.width(32), .mode("unsigned")) comparator_9 (.a(32'h22), .b(R1), .eq(ec_eq));  // open: gt, lt
  Multiplexer #(.select(2), .width(32), .disabled("Z"), .enable("false")) multiplexer_17 (
    .in0(ec_out), .in1(multiplexer_13_out), .in2({{27{1'b0}}, ec_out[4:0]}), .out(multiplexer_17_out),
    .sel({sll, \单周期硬布线控制器_1_alu_src [0]}));  // open: in3
  \sb分线  \sb分线_1  (
    .\new (ec_out[7:0]), .Address({alu_1_result[1], lessthen}), .\output (\sb分线_1_output ),
    .origin(ram_1_data));
  Shifter #(.width(32), .shift("ll")) shifter_1 (.in(multiplexer_13_out), .\dist (5'b00001), .out(shifter_1_out));
  ALU alu_1 (
    .X(R1), .Y(multiplexer_17_out), .AluOP(\单周期硬布线控制器_1_alu_op ), .Equal(alu_1_equal),
    .Result({alu_1_result_2, alu_1_result[1], lessthen}));  // open: Result_2, out_4, out_6
  Multiplexer #(.select(1), .width(32), .disabled("Z"), .enable("false")) multiplexer_18 (
    .in0(ec_out), .in1(\sb分线_1_output ), .out(MDin), .sel(sb));
  and and_9 (and_9_out, ecall, ~ec_eq);  // AND_Gate
  and and_10 (and_10_out, ec_eq, ecall);
  assign and_11_out = multiplexer_19_out & 32'hfffffffe;  // AND_Gate and_11, 32 bits wide
  and and_12 (and_12_out, alu_1_equal, \单周期硬布线控制器_1_beq );
  and and_13 (and_13_out, ~alu_1_equal, \单周期硬布线控制器_1_bne );  // AND_Gate
  Register #(.width(32), .trigger("rising"), .Select("low")) register_19 (
    .D(ec_out), .en(and_10_out), .Q(LedData), .clk(CLK));  // open: clr
  or or_26 (PCSrc, and_12_out, and_13_out);
  RAM #(.addrWidth(10), .dataWidth(32), .bus("separate"), .Select("high")) ram_1 (
    .addr(alu_1_result_2[11:2]), .din(MDin), .data(ram_1_data), .str(MemWrite), .clk(CLK), .ld(1'b1));  // open: sel, clr
  D_Flip_Flop #(.trigger("high"), .Pre_Clr_Positions("LEGACY"), .NegatePresetClear("false"), .enable("true"), .NewFFLayout("false")) d_ff_2 (
    .clk(CLK), .D(and_9_out), .Q(halt), .reset(Go));  // open: Qn, preset, en
  Multiplexer #(.select(1), .width(32), .disabled("Z"), .enable("false")) multiplexer_19 (
    .in0({alu_1_result_2, alu_1_result[1], lessthen}), .in1(ram_1_data), .out(multiplexer_19_out),
    .sel(\单周期硬布线控制器_1_memtoreg ));

  // Other names for the same wires on the sheet: R2[31:0] = ec_out

  // Notes on the sheet:
  //   中断源
  //   中断等待指示
  //   总复位信号应将除ROM以外所有存储组件全部清零
  //   多级中断测试信号模拟器
  //   数码管输出
  //   数码管输出应该用寄存器锁存，否则显示数据只能一闪而过
  //   为方便自动评测，需要输出PC，IR，寄存器堆写如数据RDin
  //   RAM写使能MemWrite、RAM写入数据MDin等信号
  //   控制位
  //   暂停节拍，不能为0
  //   戳工具置1进入计数暂停模式，ctrl+k时钟自动运行到对应节拍暂停
  //   ctrl+k关闭时钟连续运行，将控制位置零，进入单步调试模式调试
  //   指令探针
  //   指令存储器
  //   可计数暂停的时钟源
  //   指令字
  //   contents of rom_1 (hex, n*v repeats v):
  //   7d000113 100413 1f41993 41f9d993 433 c00913 800b13 140413 f47413 800293 100313 499993 89e9b3 1300533
  //   2200893 73 406282b3 fe0294e3 140413 f00f93 1f47433 1c41413 800293 100313 49d993 89e9b3 1300533
  //   2200893 73 406282b3 fe0294e3 1c45413 406b0b33 b0463 f95ff06f 2b3 fff2c293 1029293 fff2e293 500533
  //   2200893 73 f5dff06f 1112023 410113 a12023 410113 812023 410113 1312023 410113 1412023 410113 1512023
  //   410113 1612023 410113 40e073 100b13 300a13 100a93 1600433 441413 14469b3 1300533 2200893 73 fe0416e3
  //   415a0a33 fe0a10e3 40f073 ffc10113 12b03 ffc10113 12a83 ffc10113 12a03 ffc10113 12983 ffc10113 12403
  //   ffc10113 12503 ffc10113 12883 200073 1112023 410113 a12023 410113 812023 410113 1312023 410113
  //   1412023 410113 1512023 410113 1612023 410113 40e073 200b13 300a13 100a93 1600433 441413 14469b3
  //   1300533 2200893 73 fe0416e3 415a0a33 fe0a10e3 40f073 ffc10113 12b03 ffc10113 12a83 ffc10113 12a03
  //   ffc10113 12983 ffc10113 12403 ffc10113 12503 ffc10113 12883 200073 1112023 410113 a12023 410113
  //   812023 410113 1312023 410113 1412023 410113 1512023 410113 1612023 410113 40e073 300b13 300a13
  //   100a93 1600433 441413 14469b3 1300533 2200893 73 fe0416e3 415a0a33 fe0a10e3 40f073 ffc10113 12b03
  //   ffc10113 12a83 ffc10113 12a03 ffc10113 12983 ffc10113 12403 ffc10113 12503 ffc10113 12883 200073
  //   JAL
  //   JALR
  //   URET
  //   I
  //   B
  //   Beq
  //   Bne
  //   MemToReg
  //   MemWrite
  //   AluOP
  //   AluSrcB
  //   RegWrite
  //   数据存储器
endmodule

module \封装正确性测试  (
);

  wire IR1, IR2, IR3, MemW, RegW;
  wire [31:0] EX_PC, ID_PC, IF_PC, IR, LED, MDin, MDinr, MEM_PC, PC, RDin, RDinr, WB_PC;

  \单周期RISC_V  \u_单周期risc_v_1  (
    .IR1(IR1), .IR2(IR2), .IR3(IR3), .RegWrite(RegW), .MemWrite(MemW), .PC(PC), .IR(IR), .RDin(RDin),
    .MDin(MDin), .LedData(LED));
  \气泡流水线  \u_气泡流水线_1  (
    .RegWrite(RegW), .MemWrite(MemW), .IF_PC(IF_PC), .ID_PC(ID_PC), .EX_PC(EX_PC), .M_PC(MEM_PC),
    .WB_PC(WB_PC), .RDin(RDinr), .MDin(MDinr), .LedData(LED));
  \单周期_单级中断  \u_单周期_单级中断_1  (
    .IR1(IR1), .IR2(IR2), .IR3(IR3), .RegWrite(RegW), .MemWrite(MemW), .PC(PC), .IR(IR), .RDin(RDin),
    .MDin(MDin), .LedData(LED));
  \理想流水线  \u_理想流水线_1  (
    .RegWrite(RegW), .MemWrite(MemW), .IF_PC(IF_PC), .ID_PC(ID_PC), .EX_PC(EX_PC), .M_PC(MEM_PC),
    .WB_PC(WB_PC), .RDin(RDinr), .MDin(MDinr), .LedData(LED));
  \重定向流水线  \u_重定向流水线_1  (
    .RegWrite(RegW), .MemWrite(MemW), .IF_PC(IF_PC), .ID_PC(ID_PC), .EX_PC(EX_PC), .M_PC(MEM_PC),
    .WB_PC(WB_PC), .RDin(RDinr), .MDin(MDinr), .LedData(LED));
  \单周期_多级中断  \u_单周期_多级中断_1  (
    .IR1(IR1), .IR2(IR2), .IR3(IR3), .RegWrite(RegW), .MemWrite(MemW), .PC(PC), .IR(IR), .RDin(RDin),
    .MDin(MDin), .LedData(LED));

  // Notes on the sheet:
  //   单周期封装测试
  //   气泡流水封装测试
  //   单周期+单级中断封装测试
  //   请检查上面封装有无位宽不匹配，引脚标签是否和连接的标签相对应，否则无法在educoder平台上正确测试
  //   理想流水封装测试
  //   重定向流水封装测试
  //   单周期+多级中断封装测试
endmodule

module \sb分线  (
  input  [7:0] \new ,
  input  [1:0] Address,
  input  [31:0] origin,
  output [31:0] \output 
);

  wire [31:0] and_1_out, and_2_out, and_3_out, and_4_out, xor_1_out, xor_2_out, xor_3_out, xor_4_out;

  assign and_1_out = 32'hffffff00 & origin;  // AND_Gate and_1, 32 bits wide
  assign and_2_out = 32'hffff00ff & origin;  // AND_Gate and_2, 32 bits wide
  assign and_3_out = 32'hff00ffff & origin;  // AND_Gate and_3, 32 bits wide
  assign and_4_out = 32'hffffff & origin;  // AND_Gate and_4, 32 bits wide
  assign xor_1_out = {{24{1'b0}}, \new } ^ and_1_out;  // XOR_Gate xor_1, 32 bits wide
  assign xor_2_out = {{16{1'b0}}, \new , {8{1'b0}}} ^ and_2_out;  // XOR_Gate xor_2, 32 bits wide
  assign xor_3_out = {{8{1'b0}}, \new , {16{1'b0}}} ^ and_3_out;  // XOR_Gate xor_3, 32 bits wide
  assign xor_4_out = {\new , {24{1'b0}}} ^ and_4_out;  // XOR_Gate xor_4, 32 bits wide
  Multiplexer #(.select(2), .width(32), .disabled("Z"), .enable("false")) multiplexer_1 (
    .in0(xor_1_out), .in1(xor_2_out), .in2(xor_3_out), .in3(xor_4_out), .out(\output ), .sel(Address));
endmodule

// IF/ID
module \IF_ID流水寄存器  (
  input  PredictJump,
  input  [31:0] IR,
  input  [31:0] PC,
  input  [31:0] PC_4,
  input  \同步清零_高电平有效 ,
  input  CLK,
  input  \EN使能端 ,
  output PredictJump_2,
  output [31:0] IR_2,
  output [31:0] PC_2,
  output [31:0] PC_4_2
);

  wire multiplexer_1_out, pull_resistor_2_node;
  wire [31:0] multiplexer_2_out, multiplexer_3_out, multiplexer_4_out;

  Multiplexer #(.select(1), .width(1), .disabled("Z"), .enable("false")) multiplexer_1 (
    .in0(PredictJump), .in1(1'b0), .out(multiplexer_1_out), .sel(\同步清零_高电平有效 ));
  Multiplexer #(.select(1), .width(32), .disabled("Z"), .enable("false")) multiplexer_2 (
    .in0(IR), .in1({32{1'b0}}), .out(multiplexer_2_out), .sel(\同步清零_高电平有效 ));
  Multiplexer #(.select(1), .width(32), .disabled("Z"), .enable("false")) multiplexer_3 (
    .in0(PC), .in1({32{1'b0}}), .out(multiplexer_3_out), .sel(\同步清零_高电平有效 ));
  Multiplexer #(.select(1), .width(32), .disabled("Z"), .enable("false")) multiplexer_4 (
    .in0(PC_4), .in1({32{1'b0}}), .out(multiplexer_4_out), .sel(\同步清零_高电平有效 ));
  Pull_Resistor #(.pull(0)) pull_resistor_1 (.node(\同步清零_高电平有效 ));
  Pull_Resistor #(.pull(0)) pull_resistor_2 (.node(pull_resistor_2_node));
  not not_1 (pull_resistor_2_node, \EN使能端 );
  Register #(.width(1), .trigger("rising"), .Select("low")) register_1 (
    .D(multiplexer_1_out), .en(pull_resistor_2_node), .Q(PredictJump_2), .clk(CLK));  // open: clr
  Register #(.width(32), .trigger("rising"), .Select("low")) register_2 (
    .D(multiplexer_2_out), .en(pull_resistor_2_node), .Q(IR_2), .clk(CLK));  // open: clr
  Register #(.width(32), .trigger("rising"), .Select("low")) register_3 (
    .D(multiplexer_3_out), .en(pull_resistor_2_node), .Q(PC_2), .clk(CLK));  // open: clr
  Register #(.width(32), .trigger("rising"), .Select("low")) register_4 (
    .D(multiplexer_4_out), .en(pull_resistor_2_node), .Q(PC_4_2), .clk(CLK));  // open: clr
endmodule

// ID/EX
module \ID_EX流水寄存器  (
  input  ecall,
  input  jal,
  input  jalr,
  input  uret,
  input  Beq,
  input  Bne,
  input  MemToReg,
  input  MemWrite,
  input  [3:0] AluOP,
  input  Alu_Src,
  input  RegWrite,
  input  sb,
  input  clearI,
  input  setI,
  input  sll,
  input  bltu,
  input  [1:0] RsForward,
  input  [1:0] RtForward,
  input  PredictJump,
  input  [31:0] R1,
  input  [31:0] IR,
  input  [31:0] R2,
  input  [31:0] R2__sll,
  input  [31:0] \立即数 ,
  input  [4:0] W_num,
  input  [31:0] PC,
  input  [31:0] PC_4,
  input  \同步清零_高电平有效 ,
  input  CLK,
  input  \EN使能端 ,
  output ecall_2,
  output jal_2,
  output jalr_2,
  output uret_2,
  output Beq_2,
  output Bne_2,
  output MemToReg_2,
  output MemWrite_2,
  output [3:0] AluOP_2,
  output Alu_Src_2,
  output RegWrite_2,
  output sb_2,
  output clearI_2,
  output setI_2,
  output sll_2,
  output bltu_2,
  output [1:0] RsForward_2,
  output [1:0] RtForward_2,
  output PredictJump_2,
  output [31:0] R1_2,
  output [31:0] IR_2,
  output [31:0] R2_2,
  output [31:0] R2__sll_2,
  output [31:0] \立即数_2 ,
  output [4:0] W_num_2,
  output [31:0] PC_2,
  output [31:0] PC_4_2
);

  wire multiplexer_1_out, multiplexer_2_out, multiplexer_3_out, multiplexer_4_out, multiplexer_5_out,
       multiplexer_6_out, multiplexer_7_out, multiplexer_8_out, multiplexer_10_out, multiplexer_11_out,
       multiplexer_12_out, multiplexer_13_out, multiplexer_14_out, multiplexer_15_out, multiplexer_16_out,
       multiplexer_19_out, pull_resistor_2_node;
  wire [1:0] multiplexer_17_out, multiplexer_18_out;
  wire [3:0] multiplexer_9_out;
  wire [4:0] multiplexer_25_out;
  wire [31:0] multiplexer_20_out, multiplexer_21_out, multiplexer_22_out, multiplexer_23_out,
       multiplexer_24_out, multiplexer_26_out, multiplexer_27_out;

  Multiplexer #(.select(1), .width(1), .disabled("Z"), .enable("false")) multiplexer_1 (
    .in0(ecall), .in1(1'b0), .out(multiplexer_1_out), .sel(\同步清零_高电平有效 ));
  Multiplexer #(.select(1), .width(1), .disabled("Z"), .enable("false")) multiplexer_2 (
    .in0(jal), .in1(1'b0), .out(multiplexer_2_out), .sel(\同步清零_高电平有效 ));
  Multiplexer #(.select(1), .width(1), .disabled("Z"), .enable("false")) multiplexer_3 (
    .in0(jalr), .in1(1'b0), .out(multiplexer_3_out), .sel(\同步清零_高电平有效 ));
  Multiplexer #(.select(1), .width(1), .disabled("Z"), .enable("false")) multiplexer_4 (
    .in0(uret), .in1(1'b0), .out(multiplexer_4_out), .sel(\同步清零_高电平有效 ));
  Multiplexer #(.select(1), .width(1), .disabled("Z"), .enable("false")) multiplexer_5 (
    .in0(Beq), .in1(1'b0), .out(multiplexer_5_out), .sel(\同步清零_高电平有效 ));
  Multiplexer #(.select(1), .width(1), .disabled("Z"), .enable("false")) multiplexer_6 (
    .in0(Bne), .in1(1'b0), .out(multiplexer_6_out), .sel(\同步清零_高电平有效 ));
  Multiplexer #(.select(1), .width(1), .disabled("Z"), .enable("false")) multiplexer_7 (
    .in0(MemToReg), .in1(1'b0), .out(multiplexer_7_out), .sel(\同步清零_高电平有效 ));
  Multiplexer #(.select(1), .width(1), .disabled("Z"), .enable("false")) multiplexer_8 (
    .in0(MemWrite), .in1(1'b0), .out(multiplexer_8_out), .sel(\同步清零_高电平有效 ));
  Multiplexer #(.select(1), .width(4), .disabled("Z"), .enable("false")) multiplexer_9 (
    .in0(AluOP), .in1(4'b0000), .out(multiplexer_9_out), .sel(\同步清零_高电平有效 ));
  Multiplexer #(.select(1), .width(1), .disabled("Z"), .enable("false")) multiplexer_10 (
    .in0(Alu_Src), .in1(1'b0), .out(multiplexer_10_out), .sel(\同步清零_高电平有效 ));
  Multiplexer #(.select(1), .width(1), .disabled("Z"), .enable("false")) multiplexer_11 (
    .in0(RegWrite), .in1(1'b0), .out(multiplexer_11_out), .sel(\同步清零_高电平有效 ));
  Multiplexer #(.select(1), .width(1), .disabled("Z"), .enable("false")) multiplexer_12 (
    .in0(sb), .in1(1'b0), .out(multiplexer_12_out), .sel(\同步清零_高电平有效 ));
  Multiplexer #(.select(1), .width(1), .disabled("Z"), .enable("false")) multiplexer_13 (
    .in0(clearI), .in1(1'b0), .out(multiplexer_13_out), .sel(\同步清零_高电平有效 ));
  Multiplexer #(.select(1), .width(1), .disabled("Z"), .enable("false")) multiplexer_14 (
    .in0(setI), .in1(1'b0), .out(multiplexer_14_out), .sel(\同步清零_高电平有效 ));
  Multiplexer #(.select(1), .width(1), .disabled("Z"), .enable("false")) multiplexer_15 (
    .in0(sll), .in1(1'b0), .out(multiplexer_15_out), .sel(\同步清零_高电平有效 ));
  Multiplexer #(.select(1), .width(1), .disabled("Z"), .enable("false")) multiplexer_16 (
    .in0(bltu), .in1(1'b0), .out(multiplexer_16_out), .sel(\同步清零_高电平有效 ));
  Multiplexer #(.select(1), .width(2), .disabled("Z"), .enable("false")) multiplexer_17 (
    .in0(RsForward), .in1(2'b00), .out(multiplexer_17_out), .sel(\同步清零_高电平有效 ));
  Multiplexer #(.select(1), .width(2), .disabled("Z"), .enable("false")) multiplexer_18 (
    .in0(RtForward), .in1(2'b00), .out(multiplexer_18_out), .sel(\同步清零_高电平有效 ));
  Multiplexer #(.select(1), .width(1), .disabled("Z"), .enable("false")) multiplexer_19 (
    .in0(PredictJump), .in1(1'b0), .out(multiplexer_19_out), .sel(\同步清零_高电平有效 ));
  Multiplexer #(.select(1), .width(32), .disabled("Z"), .enable("false")) multiplexer_20 (
    .in0(R1), .in1({32{1'b0}}), .out(multiplexer_20_out), .sel(\同步清零_高电平有效 ));
  Multiplexer #(.select(1), .width(32), .disabled("Z"), .enable("false")) multiplexer_21 (
    .in0(IR), .in1({32{1'b0}}), .out(multiplexer_21_out), .sel(\同步清零_高电平有效 ));
  Multiplexer #(.select(1), .width(32), .disabled("Z"), .enable("false")) multiplexer_22 (
    .in0(R2), .in1({32{1'b0}}), .out(multiplexer_22_out), .sel(\同步清零_高电平有效 ));
  Multiplexer #(.select(1), .width(32), .disabled("Z"), .enable("false")) multiplexer_23 (
    .in0(R2__sll), .in1({32{1'b0}}), .out(multiplexer_23_out), .sel(\同步清零_高电平有效 ));
  Multiplexer #(.select(1), .width(32), .disabled("Z"), .enable("false")) multiplexer_24 (
    .in0(\立即数 ), .in1({32{1'b0}}), .out(multiplexer_24_out), .sel(\同步清零_高电平有效 ));
  Multiplexer #(.select(1), .width(5), .disabled("Z"), .enable("false")) multiplexer_25 (
    .in0(W_num), .in1({5{1'b0}}), .out(multiplexer_25_out), .sel(\同步清零_高电平有效 ));
  Multiplexer #(.select(1), .width(32), .disabled("Z"), .enable("false")) multiplexer_26 (
    .in0(PC), .in1({32{1'b0}}), .out(multiplexer_26_out), .sel(\同步清零_高电平有效 ));
  Multiplexer #(.select(1), .width(32), .disabled("Z"), .enable("false")) multiplexer_27 (
    .in0(PC_4), .in1({32{1'b0}}), .out(multiplexer_27_out), .sel(\同步清零_高电平有效 ));
  Pull_Resistor #(.pull(0)) pull_resistor_1 (.node(\同步清零_高电平有效 ));
  Pull_Resistor #(.pull(0)) pull_resistor_2 (.node(pull_resistor_2_node));
  not not_1 (pull_resistor_2_node, \EN使能端 );
  Register #(.width(1), .trigger("rising"), .Select("low")) register_1 (
    .D(multiplexer_1_out), .en(pull_resistor_2_node), .Q(ecall_2), .clk(CLK));  // open: clr
  Register #(.width(1), .trigger("rising"), .Select("low")) register_2 (
    .D(multiplexer_2_out), .en(pull_resistor_2_node), .Q(jal_2), .clk(CLK));  // open: clr
  Register #(.width(1), .trigger("rising"), .Select("low")) register_3 (
    .D(multiplexer_3_out), .en(pull_resistor_2_node), .Q(jalr_2), .clk(CLK));  // open: clr
  Register #(.width(1), .trigger("rising"), .Select("low")) register_4 (
    .D(multiplexer_4_out), .en(pull_resistor_2_node), .Q(uret_2), .clk(CLK));  // open: clr
  Register #(.width(1), .trigger("rising"), .Select("low")) register_5 (
    .D(multiplexer_5_out), .en(pull_resistor_2_node), .Q(Beq_2), .clk(CLK));  // open: clr
  Register #(.width(1), .trigger("rising"), .Select("low")) register_6 (
    .D(multiplexer_6_out), .en(pull_resistor_2_node), .Q(Bne_2), .clk(CLK));  // open: clr
  Register #(.width(1), .trigger("rising"), .Select("low")) register_7 (
    .D(multiplexer_7_out), .en(pull_resistor_2_node), .Q(MemToReg_2), .clk(CLK));  // open: clr
  Register #(.width(1), .trigger("rising"), .Select("low")) register_8 (
    .D(multiplexer_8_out), .en(pull_resistor_2_node), .Q(MemWrite_2), .clk(CLK));  // open: clr
  Register #(.width(4), .trigger("rising"), .Select("low")) register_9 (
    .D(multiplexer_9_out), .en(pull_resistor_2_node), .Q(AluOP_2), .clk(CLK));  // open: clr
  Register #(.width(1), .trigger("rising"), .Select("low")) register_10 (
    .D(multiplexer_10_out), .en(pull_resistor_2_node), .Q(Alu_Src_2), .clk(CLK));  // open: clr
  Register #(.width(1), .trigger("rising"), .Select("low")) register_11 (
    .D(multiplexer_11_out), .en(pull_resistor_2_node), .Q(RegWrite_2), .clk(CLK));  // open: clr
  Register #(.width(1), .trigger("rising"), .Select("low")) register_12 (
    .D(multiplexer_12_out), .en(pull_resistor_2_node), .Q(sb_2), .clk(CLK));  // open: clr
  Register #(.width(1), .trigger("rising"), .Select("low")) register_13 (
    .D(multiplexer_13_out), .en(pull_resistor_2_node), .Q(clearI_2), .clk(CLK));  // open: clr
  Register #(.width(1), .trigger("rising"), .Select("low")) register_14 (
    .D(multiplexer_14_out), .en(pull_resistor_2_node), .Q(setI_2), .clk(CLK));  // open: clr
  Register #(.width(1), .trigger("rising"), .Select("low")) register_15 (
    .D(multiplexer_15_out), .en(pull_resistor_2_node), .Q(sll_2), .clk(CLK));  // open: clr
  Register #(.width(1), .trigger("rising"), .Select("low")) register_16 (
    .D(multiplexer_16_out), .en(pull_resistor_2_node), .Q(bltu_2), .clk(CLK));  // open: clr
  Register #(.width(2), .trigger("rising"), .Select("low")) register_17 (
    .D(multiplexer_17_out), .en(pull_resistor_2_node), .Q(RsForward_2), .clk(CLK));  // open: clr
  Register #(.width(2), .trigger("rising"), .Select("low")) register_18 (
    .D(multiplexer_18_out), .en(pull_resistor_2_node), .Q(RtForward_2), .clk(CLK));  // open: clr
  Register #(.width(1), .trigger("rising"), .Select("low")) register_19 (
    .D(multiplexer_19_out), .en(pull_resistor_2_node), .Q(PredictJump_2), .clk(CLK));  // open: clr
  Register #(.width(32), .trigger("rising"), .Select("low")) register_20 (
    .D(multiplexer_20_out), .en(pull_resistor_2_node), .Q(R1_2), .clk(CLK));  // open: clr
  Register #(.width(32), .trigger("rising"), .Select("low")) register_21 (
    .D(multiplexer_21_out), .en(pull_resistor_2_node), .Q(IR_2), .clk(CLK));  // open: clr
  Register #(.width(32), .trigger("rising"), .Select("low")) register_22 (
    .D(multiplexer_22_out), .en(pull_resistor_2_node), .Q(R2_2), .clk(CLK));  // open: clr
  Register #(.width(32), .trigger("rising"), .Select("low")) register_23 (
    .D(multiplexer_23_out), .en(pull_resistor_2_node), .Q(R2__sll_2), .clk(CLK));  // open: clr
  Register #(.width(32), .trigger("rising"), .Select("low")) register_24 (
    .D(multiplexer_24_out), .en(pull_resistor_2_node), .Q(\立即数_2 ), .clk(CLK));  // open: clr
  Register #(.width(5), .trigger("rising"), .Select("low")) register_25 (
    .D(multiplexer_25_out), .en(pull_resistor_2_node), .Q(W_num_2), .clk(CLK));  // open: clr
  Register #(.width(32), .trigger("rising"), .Select("low")) register_26 (
    .D(multiplexer_26_out), .en(pull_resistor_2_node), .Q(PC_2), .clk(CLK));  // open: clr
  Register #(.width(32), .trigger("rising"), .Select("low")) register_27 (
    .D(multiplexer_27_out), .en(pull_resistor_2_node), .Q(PC_4_2), .clk(CLK));  // open: clr
endmodule
// EX/MEM
module \EX_MEM流水寄存器  (
  input  ecall,
  input  jal,
  input  jalr,
  input  uret,
  input  Beq,
  input  Bne,
  input  MemToReg,
  input  MemWrite,
  input  RegWrite,
  input  sb,
  input  clearI,
  input  setI,
  input  sll,
  input  bltu,
  input  [31:0] result,
  input  [31:0] IR,
  input  [9:0] address,
  input  lt,
  input  [31:0] R2,
  input  halt,
  input  ec_eq,
  input  [31:0] ec_out,
  input  [31:0] PC_offset,
  input  [4:0] W_num,
  input  [31:0] PC,
  input  [31:0] PC_4,
  input  \同步清零_高电平有效 ,
  input  CLK,
  input  \EN使能端 ,
  output ecall_2,
  output jal_2,
  output jalr_2,
  output uret_2,
  output Beq_2,
  output Bne_2,
  output MemToReg_2,
  output MemWrite_2,
  output RegWrite_2,
  output sb_2,
  output clearI_2,
  output ecall_3,
  output sll_2,
  output bltu_2,
  output [31:0] result_2,
  output [31:0] IR_2,
  output [9:0] address_2,
  output lt_2,
  output [31:0] R2_2,
  output halt_2,
  output ec_eq_2,
  output [31:0] ec_out_2,
  output [31:0] PC_offset_2,
  output [4:0] W_num_2,
  output [31:0] PC_2,
  output [31:0] PC_4_2
);

  wire multiplexer_1_out, multiplexer_2_out, multiplexer_3_out, multiplexer_4_out, multiplexer_5_out,
       multiplexer_6_out, multiplexer_7_out, multiplexer_8_out, multiplexer_9_out, multiplexer_10_out,
       multiplexer_11_out, multiplexer_12_out, multiplexer_13_out, multiplexer_14_out, multiplexer_18_out,
       multiplexer_20_out, multiplexer_21_out, pull_resistor_2_node;
  wire [4:0] multiplexer_24_out;
  wire [9:0] multiplexer_17_out;
  wire [31:0] multiplexer_15_out, multiplexer_16_out, multiplexer_19_out, multiplexer_22_out,
       multiplexer_23_out, multiplexer_25_out, multiplexer_26_out;

  Multiplexer #(.select(1), .width(1), .disabled("Z"), .enable("false")) multiplexer_1 (
    .in0(ecall), .in1(1'b0), .out(multiplexer_1_out), .sel(\同步清零_高电平有效 ));
  Multiplexer #(.select(1), .width(1), .disabled("Z"), .enable("false")) multiplexer_2 (
    .in0(jal), .in1(1'b0), .out(multiplexer_2_out), .sel(\同步清零_高电平有效 ));
  Multiplexer #(.select(1), .width(1), .disabled("Z"), .enable("false")) multiplexer_3 (
    .in0(jalr), .in1(1'b0), .out(multiplexer_3_out), .sel(\同步清零_高电平有效 ));
  Multiplexer #(.select(1), .width(1), .disabled("Z"), .enable("false")) multiplexer_4 (
    .in0(uret), .in1(1'b0), .out(multiplexer_4_out), .sel(\同步清零_高电平有效 ));
  Multiplexer #(.select(1), .width(1), .disabled("Z"), .enable("false")) multiplexer_5 (
    .in0(Beq), .in1(1'b0), .out(multiplexer_5_out), .sel(\同步清零_高电平有效 ));
  Multiplexer #(.select(1), .width(1), .disabled("Z"), .enable("false")) multiplexer_6 (
    .in0(Bne), .in1(1'b0), .out(multiplexer_6_out), .sel(\同步清零_高电平有效 ));
  Multiplexer #(.select(1), .width(1), .disabled("Z"), .enable("false")) multiplexer_7 (
    .in0(MemToReg), .in1(1'b0), .out(multiplexer_7_out), .sel(\同步清零_高电平有效 ));
  Multiplexer #(.select(1), .width(1), .disabled("Z"), .enable("false")) multiplexer_8 (
    .in0(MemWrite), .in1(1'b0), .out(multiplexer_8_out), .sel(\同步清零_高电平有效 ));
  Multiplexer #(.select(1), .width(1), .disabled("Z"), .enable("false")) multiplexer_9 (
    .in0(RegWrite), .in1(1'b0), .out(multiplexer_9_out), .sel(\同步清零_高电平有效 ));
  Multiplexer #(.select(1), .width(1), .disabled("Z"), .enable("false")) multiplexer_10 (
    .in0(sb), .in1(1'b0), .out(multiplexer_10_out), .sel(\同步清零_高电平有效 ));
  Multiplexer #(.select(1), .width(1), .disabled("Z"), .enable("false")) multiplexer_11 (
    .in0(clearI), .in1(1'b0), .out(multiplexer_11_out), .sel(\同步清零_高电平有效 ));
  Multiplexer #(.select(1), .width(1), .disabled("Z"), .enable("false")) multiplexer_12 (
    .in0(setI), .in1(1'b0), .out(multiplexer_12_out), .sel(\同步清零_高电平有效 ));
  Multiplexer #(.select(1), .width(1), .disabled("Z"), .enable("false")) multiplexer_13 (
    .in0(sll), .in1(1'b0), .out(multiplexer_13_out), .sel(\同步清零_高电平有效 ));
  Multiplexer #(.select(1), .width(1), .disabled("Z"), .enable("false")) multiplexer_14 (
    .in0(bltu), .in1(1'b0), .out(multiplexer_14_out), .sel(\同步清零_高电平有效 ));
  Multiplexer #(.select(1), .width(32), .disabled("Z"), .enable("false")) multiplexer_15 (
    .in0(result), .in1({32{1'b0}}), .out(multiplexer_15_out), .sel(\同步清零_高电平有效 ));
  Multiplexer #(.select(1), .width(32), .disabled("Z"), .enable("false")) multiplexer_16 (
    .in0(IR), .in1({32{1'b0}}), .out(multiplexer_16_out), .sel(\同步清零_高电平有效 ));
  Multiplexer #(.select(1), .width(10), .disabled("Z"), .enable("false")) multiplexer_17 (
    .in0(address), .in1({10{1'b0}}), .out(multiplexer_17_out), .sel(\同步清零_高电平有效 ));
  Multiplexer #(.select(1), .width(1), .disabled("Z"), .enable("false")) multiplexer_18 (
    .in0(lt), .in1(1'b0), .out(multiplexer_18_out), .sel(\同步清零_高电平有效 ));
  Multiplexer #(.select(1), .width(32), .disabled("Z"), .enable("false")) multiplexer_19 (
    .in0(R2), .in1({32{1'b0}}), .out(multiplexer_19_out), .sel(\同步清零_高电平有效 ));
  Multiplexer #(.select(1), .width(1), .disabled("Z"), .enable("false")) multiplexer_20 (
    .in0(halt), .in1(1'b0), .out(multiplexer_20_out), .sel(\同步清零_高电平有效 ));
  Multiplexer #(.select(1), .width(1), .disabled("Z"), .enable("false")) multiplexer_21 (
    .in0(ec_eq), .in1(1'b0), .out(multiplexer_21_out), .sel(\同步清零_高电平有效 ));
  Multiplexer #(.select(1), .width(32), .disabled("Z"), .enable("false")) multiplexer_22 (
    .in0(ec_out), .in1({32{1'b0}}), .out(multiplexer_22_out), .sel(\同步清零_高电平有效 ));
  Multiplexer #(.select(1), .width(32), .disabled("Z"), .enable("false")) multiplexer_23 (
    .in0(PC_offset), .in1({32{1'b0}}), .out(multiplexer_23_out), .sel(\同步清零_高电平有效 ));
  Multiplexer #(.select(1), .width(5), .disabled("Z"), .enable("false")) multiplexer_24 (
    .in0(W_num), .in1({5{1'b0}}), .out(multiplexer_24_out), .sel(\同步清零_高电平有效 ));
  Multiplexer #(.select(1), .width(32), .disabled("Z"), .enable("false")) multiplexer_25 (
    .in0(PC), .in1({32{1'b0}}), .out(multiplexer_25_out), .sel(\同步清零_高电平有效 ));
  Multiplexer #(.select(1), .width(32), .disabled("Z"), .enable("false")) multiplexer_26 (
    .in0(PC_4), .in1({32{1'b0}}), .out(multiplexer_26_out), .sel(\同步清零_高电平有效 ));
  Pull_Resistor #(.pull(0)) pull_resistor_1 (.node(\同步清零_高电平有效 ));
  Pull_Resistor #(.pull(0)) pull_resistor_2 (.node(pull_resistor_2_node));
  not not_1 (pull_resistor_2_node, \EN使能端 );
  Register #(.width(1), .trigger("rising"), .Select("low")) register_1 (
    .D(multiplexer_1_out), .en(pull_resistor_2_node), .Q(ecall_2), .clk(CLK));  // open: clr
  Register #(.width(1), .trigger("rising"), .Select("low")) register_2 (
    .D(multiplexer_2_out), .en(pull_resistor_2_node), .Q(jal_2), .clk(CLK));  // open: clr
  Register #(.width(1), .trigger("rising"), .Select("low")) register_3 (
    .D(multiplexer_3_out), .en(pull_resistor_2_node), .Q(jalr_2), .clk(CLK));  // open: clr
  Register #(.width(1), .trigger("rising"), .Select("low")) register_4 (
    .D(multiplexer_4_out), .en(pull_resistor_2_node), .Q(uret_2), .clk(CLK));  // open: clr
  Register #(.width(1), .trigger("rising"), .Select("low")) register_5 (
    .D(multiplexer_5_out), .en(pull_resistor_2_node), .Q(Beq_2), .clk(CLK));  // open: clr
  Register #(.width(1), .trigger("rising"), .Select("low")) register_6 (
    .D(multiplexer_6_out), .en(pull_resistor_2_node), .Q(Bne_2), .clk(CLK));  // open: clr
  Register #(.width(1), .trigger("rising"), .Select("low")) register_7 (
    .D(multiplexer_7_out), .en(pull_resistor_2_node), .Q(MemToReg_2), .clk(CLK));  // open: clr
  Register #(.width(1), .trigger("rising"), .Select("low")) register_8 (
    .D(multiplexer_8_out), .en(pull_resistor_2_node), .Q(MemWrite_2), .clk(CLK));  // open: clr
  Register #(.width(1), .trigger("rising"), .Select("low")) register_9 (
    .D(multiplexer_9_out), .en(pull_resistor_2_node), .Q(RegWrite_2), .clk(CLK));  // open: clr
  Register #(.width(1), .trigger("rising"), .Select("low")) register_10 (
    .D(multiplexer_10_out), .en(pull_resistor_2_node), .Q(sb_2), .clk(CLK));  // open: clr
  Register #(.width(1), .trigger("rising"), .Select("low")) register_11 (
    .D(multiplexer_11_out), .en(pull_resistor_2_node), .Q(clearI_2), .clk(CLK));  // open: clr
  Register #(.width(1), .trigger("rising"), .Select("low")) register_12 (
    .D(multiplexer_12_out), .en(pull_resistor_2_node), .Q(ecall_3), .clk(CLK));  // open: clr
  Register #(.width(1), .trigger("rising"), .Select("low")) register_13 (
    .D(multiplexer_13_out), .en(pull_resistor_2_node), .Q(sll_2), .clk(CLK));  // open: clr
  Register #(.width(1), .trigger("rising"), .Select("low")) register_14 (
    .D(multiplexer_14_out), .en(pull_resistor_2_node), .Q(bltu_2), .clk(CLK));  // open: clr
  Register #(.width(32), .trigger("rising"), .Select("low")) register_15 (
    .D(multiplexer_15_out), .en(pull_resistor_2_node), .Q(result_2), .clk(CLK));  // open: clr
  Register #(.width(32), .trigger("rising"), .Select("low")) register_16 (
    .D(multiplexer_16_out), .en(pull_resistor_2_node), .Q(IR_2), .clk(CLK));  // open: clr
  Register #(.width(10), .trigger("rising"), .Select("low")) register_17 (
    .D(multiplexer_17_out), .en(pull_resistor_2_node), .Q(address_2), .clk(CLK));  // open: clr
  Register #(.width(1), .trigger("rising"), .Select("low")) register_18 (
    .D(multiplexer_18_out), .en(pull_resistor_2_node), .Q(lt_2), .clk(CLK));  // open: clr
  Register #(.width(32), .trigger("rising"), .Select("low")) register_19 (
    .D(multiplexer_19_out), .en(pull_resistor_2_node), .Q(R2_2), .clk(CLK));  // open: clr
  Register #(.width(1), .trigger("rising"), .Select("low")) register_20 (
    .D(multiplexer_20_out), .en(pull_resistor_2_node), .Q(halt_2), .clk(CLK));  // open: clr
  Register #(.width(1), .trigger("rising"), .Select("low")) register_21 (
    .D(multiplexer_21_out), .en(pull_resistor_2_node), .Q(ec_eq_2), .clk(CLK));  // open: clr
  Register #(.width(32), .trigger("rising"), .Select("low")) register_22 (
    .D(multiplexer_22_out), .en(pull_resistor_2_node), .Q(ec_out_2), .clk(CLK));  // open: clr
  Register #(.width(32), .trigger("rising"), .Select("low")) register_23 (
    .D(multiplexer_23_out), .en(pull_resistor_2_node), .Q(PC_offset_2), .clk(CLK));  // open: clr
  Register #(.width(5), .trigger("rising"), .Select("low")) register_24 (
    .D(multiplexer_24_out), .en(pull_resistor_2_node), .Q(W_num_2), .clk(CLK));  // open: clr
  Register #(.width(32), .trigger("rising"), .Select("low")) register_25 (
    .D(multiplexer_25_out), .en(pull_resistor_2_node), .Q(PC_2), .clk(CLK));  // open: clr
  Register #(.width(32), .trigger("rising"), .Select("low")) register_26 (
    .D(multiplexer_26_out), .en(pull_resistor_2_node), .Q(PC_4_2), .clk(CLK));  // open: clr
endmodule

// MEM/WB
module \MEM_WB流水寄存器  (
  input  ecall,
  input  jal,
  input  jalr,
  input  uret,
  input  Beq,
  input  Bne,
  input  MemToReg,
  input  RegWrite,
  input  clearI,
  input  setI,
  input  sll,
  input  bltu,
  input  lt,
  input  halt,
  input  ec_eq,
  input  [31:0] ec_out,
  input  [31:0] PC_offset,
  input  [4:0] W_num,
  input  [31:0] Result,
  input  [31:0] IR,
  input  [31:0] Mem,
  input  [31:0] PC,
  input  [31:0] PC_4,
  input  \同步清零_高电平有效 ,
  input  CLK,
  input  \EN使能端 ,
  output ecall_2,
  output jal_2,
  output jalr_2,
  output uret_2,
  output Beq_2,
  output Bne_2,
  output MemToReg_2,
  output RegWrite_2,
  output clearI_2,
  output setI_2,
  output sll_2,
  output bltu_2,
  output lt_2,
  output halt_2,
  output ec_eq_2,
  output [31:0] ec_out_2,
  output [31:0] PC_offset_2,
  output [4:0] W_num_2,
  output [31:0] Result_2,
  output [31:0] Mem_2,
  output [31:0] Mem_3,
  output [31:0] PC_2,
  output [31:0] PC_4_2
);

  wire multiplexer_1_out, multiplexer_2_out, multiplexer_3_out, multiplexer_4_out, multiplexer_5_out,
       multiplexer_6_out, multiplexer_7_out, multiplexer_8_out, multiplexer_9_out, multiplexer_10_out,
       multiplexer_11_out, multiplexer_12_out, multiplexer_13_out, multiplexer_14_out, multiplexer_15_out,
       not_1_out;
  wire [4:0] multiplexer_18_out;
  wire [31:0] multiplexer_16_out, multiplexer_17_out, multiplexer_19_out, multiplexer_20_out,
       multiplexer_21_out, multiplexer_22_out, multiplexer_23_out;

  Multiplexer #(.select(1), .width(1), .disabled("Z"), .enable("false")) multiplexer_1 (
    .in0(ecall), .in1(1'b0), .out(multiplexer_1_out), .sel(\同步清零_高电平有效 ));
  Multiplexer #(.select(1), .width(1), .disabled("Z"), .enable("false")) multiplexer_2 (
    .in0(jal), .in1(1'b0), .out(multiplexer_2_out), .sel(\同步清零_高电平有效 ));
  Multiplexer #(.select(1), .width(1), .disabled("Z"), .enable("false")) multiplexer_3 (
    .in0(jalr), .in1(1'b0), .out(multiplexer_3_out), .sel(\同步清零_高电平有效 ));
  Multiplexer #(.select(1), .width(1), .disabled("Z"), .enable("false")) multiplexer_4 (
    .in0(uret), .in1(1'b0), .out(multiplexer_4_out), .sel(\同步清零_高电平有效 ));
  Multiplexer #(.select(1), .width(1), .disabled("Z"), .enable("false")) multiplexer_5 (
    .in0(Beq), .in1(1'b0), .out(multiplexer_5_out), .sel(\同步清零_高电平有效 ));
  Multiplexer #(.select(1), .width(1), .disabled("Z"), .enable("false")) multiplexer_6 (
    .in0(Bne), .in1(1'b0), .out(multiplexer_6_out), .sel(\同步清零_高电平有效 ));
  Multiplexer #(.select(1), .width(1), .disabled("Z"), .enable("false")) multiplexer_7 (
    .in0(MemToReg), .in1(1'b0), .out(multiplexer_7_out), .sel(\同步清零_高电平有效 ));
  Multiplexer #(.select(1), .width(1), .disabled("Z"), .enable("false")) multiplexer_8 (
    .in0(RegWrite), .in1(1'b0), .out(multiplexer_8_out), .sel(\同步清零_高电平有效 ));
  Multiplexer #(.select(1), .width(1), .disabled("Z"), .enable("false")) multiplexer_9 (
    .in0(clearI), .in1(1'b0), .out(multiplexer_9_out), .sel(\同步清零_高电平有效 ));
  Multiplexer #(.select(1), .width(1), .disabled("Z"), .enable("false")) multiplexer_10 (
    .in0(setI), .in1(1'b0), .out(multiplexer_10_out), .sel(\同步清零_高电平有效 ));
  Multiplexer #(.select(1), .width(1), .disabled("Z"), .enable("false")) multiplexer_11 (
    .in0(sll), .in1(1'b0), .out(multiplexer_11_out), .sel(\同步清零_高电平有效 ));
  Multiplexer #(.select(1), .width(1), .disabled("Z"), .enable("false")) multiplexer_12 (
    .in0(bltu), .in1(1'b0), .out(multiplexer_12_out), .sel(\同步清零_高电平有效 ));
  Multiplexer #(.select(1), .width(1), .disabled("Z"), .enable("false")) multiplexer_13 (
    .in0(lt), .in1(1'b0), .out(multiplexer_13_out), .sel(\同步清零_高电平有效 ));
  Multiplexer #(.select(1), .width(1), .disabled("Z"), .enable("false")) multiplexer_14 (
    .in0(halt), .in1(1'b0), .out(multiplexer_14_out), .sel(\同步清零_高电平有效 ));
  Multiplexer #(.select(1), .width(1), .disabled("Z"), .enable("false")) multiplexer_15 (
    .in0(ec_eq), .in1(1'b0), .out(multiplexer_15_out), .sel(\同步清零_高电平有效 ));
  Multiplexer #(.select(1), .width(32), .disabled("Z"), .enable("false")) multiplexer_16 (
    .in0(ec_out), .in1({32{1'b0}}), .out(multiplexer_16_out), .sel(\同步清零_高电平有效 ));
  Multiplexer #(.select(1), .width(32), .disabled("Z"), .enable("false")) multiplexer_17 (
    .in0(PC_offset), .in1({32{1'b0}}), .out(multiplexer_17_out), .sel(\同步清零_高电平有效 ));
  Multiplexer #(.select(1), .width(5), .disabled("Z"), .enable("false")) multiplexer_18 (
    .in0(W_num), .in1({5{1'b0}}), .out(multiplexer_18_out), .sel(\同步清零_高电平有效 ));
  Multiplexer #(.select(1), .width(32), .disabled("Z"), .enable("false")) multiplexer_19 (
    .in0(Result), .in1({32{1'b0}}), .out(multiplexer_19_out), .sel(\同步清零_高电平有效 ));
  Multiplexer #(.select(1), .width(32), .disabled("Z"), .enable("false")) multiplexer_20 (
    .in0(IR), .in1({32{1'b0}}), .out(multiplexer_20_out), .sel(\同步清零_高电平有效 ));
  Multiplexer #(.select(1), .width(32), .disabled("Z"), .enable("false")) multiplexer_21 (
    .in0(Mem), .in1({32{1'b0}}), .out(multiplexer_21_out), .sel(\同步清零_高电平有效 ));
  Multiplexer #(.select(1), .width(32), .disabled("Z"), .enable("false")) multiplexer_22 (
    .in0(PC), .in1({32{1'b0}}), .out(multiplexer_22_out), .sel(\同步清零_高电平有效 ));
  Multiplexer #(.select(1), .width(32), .disabled("Z"), .enable("false")) multiplexer_23 (
    .in0(PC_4), .in1({32{1'b0}}), .out(multiplexer_23_out), .sel(\同步清零_高电平有效 ));
  Pull_Resistor #(.pull(0)) pull_resistor_1 (.node(\同步清零_高电平有效 ));
  not not_1 (not_1_out, \EN使能端 );
  Register #(.width(1), .trigger("rising"), .Select("low")) register_1 (
    .D(multiplexer_1_out), .en(not_1_out), .Q(ecall_2), .clk(CLK));  // open: clr
  Register #(.width(1), .trigger("rising"), .Select("low")) register_2 (
    .D(multiplexer_2_out), .en(not_1_out), .Q(jal_2), .clk(CLK));  // open: clr
  Register #(.width(1), .trigger("rising"), .Select("low")) register_3 (
    .D(multiplexer_3_out), .en(not_1_out), .Q(jalr_2), .clk(CLK));  // open: clr
  Register #(.width(1), .trigger("rising"), .Select("low")) register_4 (
    .D(multiplexer_4_out), .en(not_1_out), .Q(uret_2), .clk(CLK));  // open: clr
  Register #(.width(1), .trigger("rising"), .Select("low")) register_5 (
    .D(multiplexer_5_out), .en(not_1_out), .Q(Beq_2), .clk(CLK));  // open: clr
  Register #(.width(1), .trigger("rising"), .Select("low")) register_6 (
    .D(multiplexer_6_out), .en(not_1_out), .Q(Bne_2), .clk(CLK));  // open: clr
  Register #(.width(1), .trigger("rising"), .Select("low")) register_7 (
    .D(multiplexer_7_out), .en(not_1_out), .Q(MemToReg_2), .clk(CLK));  // open: clr
  Register #(.width(1), .trigger("rising"), .Select("low")) register_8 (
    .D(multiplexer_8_out), .en(not_1_out), .Q(RegWrite_2), .clk(CLK));  // open: clr
  Register #(.width(1), .trigger("rising"), .Select("low")) register_9 (
    .D(multiplexer_9_out), .en(not_1_out), .Q(clearI_2), .clk(CLK));  // open: clr
  Register #(.width(1), .trigger("rising"), .Select("low")) register_10 (
    .D(multiplexer_10_out), .en(not_1_out), .Q(setI_2), .clk(CLK));  // open: clr
  Register #(.width(1), .trigger("rising"), .Select("low")) register_11 (
    .D(multiplexer_11_out), .en(not_1_out), .Q(sll_2), .clk(CLK));  // open: clr
  Register #(.width(1), .trigger("rising"), .Select("low")) register_12 (
    .D(multiplexer_12_out), .en(not_1_out), .Q(bltu_2), .clk(CLK));  // open: clr
  Register #(.width(1), .trigger("rising"), .Select("low")) register_13 (
    .D(multiplexer_13_out), .en(not_1_out), .Q(lt_2), .clk(CLK));  // open: clr
  Register #(.width(1), .trigger("rising"), .Select("low")) register_14 (
    .D(multiplexer_14_out), .en(not_1_out), .Q(halt_2), .clk(CLK));  // open: clr
  Register #(.width(1), .trigger("rising"), .Select("low")) register_15 (
    .D(multiplexer_15_out), .en(not_1_out), .Q(ec_eq_2), .clk(CLK));  // open: clr
  Register #(.width(32), .trigger("rising"), .Select("low")) register_16 (
    .D(multiplexer_16_out), .en(not_1_out), .Q(ec_out_2), .clk(CLK));  // open: clr
  Register #(.width(32), .trigger("rising"), .Select("low")) register_17 (
    .D(multiplexer_17_out), .en(not_1_out), .Q(PC_offset_2), .clk(CLK));  // open: clr
  Register #(.width(5), .trigger("rising"), .Select("low")) register_18 (
    .D(multiplexer_18_out), .en(not_1_out), .Q(W_num_2), .clk(CLK));  // open: clr
  Register #(.width(32), .trigger("rising"), .Select("low")) register_19 (
    .D(multiplexer_19_out), .en(not_1_out), .Q(Result_2), .clk(CLK));  // open: clr
  Register #(.width(32), .trigger("rising"), .Select("low")) register_20 (
    .D(multiplexer_20_out), .en(not_1_out), .Q(Mem_2), .clk(CLK));  // open: clr
  Register #(.width(32), .trigger("rising"), .Select("low")) register_21 (
    .D(multiplexer_21_out), .en(not_1_out), .Q(Mem_3), .clk(CLK));  // open: clr
  Register #(.width(32), .trigger("rising"), .Select("low")) register_22 (
    .D(multiplexer_22_out), .en(not_1_out), .Q(PC_2), .clk(CLK));  // open: clr
  Register #(.width(32), .trigger("rising"), .Select("low")) register_23 (
    .D(multiplexer_23_out), .en(not_1_out), .Q(PC_4_2), .clk(CLK));  // open: clr
  Pull_Resistor #(.pull(0)) pull_resistor_2 (.node(not_1_out));
endmodule

module \气泡逻辑  (
  input  [4:0] R1,
  input  I,
  input  B,
  input  [31:0] IR,
  input  [4:0] R2,
  input  BranchTakens,
  input  J,
  input  [4:0] EX_WriteReg_num,
  input  EX_RegWrite,
  input  S,
  input  [4:0] MEM_WriteReg_num,
  input  MEM_RegWrite,
  output ID_EX_CLR,
  output IF_ID_CLR,
  output IF_ID_EN,
  output PC_EN,
  output stall
);

  wire and_2_out, and_3_out, and_4_out, and_5_out, comparator_1_eq, comparator_2_eq, comparator_3_eq,
       comparator_4_eq, comparator_5_eq, comparator_6_eq, comparator_7_eq, or_1_out, R, rs__0, rsUsed, rt__0,
       rtUsed;

  or or_1 (or_1_out, I, B, J, S);
  Comparator #(.width(32), .mode("unsigned")) comparator_1 (
    .a(IR), .b({32{1'b0}}), .eq(comparator_1_eq));  // open: gt, lt
  Comparator #(.width(5), .mode("unsigned")) comparator_2 (
    .a(R1), .b({5{1'b0}}), .eq(comparator_2_eq));  // open: gt, lt
  Comparator #(.width(5), .mode("unsigned")) comparator_3 (
    .a(R2), .b({5{1'b0}}), .eq(comparator_3_eq));  // open: gt, lt
  Comparator #(.width(5), .mode("unsigned")) comparator_4 (
    .a(R1), .b(EX_WriteReg_num), .eq(comparator_4_eq));  // open: gt, lt
  Comparator #(.width(5), .mode("unsigned")) comparator_5 (
    .a(R2), .b(EX_WriteReg_num), .eq(comparator_5_eq));  // open: gt, lt
  Comparator #(.width(5), .mode("unsigned")) comparator_6 (
    .a(R1), .b(MEM_WriteReg_num), .eq(comparator_6_eq));  // open: gt, lt
  Comparator #(.width(5), .mode("unsigned")) comparator_7 (
    .a(R2), .b(MEM_WriteReg_num), .eq(comparator_7_eq));  // open: gt, lt
  and and_1 (R, ~or_1_out, ~comparator_1_eq);  // AND_Gate
  not not_1 (rs__0, comparator_2_eq);
  not not_2 (rt__0, comparator_3_eq);
  and and_2 (and_2_out, rsUsed, rs__0, EX_RegWrite, comparator_4_eq);
  and and_3 (and_3_out, rtUsed, rt__0, EX_RegWrite, comparator_5_eq);
  and and_4 (and_4_out, rsUsed, rs__0, MEM_RegWrite, comparator_6_eq);
  and and_5 (and_5_out, rtUsed, rt__0, MEM_RegWrite, comparator_7_eq);
  or or_2 (rsUsed, I, B, R, S);
  or or_3 (stall, and_2_out, and_3_out, and_4_out, and_5_out);
  or or_4 (rtUsed, B, R, S);
  or or_5 (ID_EX_CLR, stall, BranchTakens);
  Multiplexer #(.select(1), .width(1), .disabled("Z"), .enable("false")) multiplexer_1 (
    .in0(stall), .in1(1'b0), .out(IF_ID_EN), .sel(BranchTakens));
  not not_3 (PC_EN, stall);

  assign IF_ID_CLR = BranchTakens;

  // Other names for the same wires on the sheet: DataHazzard = stall
endmodule

module \重定向逻辑  (
  input  [4:0] R1,
  input  BranchTakens,
  input  I,
  input  B,
  input  [31:0] IR,
  input  [4:0] R2,
  input  EX_MemRead__MemToReg,
  input  J,
  input  [4:0] EX_WriteReg_num,
  input  EX_RegWrite,
  input  S,
  input  [4:0] MEM_WriteReg_num,
  input  MEM_RegWrite,
  output [1:0] RsForward,
  output IF_ID_CLR,
  output [1:0] RtForward,
  output ID_EX_CLR,
  output PC_EN
);

  wire and_2_out, and_3_out, and_4_out, and_5_out, and_6_out, and_7_out, and_8_out, and_9_out,
       comparator_1_eq, comparator_2_eq, comparator_3_eq, comparator_4_eq, comparator_5_eq, comparator_6_eq,
       comparator_7_eq, comparator_8_eq, comparator_9_eq, LoadUse, or_1_out, R, rs__0, rsUsed, rt__0, rtUsed;
  wire [1:0] and_10_out, and_12_out;
  wire [7:0] counter_1_q;

  or or_1 (or_1_out, I, B, J, S);
  Comparator #(.width(32), .mode("unsigned")) comparator_1 (
    .a(IR), .b({32{1'b0}}), .eq(comparator_1_eq));  // open: gt, lt
  Comparator #(.width(5), .mode("unsigned")) comparator_2 (
    .a(R1), .b({5{1'b0}}), .eq(comparator_2_eq));  // open: gt, lt
  Comparator #(.width(5), .mode("unsigned")) comparator_3 (
    .a(R2), .b({5{1'b0}}), .eq(comparator_3_eq));  // open: gt, lt
  Comparator #(.width(5), .mode("unsigned")) comparator_4 (
    .a(R1), .b(EX_WriteReg_num), .eq(comparator_4_eq));  // open: gt, lt
  Comparator #(.width(5), .mode("unsigned")) comparator_5 (
    .a(R2), .b(EX_WriteReg_num), .eq(comparator_5_eq));  // open: gt, lt
  and and_1 (R, ~or_1_out, ~comparator_1_eq);  // AND_Gate
  not not_1 (rs__0, comparator_2_eq);
  not not_2 (rt__0, comparator_3_eq);
  or or_2 (ID_EX_CLR, BranchTakens, LoadUse);
  not not_3 (PC_EN, LoadUse);
  and and_2 (and_2_out, rsUsed, rs__0, EX_MemRead__MemToReg, comparator_4_eq);
  and and_3 (and_3_out, rtUsed, rt__0, EX_MemRead__MemToReg, comparator_5_eq);
  or or_3 (LoadUse, and_2_out, and_3_out);
  or or_4 (rsUsed, I, B, R, S);
  Comparator #(.width(5), .mode("unsigned")) comparator_6 (
    .a(R1), .b(MEM_WriteReg_num), .eq(comparator_6_eq));  // open: gt, lt
  Comparator #(.width(5), .mode("unsigned")) comparator_7 (
    .a(R1), .b(EX_WriteReg_num), .eq(comparator_7_eq));  // open: gt, lt
  Comparator #(.width(5), .mode("unsigned")) comparator_8 (
    .a(R2), .b(MEM_WriteReg_num), .eq(comparator_8_eq));  // open: gt, lt
  Comparator #(.width(5), .mode("unsigned")) comparator_9 (
    .a(R2), .b(EX_WriteReg_num), .eq(comparator_9_eq));  // open: gt, lt
  or or_5 (rtUsed, B, R, S);
  and and_4 (and_4_out, rsUsed, rs__0);
  and and_5 (and_5_out, MEM_RegWrite, comparator_6_eq);
  and and_6 (and_6_out, EX_RegWrite, comparator_7_eq);
  and and_7 (and_7_out, rtUsed, rt__0);
  and and_8 (and_8_out, MEM_RegWrite, comparator_8_eq);
  and and_9 (and_9_out, EX_RegWrite, comparator_9_eq);
  and and_10 (and_10_out[0], and_4_out, and_5_out);
  and and_11 (and_10_out[1], and_4_out, and_6_out);
  Multiplexer #(.select(2), .width(2), .disabled("Z"), .enable("false")) multiplexer_1 (
    .in0(2'b00), .in1(2'b01), .in2(2'b10), .in3(2'b10), .out(RsForward), .sel(and_10_out));
  and and_12 (and_12_out[0], and_7_out, and_8_out);
  and and_13 (and_12_out[1], and_7_out, and_9_out);
  Multiplexer #(.select(2), .width(2), .disabled("Z"), .enable("false")) multiplexer_2 (
    .in0(2'b00), .in1(2'b01), .in2(2'b10), .in3(2'b10), .out(RtForward), .sel(and_12_out));
  // Probe on counter_1_q
  Counter #(.width(8), .max('hff), .ongoal("wrap"), .trigger("rising"), .behavior("new")) counter_1 (
    .Q(counter_1_q), .clk(BranchTakens));  // open: load, D, count, carry, clr, preset, down

  assign IF_ID_CLR = BranchTakens;

  // Other names for the same wires on the sheet: EX_MemRead = EX_MemRead__MemToReg

  // Notes on the sheet:
  //   stall
endmodule

module \重定向流水线_单级中断  (
  input  IR1,
  input  IR2,
  input  IR3,
  output RegWrite,
  output MemWrite,
  output [31:0] IF_PC,
  output [31:0] ID_PC,
  output [31:0] EX_PC,
  output [31:0] M_PC,
  output [31:0] WB_PC,
  output [31:0] RDin,
  output [31:0] MDin,
  output [31:0] LedData
);

  wire alu_1_equal, and_1_out, and_3_out, and_4_out, and_5_out, and_6_out, and_7_out, and_8_out, and_9_out,
       and_10_out, and_15_out, B, bltu, Branch, clear1, clear2, clear3, CLK, clock_1_out, comparator_1_eq,
       comparator_1_lt, comparator_3_eq, comparator_4_eq, comparator_5_eq, comparator_6_eq, d_ff_1_q,
       decoder_1_out1, decoder_1_out2, decoder_1_out3, ec_eq, ecall, ecall_star, Ex_ec_eq, EX_JALR,
       \ex_mem流水寄存器_1_bltu_2 , \ex_mem流水寄存器_1_ec_eq_2 , \ex_mem流水寄存器_1_ecall_2 , \ex_mem流水寄存器_1_jal_2 ,
       \ex_mem流水寄存器_1_jalr_2 , \ex_mem流水寄存器_1_memtoreg_2 , \ex_mem流水寄存器_1_regwrite_2 , Go, halt, I,
       \id_ex流水寄存器_1_beq_2 , \id_ex流水寄存器_1_bne_2 , \id_ex流水寄存器_1_ecall_2 , \id_ex流水寄存器_1_jal_2 ,
       \id_ex流水寄存器_1_memtoreg_2 , \id_ex流水寄存器_1_memwrite_2 , \id_ex流水寄存器_1_regwrite_2 , \id_ex流水寄存器_1_sb_2 ,
       IE, INT, IR1_t, IR2_t, IR3_t, IRA, IRB, IRC, J, JAL, JAL_star, JALR, JALR_star, lessthen,
       \mem_wb流水寄存器_1_memtoreg_2 , nand_1_out, not_1_out, not_2_out, not_3_out, or_1_out, or_8_out,
       or_10_out, or_12_out, or_14_out, or_15_out, or_16_out, or_17_out, PC_EN, PCSrc, register_2_q,
       register_3_q, register_4_q, register_7_q, register_8_q, register_9_q, RST, S_type, sb_star, URET, w1,
       w2, w3, \中断信号 , \单周期硬布线控制器_1_alu_src , \单周期硬布线控制器_1_beq , \单周期硬布线控制器_1_bltu , \单周期硬布线控制器_1_bne ,
       \单周期硬布线控制器_1_cleari , \单周期硬布线控制器_1_memtoreg , \单周期硬布线控制器_1_memwrite , \单周期硬布线控制器_1_regwrite ,
       \单周期硬布线控制器_1_sb , \单周期硬布线控制器_1_seti , \单周期硬布线控制器_1_sll , \重定向逻辑_1_id_ex_clr , \重定向逻辑_1_if_id_clr ;
  wire [1:0] \id_ex流水寄存器_1_alu_src_2 , \id_ex流水寄存器_1_rsforward_2 , \id_ex流水寄存器_1_rtforward_2 , register_5_q,
       \中断号 , \重定向逻辑_1_rsforward , \重定向逻辑_1_rtforward ;
  wire [3:0] \id_ex流水寄存器_1_aluop_2 , \单周期硬布线控制器_1_alu_op ;
  wire [4:0] EX_W_num, ID_R1_num, ID_R2_num, MEM_W_num, \mem_wb流水寄存器_1_w_num_2 ;
  wire [9:0] \ex_mem流水寄存器_1_address_2 ;
  wire [12:0] CNT_num;
  wire [15:0] \LoadUse次数 , \总周期数 , \插入气泡数 , \无条件分支数 , \条件分支成功数 ;
  wire [31:0] adder_1_out, adder_2_out, and_2_out, bit_extender_1_out, bit_extender_2_out,
       bit_extender_3_out, bit_extender_4_out, ec_out, EX_ec_out, EX_IR, \ex_mem流水寄存器_1_ec_out_2 ,
       \ex_mem流水寄存器_1_pc_4_2 , \ex_mem流水寄存器_1_pc_offset_2 , \ex_mem流水寄存器_1_r2_2 , \ex_mem流水寄存器_1_result_2 ,
       \id_ex流水寄存器_1_pc_4_2 , \id_ex流水寄存器_1_r1_2 , \id_ex流水寄存器_1_r2_2 , \id_ex流水寄存器_1_r2__sll_2 ,
       \id_ex流水寄存器_1_立即数_2 , ID_IR, \if_id流水寄存器_1_pc_4_2 , IF_IR, INT_PC, MEM_IR, \mem_wb流水寄存器_1_mem_3 ,
       \mem_wb流水寄存器_1_pc_4_2 , \mem_wb流水寄存器_1_result_2 , multiplexer_1_out, multiplexer_3_out,
       multiplexer_5_out, multiplexer_8_out, multiplexer_10_out, multiplexer_12_out, ram_1_data,
       regifile_1_r1, regifile_1_r2, RET_PC, \sb分线_1_output , shifter_1_out, WB_IR, \原地址 ;
  wire [31:1] alu_1_result;

  Button \u_总复位  (.out(RST));
  Button _1 (.out(IR1_t));
  Button _2 (.out(IR2_t));
  Button _3 (.out(IR3_t));
  // Probe on \总周期数 
  // Probe on \总周期数 
  Button \u_继续运行  (.out(Go));
  LED #(.active("true")) led_1 (.in(w1));
  LED #(.active("true")) led_2 (.in(w2));
  LED #(.active("true")) led_3 (.in(w3));
  Hex_Digit_Display hex_digit_display_1 (.value(LedData[31:28]));  // open: dp
  // Probe on IF_PC[19:0]
  // RiscV_Probe riscv_probe_1: pin names not known; wires that end beside it: IF_IR
  Multiplexer #(.select(1), .width(32), .disabled("Z"), .enable("false")) multiplexer_1 (
    .in0(\原地址 ), .in1(RET_PC), .out(multiplexer_1_out), .sel(URET));
  Multiplexer #(.select(2), .width(32), .disabled("Z"), .enable("false")) multiplexer_2 (
    .in0(adder_1_out), .in1(adder_2_out), .in2(and_2_out), .out(\原地址 ), .sel({EX_JALR, PCSrc}));  // open: in3
  Hex_Digit_Display hex_digit_display_2 (.value(LedData[27:24]));  // open: dp
  Hex_Digit_Display hex_digit_display_3 (.value(LedData[23:20]));  // open: dp
  // Probe on ID_PC[19:0]
  // RiscV_Probe riscv_probe_2: pin names not known; wires that end beside it: ID_IR
  \重定向逻辑  \u_重定向逻辑_1  (
    .R1(ID_R1_num), .I(I), .B(B), .IR(ID_IR), .R2(ID_R2_num), .BranchTakens(Branch), .J(JAL),
    .EX_WriteReg_num(EX_W_num), .EX_RegWrite(\id_ex流水寄存器_1_regwrite_2 ), .S(S_type),
    .MEM_WriteReg_num(MEM_W_num), .MEM_RegWrite(\ex_mem流水寄存器_1_regwrite_2 ),
    .EX_MemRead__MemToReg(\id_ex流水寄存器_1_memtoreg_2 ), .PC_EN(PC_EN), .ID_EX_CLR(\重定向逻辑_1_id_ex_clr ),
    .IF_ID_CLR(\重定向逻辑_1_if_id_clr ), .RsForward(\重定向逻辑_1_rsforward ), .RtForward(\重定向逻辑_1_rtforward ));
  Multiplexer #(.select(1), .width(32), .disabled("Z"), .enable("false")) multiplexer_3 (
    .in0(multiplexer_1_out), .in1(INT_PC), .out(multiplexer_3_out), .sel(INT));
  and and_1 (and_1_out, not_1_out, PC_EN);
  not not_1 (not_1_out, halt);
  Hex_Digit_Display hex_digit_display_4 (.value(LedData[15:12]));  // open: dp
  Hex_Digit_Display hex_digit_display_5 (.value(LedData[19:16]));  // open: dp
  not not_2 (not_2_out, halt);
  Counter #(.width(16), .max('hffff), .ongoal("wrap"), .trigger("rising"), .behavior("new")) counter_1 (
    .D(16'h1), .count(not_2_out), .Q(\总周期数 ), .clk(CLK));  // open: load, carry, clr, preset, down
  Register #(.width(32), .trigger("rising"), .Select("low")) PC (
    .D(multiplexer_3_out), .en(and_1_out), .Q(IF_PC), .clk(CLK), .clr(RST));
  Hex_Digit_Display hex_digit_display_6 (.value(LedData[7:4]));  // open: dp
  Hex_Digit_Display hex_digit_display_7 (.value(LedData[11:8]));  // open: dp
  // Probe on EX_PC[19:0]
  // RiscV_Probe riscv_probe_3: pin names not known; wires that end beside it: EX_IR
  Adder #(.width(32)) adder_1 (.a(IF_PC), .b(32'h4), .out(adder_1_out));  // open: cin, cout
  Hex_Digit_Display hex_digit_display_8 (.value(LedData[3:0]));  // open: dp
  // Probe on IF_PC
  // Probe on \总周期数 
  // Probe on M_PC[19:0]
  // RiscV_Probe riscv_probe_4: pin names not known; wires that end beside it: MEM_IR
  ROM #(.addrWidth(10), .dataWidth(32), .Select("high")) rom_1 (.addr(IF_PC[11:2]), .data(IF_IR));
  // Probe on \总周期数 
  // Probe on \无条件分支数 
  // Probe on \条件分支成功数 
  // Probe on \插入气泡数 
  // Probe on \LoadUse次数 
  not not_3 (not_3_out, PC_EN);
  or or_1 (or_1_out, not_3_out, halt);
  \IF_ID流水寄存器  \if_id流水寄存器_1  (
    .IR(IF_IR), .PC(IF_PC), .PC_4(adder_1_out), .IR_2(ID_IR), .PC_2(ID_PC), .PC_4_2(\if_id流水寄存器_1_pc_4_2 ),
    .\同步清零_高电平有效 (\重定向逻辑_1_if_id_clr ), .CLK(CLK), .\EN使能端 (or_1_out));  // open: PredictJump, PredictJump_2
  // Probe on IF_PC[11:0]
  // Probe on WB_PC[19:0]
  // RiscV_Probe riscv_probe_5: pin names not known; wires that end beside it: WB_IR
  // RiscV_Probe riscv_probe_6: pin names not known; wires that end beside it: ID_IR
  // Probe on EX_PC[11:0]
  // Probe on ID_PC[11:0]
  // Probe on M_PC[11:0]
  D_Flip_Flop #(.trigger("high"), .Pre_Clr_Positions("LEGACY"), .NegatePresetClear("false"), .enable("true"), .NewFFLayout("false")) d_ff_1 (.Q(d_ff_1_q));  // open: clk, D, Qn, preset, en, reset
  // Probe on 13'h13
  \单周期硬布线控制器  \u_单周期硬布线控制器_1  (
    .Funct({ID_IR[30], ID_IR[25], ID_IR[14:12]}), .OP(ID_IR[6:2]), .ALU_OP(\单周期硬布线控制器_1_alu_op ),
    .MemToReg(\单周期硬布线控制器_1_memtoreg ), .MemWrite(\单周期硬布线控制器_1_memwrite ), .ALU_SRC(\单周期硬布线控制器_1_alu_src ),
    .RegWrite(\单周期硬布线控制器_1_regwrite ), .ecall(ecall), .S_type(S_type), .Jalr(JALR), .Beq(\单周期硬布线控制器_1_beq ),
    .JAL(JAL), .Bne(\单周期硬布线控制器_1_bne ), .in_3(ID_IR[21]), .uret(URET), .I(I), .B(B),
    .clearI(\单周期硬布线控制器_1_cleari ), .sb(\单周期硬布线控制器_1_sb ), .sll(\单周期硬布线控制器_1_sll ), .setI(\单周期硬布线控制器_1_seti ),
    .bltu(\单周期硬布线控制器_1_bltu ));
  assign bit_extender_1_out = {{20{ID_IR[31]}}, ID_IR[31:20]};  // Bit_Extender bit_extender_1
  assign bit_extender_2_out = {{20{ID_IR[31]}}, {ID_IR[31:25], ID_IR[11:7]}};  // Bit_Extender bit_extender_2
  assign bit_extender_3_out = {{20{ID_IR[31]}}, {ID_IR[31], ID_IR[7], ID_IR[30:25], ID_IR[11:8]}};  // Bit_Extender bit_extender_3
  assign bit_extender_4_out = {{12{ID_IR[31]}}, {ID_IR[31], ID_IR[19:12], ID_IR[20], ID_IR[30:21]}};  // Bit_Extender bit_extender_4
  // Probe on WB_PC[11:0]
  Comparator #(.width(13), .mode("twosComplement")) comparator_1 (
    .a(CNT_num), .b(13'h13), .eq(comparator_1_eq), .lt(comparator_1_lt));  // open: gt
  Clock #(.highDuration(1), .lowDuration(1)) clock_1 (.out(clock_1_out));
  Multiplexer #(.select(1), .width(32), .disabled("Z"), .enable("false")) multiplexer_4 (
    .in0(multiplexer_12_out), .in1(\mem_wb流水寄存器_1_pc_4_2 ), .out(RDin), .sel(J));
  Multiplexer #(.select(4), .width(32), .disabled("Z"), .enable("false")) multiplexer_5 (
    .in1(bit_extender_1_out), .in2(bit_extender_2_out), .in4(bit_extender_3_out), .in8(bit_extender_4_out),
    .out(multiplexer_5_out), .sel({JAL, B, S_type, I}));  // open: in0, in3, in5, in6, in7, in9, in10, in11, in12, in13, in14, in15
  nand nand_1 (nand_1_out, d_ff_1_q, comparator_1_eq);
  Counter #(.width(13), .max('h1fff), .ongoal("stay"), .trigger("rising"), .behavior("old")) counter_2 (
    .count(comparator_1_lt), .Q(CNT_num), .clk(clock_1_out));  // open: load, D, carry, clr, preset
  Multiplexer #(.select(1), .width(5), .disabled("Z"), .enable("false")) multiplexer_6 (
    .in0(ID_IR[19:15]), .in1(5'b10001), .out(ID_R1_num), .sel(ecall));
  Multiplexer #(.select(1), .width(5), .disabled("Z"), .enable("false")) multiplexer_7 (
    .in0(ID_IR[24:20]), .in1(5'b01010), .out(ID_R2_num), .sel(ecall));
  assign CLK = nand_1_out ? clock_1_out : 1'bz;  // Controlled_Buffer controlled_buffer_1
  Regifile regifile_1 (
    .Din(RDin), .Clk(CLK), .R1(regifile_1_r1), .R2(regifile_1_r2), .WE(RegWrite),
    .W_num(\mem_wb流水寄存器_1_w_num_2 ), .R1_num(ID_R1_num), .R2_num(ID_R2_num));
  Pull_Resistor #(.pull(1)) pull_resistor_1 (.node(CLK));
  // OR_Gate or_2 has open pins: in0=IR1, in1=IRA, out=open
  \ID_EX流水寄存器  \id_ex流水寄存器_1  (
    .ecall(ecall), .jal(JAL), .jalr(JALR), .uret(URET), .Beq(\单周期硬布线控制器_1_beq ), .Bne(\单周期硬布线控制器_1_bne ),
    .MemToReg(\单周期硬布线控制器_1_memtoreg ), .MemWrite(\单周期硬布线控制器_1_memwrite ), .AluOP(\单周期硬布线控制器_1_alu_op ),
    .Alu_Src(\单周期硬布线控制器_1_alu_src ), .RegWrite(\单周期硬布线控制器_1_regwrite ), .sb(\单周期硬布线控制器_1_sb ),
    .clearI(\单周期硬布线控制器_1_cleari ), .setI(\单周期硬布线控制器_1_seti ), .sll(\单周期硬布线控制器_1_sll ), .R1(regifile_1_r1),
    .R2__sll({{27{1'b0}}, regifile_1_r2[4:0]}), .\立即数 (multiplexer_5_out), .W_num(ID_IR[11:7]), .PC(ID_PC),
    .PC_4(\if_id流水寄存器_1_pc_4_2 ), .ecall_2(\id_ex流水寄存器_1_ecall_2 ), .jal_2(\id_ex流水寄存器_1_jal_2 ),
    .jalr_2(EX_JALR), .Beq_2(\id_ex流水寄存器_1_beq_2 ), .Bne_2(\id_ex流水寄存器_1_bne_2 ),
    .MemToReg_2(\id_ex流水寄存器_1_memtoreg_2 ), .MemWrite_2(\id_ex流水寄存器_1_memwrite_2 ),
    .AluOP_2(\id_ex流水寄存器_1_aluop_2 ), .Alu_Src_2(\id_ex流水寄存器_1_alu_src_2 [0]),
    .RegWrite_2(\id_ex流水寄存器_1_regwrite_2 ), .sb_2(\id_ex流水寄存器_1_sb_2 ), .sll_2(\id_ex流水寄存器_1_alu_src_2 [1]),
    .R1_2(\id_ex流水寄存器_1_r1_2 ), .R2__sll_2(\id_ex流水寄存器_1_r2__sll_2 ), .\立即数_2 (\id_ex流水寄存器_1_立即数_2 ),
    .W_num_2(EX_W_num), .PC_2(EX_PC), .PC_4_2(\id_ex流水寄存器_1_pc_4_2 ), .\同步清零_高电平有效 (\重定向逻辑_1_id_ex_clr ),
    .CLK(CLK), .\EN使能端 (halt), .bltu(\单周期硬布线控制器_1_bltu ), .bltu_2(bltu), .R2(regifile_1_r2),
    .R2_2(\id_ex流水寄存器_1_r2_2 ), .IR(ID_IR), .IR_2(EX_IR), .RsForward(\重定向逻辑_1_rsforward ),
    .RsForward_2(\id_ex流水寄存器_1_rsforward_2 ), .RtForward(\重定向逻辑_1_rtforward ),
    .RtForward_2(\id_ex流水寄存器_1_rtforward_2 ));  // open: uret_2, clearI_2, setI_2, PredictJump, PredictJump_2
  Multiplexer #(.select(2), .width(32), .disabled("Z"), .enable("false")) multiplexer_8 (
    .in0(\id_ex流水寄存器_1_r1_2 ), .in1(multiplexer_12_out), .in2(\ex_mem流水寄存器_1_result_2 ),
    .out(multiplexer_8_out), .sel(\id_ex流水寄存器_1_rsforward_2 ));  // open: in3
  Multiplexer #(.select(2), .width(32), .disabled("Z"), .enable("false")) multiplexer_9 (
    .in0(\id_ex流水寄存器_1_r2_2 ), .in1(multiplexer_12_out), .in2(\ex_mem流水寄存器_1_result_2 ), .out(EX_ec_out),
    .sel(\id_ex流水寄存器_1_rtforward_2 ));  // open: in3
  // OR_Gate or_3 has open pins: in0=IR2, in1=IRB, out=open
  Multiplexer #(.select(2), .width(32), .disabled("Z"), .enable("false")) multiplexer_10 (
    .in0(EX_ec_out), .in1(\id_ex流水寄存器_1_立即数_2 ), .in2(\id_ex流水寄存器_1_r2__sll_2 ), .out(multiplexer_10_out),
    .sel(\id_ex流水寄存器_1_alu_src_2 ));  // open: in3
  Shifter #(.width(32), .shift("ll")) shifter_1 (.in(\id_ex流水寄存器_1_立即数_2 ), .\dist (5'b00001), .out(shifter_1_out));
  // OR_Gate or_4 has open pins: in0=IR3, in1=IRC, out=open
  ALU alu_1 (
    .X(multiplexer_8_out), .Y(multiplexer_10_out), .AluOP(\id_ex流水寄存器_1_aluop_2 ), .Equal(alu_1_equal),
    .Result({alu_1_result, lessthen}));  // open: Result_2, out_4, out_6
  assign and_2_out = {alu_1_result, lessthen} & 32'hfffffffe;  // AND_Gate and_2, 32 bits wide
  and and_3 (and_3_out, bltu, lessthen);
  and and_4 (and_4_out, alu_1_equal, \id_ex流水寄存器_1_beq_2 );
  and and_5 (and_5_out, ~alu_1_equal, \id_ex流水寄存器_1_bne_2 );  // AND_Gate
  Comparator #(.width(32), .mode("unsigned")) comparator_2 (
    .a(32'h22), .b(multiplexer_8_out), .eq(Ex_ec_eq));  // open: gt, lt
  Adder #(.width(32)) adder_2 (.a(shifter_1_out), .b(EX_PC), .out(adder_2_out));  // open: cin, cout
  or or_5 (PCSrc, and_3_out, and_4_out, and_5_out, \id_ex流水寄存器_1_jal_2 );
  or or_6 (Branch, and_3_out, and_4_out, and_5_out, \id_ex流水寄存器_1_jal_2 , EX_JALR);
  \EX_MEM流水寄存器  \ex_mem流水寄存器_1  (
    .W_num(EX_W_num), .W_num_2(MEM_W_num), .PC(EX_PC), .PC_2(M_PC), .PC_4(\id_ex流水寄存器_1_pc_4_2 ),
    .PC_4_2(\ex_mem流水寄存器_1_pc_4_2 ), .CLK(CLK), .\EN使能端 (halt), .lt(lessthen), .PC_offset(adder_2_out),
    .PC_offset_2(\ex_mem流水寄存器_1_pc_offset_2 ), .result({alu_1_result, lessthen}),
    .result_2(\ex_mem流水寄存器_1_result_2 ), .address(alu_1_result[11:2]), .address_2(\ex_mem流水寄存器_1_address_2 ),
    .ecall(\id_ex流水寄存器_1_ecall_2 ), .ecall_2(\ex_mem流水寄存器_1_ecall_2 ), .jal(\id_ex流水寄存器_1_jal_2 ),
    .jal_2(\ex_mem流水寄存器_1_jal_2 ), .jalr(EX_JALR), .jalr_2(\ex_mem流水寄存器_1_jalr_2 ),
    .MemToReg(\id_ex流水寄存器_1_memtoreg_2 ), .MemToReg_2(\ex_mem流水寄存器_1_memtoreg_2 ),
    .MemWrite(\id_ex流水寄存器_1_memwrite_2 ), .MemWrite_2(MemWrite), .RegWrite(\id_ex流水寄存器_1_regwrite_2 ),
    .RegWrite_2(\ex_mem流水寄存器_1_regwrite_2 ), .sb(\id_ex流水寄存器_1_sb_2 ), .sb_2(sb_star), .R2(EX_ec_out),
    .R2_2(\ex_mem流水寄存器_1_r2_2 ), .bltu(bltu), .bltu_2(\ex_mem流水寄存器_1_bltu_2 ), .IR(EX_IR), .IR_2(MEM_IR),
    .ec_eq(Ex_ec_eq), .ec_eq_2(\ex_mem流水寄存器_1_ec_eq_2 ), .ec_out(EX_ec_out),
    .ec_out_2(\ex_mem流水寄存器_1_ec_out_2 ));  // open: 同步清零_高电平有效, lt_2, uret, uret_2, Beq, Beq_2, Bne, Bne_2, clearI, clearI_2, setI, ecall_3, sll, sll_2, halt, halt_2
  \sb分线  \sb分线_1  (
    .\new (\ex_mem流水寄存器_1_r2_2 [7:0]), .Address(\ex_mem流水寄存器_1_result_2 [1:0]), .\output (\sb分线_1_output ),
    .origin(ram_1_data));
  Multiplexer #(.select(1), .width(32), .disabled("Z"), .enable("false")) multiplexer_11 (
    .in0(\ex_mem流水寄存器_1_r2_2 ), .in1(\sb分线_1_output ), .out(MDin), .sel(sb_star));
  RAM #(.addrWidth(10), .dataWidth(32), .bus("separate"), .Select("high")) ram_1 (
    .addr(\ex_mem流水寄存器_1_address_2 ), .din(MDin), .data(ram_1_data), .str(MemWrite), .clk(CLK), .ld(1'b1));  // open: sel, clr
  \MEM_WB流水寄存器  \mem_wb流水寄存器_1  (
    .W_num(MEM_W_num), .W_num_2(\mem_wb流水寄存器_1_w_num_2 ), .PC(M_PC), .PC_2(WB_PC),
    .PC_4(\ex_mem流水寄存器_1_pc_4_2 ), .PC_4_2(\mem_wb流水寄存器_1_pc_4_2 ), .CLK(CLK), .\EN使能端 (halt),
    .RegWrite(\ex_mem流水寄存器_1_regwrite_2 ), .RegWrite_2(RegWrite), .MemToReg(\ex_mem流水寄存器_1_memtoreg_2 ),
    .MemToReg_2(\mem_wb流水寄存器_1_memtoreg_2 ), .jalr(\ex_mem流水寄存器_1_jalr_2 ), .jalr_2(JALR_star),
    .jal(\ex_mem流水寄存器_1_jal_2 ), .jal_2(JAL_star), .ecall(\ex_mem流水寄存器_1_ecall_2 ), .ecall_2(ecall_star),
    .Result(\ex_mem流水寄存器_1_result_2 ), .Result_2(\mem_wb流水寄存器_1_result_2 ), .Mem(ram_1_data),
    .Mem_3(\mem_wb流水寄存器_1_mem_3 ), .PC_offset(\ex_mem流水寄存器_1_pc_offset_2 ), .bltu(\ex_mem流水寄存器_1_bltu_2 ),
    .IR(MEM_IR), .Mem_2(WB_IR), .ec_out(\ex_mem流水寄存器_1_ec_out_2 ), .ec_out_2(ec_out),
    .ec_eq(\ex_mem流水寄存器_1_ec_eq_2 ), .ec_eq_2(ec_eq));  // open: 同步清零_高电平有效, lt, lt_2, PC_offset_2, bltu_2, uret, uret_2, Beq, Beq_2, Bne, Bne_2, clearI, clearI_2, setI, setI_2, sll, sll_2, halt, halt_2
  Multiplexer #(.select(1), .width(32), .disabled("Z"), .enable("false")) multiplexer_12 (
    .in0(\mem_wb流水寄存器_1_result_2 ), .in1(\mem_wb流水寄存器_1_mem_3 ), .out(multiplexer_12_out),
    .sel(\mem_wb流水寄存器_1_memtoreg_2 ));
  or or_7 (J, JAL_star, JALR_star);
  and and_6 (and_6_out, ecall_star, ~ec_eq);  // AND_Gate
  Register #(.width(32), .trigger("rising"), .Select("low")) register_1 (
    .D(ec_out), .en(and_7_out), .Q(LedData), .clk(CLK));  // open: clr
  and and_7 (and_7_out, ec_eq, ecall_star);
  D_Flip_Flop #(.trigger("high"), .Pre_Clr_Positions("LEGACY"), .NegatePresetClear("false"), .enable("true"), .NewFFLayout("false")) d_ff_2 (
    .clk(CLK), .D(and_6_out), .Q(halt), .reset(Go));  // open: Qn, preset, en
  or or_8 (or_8_out, register_7_q, RST);
  or or_9 (w1, register_7_q, register_2_q);
  or or_10 (or_10_out, register_8_q, RST);
  or or_11 (w2, register_8_q, register_3_q);
  or or_12 (or_12_out, register_9_q, RST);
  or or_13 (w3, register_9_q, register_4_q);
  Register #(.width(1), .trigger("rising"), .Select("low")) register_2 (
    .D(1'b1), .Q(register_2_q), .clk(IR1_t), .clr(or_8_out));  // open: en
  Register #(.width(1), .trigger("rising"), .Select("low")) register_3 (
    .D(1'b1), .Q(register_3_q), .clk(IR2_t), .clr(or_10_out));  // open: en
  Register #(.width(1), .trigger("rising"), .Select("low")) register_4 (
    .D(1'b1), .Q(register_4_q), .clk(IR3_t), .clr(or_12_out));  // open: en
  Register #(.width(2), .trigger("rising"), .Select("low")) register_5 (
    .D(\中断号 ), .en(INT), .Q(register_5_q), .clk(CLK), .clr(RST));
  Register #(.width(32), .trigger("rising"), .Select("low")) register_6 (
    .D(\原地址 ), .en(INT), .Q(RET_PC), .clk(CLK), .clr(RST));
  Comparator #(.width(16), .mode("twosComplement")) comparator_3 (
    .a(16'h23b), .b(\总周期数 ), .eq(comparator_3_eq));  // open: gt, lt
  Comparator #(.width(16), .mode("twosComplement")) comparator_4 (
    .a(\总周期数 ), .b(16'h1), .eq(comparator_4_eq));  // open: gt, lt
  Comparator #(.width(16), .mode("twosComplement")) comparator_5 (
    .a(\总周期数 ), .b(16'h4), .eq(comparator_5_eq));  // open: gt, lt
  Comparator #(.width(16), .mode("twosComplement")) comparator_6 (
    .a(\总周期数 ), .b(16'h7), .eq(comparator_6_eq));  // open: gt, lt
  or or_14 (or_14_out, register_2_q, register_7_q);
  and and_8 (and_8_out, or_14_out, ~clear1);  // AND_Gate
  or or_15 (or_15_out, register_3_q, register_8_q);
  and and_9 (and_9_out, or_15_out, ~clear2);  // AND_Gate
  or or_16 (or_16_out, register_4_q, register_9_q);
  and and_10 (and_10_out, or_16_out, ~clear3);  // AND_Gate
  and and_11 (INT, IE, \中断信号 );
  Decoder #(.select(2), .tristate("false"), .disabled("Z"), .enable("false")) decoder_1 (
    .out1(decoder_1_out1), .out2(decoder_1_out2), .out3(decoder_1_out3), .sel(register_5_q));  // open: out0
  or or_17 (or_17_out, comparator_3_eq, comparator_4_eq);
  Pull_Resistor #(.pull(0)) pull_resistor_2 (.node(IRA));
  assign IRA = or_17_out ? ~CLK : 1'bz;  // Controlled_Inverter controlled_inverter_1
  Pull_Resistor #(.pull(0)) pull_resistor_3 (.node(IRB));
  assign IRB = comparator_5_eq ? ~CLK : 1'bz;  // Controlled_Inverter controlled_inverter_2
  Pull_Resistor #(.pull(0)) pull_resistor_4 (.node(IRC));
  assign IRC = comparator_6_eq ? ~CLK : 1'bz;  // Controlled_Inverter controlled_inverter_3
  Register #(.width(1), .trigger("rising"), .Select("low")) register_7 (
    .D(and_8_out), .Q(register_7_q), .clk(CLK), .clr(RST));  // open: en
  Register #(.width(1), .trigger("rising"), .Select("low")) register_8 (
    .D(and_9_out), .Q(register_8_q), .clk(CLK), .clr(RST));  // open: en
  Register #(.width(1), .trigger("rising"), .Select("low")) register_9 (
    .D(and_10_out), .Q(register_9_q), .clk(CLK), .clr(RST));  // open: en
  and and_12 (clear1, decoder_1_out1, URET);
  and and_13 (clear2, decoder_1_out2, URET);
  and and_14 (clear3, decoder_1_out3, URET);
  Priority_Encoder #(.select(2), .disabled("Z")) priority_encoder_1 (
    .in1(register_7_q), .in2(register_8_q), .in3(register_9_q), .out(\中断号 ), .gs(\中断信号 ));  // open: in0, en_out, en_in
  and and_15 (and_15_out, ~URET, \中断信号 );  // AND_Gate
  Button button_1 (.out(RST));
  Multiplexer #(.select(2), .width(32), .disabled("Z"), .enable("false")) multiplexer_13 (
    .in1(32'h30ac), .in2(32'h3150), .in3(32'h31f4), .out(INT_PC), .sel(\中断号 ));  // open: in0
  D_Flip_Flop #(.trigger("rising"), .Pre_Clr_Positions("LEGACY"), .NegatePresetClear("false"), .enable("true"), .NewFFLayout("false")) d_ff_3 (
    .clk(CLK), .D(and_15_out), .Qn(IE));  // open: Q, preset, en, reset

  // Other names for the same wires on the sheet: IR[31:0] = ID_IR; MEM_PC[31:0] = M_PC

  // Notes on the sheet:
  //   中断源
  //   时空图监测，可删除
  //   中断等待指示
  //   数码管输出
  //   指令存储器
  //   指令字
  //   contents of rom_1 (hex, n*v repeats v):
  //   7d000113 100413 1f41993 41f9d993 433 c00913 800b13 140413 f47413 800293 100313 499993 89e9b3 1300533
  //   2200893 73 406282b3 fe0294e3 140413 f00f93 1f47433 1c41413 800293 100313 49d993 89e9b3 1300533
  //   2200893 73 406282b3 fe0294e3 1c45413 406b0b33 b0463 f95ff06f 2b3 fff2c293 1029293 fff2e293 500533
  //   2200893 73 f5dff06f 1112023 410113 a12023 410113 812023 410113 1312023 410113 1412023 410113 1512023
  //   410113 1612023 410113 100b13 300a13 100a93 1600433 441413 14469b3 1300533 2200893 73 fe0416e3
  //   415a0a33 fe0a10e3 ffc10113 12b03 ffc10113 12a83 ffc10113 12a03 ffc10113 12983 ffc10113 12403
  //   ffc10113 12503 ffc10113 12883 200073 1112023 410113 a12023 410113 812023 410113 1312023 410113
  //   1412023 410113 1512023 410113 1612023 410113 200b13 300a13 100a93 1600433 441413 14469b3 1300533
  //   2200893 73 fe0416e3 415a0a33 fe0a10e3 ffc10113 12b03 ffc10113 12a83 ffc10113 12a03 ffc10113 12983
  //   ffc10113 12403 ffc10113 12503 ffc10113 12883 200073 1112023 410113 a12023 410113 812023 410113
  //   1312023 410113 1412023 410113 1512023 410113 1612023 410113 300b13 300a13 100a93 1600433 441413
  //   14469b3 1300533 2200893 73 fe0416e3 415a0a33 fe0a10e3 ffc10113 12b03 ffc10113 12a83 ffc10113 12a03
  //   ffc10113 12983 ffc10113 12403 ffc10113 12503 ffc10113 12883 200073
  //   指令探针
  //   控制位
  //   JAL
  //   JALR
  //   I
  //   B
  //   流水调试日志用
  //   暂停节拍，不能为0
  //   URET
  //   戳工具置1进入计数暂停模式，ctrl+k时钟自动运行到对应节拍暂停
  //   ctrl+k关闭时钟连续运行，将控制位置零，进入单步调试模式调试
  //   可计数暂停的时钟源
  //   ecall
  //   jal
  //   jalr
  //   uret
  //   Beq
  //   Bne
  //   MemToReg
  //   MemWrite
  //   AluOP
  //   Alu_Src
  //   RegWrite
  //   sb
  //   clearI
  //   setI
  //   sll
  //   sll指令输入线
  //   立即数
  //   写入信号
  //   PC+4
  //   为方便自动评测，需要输出流水线各段保存的PC值，注意是PC不是PC+4，另外ID段寄存器写入信息，Mem段内存写入信息也要输出
  //   ecall
  //   jal
  //   jalr
  //   MemToReg
  //   MemWrite
  //   RegWrite
  //   写入信号
  //   PC+4
  //   jal
  //   jalr
  //   MemToReg
  //   RegWrite
  //   数据存储器
  //   ecall
  //   R2*
  //   Result
  //   Mem
  //   lessthen
  //   写入信号
  //   PC+4
  //   单级中断测试信号模拟器
endmodule

// BTB
module \BTB表  (
  input  [31:0] PC,
  input  [31:0] Ex_BranchAddr,
  input  CLK,
  input  [31:0] Ex_PC,
  input  EX_Branch,
  input  EX_BranchTaken,
  output [31:0] JumpAddr,
  output PredictJump
);

  wire and_17_out, and_19_out, and_27_out, and_28_out, and_29_out, and_30_out, and_31_out, and_32_out,
       and_33_out, and_34_out, comparator_1_eq, comparator_2_eq, comparator_3_eq, comparator_4_eq,
       comparator_5_eq, comparator_6_eq, comparator_7_eq, comparator_8_eq, comparator_9_eq, comparator_10_eq,
       comparator_11_eq, comparator_12_eq, comparator_13_eq, comparator_14_eq, comparator_15_eq,
       comparator_16_eq, d_ff_1_q, d_ff_2_q, d_ff_3_q, d_ff_4_q, d_ff_5_q, d_ff_6_q, d_ff_7_q, d_ff_8_q,
       decoder_1_out0, decoder_1_out1, decoder_1_out2, decoder_1_out3, decoder_1_out4, decoder_1_out5,
       decoder_1_out6, decoder_1_out7, decoder_2_out0, decoder_2_out1, decoder_2_out2, decoder_2_out3,
       decoder_2_out4, decoder_2_out5, decoder_2_out6, decoder_2_out7, Load1, Load2, Load3, Load4, Load5,
       Load6, Load7, Load8, Miss_EX, not_1_out, not_2_out, not_3_out, not_4_out, not_5_out, not_6_out,
       not_7_out, not_8_out, or_1_out, or_2_out, or_3_out, or_4_out, or_5_out, or_6_out, or_7_out, or_8_out,
       or_9_out, or_10_out, or_11_out, or_12_out, or_13_out, or_14_out, or_15_out, or_16_out, or_17_out,
       store1, store2, store3, store4, store5, store6, store7, store8, undriven, undriven_2, valid1, valid2,
       valid3, valid4, valid5, valid6, valid7, valid8, write1, write2, write3, write4, write5, write6,
       write7, write8;
  wire [0:0] controlled_buffer_9_out, controlled_buffer_10_out, controlled_buffer_11_out,
       controlled_buffer_12_out, controlled_buffer_13_out, controlled_buffer_14_out,
       controlled_buffer_15_out, controlled_buffer_16_out;
  wire [1:0] predict1, predict2, predict3, predict4, predict5, predict6, predict7, predict8,
       \预测跳转逻辑_1_nextlow , \预测跳转逻辑_2_nextlow , \预测跳转逻辑_3_nextlow , \预测跳转逻辑_4_nextlow , \预测跳转逻辑_5_nextlow ,
       \预测跳转逻辑_6_nextlow , \预测跳转逻辑_7_nextlow , \预测跳转逻辑_8_nextlow ;
  wire [2:0] multiplexer_1_out, priority_encoder_1_out, \并行比较max_1_max_num , \并行比较max_2_max_num ,
       \并行比较max_3_max_num , \并行比较max_4_max_num , \并行比较max_5_max_num , \并行比较max_6_max_num ,
       \并行比较max_7_max_num ;
  wire [7:0] counter_9_q, counter_10_q;
  wire [15:0] count1, count2, count3, count4, count5, count6, count7, count8, \并行比较max_1_max ,
       \并行比较max_2_max , \并行比较max_3_max , \并行比较max_4_max , \并行比较max_5_max , \并行比较max_6_max ;
  wire [31:0] BranchAddr1, BranchAddr2, BranchAddr3, BranchAddr4, BranchAddr5, BranchAddr6, BranchAddr7,
       BranchAddr8, register_25_q, register_26_q, register_27_q, register_28_q, register_29_q, register_30_q,
       register_31_q, register_32_q;

  Register #(.width(1), .trigger("rising"), .Select("low")) register_1 (
    .D(1'b1), .en(write1), .Q(valid1), .clk(CLK));  // open: clr
  Register #(.width(1), .trigger("rising"), .Select("low")) register_2 (
    .D(1'b1), .en(write2), .Q(valid2), .clk(CLK));  // open: clr
  Register #(.width(1), .trigger("rising"), .Select("low")) register_3 (
    .D(1'b1), .en(write3), .Q(valid3), .clk(CLK));  // open: clr
  Register #(.width(1), .trigger("rising"), .Select("low")) register_4 (
    .D(1'b1), .en(write4), .Q(valid4), .clk(CLK));  // open: clr
  Register #(.width(1), .trigger("rising"), .Select("low")) register_5 (
    .D(1'b1), .en(write5), .Q(valid5), .clk(CLK));  // open: clr
  Register #(.width(1), .trigger("rising"), .Select("low")) register_6 (
    .D(1'b1), .en(write6), .Q(valid6), .clk(CLK));  // open: clr
  Register #(.width(1), .trigger("rising"), .Select("low")) register_7 (
    .D(1'b1), .en(write7), .Q(valid7), .clk(CLK));  // open: clr
  Register #(.width(1), .trigger("rising"), .Select("low")) register_8 (
    .D(1'b1), .en(write8), .Q(valid8), .clk(CLK));  // open: clr
  Register #(.width(32), .trigger("rising"), .Select("low")) register_9 (
    .D(Ex_PC), .en(write1), .Q(BranchAddr1), .clk(CLK));  // open: clr
  Register #(.width(32), .trigger("rising"), .Select("low")) register_10 (
    .D(Ex_PC), .en(write2), .Q(BranchAddr2), .clk(CLK));  // open: clr
  Register #(.width(32), .trigger("rising"), .Select("low")) register_11 (
    .D(Ex_PC), .en(write3), .Q(BranchAddr3), .clk(CLK));  // open: clr
  Register #(.width(32), .trigger("rising"), .Select("low")) register_12 (
    .D(Ex_PC), .en(write4), .Q(BranchAddr4), .clk(CLK));  // open: clr
  Register #(.width(32), .trigger("rising"), .Select("low")) register_13 (
    .D(Ex_PC), .en(write5), .Q(BranchAddr5), .clk(CLK));  // open: clr
  Register #(.width(32), .trigger("rising"), .Select("low")) register_14 (
    .D(Ex_PC), .en(write6), .Q(BranchAddr6), .clk(CLK));  // open: clr
  Register #(.width(32), .trigger("rising"), .Select("low")) register_15 (
    .D(Ex_PC), .en(write7), .Q(BranchAddr7), .clk(CLK));  // open: clr
  Register #(.width(32), .trigger("rising"), .Select("low")) register_16 (
    .D(Ex_PC), .en(write8), .Q(BranchAddr8), .clk(CLK));  // open: clr
  or or_1 (or_1_out, write1, Load1);
  or or_2 (or_2_out, write2, Load2);
  or or_3 (or_3_out, write3, Load3);
  or or_4 (or_4_out, write4, Load4);
  or or_5 (or_5_out, write5, Load5);
  or or_6 (or_6_out, write6, Load6);
  or or_7 (or_7_out, write7, Load7);
  or or_8 (or_8_out, write8, Load8);
  Counter #(.width(16), .max('hffff), .ongoal("wrap"), .trigger("rising"), .behavior("new")) counter_1 (
    .Q(count1), .clk(CLK), .clr(d_ff_1_q));  // open: load, D, count, carry, preset, down
  D_Flip_Flop #(.trigger("rising"), .Pre_Clr_Positions("LEGACY"), .NegatePresetClear("false"), .enable("true"), .NewFFLayout("false")) d_ff_1 (
    .clk(CLK), .D(or_1_out), .Q(d_ff_1_q));  // open: Qn, preset, en, reset
  Counter #(.width(16), .max('hffff), .ongoal("wrap"), .trigger("rising"), .behavior("new")) counter_2 (
    .Q(count2), .clk(CLK), .clr(d_ff_2_q));  // open: load, D, count, carry, preset, down
  D_Flip_Flop #(.trigger("rising"), .Pre_Clr_Positions("LEGACY"), .NegatePresetClear("false"), .enable("true"), .NewFFLayout("false")) d_ff_2 (
    .clk(CLK), .D(or_2_out), .Q(d_ff_2_q));  // open: Qn, preset, en, reset
  Counter #(.width(16), .max('hffff), .ongoal("wrap"), .trigger("rising"), .behavior("new")) counter_3 (
    .Q(count3), .clk(CLK), .clr(d_ff_3_q));  // open: load, D, count, carry, preset, down
  D_Flip_Flop #(.trigger("rising"), .Pre_Clr_Positions("LEGACY"), .NegatePresetClear("false"), .enable("true"), .NewFFLayout("false")) d_ff_3 (
    .clk(CLK), .D(or_3_out), .Q(d_ff_3_q));  // open: Qn, preset, en, reset
  Counter #(.width(16), .max('hffff), .ongoal("wrap"), .trigger("rising"), .behavior("new")) counter_4 (
    .Q(count4), .clk(CLK), .clr(d_ff_4_q));  // open: load, D, count, carry, preset, down
  D_Flip_Flop #(.trigger("rising"), .Pre_Clr_Positions("LEGACY"), .NegatePresetClear("false"), .enable("true"), .NewFFLayout("false")) d_ff_4 (
    .clk(CLK), .D(or_4_out), .Q(d_ff_4_q));  // open: Qn, preset, en, reset
  Counter #(.width(16), .max('hffff), .ongoal("wrap"), .trigger("rising"), .behavior("new")) counter_5 (
    .Q(count5), .clk(CLK), .clr(d_ff_5_q));  // open: load, D, count, carry, preset, down
  D_Flip_Flop #(.trigger("rising"), .Pre_Clr_Positions("LEGACY"), .NegatePresetClear("false"), .enable("true"), .NewFFLayout("false")) d_ff_5 (
    .clk(CLK), .D(or_5_out), .Q(d_ff_5_q));  // open: Qn, preset, en, reset
  Counter #(.width(16), .max('hffff), .ongoal("wrap"), .trigger("rising"), .behavior("new")) counter_6 (
    .Q(count6), .clk(CLK), .clr(d_ff_6_q));  // open: load, D, count, carry, preset, down
  D_Flip_Flop #(.trigger("rising"), .Pre_Clr_Positions("LEGACY"), .NegatePresetClear("false"), .enable("true"), .NewFFLayout("false")) d_ff_6 (
    .clk(CLK), .D(or_6_out), .Q(d_ff_6_q));  // open: Qn, preset, en, reset
  Counter #(.width(16), .max('hffff), .ongoal("wrap"), .trigger("rising"), .behavior("new")) counter_7 (
    .Q(count7), .clk(CLK), .clr(d_ff_7_q));  // open: load, D, count, carry, preset, down
  D_Flip_Flop #(.trigger("rising"), .Pre_Clr_Positions("LEGACY"), .NegatePresetClear("false"), .enable("true"), .NewFFLayout("false")) d_ff_7 (
    .clk(CLK), .D(or_7_out), .Q(d_ff_7_q));  // open: Qn, preset, en, reset
  Counter #(.width(16), .max('hffff), .ongoal("wrap"), .trigger("rising"), .behavior("new")) counter_8 (
    .Q(count8), .clk(CLK), .clr(d_ff_8_q));  // open: load, D, count, carry, preset, down
  D_Flip_Flop #(.trigger("rising"), .Pre_Clr_Positions("LEGACY"), .NegatePresetClear("false"), .enable("true"), .NewFFLayout("false")) d_ff_8 (
    .clk(CLK), .D(or_8_out), .Q(d_ff_8_q));  // open: Qn, preset, en, reset
  Register #(.width(2), .trigger("rising"), .Select("low")) register_17 (.clk(CLK));  // open: D, en, Q, clr
  Register #(.width(2), .trigger("rising"), .Select("low")) register_18 (.clk(CLK));  // open: D, en, Q, clr
  Register #(.width(2), .trigger("rising"), .Select("low")) register_19 (.clk(CLK));  // open: D, en, Q, clr
  Register #(.width(2), .trigger("rising"), .Select("low")) register_20 (.clk(CLK));  // open: D, en, Q, clr
  Register #(.width(2), .trigger("rising"), .Select("low")) register_21 (.clk(CLK));  // open: D, en, Q, clr
  Register #(.width(2), .trigger("rising"), .Select("low")) register_22 (.clk(CLK));  // open: D, en, Q, clr
  Register #(.width(2), .trigger("rising"), .Select("low")) register_23 (.clk(CLK));  // open: D, en, Q, clr
  Register #(.width(2), .trigger("rising"), .Select("low")) register_24 (.clk(CLK));  // open: D, en, Q, clr
  Register #(.width(32), .trigger("rising"), .Select("low")) register_25 (
    .D(Ex_BranchAddr), .en(write1), .Q(register_25_q), .clk(CLK));  // open: clr
  Register #(.width(32), .trigger("rising"), .Select("low")) register_26 (
    .D(Ex_BranchAddr), .en(write2), .Q(register_26_q), .clk(CLK));  // open: clr
  Register #(.width(32), .trigger("rising"), .Select("low")) register_27 (
    .D(Ex_BranchAddr), .en(write3), .Q(register_27_q), .clk(CLK));  // open: clr
  Register #(.width(32), .trigger("rising"), .Select("low")) register_28 (
    .D(Ex_BranchAddr), .en(write4), .Q(register_28_q), .clk(CLK));  // open: clr
  Register #(.width(32), .trigger("rising"), .Select("low")) register_29 (
    .D(Ex_BranchAddr), .en(write5), .Q(register_29_q), .clk(CLK));  // open: clr
  Register #(.width(32), .trigger("rising"), .Select("low")) register_30 (
    .D(Ex_BranchAddr), .en(write6), .Q(register_30_q), .clk(CLK));  // open: clr
  Register #(.width(32), .trigger("rising"), .Select("low")) register_31 (
    .D(Ex_BranchAddr), .en(write7), .Q(register_31_q), .clk(CLK));  // open: clr
  Register #(.width(32), .trigger("rising"), .Select("low")) register_32 (
    .D(Ex_BranchAddr), .en(write8), .Q(register_32_q), .clk(CLK));  // open: clr
  assign JumpAddr = Load1 ? register_25_q : 32'bz;  // Controlled_Buffer controlled_buffer_1
  assign JumpAddr = Load2 ? register_26_q : 32'bz;  // Controlled_Buffer controlled_buffer_2
  assign JumpAddr = Load3 ? register_27_q : 32'bz;  // Controlled_Buffer controlled_buffer_3
  assign JumpAddr = Load4 ? register_28_q : 32'bz;  // Controlled_Buffer controlled_buffer_4
  assign JumpAddr = Load5 ? register_29_q : 32'bz;  // Controlled_Buffer controlled_buffer_5
  assign JumpAddr = Load6 ? register_30_q : 32'bz;  // Controlled_Buffer controlled_buffer_6
  assign JumpAddr = Load7 ? register_31_q : 32'bz;  // Controlled_Buffer controlled_buffer_7
  assign JumpAddr = Load8 ? register_32_q : 32'bz;  // Controlled_Buffer controlled_buffer_8
  Comparator #(.width(32), .mode("unsigned")) comparator_1 (
    .a(BranchAddr1), .b(PC), .eq(comparator_1_eq));  // open: gt, lt
  Comparator #(.width(32), .mode("unsigned")) comparator_2 (
    .a(BranchAddr2), .b(PC), .eq(comparator_2_eq));  // open: gt, lt
  Comparator #(.width(32), .mode("unsigned")) comparator_3 (
    .a(BranchAddr3), .b(PC), .eq(comparator_3_eq));  // open: gt, lt
  Comparator #(.width(32), .mode("unsigned")) comparator_4 (
    .a(BranchAddr4), .b(PC), .eq(comparator_4_eq));  // open: gt, lt
  Comparator #(.width(32), .mode("unsigned")) comparator_5 (
    .a(BranchAddr5), .b(PC), .eq(comparator_5_eq));  // open: gt, lt
  Comparator #(.width(32), .mode("unsigned")) comparator_6 (
    .a(BranchAddr6), .b(PC), .eq(comparator_6_eq));  // open: gt, lt
  Comparator #(.width(32), .mode("unsigned")) comparator_7 (
    .a(BranchAddr7), .b(PC), .eq(comparator_7_eq));  // open: gt, lt
  Comparator #(.width(32), .mode("unsigned")) comparator_8 (
    .a(BranchAddr8), .b(PC), .eq(comparator_8_eq));  // open: gt, lt
  Comparator #(.width(32), .mode("unsigned")) comparator_9 (
    .a(BranchAddr1), .b(Ex_PC), .eq(comparator_9_eq));  // open: gt, lt
  Comparator #(.width(32), .mode("unsigned")) comparator_10 (
    .a(BranchAddr2), .b(Ex_PC), .eq(comparator_10_eq));  // open: gt, lt
  Comparator #(.width(32), .mode("unsigned")) comparator_11 (
    .a(BranchAddr3), .b(Ex_PC), .eq(comparator_11_eq));  // open: gt, lt
  Comparator #(.width(32), .mode("unsigned")) comparator_12 (
    .a(BranchAddr4), .b(Ex_PC), .eq(comparator_12_eq));  // open: gt, lt
  Comparator #(.width(32), .mode("unsigned")) comparator_13 (
    .a(BranchAddr5), .b(Ex_PC), .eq(comparator_13_eq));  // open: gt, lt
  Comparator #(.width(32), .mode("unsigned")) comparator_14 (
    .a(BranchAddr6), .b(Ex_PC), .eq(comparator_14_eq));  // open: gt, lt
  Comparator #(.width(32), .mode("unsigned")) comparator_15 (
    .a(BranchAddr7), .b(Ex_PC), .eq(comparator_15_eq));  // open: gt, lt
  Comparator #(.width(32), .mode("unsigned")) comparator_16 (
    .a(BranchAddr8), .b(Ex_PC), .eq(comparator_16_eq));  // open: gt, lt
  and and_1 (Load1, valid1, comparator_1_eq);
  and and_2 (Load2, valid2, comparator_2_eq);
  and and_3 (Load3, valid3, comparator_3_eq);
  and and_4 (Load4, valid4, comparator_4_eq);
  and and_5 (Load5, valid5, comparator_5_eq);
  and and_6 (Load6, valid6, comparator_6_eq);
  and and_7 (Load7, valid7, comparator_7_eq);
  and and_8 (Load8, valid8, comparator_8_eq);
  and and_9 (store1, valid1, comparator_9_eq);
  and and_10 (store2, valid2, comparator_10_eq);
  and and_11 (store3, valid3, comparator_11_eq);
  and and_12 (store4, valid4, comparator_12_eq);
  and and_13 (store5, valid5, comparator_13_eq);
  and and_14 (store6, valid6, comparator_14_eq);
  and and_15 (store7, valid7, comparator_15_eq);
  and and_16 (store8, valid8, comparator_16_eq);
  or or_9 (or_9_out, Load1, Load2, Load3, Load4, Load5, Load6, Load7, Load8);
  // Probe on counter_9_q
  Counter #(.width(8), .max('hff), .ongoal("wrap"), .trigger("rising"), .behavior("new")) counter_9 (
    .Q(counter_9_q), .clk(or_9_out));  // open: load, D, count, carry, clr, preset, down
  nor nor_1 (Miss_EX, store1, store2, store3, store4, store5, store6, store7, store8);
  Counter #(.width(8), .max('hff), .ongoal("wrap"), .trigger("rising"), .behavior("new")) counter_10 (
    .Q(counter_10_q), .clk(Miss_EX));  // open: load, D, count, carry, clr, preset, down
  \并行比较MAX  \u_并行比较max_1  (
    .X(count1), .Y(count2), .Y_num(3'b001), .X_num(3'b000), .MAX(\并行比较max_1_max ),
    .MAX_num(\并行比较max_1_max_num ));
  \并行比较MAX  \u_并行比较max_2  (
    .X(count3), .Y(count4), .Y_num(3'b011), .X_num(3'b010), .MAX(\并行比较max_2_max ),
    .MAX_num(\并行比较max_2_max_num ));
  \并行比较MAX  \u_并行比较max_3  (
    .X(count5), .Y(count6), .Y_num(3'b101), .X_num(3'b100), .MAX(\并行比较max_3_max ),
    .MAX_num(\并行比较max_3_max_num ));
  \并行比较MAX  \u_并行比较max_4  (
    .X(count7), .Y(count8), .Y_num(3'b111), .X_num(3'b110), .MAX(\并行比较max_4_max ),
    .MAX_num(\并行比较max_4_max_num ));
  // Probe on counter_10_q
  \并行比较MAX  \u_并行比较max_5  (
    .X(\并行比较max_1_max ), .Y(\并行比较max_2_max ), .Y_num(\并行比较max_2_max_num ), .X_num(\并行比较max_1_max_num ),
    .MAX(\并行比较max_5_max ), .MAX_num(\并行比较max_5_max_num ));
  \并行比较MAX  \u_并行比较max_6  (
    .X(\并行比较max_3_max ), .Y(\并行比较max_4_max ), .Y_num(\并行比较max_4_max_num ), .X_num(\并行比较max_3_max_num ),
    .MAX(\并行比较max_6_max ), .MAX_num(\并行比较max_6_max_num ));
  and and_17 (and_17_out, valid1, valid2, valid3, valid4, valid5, valid6, valid7, valid8);
  not not_1 (not_1_out, valid1);
  not not_2 (not_2_out, valid2);
  not not_3 (not_3_out, valid3);
  not not_4 (not_4_out, valid4);
  not not_5 (not_5_out, valid5);
  not not_6 (not_6_out, valid6);
  not not_7 (not_7_out, valid7);
  not not_8 (not_8_out, valid8);
  \并行比较MAX  \u_并行比较max_7  (
    .X(\并行比较max_5_max ), .Y(\并行比较max_6_max ), .Y_num(\并行比较max_6_max_num ), .X_num(\并行比较max_5_max_num ),
    .MAX_num(\并行比较max_7_max_num ));  // open: MAX
  Priority_Encoder #(.select(3), .disabled("Z")) priority_encoder_1 (
    .in0(not_1_out), .in1(not_2_out), .in2(not_3_out), .in3(not_4_out), .in4(not_5_out), .in5(not_6_out),
    .in6(not_7_out), .in7(not_8_out), .out(priority_encoder_1_out), .en_out(and_17_out));  // open: gs, en_in
  Decoder #(.select(3), .tristate("false"), .disabled("Z"), .enable("true")) decoder_1 (
    .out0(decoder_1_out0), .out1(decoder_1_out1), .out2(decoder_1_out2), .out3(decoder_1_out3),
    .out4(decoder_1_out4), .out5(decoder_1_out5), .out6(decoder_1_out6), .out7(decoder_1_out7));  // open: sel, en
  Decoder #(.select(3), .tristate("false"), .disabled("Z"), .enable("true")) decoder_2 (
    .out0(decoder_2_out0), .out1(decoder_2_out1), .out2(decoder_2_out2), .out3(decoder_2_out3),
    .out4(decoder_2_out4), .out5(decoder_2_out5), .out6(decoder_2_out6), .out7(decoder_2_out7));  // open: sel, en
  or or_10 (or_10_out, decoder_2_out0, decoder_1_out0);
  // AND_Gate and_18 has open pins: in0=or_10_out, in1=undriven_2, in2=undriven, out=open
  and and_19 (and_19_out, EX_Branch, Miss_EX);
  Demultiplexer #(.select(3), .width(1), .tristate("false"), .disabled("Z"), .enable("false")) demultiplexer_1 (
    .out0(write1), .out1(write2), .out2(write3), .out3(write4), .out4(write5), .out5(write6), .out6(write7),
    .out7(write8), .in(and_19_out), .sel(multiplexer_1_out));
  Multiplexer #(.select(1), .width(3), .disabled("Z"), .enable("false")) multiplexer_1 (
    .in0(priority_encoder_1_out), .in1(\并行比较max_7_max_num ), .out(multiplexer_1_out), .sel(and_17_out));
  or or_11 (or_11_out, decoder_2_out1, decoder_1_out1);
  // AND_Gate and_20 has open pins: in0=or_11_out, in1=undriven_2, in2=undriven, out=open
  or or_12 (or_12_out, decoder_2_out3, decoder_1_out3);
  or or_13 (or_13_out, decoder_2_out2, decoder_1_out2);
  // AND_Gate and_21 has open pins: in0=or_13_out, in1=undriven_2, in2=undriven, out=open
  or or_14 (or_14_out, decoder_2_out4, decoder_1_out4);
  // AND_Gate and_22 has open pins: in0=or_12_out, in1=undriven_2, in2=undriven, out=open
  // AND_Gate and_23 has open pins: in0=or_14_out, in1=undriven_2, in2=undriven, out=open
  or or_15 (or_15_out, decoder_2_out5, decoder_1_out5);
  // AND_Gate and_24 has open pins: in0=or_15_out, in1=undriven_2, in2=undriven, out=open
  or or_16 (or_16_out, decoder_2_out6, decoder_1_out6);
  or or_17 (or_17_out, decoder_2_out7, decoder_1_out7);
  // AND_Gate and_25 has open pins: in0=or_16_out, in1=undriven_2, in2=undriven, out=open
  // AND_Gate and_26 has open pins: in0=or_17_out, in1=undriven_2, in2=undriven, out=open
  \预测跳转逻辑  \u_预测跳转逻辑_1  (
    .High(predict1[1]), .Low(predict1[0]), .Jump(EX_BranchTaken), .NextHigh(\预测跳转逻辑_1_nextlow [1]),
    .NextLow(\预测跳转逻辑_1_nextlow [0]));
  and and_27 (and_27_out, EX_Branch, store1);
  \预测跳转逻辑  \u_预测跳转逻辑_2  (
    .High(predict2[1]), .Low(predict2[0]), .Jump(EX_BranchTaken), .NextHigh(\预测跳转逻辑_2_nextlow [1]),
    .NextLow(\预测跳转逻辑_2_nextlow [0]));
  and and_28 (and_28_out, EX_Branch, store2);
  \预测跳转逻辑  \u_预测跳转逻辑_3  (
    .High(predict3[1]), .Low(predict3[0]), .Jump(EX_BranchTaken), .NextHigh(\预测跳转逻辑_3_nextlow [1]),
    .NextLow(\预测跳转逻辑_3_nextlow [0]));
  and and_29 (and_29_out, EX_Branch, store3);
  \预测跳转逻辑  \u_预测跳转逻辑_4  (
    .High(predict4[1]), .Low(predict4[0]), .Jump(EX_BranchTaken), .NextHigh(\预测跳转逻辑_4_nextlow [1]),
    .NextLow(\预测跳转逻辑_4_nextlow [0]));
  and and_30 (and_30_out, EX_Branch, store4);
  \预测跳转逻辑  \u_预测跳转逻辑_5  (
    .High(predict5[1]), .Low(predict5[0]), .Jump(EX_BranchTaken), .NextHigh(\预测跳转逻辑_5_nextlow [1]),
    .NextLow(\预测跳转逻辑_5_nextlow [0]));
  and and_31 (and_31_out, EX_Branch, store5);
  \预测跳转逻辑  \u_预测跳转逻辑_6  (
    .High(predict6[1]), .Low(predict6[0]), .Jump(EX_BranchTaken), .NextHigh(\预测跳转逻辑_6_nextlow [1]),
    .NextLow(\预测跳转逻辑_6_nextlow [0]));
  and and_32 (and_32_out, EX_Branch, store6);
  \预测跳转逻辑  \u_预测跳转逻辑_7  (
    .High(predict7[1]), .Low(predict7[0]), .Jump(EX_BranchTaken), .NextHigh(\预测跳转逻辑_7_nextlow [1]),
    .NextLow(\预测跳转逻辑_7_nextlow [0]));
  and and_33 (and_33_out, EX_Branch, store7);
  \预测跳转逻辑  \u_预测跳转逻辑_8  (
    .High(predict8[1]), .Low(predict8[0]), .Jump(EX_BranchTaken), .NextHigh(\预测跳转逻辑_8_nextlow [1]),
    .NextLow(\预测跳转逻辑_8_nextlow [0]));
  and and_34 (and_34_out, EX_Branch, store8);
  Register #(.width(2), .trigger("rising"), .Select("low")) register_33 (
    .D(\预测跳转逻辑_1_nextlow ), .en(and_27_out), .Q(predict1), .clk(CLK));  // open: clr
  Register #(.width(2), .trigger("rising"), .Select("low")) register_34 (
    .D(\预测跳转逻辑_2_nextlow ), .en(and_28_out), .Q(predict2), .clk(CLK));  // open: clr
  Register #(.width(2), .trigger("rising"), .Select("low")) register_35 (
    .D(\预测跳转逻辑_3_nextlow ), .en(and_29_out), .Q(predict3), .clk(CLK));  // open: clr
  Register #(.width(2), .trigger("rising"), .Select("low")) register_36 (
    .D(\预测跳转逻辑_4_nextlow ), .en(and_30_out), .Q(predict4), .clk(CLK));  // open: clr
  Register #(.width(2), .trigger("rising"), .Select("low")) register_37 (
    .D(\预测跳转逻辑_5_nextlow ), .en(and_31_out), .Q(predict5), .clk(CLK));  // open: clr
  Register #(.width(2), .trigger("rising"), .Select("low")) register_38 (
    .D(\预测跳转逻辑_6_nextlow ), .en(and_32_out), .Q(predict6), .clk(CLK));  // open: clr
  Register #(.width(2), .trigger("rising"), .Select("low")) register_39 (
    .D(\预测跳转逻辑_7_nextlow ), .en(and_33_out), .Q(predict7), .clk(CLK));  // open: clr
  Register #(.width(2), .trigger("rising"), .Select("low")) register_40 (
    .D(\预测跳转逻辑_8_nextlow ), .en(and_34_out), .Q(predict8), .clk(CLK));  // open: clr
  assign {PredictJump, controlled_buffer_9_out[0]} = Load1 ? predict1 : 2'bz;  // Controlled_Buffer controlled_buffer_9
  assign {PredictJump, controlled_buffer_10_out[0]} = Load2 ? predict2 : 2'bz;  // Controlled_Buffer controlled_buffer_10
  assign {PredictJump, controlled_buffer_11_out[0]} = Load3 ? predict3 : 2'bz;  // Controlled_Buffer controlled_buffer_11
  assign {PredictJump, controlled_buffer_12_out[0]} = Load4 ? predict4 : 2'bz;  // Controlled_Buffer controlled_buffer_12
  assign {PredictJump, controlled_buffer_13_out[0]} = Load5 ? predict5 : 2'bz;  // Controlled_Buffer controlled_buffer_13
  assign {PredictJump, controlled_buffer_14_out[0]} = Load6 ? predict6 : 2'bz;  // Controlled_Buffer controlled_buffer_14
  assign {PredictJump, controlled_buffer_15_out[0]} = Load7 ? predict7 : 2'bz;  // Controlled_Buffer controlled_buffer_15
  assign {PredictJump, controlled_buffer_16_out[0]} = Load8 ? predict8 : 2'bz;  // Controlled_Buffer controlled_buffer_16
  Pull_Resistor #(.pull(0)) pull_resistor_1 (.node(PredictJump));

  // Other names for the same wires on the sheet: EX_BranchPC_Write[31:0] = Ex_PC
endmodule

module \预测跳转逻辑  (
  input  High,
  input  Low,
  input  Jump,
  output NextHigh,
  output NextLow
);

  wire and_1_out, and_2_out, and_3_out, and_4_out;

  and and_1 (and_1_out, Low, Jump);
  and and_2 (and_2_out, High, ~Low);  // AND_Gate
  and and_3 (and_3_out, ~High, ~Low, Jump);  // AND_Gate
  and and_4 (and_4_out, High, ~Low, ~Jump);  // AND_Gate
  or or_1 (NextHigh, and_1_out, and_2_out);
  or or_2 (NextLow, and_3_out, and_4_out);
endmodule

// MAX
module \并行比较MAX  (
  input  [15:0] X,
  input  [15:0] Y,
  input  [2:0] Y_num,
  input  [2:0] X_num,
  output [15:0] MAX,
  output [2:0] MAX_num
);

  wire comparator_1_eq, comparator_1_gt, or_1_out;

  Comparator #(.width(16), .mode("unsigned")) comparator_1 (
    .a(X), .b(Y), .gt(comparator_1_gt), .eq(comparator_1_eq));  // open: lt
  Multiplexer #(.select(1), .width(16), .disabled("Z"), .enable("true")) multiplexer_1 (
    .in0(Y), .in1(X), .out(MAX), .sel(or_1_out), .en(1'b1));
  or or_1 (or_1_out, comparator_1_gt, comparator_1_eq);
  Multiplexer #(.select(1), .width(3), .disabled("Z"), .enable("false")) multiplexer_2 (
    .in0(Y_num), .in1(X_num), .out(MAX_num), .sel(or_1_out));

  // Notes on the sheet:
  //   输出两个输入中的较大值，并输出较大值的2位编号
endmodule
