// Logisim project final.circ as structural Verilog: 25 circuits, main circuit ◇单周期RISC-V
module \单周期RISC_V  (
  input  IR1,
  input  IR2,
  input  IR3,
  output RegWrite,
  output MemWrite,
  output [31:0] PC,
  output [31:0] IR,
  output [31:0] RDin,
  output [31:0] MDin,
  output [31:0] LedData
);

  wire alu_1_equal, AluSrcB, and_2_out, and_3_out, and_4_out, and_5_out, and_6_out, BLTU, branch, CLK,
       clock_1_out, comparator_1_eq, comparator_2_lt, comparator_3_eq, comparator_3_lt, d_ff_1_q, ecall, Go,
       halt, IR1_t, IR2_t, IR3_t, IRA, IRB, IRC, JAL, JALR, MemToReg, nand_1_out, not_1_out, not_2_out,
       not_3_out, not_4_out, not_5_out, or_1_out, or_6_out, riscv_probe_1_p2, RST, S_Type, SB, W1, W2, W3,
       \单周期硬布线控制器_1_beq , \单周期硬布线控制器_1_bne ;
  wire [1:0] select;
  wire [3:0] AluOP, mips_ram_1_p4, multiplexer_12_out;
  wire [4:0] bit_extender_4_out, multiplexer_4_out, multiplexer_6_out, shifter_3_out;
  wire [9:0] alu_1_result;
  wire [11:0] multiplexer_5_out, shifter_1_out;
  wire [12:0] CNT_num;
  wire [15:0] \总周期数 ;
  wire [19:0] shifter_2_out;
  wire [31:0] adder_1_out, and_1_out, bit_extender_2_out, bit_extender_3_out, branchdata, jaldata, jalrin,
       mips_ram_1_p6, multiplexer_1_out, multiplexer_2_out, multiplexer_3_out, multiplexer_8_out,
       multiplexer_9_out, multiplexer_10_out, PC_4, R1Data, shifter_4_out;
  wire [31:12] alu_1_result_2;

  Button \u_继续运行  (.out(Go));
  Button _1 (.out(IRA));
  Button _2 (.out(IRB));
  Button _3 (.out(IRC));
  LED #(.active("true")) led_1 (.in(W1));
  LED #(.active("true")) led_2 (.in(W2));
  LED #(.active("true")) led_3 (.in(W3));
  assign and_1_out = 32'hfffffffe & adder_1_out;  // AND_Gate and_1, 32 bits wide
  Multiplexer #(.select(1), .width(32), .disabled("Z"), .enable("false")) multiplexer_1 (
    .in0(PC_4), .in1(and_1_out), .out(multiplexer_1_out), .sel(JALR));
  Multiplexer #(.select(1), .width(32), .disabled("Z"), .enable("false")) multiplexer_2 (
    .in0(multiplexer_1_out), .in1(jaldata), .out(multiplexer_2_out), .sel(JAL));
  Button u_CLK (.out(RST));
  Hex_Digit_Display hex_digit_display_1 (.value(LedData[31:28]));  // open: dp
  Multiplexer #(.select(1), .width(32), .disabled("Z"), .enable("false")) multiplexer_3 (
    .in0(multiplexer_2_out), .in1(branchdata), .out(multiplexer_3_out), .sel(branch));
  Register #(.width(32), .trigger("rising"), .Select("low")) u_PC (
    .D(multiplexer_3_out), .en(or_1_out), .Q(PC), .clk(CLK), .clr(RST));
  or or_1 (or_1_out, Go, not_1_out);
  not not_1 (not_1_out, halt);
  Hex_Digit_Display hex_digit_display_2 (.value(LedData[23:20]));  // open: dp
  Hex_Digit_Display hex_digit_display_3 (.value(LedData[27:24]));  // open: dp
  Adder #(.width(32)) adder_1 (.a(jalrin), .b(R1Data), .out(adder_1_out));  // open: cin, cout
  Adder #(.width(32)) adder_2 (.a(PC), .b(32'h4), .out(PC_4));  // open: cin, cout
  Hex_Digit_Display hex_digit_display_4 (.value(LedData[19:16]));  // open: dp
  Hex_Digit_Display hex_digit_display_5 (.value(LedData[15:12]));  // open: dp
  // RiscV_Probe riscv_probe_1: pin names not known; wires that end beside it: IR, riscv_probe_1_p2, 5'b00001, JALR, 5'b00001, JALR, IR[24:20]
  not not_2 (not_2_out, halt);
  Counter #(.width(16), .max('hffff), .ongoal("wrap"), .trigger("rising"), .behavior("new")) counter_1 (
    .count(not_2_out), .Q(\总周期数 ), .clk(CLK));  // open: load, D, carry, clr, preset, down
  Hex_Digit_Display hex_digit_display_6 (.value(LedData[7:4]));  // open: dp
  Hex_Digit_Display hex_digit_display_7 (.value(LedData[11:8]));  // open: dp
  // Probe on \总周期数 
  ROM #(.addrWidth(10), .dataWidth(32), .Select("high")) rom_1 (.addr(PC[11:2]), .data(IR));
  Hex_Digit_Display hex_digit_display_8 (.value(LedData[3:0]));  // open: dp
  \单周期硬布线控制器  \u_单周期硬布线控制器_1  (
    .Funct({IR[30], IR[25], IR[14:12]}), .OP(IR[6:2]), .ALU_OP(AluOP), .MemToReg(MemToReg),
    .MemWrite(MemWrite), .ALU_SRC(AluSrcB), .RegWrite(RegWrite), .ecall(ecall), .in_3(IR[21]),
    .uret(riscv_probe_1_p2), .JAL(JAL), .SB(SB), .Jalr(JALR), .BLTU(BLTU), .Bne(\单周期硬布线控制器_1_bne ),
    .Beq(\单周期硬布线控制器_1_beq ), .S_type(S_Type));  // open: I, B
  Multiplexer #(.select(1), .width(5), .disabled("Z"), .enable("false")) multiplexer_4 (
    .in0(IR[19:15]), .in1(5'b10001), .out(multiplexer_4_out), .sel(ecall));
  Multiplexer #(.select(1), .width(12), .disabled("Z"), .enable("false")) multiplexer_5 (
    .in0(IR[31:20]), .in1({IR[31:25], IR[11:7]}), .out(multiplexer_5_out), .sel(S_Type));
  Shifter #(.width(12), .shift("ll")) shifter_1 (
    .in({IR[31], IR[7], IR[30:25], IR[11:8]}), .\dist (4'b0001), .out(shifter_1_out));
  or or_2 (IR1_t, IR1, IRA);
  // Probe on multiplexer_4_out
  Multiplexer #(.select(1), .width(5), .disabled("Z"), .enable("false")) multiplexer_6 (
    .in0(IR[24:20]), .in1(5'b01010), .out(multiplexer_6_out), .sel(ecall));
  assign jalrin = {{20{multiplexer_5_out[11]}}, multiplexer_5_out};  // Bit_Extender bit_extender_1
  Multiplexer #(.select(1), .width(32), .disabled("Z"), .enable("false")) multiplexer_7 (
    .in0(multiplexer_10_out), .in1(mips_ram_1_p6), .out(RDin), .sel(MemToReg));
  assign bit_extender_2_out = {{20{shifter_1_out[11]}}, shifter_1_out};  // Bit_Extender bit_extender_2
  Shifter #(.width(20), .shift("ll")) shifter_2 (
    .in({IR[31], IR[19:12], IR[20], IR[30:21]}), .\dist (5'b00001), .out(shifter_2_out));
  assign bit_extender_3_out = {{12{shifter_2_out[19]}}, shifter_2_out};  // Bit_Extender bit_extender_3
  or or_3 (IR2_t, IR2, IRB);
  Regifile regifile_1 (
    .Din(RDin), .Clk(CLK), .R1(R1Data), .R2(MDin), .WE(RegWrite), .W_num(IR[11:7]),
    .R1_num(multiplexer_4_out), .R2_num(multiplexer_6_out));
  Adder #(.width(32)) adder_3 (.a(bit_extender_2_out), .b(PC), .out(branchdata));  // open: cin, cout
  Adder #(.width(32)) adder_4 (.a(bit_extender_3_out), .b(PC), .out(jaldata));  // open: cin, cout
  // Probe on R1Data
  Multiplexer #(.select(1), .width(32), .disabled("Z"), .enable("false")) multiplexer_8 (
    .in0(MDin), .in1(jalrin), .out(multiplexer_8_out), .sel(AluSrcB));
  Comparator #(.width(32), .mode("twosComplement")) comparator_1 (
    .a(R1Data), .b(32'h22), .eq(comparator_1_eq));  // open: gt, lt
  or or_4 (IR3_t, IR3, IRC);
  Comparator #(.width(32), .mode("unsigned")) comparator_2 (
    .a(R1Data), .b(MDin), .lt(comparator_2_lt));  // open: gt, eq
  ALU alu_1 (
    .X(R1Data), .Y(multiplexer_8_out), .AluOP(AluOP), .Equal(alu_1_equal),
    .Result({alu_1_result_2, alu_1_result, select}));  // open: Result_2, out_4, out_6
  assign bit_extender_4_out = {{3{select[1]}}, select};  // Bit_Extender bit_extender_4
  Shifter #(.width(5), .shift("ll")) shifter_3 (.in(bit_extender_4_out), .\dist (3'b011), .out(shifter_3_out));
  not not_3 (not_3_out, comparator_1_eq);
  and and_2 (and_2_out, alu_1_equal, \单周期硬布线控制器_1_beq );
  not not_4 (not_4_out, alu_1_equal);
  and and_3 (and_3_out, not_4_out, \单周期硬布线控制器_1_bne );
  Multiplexer #(.select(1), .width(32), .disabled("Z"), .enable("false")) multiplexer_9 (
    .in0(MDin), .in1(shifter_4_out), .out(multiplexer_9_out), .sel(SB));
  Shifter #(.width(32), .shift("ll")) shifter_4 (.in(MDin), .\dist (shifter_3_out), .out(shifter_4_out));
  and and_4 (and_4_out, ecall, not_3_out);
  and and_5 (and_5_out, ecall, comparator_1_eq);
  or or_5 (branch, and_2_out, and_3_out, and_6_out);
  and and_6 (and_6_out, BLTU, comparator_2_lt);
  Multiplexer #(.select(1), .width(32), .disabled("Z"), .enable("false")) multiplexer_10 (
    .in0({alu_1_result_2, alu_1_result, select}), .in1(PC_4), .out(multiplexer_10_out), .sel(or_6_out));
  or or_6 (or_6_out, JAL, JALR);
  Register #(.width(1), .trigger("rising"), .Select("low")) register_1 (
    .D(and_4_out), .en(not_5_out), .Q(halt), .clk(CLK), .clr(Go));
  not not_5 (not_5_out, halt);
  // MIPS_RAM mips_ram_1: pin names not known; wires that end beside it: alu_1_result, multiplexer_9_out, MemWrite, mips_ram_1_p4, CLK, mips_ram_1_p6
  Multiplexer #(.select(1), .width(4), .disabled("Z"), .enable("false")) multiplexer_11 (
    .in0(4'b1111), .in1(multiplexer_12_out), .out(mips_ram_1_p4), .sel(SB));
  Multiplexer #(.select(2), .width(4), .disabled("Z"), .enable("false")) multiplexer_12 (
    .in0(4'b0001), .in1(4'b0010), .in2(4'b0100), .in3(4'b1000), .out(multiplexer_12_out), .sel(select));
  Register #(.width(32), .trigger("rising"), .Select("low")) PC_2 (
    .D(MDin), .en(and_5_out), .Q(LedData), .clk(CLK));  // open: clr
  D_Flip_Flop #(.trigger("high"), .Pre_Clr_Positions("LEGACY"), .NegatePresetClear("false"), .enable("true"), .NewFFLayout("false")) d_ff_1 (.Q(d_ff_1_q));  // open: clk, D, Qn, preset, en, reset
  // Probe on 13'hc
  Comparator #(.width(13), .mode("twosComplement")) comparator_3 (
    .a(CNT_num), .b(13'hc), .eq(comparator_3_eq), .lt(comparator_3_lt));  // open: gt
  Clock #(.highDuration(1), .lowDuration(1)) clock_1 (.out(clock_1_out));
  Counter #(.width(13), .max('h1fff), .ongoal("stay"), .trigger("rising"), .behavior("old")) counter_2 (
    .count(comparator_3_lt), .Q(CNT_num), .clk(clock_1_out));  // open: load, D, carry, clr, preset
  nand nand_1 (nand_1_out, d_ff_1_q, comparator_3_eq);
  assign CLK = nand_1_out ? clock_1_out : 1'bz;  // Controlled_Buffer controlled_buffer_1
  Pull_Resistor #(.pull(1)) pull_resistor_1 (.node(CLK));

  // Notes on the sheet:
  //   中断源
  //   中断等待指示
  //   数码管输出
  //   指令探针
  //   指令存储器
  //   指令字
  //   contents of rom_1 (hex, n*v repeats v):
  //   100493 100006f 100493 200913 300993 100006f 100493 200913 300993 100006f 100493 200913 300993
  //   100006f 100493 200913 300993 3c0000ef 100413 100493 1f49493 900533 2200893 73 24d493 48463 fedff06f
  //   900533 2200893 73 100493 249493 900533 2200893 73 48463 fedff06f 100493 1f49493 900533 2200893 73
  //   4034d493 900533 2200893 73 4044d493 900533 2200893 73 4044d493 900533 2200893 73 4044d493 900533
  //   2200893 73 4044d493 900533 2200893 73 4044d493 900533 2200893 73 4044d493 900533 2200893 73 4044d493
  //   900533 2200893 73 100413 1f41993 41f9d993 433 c00913 300b13 140413 f47413 800293 100313 499993
  //   89e9b3 1300533 2200893 73 406282b3 fe0294e3 140413 f00f93 1f47433 1c41413 800293 100313 49d993
  //   89e9b3 1300533 2200893 73 406282b3 fe0294e3 1c45413 406b0b33 b0463 f95ff06f 2b3 fff2c293 829293
  //   ff2e293 500533 2200893 73 fff00413 493 84a023 140413 448493 84a023 140413 448493 84a023 140413
  //   448493 84a023 140413 448493 84a023 140413 448493 84a023 140413 448493 84a023 140413 448493 84a023
  //   140413 448493 84a023 140413 448493 84a023 140413 448493 84a023 140413 448493 84a023 140413 448493
  //   84a023 140413 448493 84a023 140413 448493 84a023 140413 448493 84a023 140413 448493 140413 433
  //   3c00493 42983 4aa03 149a2b3 28663 134a023 1442023 ffc48493 fe9412e3 800533 2200893 73 440413 3c00493
  //   fc9416e3 3200893 73 100293 300313 800493 849493 7648493 900533 2200893 73 800e13 5494b3 6494b3
  //   900533 2200893 73 fffe0e13 fe0e14e3 a00893 73 100293 300313 800493 849493 7648493 1449493 900533
  //   2200893 73 800e13 4054d4b3 4064d4b3 900533 2200893 73 fffe0e13 fe0e14e3 a00893 73 313 2000e13 493
  //   100913 930023 900533 2200893 73 12484b3 130313 fffe0e13 fe0e12e3 800e13 313 32483 900533 2200893 73
  //   430313 fffe0e13 fe0e14e3 a00893 73 ff100493 900533 2200893 73 148493 fe9068e3 900533 2200893 73
  //   a00893 73 a00893 73 413 140413 800533 2200893 73 240413 800533 2200893 73 340413 800533 2200893 73
  //   440413 800533 2200893 73 540413 800533 2200893 73 640413 800533 2200893 73 740413 800533 2200893 73
  //   840413 800533 2200893 2200893 73 8067
  //   Beq
  //   Bne
  //   MemToReg
  //   MemWrite
  //   AluOP
  //   AluSrcB
  //   RegWrite
  //   数据存储器
  //   为方便自动评测，需要输出PC，IR，寄存器堆写如数据RDin
  //   RAM写使能MemWrite、RAM写入数据MDin等信号
  //   控制位
  //   暂停节拍，不能为0
  //   戳工具置1进入计数暂停模式，ctrl+k时钟自动运行到对应节拍暂停
  //   ctrl+k关闭时钟连续运行，将控制位置零，进入单步调试模式调试
  //   用这个时钟源需要去掉电路中的其他时钟源
  //   数码管输出应该用寄存器锁存，否则显示数据只能一闪而过
  //   可计数暂停的时钟源
endmodule

// 单周期硬布线控制器
module \单周期硬布线控制器  (
  input  [4:0] OP,
  input  [4:0] Funct,
  input  in_3,
  output [3:0] ALU_OP,
  output uret,
  output MemToReg,
  output ecall,
  output MemWrite,
  output ALU_SRC,
  output RegWrite,
  output SB,
  output BLTU,
  output S_type,
  output Beq,
  output Bne,
  output Jalr,
  output JAL,
  output I,
  output B
);

  wire \控制信号自动生成_1_ecall ;

  \运算控制器自动生成  \u_运算控制器自动生成_1  (
    .OP2(OP[0]), .OP3(OP[1]), .OP4(OP[2]), .OP5(OP[3]), .OP6(OP[4]), .F12(Funct[0]), .F13(Funct[1]),
    .F14(Funct[2]), .F25(Funct[3]), .F30(Funct[4]), .S0(ALU_OP[0]), .S1(ALU_OP[1]), .S2(ALU_OP[2]),
    .S3(ALU_OP[3]));
  \控制信号自动生成  \u_控制信号自动生成_1  (
    .OP2(OP[0]), .OP3(OP[1]), .MemToReg(MemToReg), .OP4(OP[2]), .OP5(OP[3]), .OP6(OP[4]), .F12(Funct[0]),
    .MemWrite(MemWrite), .F13(Funct[1]), .F14(Funct[2]), .F25(Funct[3]), .F30(Funct[4]), .ALU_SRC(ALU_SRC),
    .RegWrite(RegWrite), .SB(SB), .BLTU(BLTU), .ecall(\控制信号自动生成_1_ecall ), .S_Type(S_type), .CSRRCI(I),
    .CSRRSI(B), .BEQ(Beq), .BNE(Bne), .JALR(Jalr), .JAL(JAL));
  and and_1 (uret, in_3, \控制信号自动生成_1_ecall );
  and and_2 (ecall, ~in_3, \控制信号自动生成_1_ecall );  // AND_Gate

  // Other names for the same wires on the sheet: IR21 = in_3; OP_CODE[4:0] = OP

  // Notes on the sheet:
  //   运算器控制器，根据指令生成运算器功能选择信号
  //   控制信号生成，产生数据通路需要的其他控制信号
endmodule

// 运算器控制器
module \运算控制器自动生成  (
  input  OP2,
  input  OP3,
  input  OP4,
  input  OP5,
  input  OP6,
  input  F12,
  input  F13,
  input  F14,
  input  F25,
  input  F30,
  output S0,
  output S1,
  output S2,
  output S3
);

  wire and_1_out, and_2_out, and_3_out, and_4_out, and_5_out, and_6_out, and_7_out, and_8_out, and_9_out,
       and_10_out, and_11_out, and_12_out, and_13_out, and_14_out, and_15_out, and_16_out, and_17_out,
       and_18_out, and_19_out, and_20_out, and_21_out, and_22_out, and_23_out, and_24_out, and_25_out,
       and_26_out, and_27_out, and_28_out, and_29_out, and_30_out, and_31_out, and_32_out, and_33_out,
       not_1_out, not_2_out, not_3_out, not_4_out, not_5_out, not_6_out, not_7_out, not_8_out, not_9_out,
       not_10_out, not_11_out, not_12_out, not_13_out, not_14_out, not_15_out, not_16_out, not_17_out,
       not_18_out, not_19_out, not_20_out, not_21_out, not_22_out, not_23_out, not_24_out, not_25_out,
       not_26_out, not_27_out, not_28_out, not_29_out, not_30_out, not_31_out, not_32_out, not_33_out,
       not_34_out, not_35_out, not_36_out, not_37_out, not_38_out, not_39_out, not_40_out, not_41_out,
       not_42_out, not_43_out, not_44_out, not_45_out, not_46_out, not_47_out, not_48_out, not_49_out,
       not_50_out, not_51_out, not_52_out, not_53_out, not_54_out, not_55_out, not_56_out, not_57_out,
       not_58_out, not_59_out, not_60_out, not_61_out, not_62_out, not_63_out, not_64_out, not_65_out,
       not_66_out, not_67_out, not_68_out, not_69_out, not_70_out, not_71_out, not_72_out, not_73_out,
       not_74_out, not_75_out, not_76_out, not_77_out, not_78_out, not_79_out, not_80_out, not_81_out,
       not_82_out, not_83_out, not_84_out, not_85_out, not_86_out, not_87_out, not_88_out, not_89_out,
       not_90_out, not_91_out, not_92_out, not_93_out, not_94_out, not_95_out, not_96_out, not_97_out,
       not_98_out, not_99_out, not_100_out, not_101_out, not_102_out, not_103_out, not_104_out, not_105_out,
       not_106_out, not_107_out, not_108_out, not_109_out, not_110_out, not_111_out, not_112_out,
       not_113_out, not_114_out, not_115_out, not_116_out, not_117_out, not_118_out, not_119_out,
       not_120_out, not_121_out, not_122_out, not_123_out, not_124_out, not_125_out, not_126_out,
       not_127_out, not_128_out, not_129_out, not_130_out, not_131_out, not_132_out, not_133_out,
       not_134_out, not_135_out, not_136_out, not_137_out, not_138_out, not_139_out, not_140_out,
       not_141_out, not_142_out, not_143_out, not_144_out, not_145_out, not_146_out, not_147_out,
       not_148_out, not_149_out, not_150_out, not_151_out, not_152_out, not_153_out, not_154_out,
       not_155_out, not_156_out, not_157_out, not_158_out, not_159_out, not_160_out, not_161_out,
       not_162_out, not_163_out, not_164_out, not_165_out, not_166_out, not_167_out, not_168_out,
       not_169_out, not_170_out, not_171_out, not_172_out, not_173_out, not_174_out;

  not not_1 (not_1_out, OP2);
  not not_2 (not_2_out, OP3);
  not not_3 (not_3_out, OP4);
  not not_4 (not_4_out, OP6);
  not not_5 (not_5_out, F12);
  not not_6 (not_6_out, F14);
  not not_7 (not_7_out, OP2);
  not not_8 (not_8_out, OP3);
  not not_9 (not_9_out, OP5);
  not not_10 (not_10_out, OP6);
  not not_11 (not_11_out, F12);
  not not_12 (not_12_out, F13);
  not not_13 (not_13_out, OP2);
  not not_14 (not_14_out, OP3);
  not not_15 (not_15_out, OP5);
  not not_16 (not_16_out, OP6);
  not not_17 (not_17_out, F12);
  not not_18 (not_18_out, F14);
  not not_19 (not_19_out, OP2);
  not not_20 (not_20_out, OP3);
  not not_21 (not_21_out, OP6);
  not not_22 (not_22_out, F12);
  not not_23 (not_23_out, F14);
  not not_24 (not_24_out, F25);
  not not_25 (not_25_out, F30);
  not not_26 (not_26_out, OP2);
  not not_27 (not_27_out, OP3);
  not not_28 (not_28_out, OP5);
  not not_29 (not_29_out, OP6);
  not not_30 (not_30_out, F13);
  not not_31 (not_31_out, F25);
  not not_32 (not_32_out, OP2);
  not not_33 (not_33_out, OP3);
  not not_34 (not_34_out, OP5);
  not not_35 (not_35_out, OP6);
  not not_36 (not_36_out, OP2);
  not not_37 (not_37_out, OP3);
  not not_38 (not_38_out, OP6);
  not not_39 (not_39_out, F25);
  not not_40 (not_40_out, F30);
  not not_41 (not_41_out, OP4);
  not not_42 (not_42_out, F12);
  not not_43 (not_43_out, F13);
  not not_44 (not_44_out, F14);
  not not_45 (not_45_out, OP4);
  not not_46 (not_46_out, F25);
  not not_47 (not_47_out, F13);
  not not_48 (not_48_out, OP6);
  not not_49 (not_49_out, OP3);
  not not_50 (not_50_out, OP2);
  not not_51 (not_51_out, F14);
  not not_52 (not_52_out, F13);
  not not_53 (not_53_out, F12);
  not not_54 (not_54_out, OP6);
  not not_55 (not_55_out, OP4);
  not not_56 (not_56_out, OP3);
  not not_57 (not_57_out, OP2);
  not not_58 (not_58_out, OP2);
  not not_59 (not_59_out, OP3);
  not not_60 (not_60_out, OP4);
  not not_61 (not_61_out, F13);
  not not_62 (not_62_out, F14);
  not not_63 (not_63_out, OP2);
  not not_64 (not_64_out, OP3);
  not not_65 (not_65_out, OP5);
  not not_66 (not_66_out, OP6);
  not not_67 (not_67_out, F12);
  not not_68 (not_68_out, F14);
  not not_69 (not_69_out, OP2);
  not not_70 (not_70_out, OP3);
  not not_71 (not_71_out, OP6);
  not not_72 (not_72_out, F12);
  not not_73 (not_73_out, F14);
  not not_74 (not_74_out, F25);
  not not_75 (not_75_out, F30);
  not not_76 (not_76_out, OP2);
  not not_77 (not_77_out, OP3);
  not not_78 (not_78_out, OP5);
  not not_79 (not_79_out, OP6);
  not not_80 (not_80_out, F25);
  not not_81 (not_81_out, F30);
  not not_82 (not_82_out, OP2);
  not not_83 (not_83_out, OP3);
  not not_84 (not_84_out, OP5);
  not not_85 (not_85_out, OP6);
  not not_86 (not_86_out, OP2);
  not not_87 (not_87_out, OP3);
  not not_88 (not_88_out, OP6);
  not not_89 (not_89_out, F25);
  not not_90 (not_90_out, F30);
  not not_91 (not_91_out, OP2);
  not not_92 (not_92_out, OP3);
  not not_93 (not_93_out, OP6);
  not not_94 (not_94_out, F12);
  not not_95 (not_95_out, F13);
  not not_96 (not_96_out, F14);
  not not_97 (not_97_out, F25);
  not not_98 (not_98_out, F12);
  not not_99 (not_99_out, OP4);
  not not_100 (not_100_out, OP3);
  not not_101 (not_101_out, OP2);
  not not_102 (not_102_out, OP2);
  not not_103 (not_103_out, OP3);
  not not_104 (not_104_out, OP4);
  not not_105 (not_105_out, OP6);
  not not_106 (not_106_out, F12);
  not not_107 (not_107_out, F14);
  not not_108 (not_108_out, OP2);
  not not_109 (not_109_out, OP3);
  not not_110 (not_110_out, OP4);
  not not_111 (not_111_out, F13);
  not not_112 (not_112_out, F14);
  not not_113 (not_113_out, OP3);
  not not_114 (not_114_out, OP4);
  not not_115 (not_115_out, F12);
  not not_116 (not_116_out, F13);
  not not_117 (not_117_out, F14);
  not not_118 (not_118_out, OP2);
  not not_119 (not_119_out, OP3);
  not not_120 (not_120_out, OP5);
  not not_121 (not_121_out, OP6);
  not not_122 (not_122_out, F12);
  not not_123 (not_123_out, F13);
  not not_124 (not_124_out, F14);
  not not_125 (not_125_out, OP2);
  not not_126 (not_126_out, OP3);
  not not_127 (not_127_out, OP6);
  not not_128 (not_128_out, F12);
  not not_129 (not_129_out, F13);
  not not_130 (not_130_out, F14);
  not not_131 (not_131_out, F25);
  not not_132 (not_132_out, OP2);
  not not_133 (not_133_out, OP3);
  not not_134 (not_134_out, OP5);
  not not_135 (not_135_out, OP6);
  not not_136 (not_136_out, OP2);
  not not_137 (not_137_out, OP3);
  not not_138 (not_138_out, OP6);
  not not_139 (not_139_out, F25);
  not not_140 (not_140_out, F30);
  not not_141 (not_141_out, OP4);
  not not_142 (not_142_out, F14);
  not not_143 (not_143_out, F13);
  not not_144 (not_144_out, F12);
  not not_145 (not_145_out, OP6);
  not not_146 (not_146_out, OP4);
  not not_147 (not_147_out, OP3);
  not not_148 (not_148_out, OP2);
  not not_149 (not_149_out, F12);
  not not_150 (not_150_out, OP4);
  not not_151 (not_151_out, OP3);
  not not_152 (not_152_out, OP2);
  not not_153 (not_153_out, OP2);
  not not_154 (not_154_out, OP3);
  not not_155 (not_155_out, OP5);
  not not_156 (not_156_out, OP6);
  not not_157 (not_157_out, F12);
  not not_158 (not_158_out, OP2);
  not not_159 (not_159_out, OP3);
  not not_160 (not_160_out, OP5);
  not not_161 (not_161_out, OP6);
  not not_162 (not_162_out, F12);
  not not_163 (not_163_out, OP2);
  not not_164 (not_164_out, OP3);
  not not_165 (not_165_out, OP6);
  not not_166 (not_166_out, F12);
  not not_167 (not_167_out, F25);
  not not_168 (not_168_out, F30);
  not not_169 (not_169_out, OP2);
  not not_170 (not_170_out, OP3);
  not not_171 (not_171_out, OP6);
  not not_172 (not_172_out, F14);
  not not_173 (not_173_out, F25);
  not not_174 (not_174_out, F30);
  and and_1 (and_1_out, not_1_out, not_2_out, not_3_out, not_4_out, not_5_out, F13, not_6_out);
  and and_2 (and_2_out, not_7_out, not_8_out, OP4, not_9_out, not_10_out, not_11_out, not_12_out);
  and and_3 (and_3_out, not_13_out, not_14_out, OP4, not_15_out, not_16_out, not_17_out, not_18_out);
  and and_4 (and_4_out, not_19_out, not_20_out, OP4, not_21_out, not_22_out, not_23_out, not_24_out, not_25_out);
  and and_5 (and_5_out, not_26_out, not_27_out, OP4, not_28_out, not_29_out, not_30_out, F14, not_31_out, F30);
  and and_6 (and_6_out, not_32_out, not_33_out, OP4, not_34_out, not_35_out, F12, F13, F14);
  and and_7 (and_7_out, not_36_out, not_37_out, OP4, not_38_out, F12, F13, F14, not_39_out, not_40_out);
  and and_8 (and_8_out, OP2, not_41_out, OP5, OP6, not_42_out, not_43_out, not_44_out);
  and and_9 (and_9_out, OP2, OP3, not_45_out, OP5, OP6);
  and and_10 (and_10_out, F30, not_46_out, F14, not_47_out, F12, not_48_out, OP5, OP4, not_49_out, not_50_out);
  and and_11 (and_11_out, not_51_out, not_52_out, not_53_out, not_54_out, OP5, not_55_out, not_56_out, not_57_out);
  and and_12 (and_12_out, not_58_out, not_59_out, not_60_out, OP5, OP6, not_61_out, not_62_out);
  and and_13 (and_13_out, not_63_out, not_64_out, OP4, not_65_out, not_66_out, not_67_out, F13, not_68_out);
  and and_14 (and_14_out, not_69_out, not_70_out, OP4, not_71_out, not_72_out, F13, not_73_out, not_74_out, not_75_out);
  and and_15 (and_15_out, not_76_out, not_77_out, OP4, not_78_out, not_79_out, F12, F14, not_80_out, not_81_out);
  and and_16 (and_16_out, not_82_out, not_83_out, OP4, not_84_out, not_85_out, F12, F13, F14);
  and and_17 (and_17_out, not_86_out, not_87_out, OP4, not_88_out, F12, F13, F14, not_89_out, not_90_out);
  and and_18 (and_18_out, not_91_out, not_92_out, OP4, OP5, not_93_out, not_94_out, not_95_out, not_96_out, not_97_out, F30);
  and and_19 (and_19_out, F14, F13, not_98_out, OP6, OP5, not_99_out, not_100_out, not_101_out);
  and and_20 (and_20_out, not_102_out, not_103_out, not_104_out, not_105_out, not_106_out, F13, not_107_out);
  and and_21 (and_21_out, not_108_out, not_109_out, not_110_out, OP5, OP6, not_111_out, not_112_out);
  and and_22 (and_22_out, not_113_out, not_114_out, OP5, OP6, not_115_out, not_116_out, not_117_out);
  and and_23 (and_23_out, not_118_out, not_119_out, OP4, not_120_out, not_121_out, not_122_out, not_123_out, not_124_out);
  and and_24 (and_24_out, not_125_out, not_126_out, OP4, not_127_out, not_128_out, not_129_out, not_130_out, not_131_out);
  and and_25 (and_25_out, not_132_out, not_133_out, OP4, not_134_out, not_135_out, F12, F13, F14);
  and and_26 (and_26_out, not_136_out, not_137_out, OP4, OP5, not_138_out, F12, F13, not_139_out, not_140_out);
  and and_27 (and_27_out, OP2, OP3, not_141_out, OP5, OP6);
  and and_28 (and_28_out, not_142_out, not_143_out, not_144_out, not_145_out, OP5, not_146_out, not_147_out, not_148_out);
  and and_29 (and_29_out, F14, F13, not_149_out, OP6, OP5, not_150_out, not_151_out, not_152_out);
  and and_30 (and_30_out, not_153_out, not_154_out, OP4, not_155_out, not_156_out, not_157_out, F14);
  and and_31 (and_31_out, not_158_out, not_159_out, OP4, not_160_out, not_161_out, not_162_out, F13);
  and and_32 (and_32_out, not_163_out, not_164_out, OP4, not_165_out, not_166_out, F13, not_167_out, not_168_out);
  and and_33 (and_33_out, not_169_out, not_170_out, OP4, OP5, not_171_out, F13, not_172_out, not_173_out, not_174_out);
  or or_1 (S3, and_30_out, and_31_out, and_32_out, and_33_out);
  or or_2 (S0, and_1_out, and_2_out, and_3_out, and_4_out, and_5_out, and_6_out, and_7_out, and_8_out, and_9_out, and_10_out, and_11_out);
  or or_3 (S1, and_12_out, and_13_out, and_14_out, and_15_out, and_16_out, and_17_out, and_18_out, and_19_out);
  or or_4 (S2, and_20_out, and_21_out, and_22_out, and_23_out, and_24_out, and_25_out, and_26_out, and_27_out, and_28_out, and_29_out);
endmodule

// 控制信号生成
module \控制信号自动生成  (
  input  OP2,
  input  OP3,
  input  OP4,
  input  OP5,
  input  OP6,
  input  F12,
  input  F13,
  input  F14,
  input  F25,
  input  F30,
  output MemToReg,
  output MemWrite,
  output ALU_SRC,
  output RegWrite,
  output SB,
  output BLTU,
  output ecall,
  output S_Type,
  output CSRRCI,
  output CSRRSI,
  output BEQ,
  output BNE,
  output JALR,
  output JAL
);

  wire and_3_out, and_4_out, and_5_out, and_6_out, and_7_out, and_8_out, and_9_out, and_10_out, and_11_out,
       and_12_out, and_13_out, and_14_out, and_15_out, and_16_out, and_17_out, and_18_out, and_19_out,
       and_24_out, and_25_out, and_26_out, and_27_out, and_28_out, and_29_out, and_30_out, and_31_out,
       not_1_out, not_2_out, not_3_out, not_4_out, not_5_out, not_6_out, not_7_out, not_8_out, not_9_out,
       not_10_out, not_11_out, not_12_out, not_13_out, not_14_out, not_15_out, not_16_out, not_17_out,
       not_18_out, not_19_out, not_20_out, not_21_out, not_22_out, not_23_out, not_24_out, not_25_out,
       not_26_out, not_27_out, not_28_out, not_29_out, not_30_out, not_31_out, not_32_out, not_33_out,
       not_34_out, not_35_out, not_36_out, not_37_out, not_38_out, not_39_out, not_40_out, not_41_out,
       not_42_out, not_43_out, not_44_out, not_45_out, not_46_out, not_47_out, not_48_out, not_49_out,
       not_50_out, not_51_out, not_52_out, not_53_out, not_54_out, not_55_out, not_56_out, not_57_out,
       not_58_out, not_59_out, not_60_out, not_61_out, not_62_out, not_63_out, not_64_out, not_65_out,
       not_66_out, not_67_out, not_68_out, not_69_out, not_70_out, not_71_out, not_72_out, not_73_out,
       not_74_out, not_75_out, not_76_out, not_77_out, not_78_out, not_79_out, not_80_out, not_81_out,
       not_82_out, not_83_out, not_84_out, not_85_out, not_86_out, not_87_out, not_88_out, not_89_out,
       not_90_out, not_91_out, not_92_out, not_93_out, not_94_out, not_95_out, not_96_out, not_97_out,
       not_98_out, not_99_out, not_100_out, not_101_out, not_102_out, not_103_out, not_104_out, not_105_out,
       not_106_out, not_107_out, not_108_out, not_109_out, not_110_out, not_111_out, not_112_out,
       not_113_out, not_114_out, not_115_out, not_116_out, not_117_out, not_118_out, not_119_out,
       not_120_out, not_121_out, not_122_out, not_123_out, not_124_out, not_125_out, not_126_out,
       not_127_out, not_128_out, not_129_out, not_130_out, not_131_out, not_132_out, not_133_out,
       not_134_out, not_135_out, not_136_out, not_137_out, not_138_out, not_139_out, not_140_out,
       not_141_out, not_142_out, not_143_out, not_144_out, not_145_out, not_146_out, not_147_out,
       not_148_out, not_149_out, not_150_out, not_151_out, not_152_out, not_153_out, not_154_out,
       not_155_out, not_156_out, not_157_out, not_158_out, not_159_out, not_160_out, not_161_out,
       not_162_out, not_163_out, not_164_out, not_165_out, not_166_out, not_167_out, not_168_out,
       not_169_out, not_170_out, not_171_out, not_172_out, not_173_out, not_174_out, not_175_out,
       not_176_out, not_177_out, not_178_out, not_179_out, not_180_out, not_181_out, not_182_out;

  not not_1 (not_1_out, OP2);
  not not_2 (not_2_out, OP3);
  not not_3 (not_3_out, OP4);
  not not_4 (not_4_out, OP5);
  not not_5 (not_5_out, OP6);
  not not_6 (not_6_out, F12);
  not not_7 (not_7_out, F14);
  not not_8 (not_8_out, OP2);
  not not_9 (not_9_out, OP3);
  not not_10 (not_10_out, OP4);
  not not_11 (not_11_out, OP6);
  not not_12 (not_12_out, F12);
  not not_13 (not_13_out, F14);
  not not_14 (not_14_out, OP2);
  not not_15 (not_15_out, OP3);
  not not_16 (not_16_out, OP5);
  not not_17 (not_17_out, OP6);
  not not_18 (not_18_out, F12);
  not not_19 (not_19_out, F14);
  not not_20 (not_20_out, OP2);
  not not_21 (not_21_out, OP3);
  not not_22 (not_22_out, OP4);
  not not_23 (not_23_out, OP6);
  not not_24 (not_24_out, F12);
  not not_25 (not_25_out, F14);
  not not_26 (not_26_out, OP2);
  not not_27 (not_27_out, OP3);
  not not_28 (not_28_out, OP5);
  not not_29 (not_29_out, OP6);
  not not_30 (not_30_out, F12);
  not not_31 (not_31_out, OP2);
  not not_32 (not_32_out, OP3);
  not not_33 (not_33_out, OP5);
  not not_34 (not_34_out, OP6);
  not not_35 (not_35_out, F13);
  not not_36 (not_36_out, F25);
  not not_37 (not_37_out, F30);
  not not_38 (not_38_out, OP2);
  not not_39 (not_39_out, OP3);
  not not_40 (not_40_out, OP5);
  not not_41 (not_41_out, OP6);
  not not_42 (not_42_out, F25);
  not not_43 (not_43_out, OP2);
  not not_44 (not_44_out, OP3);
  not not_45 (not_45_out, OP5);
  not not_46 (not_46_out, OP6);
  not not_47 (not_47_out, OP3);
  not not_48 (not_48_out, OP4);
  not not_49 (not_49_out, F12);
  not not_50 (not_50_out, F13);
  not not_51 (not_51_out, F14);
  not not_52 (not_52_out, OP2);
  not not_53 (not_53_out, OP3);
  not not_54 (not_54_out, OP5);
  not not_55 (not_55_out, OP6);
  not not_56 (not_56_out, F12);
  not not_57 (not_57_out, F14);
  not not_58 (not_58_out, OP2);
  not not_59 (not_59_out, OP3);
  not not_60 (not_60_out, OP5);
  not not_61 (not_61_out, OP6);
  not not_62 (not_62_out, F12);
  not not_63 (not_63_out, OP2);
  not not_64 (not_64_out, OP3);
  not not_65 (not_65_out, OP6);
  not not_66 (not_66_out, F12);
  not not_67 (not_67_out, F13);
  not not_68 (not_68_out, F14);
  not not_69 (not_69_out, F25);
  not not_70 (not_70_out, OP2);
  not not_71 (not_71_out, OP3);
  not not_72 (not_72_out, OP6);
  not not_73 (not_73_out, F13);
  not not_74 (not_74_out, F14);
  not not_75 (not_75_out, F25);
  not not_76 (not_76_out, F30);
  not not_77 (not_77_out, OP2);
  not not_78 (not_78_out, OP3);
  not not_79 (not_79_out, OP5);
  not not_80 (not_80_out, OP6);
  not not_81 (not_81_out, F25);
  not not_82 (not_82_out, OP2);
  not not_83 (not_83_out, OP3);
  not not_84 (not_84_out, OP5);
  not not_85 (not_85_out, OP6);
  not not_86 (not_86_out, OP2);
  not not_87 (not_87_out, OP3);
  not not_88 (not_88_out, OP6);
  not not_89 (not_89_out, F13);
  not not_90 (not_90_out, F25);
  not not_91 (not_91_out, OP2);
  not not_92 (not_92_out, OP3);
  not not_93 (not_93_out, OP6);
  not not_94 (not_94_out, F25);
  not not_95 (not_95_out, F30);
  not not_96 (not_96_out, OP4);
  not not_97 (not_97_out, F12);
  not not_98 (not_98_out, F13);
  not not_99 (not_99_out, F14);
  not not_100 (not_100_out, OP4);
  not not_101 (not_101_out, OP2);
  not not_102 (not_102_out, OP3);
  not not_103 (not_103_out, OP4);
  not not_104 (not_104_out, OP6);
  not not_105 (not_105_out, F12);
  not not_106 (not_106_out, F13);
  not not_107 (not_107_out, F14);
  not not_108 (not_108_out, OP2);
  not not_109 (not_109_out, OP3);
  not not_110 (not_110_out, OP4);
  not not_111 (not_111_out, F12);
  not not_112 (not_112_out, OP2);
  not not_113 (not_113_out, OP3);
  not not_114 (not_114_out, F12);
  not not_115 (not_115_out, F13);
  not not_116 (not_116_out, F14);
  not not_117 (not_117_out, F25);
  not not_118 (not_118_out, F30);
  not not_119 (not_119_out, OP2);
  not not_120 (not_120_out, OP3);
  not not_121 (not_121_out, OP4);
  not not_122 (not_122_out, OP6);
  not not_123 (not_123_out, F12);
  not not_124 (not_124_out, F14);
  not not_125 (not_125_out, OP2);
  not not_126 (not_126_out, OP3);
  not not_127 (not_127_out, OP5);
  not not_128 (not_128_out, OP6);
  not not_129 (not_129_out, F12);
  not not_130 (not_130_out, F14);
  not not_131 (not_131_out, OP2);
  not not_132 (not_132_out, OP3);
  not not_133 (not_133_out, OP5);
  not not_134 (not_134_out, OP6);
  not not_135 (not_135_out, F12);
  not not_136 (not_136_out, OP2);
  not not_137 (not_137_out, OP3);
  not not_138 (not_138_out, OP5);
  not not_139 (not_139_out, OP6);
  not not_140 (not_140_out, F13);
  not not_141 (not_141_out, F25);
  not not_142 (not_142_out, F30);
  not not_143 (not_143_out, OP2);
  not not_144 (not_144_out, OP3);
  not not_145 (not_145_out, OP5);
  not not_146 (not_146_out, OP6);
  not not_147 (not_147_out, F25);
  not not_148 (not_148_out, OP2);
  not not_149 (not_149_out, OP3);
  not not_150 (not_150_out, OP5);
  not not_151 (not_151_out, OP6);
  not not_152 (not_152_out, OP3);
  not not_153 (not_153_out, OP4);
  not not_154 (not_154_out, F12);
  not not_155 (not_155_out, F13);
  not not_156 (not_156_out, F14);
  not not_157 (not_157_out, OP2);
  not not_158 (not_158_out, OP3);
  not not_159 (not_159_out, OP4);
  not not_160 (not_160_out, F13);
  not not_161 (not_161_out, F14);
  not not_162 (not_162_out, OP2);
  not not_163 (not_163_out, OP3);
  not not_164 (not_164_out, OP4);
  not not_165 (not_165_out, F12);
  not not_166 (not_166_out, OP2);
  not not_167 (not_167_out, OP3);
  not not_168 (not_168_out, OP4);
  not not_169 (not_169_out, F12);
  not not_170 (not_170_out, F13);
  not not_171 (not_171_out, F14);
  not not_172 (not_172_out, OP2);
  not not_173 (not_173_out, OP3);
  not not_174 (not_174_out, OP4);
  not not_175 (not_175_out, F13);
  not not_176 (not_176_out, F14);
  not not_177 (not_177_out, OP3);
  not not_178 (not_178_out, OP4);
  not not_179 (not_179_out, F12);
  not not_180 (not_180_out, F13);
  not not_181 (not_181_out, F14);
  not not_182 (not_182_out, OP4);
  and and_1 (MemToReg, not_1_out, not_2_out, not_3_out, not_4_out, not_5_out, not_6_out, F13, not_7_out);
  and and_2 (MemWrite, not_8_out, not_9_out, not_10_out, OP5, not_11_out, not_12_out, not_13_out);
  and and_3 (and_3_out, not_14_out, not_15_out, not_16_out, not_17_out, not_18_out, F13, not_19_out);
  and and_4 (and_4_out, not_20_out, not_21_out, not_22_out, OP5, not_23_out, not_24_out, not_25_out);
  and and_5 (and_5_out, not_26_out, not_27_out, OP4, not_28_out, not_29_out, not_30_out);
  and and_6 (and_6_out, not_31_out, not_32_out, OP4, not_33_out, not_34_out, not_35_out, not_36_out, not_37_out);
  and and_7 (and_7_out, not_38_out, not_39_out, OP4, not_40_out, not_41_out, F14, not_42_out);
  and and_8 (and_8_out, not_43_out, not_44_out, OP4, not_45_out, not_46_out, F13, F14);
  and and_9 (and_9_out, OP2, not_47_out, not_48_out, OP5, OP6, not_49_out, not_50_out, not_51_out);
  and and_10 (and_10_out, not_52_out, not_53_out, not_54_out, not_55_out, not_56_out, F13, not_57_out);
  and and_11 (and_11_out, not_58_out, not_59_out, OP4, not_60_out, not_61_out, not_62_out);
  and and_12 (and_12_out, not_63_out, not_64_out, OP4, not_65_out, not_66_out, not_67_out, not_68_out, not_69_out);
  and and_13 (and_13_out, not_70_out, not_71_out, OP4, not_72_out, not_73_out, not_74_out, not_75_out, not_76_out);
  and and_14 (and_14_out, not_77_out, not_78_out, OP4, not_79_out, not_80_out, F14, not_81_out);
  and and_15 (and_15_out, not_82_out, not_83_out, OP4, not_84_out, not_85_out, F13, F14);
  and and_16 (and_16_out, not_86_out, not_87_out, OP4, not_88_out, F12, not_89_out, F14, not_90_out, F30);
  and and_17 (and_17_out, not_91_out, not_92_out, OP4, OP5, not_93_out, F13, not_94_out, not_95_out);
  and and_18 (and_18_out, OP2, not_96_out, OP5, OP6, not_97_out, not_98_out, not_99_out);
  and and_19 (and_19_out, OP2, OP3, not_100_out, OP5, OP6);
  and and_20 (SB, not_101_out, not_102_out, not_103_out, OP5, not_104_out, not_105_out, not_106_out, not_107_out);
  and and_21 (BLTU, not_108_out, not_109_out, not_110_out, OP5, OP6, not_111_out, F13, F14);
  and and_22 (ecall, not_112_out, not_113_out, OP4, OP5, OP6, not_114_out, not_115_out, not_116_out, not_117_out, not_118_out);
  and and_23 (S_Type, not_119_out, not_120_out, not_121_out, OP5, not_122_out, not_123_out, not_124_out);
  and and_24 (and_24_out, not_125_out, not_126_out, not_127_out, not_128_out, not_129_out, F13, not_130_out);
  and and_25 (and_25_out, not_131_out, not_132_out, OP4, not_133_out, not_134_out, not_135_out);
  and and_26 (and_26_out, not_136_out, not_137_out, OP4, not_138_out, not_139_out, not_140_out, not_141_out, not_142_out);
  and and_27 (and_27_out, not_143_out, not_144_out, OP4, not_145_out, not_146_out, F14, not_147_out);
  and and_28 (and_28_out, not_148_out, not_149_out, OP4, not_150_out, not_151_out, F13, F14);
  and and_29 (and_29_out, OP2, not_152_out, not_153_out, OP5, OP6, not_154_out, not_155_out, not_156_out);
  and and_30 (and_30_out, not_157_out, not_158_out, not_159_out, OP5, OP6, not_160_out, not_161_out);
  and and_31 (and_31_out, not_162_out, not_163_out, not_164_out, OP5, OP6, not_165_out, F13, F14);
  and and_32 (BEQ, not_166_out, not_167_out, not_168_out, OP5, OP6, not_169_out, not_170_out, not_171_out);
  and and_33 (BNE, not_172_out, not_173_out, not_174_out, OP5, OP6, F12, not_175_out, not_176_out);
  and and_34 (JALR, OP2, not_177_out, not_178_out, OP5, OP6, not_179_out, not_180_out, not_181_out);
  and and_35 (JAL, OP2, OP3, not_182_out, OP5, OP6);
  or or_1 (ALU_SRC, and_3_out, and_4_out, and_5_out, and_6_out, and_7_out, and_8_out, and_9_out);
  or or_2 (CSRRCI, and_24_out, and_25_out, and_26_out, and_27_out, and_28_out, and_29_out);
  or or_3 (CSRRSI, and_30_out, and_31_out);
  or or_4 (RegWrite, and_10_out, and_11_out, and_12_out, and_13_out, and_14_out, and_15_out, and_16_out, and_17_out, and_18_out, and_19_out);
endmodule

// ALU
module ALU (
  input  [31:0] X,
  input  [31:0] Y,
  input  [3:0] AluOP,
  output out_4,
  output Equal,
  output out_6,
  output [31:0] Result,
  output [31:0] Result_2
);

  wire [0:0] comparator_1_lt, comparator_2_lt;
  wire [31:0] adder_1_out, AND_out, divider_1_out, divider_1_rem, multiplier_1_cout, multiplier_1_out,
       NOR_out, OR_out, shifter_1_out, shifter_2_out, shifter_3_out, subtractor_1_out, XOR_out;

  assign AND_out = X & Y;  // AND_Gate AND, 32 bits wide
  assign OR_out = X | Y;  // OR_Gate OR, 32 bits wide
  Shifter #(.width(32), .shift("ll")) shifter_1 (.in(X), .\dist (Y[4:0]), .out(shifter_1_out));
  Shifter #(.width(32), .shift("ar")) shifter_2 (.in(X), .\dist (Y[4:0]), .out(shifter_2_out));
  Shifter #(.width(32), .shift("lr")) shifter_3 (.in(X), .\dist (Y[4:0]), .out(shifter_3_out));
  Multiplier #(.width(32)) multiplier_1 (.a(X), .b(Y), .out(multiplier_1_out), .cout(multiplier_1_cout));  // open: cin
  Divider #(.width(32)) divider_1 (.a(X), .b(Y), .out(divider_1_out), .rem(divider_1_rem));  // open: upper
  Adder #(.width(32)) adder_1 (.a(X), .b(Y), .out(adder_1_out));  // open: cin, cout
  Subtractor #(.width(32)) subtractor_1 (.a(X), .b(Y), .out(subtractor_1_out));  // open: bin, bout
  assign XOR_out = X ^ Y;  // XOR_Gate XOR, 32 bits wide
  assign NOR_out = ~(X | Y);  // NOR_Gate NOR, 32 bits wide
  Comparator #(.width(32), .mode("twosComplement")) comparator_1 (
    .a(X), .b(Y), .eq(Equal), .lt(comparator_1_lt[0]));  // open: gt
  Comparator #(.width(32), .mode("unsigned")) comparator_2 (.a(X), .b(Y), .lt(comparator_2_lt[0]));  // open: gt, eq
  Multiplexer #(.select(4), .width(32), .disabled("Z"), .enable("false")) multiplexer_1 (
    .in0(shifter_1_out), .in1(shifter_2_out), .in2(shifter_3_out), .in3(multiplier_1_out),
    .in4(divider_1_out), .in5(adder_1_out), .in6(subtractor_1_out), .in7(AND_out), .in8(OR_out),
    .in9(XOR_out), .in10(NOR_out), .in11({{31{1'b0}}, comparator_1_lt[0]}),
    .in12({{31{1'b0}}, comparator_2_lt[0]}), .in13({32{1'b0}}), .in14({32{1'b0}}), .in15({32{1'b0}}),
    .out(Result), .sel(AluOP));
  Multiplexer #(.select(4), .width(32), .disabled("Z"), .enable("false")) multiplexer_2 (
    .in0({32{1'b0}}), .in1({32{1'b0}}), .in2({32{1'b0}}), .in3(multiplier_1_cout), .in4(divider_1_rem),
    .in5({32{1'b0}}), .in6({32{1'b0}}), .in7({32{1'b0}}), .in8({32{1'b0}}), .in9({32{1'b0}}),
    .in10({32{1'b0}}), .in11({32{1'b0}}), .in12({32{1'b0}}), .in13({32{1'b0}}), .in14({32{1'b0}}),
    .in15({32{1'b0}}), .out(Result_2), .sel(AluOP));
  Multiplexer #(.select(4), .width(1), .disabled("Z"), .enable("false")) multiplexer_3 (
    .in0(1'b0), .in1(1'b0), .in2(1'b0), .in3(1'b0), .in4(1'b0), .in5(1'b0), .in6(1'b0), .in7(1'b0),
    .in8(1'b0), .in9(1'b0), .in10(1'b0), .in11(comparator_1_lt[0]), .in12(comparator_2_lt[0]), .in13(1'b0),
    .in14(1'b0), .in15(1'b0), .out(out_6), .sel(AluOP));
  not not_1 (out_4, out_6);

  // Other names for the same wires on the sheet: Result2[31:0] = Result_2; S[3:0] = AluOP; tunnel = out_6;
  //   tunnel_t = out_4

  // Notes on the sheet:
  //   不要改变此引脚区域内容，也不要改变ALU封装形式
  //   输入引脚
  //   输出引脚
endmodule

module Regifile (
  input  [31:0] Din,
  input  Clk,
  input  WE,
  input  [4:0] R1_num,
  input  [4:0] W_num,
  input  [4:0] R2_num,
  output [31:0] R1,
  output [31:0] R2
);

  // RegisterFile registerfile_1: pin names not known; wires that end beside it: Din, Clk, WE, W_num, R1_num, R2_num, R1, R2
endmodule

module \理想流水线  (
  output RegWrite,
  output MemWrite,
  output [31:0] IF_PC,
  output [31:0] ID_PC,
  output [31:0] EX_PC,
  output [31:0] M_PC,
  output [31:0] WB_PC,
  output [31:0] RDin,
  output [31:0] MDin,
  output [31:0] LedData
);

  wire alu_1_equal, AluSrcB, and_2_out, and_3_out, and_4_out, and_5_out, BLTU, branch, CLK, clock_1_out,
       comparator_1_lt, comparator_2_eq, comparator_3_eq, comparator_3_lt, d_ff_1_q, ecall, ex_mem_1_haltout,
       ex_mem_1_memtoreginout, ex_mem_1_reqwriteout, Go, halt, id_ex_1_beqout, id_ex_1_bneout,
       id_ex_1_regwriteout, IR1, IR2, IR3, JAL, JALex, JALR, JALRex, LedFlag, mem_wb_1_memtoregout, MemToReg,
       MemW, nand_1_out, not_1_out, not_2_out, not_3_out, not_4_out, or_1_out, or_2_out, riscv_probe_6_p2,
       RST, S_Type, SB, SBMem, W1, W2, W3, \单周期硬布线控制器_1_alu_src , \单周期硬布线控制器_1_beq , \单周期硬布线控制器_1_bltu ,
       \单周期硬布线控制器_1_bne , \单周期硬布线控制器_1_ecall , \单周期硬布线控制器_1_jal , \单周期硬布线控制器_1_jalr , \单周期硬布线控制器_1_memtoreg ,
       \单周期硬布线控制器_1_memwrite , \单周期硬布线控制器_1_regwrite , \单周期硬布线控制器_1_sb ;
  wire [1:0] select;
  wire [3:0] AluOP, mips_ram_1_p4, multiplexer_13_out, \单周期硬布线控制器_1_alu_op ;
  wire [4:0] bit_extender_4_out, multiplexer_4_out, multiplexer_6_out, multiplexer_7_out, shifter_3_out,
       W_in, W_out, W_outex, W_outmem;
  wire [11:0] multiplexer_8_out, shifter_1_out;
  wire [12:0] CNT_num;
  wire [15:0] \LoadUse次数 , \总周期数 , \插入气泡数 , \无条件分支数 , \条件分支成功数 ;
  wire [19:0] shifter_2_out;
  wire [31:0] adder_1_out, alu_1_result, and_1_out, branchdata, EX_IR, ex_mem_1_aluout, id_ex_1_imm2out,
       id_ex_1_imm3out, ID_IR, IF_IR, Imm1, Imm2, Imm3, jaldata, jalrin, JmpoutMem, MDinexe, MDinMem, MEM_IR,
       mem_wb_1_dout, mem_wb_1_jmpout, mips_ram_1_p6, multiplexer_1_out, multiplexer_2_out,
       multiplexer_3_out, multiplexer_9_out, multiplexer_10_out, PC_4, R1Data, regifile_1_r1, regifile_1_r2,
       shifter_4_out, WB_IR;

  Button \u_总复位  (.out(RST));
  Button _1 (.out(IR1));
  Button _2 (.out(IR2));
  Button _3 (.out(IR3));
  // Probe on \总周期数 
  // Probe on \总周期数 
  Button \u_继续运行  (.out(Go));
  LED #(.active("true")) led_1 (.in(W1));
  LED #(.active("true")) led_2 (.in(W2));
  LED #(.active("true")) led_3 (.in(W3));
  Multiplexer #(.select(1), .width(32), .disabled("Z"), .enable("false")) multiplexer_1 (
    .in0(PC_4), .in1(and_1_out), .out(multiplexer_1_out), .sel(JALR));
  Hex_Digit_Display hex_digit_display_1 (.value(LedData[31:28]));  // open: dp
  // Probe on IF_PC[19:0]
  // RiscV_Probe riscv_probe_1: pin names not known; wires that end beside it: IF_IR
  assign and_1_out = 32'hfffffffe & adder_1_out;  // AND_Gate and_1, 32 bits wide
  Multiplexer #(.select(1), .width(32), .disabled("Z"), .enable("false")) multiplexer_2 (
    .in0(multiplexer_1_out), .in1(jaldata), .out(multiplexer_2_out), .sel(JAL));
  Multiplexer #(.select(1), .width(32), .disabled("Z"), .enable("false")) multiplexer_3 (
    .in0(multiplexer_2_out), .in1(branchdata), .out(multiplexer_3_out), .sel(branch));
  or or_1 (or_1_out, Go, not_1_out);
  Hex_Digit_Display hex_digit_display_2 (.value(LedData[27:24]));  // open: dp
  Hex_Digit_Display hex_digit_display_3 (.value(LedData[23:20]));  // open: dp
  // Probe on ID_PC[19:0]
  // RiscV_Probe riscv_probe_2: pin names not known; wires that end beside it: ID_IR
  Adder #(.width(32)) adder_1 (.a(jalrin), .b(R1Data), .out(adder_1_out));  // open: cin, cout
  Register #(.width(32), .trigger("rising"), .Select("low")) PC (
    .D(multiplexer_3_out), .en(or_1_out), .Q(IF_PC), .clk(CLK), .clr(RST));
  not not_1 (not_1_out, halt);
  Hex_Digit_Display hex_digit_display_4 (.value(LedData[19:16]));  // open: dp
  Hex_Digit_Display hex_digit_display_5 (.value(LedData[15:12]));  // open: dp
  Adder #(.width(32)) adder_2 (.a(IF_PC), .b(32'h4), .out(PC_4));  // open: cin, cout
  not not_2 (not_2_out, halt);
  Hex_Digit_Display hex_digit_display_6 (.value(LedData[11:8]));  // open: dp
  Hex_Digit_Display hex_digit_display_7 (.value(LedData[7:4]));  // open: dp
  // Probe on EX_PC[19:0]
  // RiscV_Probe riscv_probe_3: pin names not known; wires that end beside it: EX_IR
  Counter #(.width(16), .max('hffff), .ongoal("wrap"), .trigger("rising"), .behavior("new")) counter_1 (
    .count(not_2_out), .Q(\总周期数 ), .clk(CLK));  // open: load, D, carry, clr, preset, down
  Hex_Digit_Display hex_digit_display_8 (.value(LedData[3:0]));  // open: dp
  ROM #(.addrWidth(10), .dataWidth(32), .Select("high")) rom_1 (.addr(IF_PC[11:2]), .data(IF_IR));
  // Probe on \总周期数 
  // Probe on M_PC[19:0]
  // RiscV_Probe riscv_probe_4: pin names not known; wires that end beside it: MEM_IR
  IF_ID if_id_1 (
    .PCin(IF_PC), .IRin(IF_IR), .CLK(CLK), .PCout(ID_PC), .IRout(ID_IR));  // open: 同步清零_气泡_高电平有效, 使能端_低电平有效_stall_高电平有效, Pjmpin, Pjmpout
  // Probe on \总周期数 
  // Probe on \无条件分支数 
  // Probe on \条件分支成功数 
  // Probe on \插入气泡数 
  // Probe on \LoadUse次数 
  // RiscV_Probe riscv_probe_5: pin names not known; wires that end beside it: ID_IR
  // Probe on IF_PC[11:0]
  // Probe on WB_PC[19:0]
  // RiscV_Probe riscv_probe_6: pin names not known; wires that end beside it: WB_IR, riscv_probe_6_p2
  Multiplexer #(.select(1), .width(5), .disabled("Z"), .enable("false")) multiplexer_4 (
    .in0(ID_IR[24:20]), .in1(5'b00001), .out(multiplexer_4_out), .sel(JALR));
  Multiplexer #(.select(1), .width(5), .disabled("Z"), .enable("false")) multiplexer_5 (
    .in0(ID_IR[11:7]), .in1(5'b00001), .out(W_in), .sel(JALR));
  Register #(.width(32), .trigger("rising"), .Select("low")) PC_2 (
    .D(MDin), .en(LedFlag), .Q(LedData), .clk(CLK));  // open: clr
  // Probe on ID_PC[11:0]
  // Probe on EX_PC[11:0]
  \单周期硬布线控制器  \u_单周期硬布线控制器_1  (
    .Funct({ID_IR[30], ID_IR[25], ID_IR[14:12]}), .OP(ID_IR[6:2]), .ALU_OP(\单周期硬布线控制器_1_alu_op ),
    .MemToReg(\单周期硬布线控制器_1_memtoreg ), .MemWrite(\单周期硬布线控制器_1_memwrite ), .ALU_SRC(\单周期硬布线控制器_1_alu_src ),
    .RegWrite(\单周期硬布线控制器_1_regwrite ), .ecall(\单周期硬布线控制器_1_ecall ), .in_3(ID_IR[21]),
    .uret(riscv_probe_6_p2), .JAL(\单周期硬布线控制器_1_jal ), .SB(\单周期硬布线控制器_1_sb ), .Jalr(\单周期硬布线控制器_1_jalr ),
    .BLTU(\单周期硬布线控制器_1_bltu ), .Bne(\单周期硬布线控制器_1_bne ), .Beq(\单周期硬布线控制器_1_beq ), .S_type(S_Type));  // open: I, B
  // Probe on multiplexer_6_out
  Multiplexer #(.select(1), .width(5), .disabled("Z"), .enable("false")) multiplexer_6 (
    .in0(ID_IR[19:15]), .in1(5'b10001), .out(multiplexer_6_out), .sel(\单周期硬布线控制器_1_ecall ));
  Multiplexer #(.select(1), .width(5), .disabled("Z"), .enable("false")) multiplexer_7 (
    .in0(multiplexer_4_out), .in1(5'b01010), .out(multiplexer_7_out), .sel(\单周期硬布线控制器_1_ecall ));
  // Probe on W_in
  assign Imm1 = {{20{multiplexer_8_out[11]}}, multiplexer_8_out};  // Bit_Extender bit_extender_1
  Multiplexer #(.select(1), .width(12), .disabled("Z"), .enable("false")) multiplexer_8 (
    .in0(ID_IR[31:20]), .in1({ID_IR[31:25], ID_IR[11:7]}), .out(multiplexer_8_out), .sel(S_Type));
  assign Imm2 = {{20{shifter_1_out[11]}}, shifter_1_out};  // Bit_Extender bit_extender_2
  Shifter #(.width(12), .shift("ll")) shifter_1 (
    .in({ID_IR[31], ID_IR[7], ID_IR[30:25], ID_IR[11:8]}), .\dist (4'b0001), .out(shifter_1_out));
  Shifter #(.width(20), .shift("ll")) shifter_2 (
    .in({ID_IR[31], ID_IR[19:12], ID_IR[20], ID_IR[30:21]}), .\dist (5'b00001), .out(shifter_2_out));
  // Probe on M_PC[11:0]
  assign Imm3 = {{12{shifter_2_out[19]}}, shifter_2_out};  // Bit_Extender bit_extender_3
  // Probe on WB_PC[11:0]
  Regifile regifile_1 (
    .Din(RDin), .Clk(CLK), .R1(regifile_1_r1), .R2(regifile_1_r2), .WE(RegWrite), .W_num(W_out),
    .R1_num(multiplexer_6_out), .R2_num(multiplexer_7_out));
  ID_EX id_ex_1 (
    .Beqin(\单周期硬布线控制器_1_beq ), .Bnein(\单周期硬布线控制器_1_bne ), .MemToRegin(\单周期硬布线控制器_1_memtoreg ),
    .MemWritein(\单周期硬布线控制器_1_memwrite ), .ALUopin(\单周期硬布线控制器_1_alu_op ), .ALUSRCBin(\单周期硬布线控制器_1_alu_src ),
    .RegWritein(\单周期硬布线控制器_1_regwrite ), .Ecallin(\单周期硬布线控制器_1_ecall ), .Jarin(\单周期硬布线控制器_1_jal ),
    .Jarlin(\单周期硬布线控制器_1_jalr ), .Bltuin(\单周期硬布线控制器_1_bltu ), .R2in(regifile_1_r2), .R1in(regifile_1_r1),
    .PCin(ID_PC), .Imm1in(Imm1), .CLK(CLK), .Beqout(id_ex_1_beqout), .Bneout(id_ex_1_bneout),
    .MemToReginout(MemToReg), .MemWriteout(MemW), .ALUopout(AluOP), .ALUSRCBout(AluSrcB),
    .RegWriteout(id_ex_1_regwriteout), .Ecallout(ecall), .Jarout(JALex), .Jarlout(JALRex), .Bltuout(BLTU),
    .R2out(MDinexe), .R1out(R1Data), .PCout(EX_PC), .Imm1out(jalrin), .Stypein(S_Type),
    .SBin(\单周期硬布线控制器_1_sb ), .SBout(SB), .W_in(W_in), .W_out(W_outex), .Imm2in(Imm2),
    .Imm2out(id_ex_1_imm2out), .Imm3in(Imm3), .Imm3out(id_ex_1_imm3out), .IRin(ID_IR), .IRout(EX_IR));  // open: Uretin, Uretout, 同步清零_气泡_高电平有效, Stypeout, Stall, fwdR1in, fwdR1out, fwdR2in, fwdR2out, pjmpin, pjmpout
  Multiplexer #(.select(1), .width(32), .disabled("Z"), .enable("false")) multiplexer_9 (
    .in0(MDinexe), .in1(jalrin), .out(multiplexer_9_out), .sel(AluSrcB));
  Adder #(.width(32)) adder_3 (.a(id_ex_1_imm2out), .b(EX_PC), .out(branchdata));  // open: cin, cout
  Comparator #(.width(32), .mode("unsigned")) comparator_1 (
    .a(R1Data), .b(MDinexe), .lt(comparator_1_lt));  // open: gt, eq
  Comparator #(.width(32), .mode("twosComplement")) comparator_2 (
    .a(R1Data), .b(32'h22), .eq(comparator_2_eq));  // open: gt, lt
  Adder #(.width(32)) adder_4 (.a(id_ex_1_imm3out), .b(EX_PC), .out(jaldata));  // open: cin, cout
  and and_2 (and_2_out, alu_1_equal, id_ex_1_beqout);
  not not_3 (not_3_out, alu_1_equal);
  and and_3 (and_3_out, not_3_out, id_ex_1_bneout);
  ALU alu_1 (
    .X(R1Data), .Y(multiplexer_9_out), .AluOP(AluOP), .Equal(alu_1_equal), .Result(alu_1_result));  // open: Result_2, out_4, out_6
  Multiplexer #(.select(1), .width(32), .disabled("Z"), .enable("false")) multiplexer_10 (
    .in0(alu_1_result), .in1(PC_4), .out(multiplexer_10_out), .sel(or_2_out));
  or or_2 (or_2_out, JALex, JALRex);
  not not_4 (not_4_out, comparator_2_eq);
  D_Flip_Flop #(.trigger("high"), .Pre_Clr_Positions("LEGACY"), .NegatePresetClear("false"), .enable("true"), .NewFFLayout("false")) d_ff_1 (.Q(d_ff_1_q));  // open: clk, D, Qn, preset, en, reset
  or or_3 (branch, and_2_out, and_3_out, and_4_out);
  and and_4 (and_4_out, BLTU, comparator_1_lt);
  and and_5 (and_5_out, ecall, not_4_out);
  and and_6 (LedFlag, ecall, comparator_2_eq);
  // Probe on 13'hc
  Clock #(.highDuration(1), .lowDuration(1)) clock_1 (.out(clock_1_out));
  EX_MEM ex_mem_1 (
    .SBin(SB), .RegWritein(id_ex_1_regwriteout), .MemToRegin(MemToReg), .MemWritein(MemW),
    .haltin(and_5_out), .W_lin(W_outex), .Aluin(alu_1_result), .PCin(EX_PC), .Selectin(alu_1_result[1:0]),
    .Jmpin(multiplexer_10_out), .Mdin(MDinexe), .CLK(CLK), .SBout(SBMem), .ReqWriteout(ex_mem_1_reqwriteout),
    .MemToReginout(ex_mem_1_memtoreginout), .MemWriteout(MemWrite), .haltout(ex_mem_1_haltout),
    .w_out(W_outmem), .Aluout(ex_mem_1_aluout), .PCout(M_PC), .Selectout(select), .Jmpout(JmpoutMem),
    .MdinoutMem(MDinMem), .IRin(EX_IR), .IRout(MEM_IR), .jarlin(JALRex));  // open: ALUSRCBin, Ecallin, Jarin, Uretin, ALUSRCBout, Ecallout, Jarout, Uretout, 同步清零_气泡_高电平有效, 使能端_低电平有效_stall_高电平有效, jarlout, R1in, R1out, R2in, R2out
  Comparator #(.width(13), .mode("twosComplement")) comparator_3 (
    .a(CNT_num), .b(13'hc), .eq(comparator_3_eq), .lt(comparator_3_lt));  // open: gt
  Multiplexer #(.select(1), .width(32), .disabled("Z"), .enable("false")) multiplexer_11 (
    .in0(MDinMem), .in1(shifter_4_out), .out(MDin), .sel(SBMem));
  assign bit_extender_4_out = {{3{select[1]}}, select};  // Bit_Extender bit_extender_4
  Shifter #(.width(5), .shift("ll")) shifter_3 (.in(bit_extender_4_out), .\dist (3'b011), .out(shifter_3_out));
  nand nand_1 (nand_1_out, d_ff_1_q, comparator_3_eq);
  Counter #(.width(13), .max('h1fff), .ongoal("stay"), .trigger("rising"), .behavior("old")) counter_2 (
    .count(comparator_3_lt), .Q(CNT_num), .clk(clock_1_out));  // open: load, D, carry, clr, preset
  assign CLK = nand_1_out ? clock_1_out : 1'bz;  // Controlled_Buffer controlled_buffer_1
  Pull_Resistor #(.pull(1)) pull_resistor_1 (.node(CLK));
  Shifter #(.width(32), .shift("ll")) shifter_4 (.in(MDinMem), .\dist (shifter_3_out), .out(shifter_4_out));
  // MIPS_RAM mips_ram_1: pin names not known; wires that end beside it: ex_mem_1_aluout[11:2], MDin, MemWrite, mips_ram_1_p4, CLK, mips_ram_1_p6
  Multiplexer #(.select(1), .width(4), .disabled("Z"), .enable("false")) multiplexer_12 (
    .in0(4'b1111), .in1(multiplexer_13_out), .out(mips_ram_1_p4), .sel(SBMem));
  Multiplexer #(.select(2), .width(4), .disabled("Z"), .enable("false")) multiplexer_13 (
    .in0(4'b0001), .in1(4'b0010), .in2(4'b0100), .in3(4'b1000), .out(multiplexer_13_out), .sel(select));
  MEM_WB mem_wb_1 (
    .MemToRegin(ex_mem_1_memtoreginout), .RegWritein(ex_mem_1_reqwriteout), .haltin(ex_mem_1_haltout),
    .Din(mips_ram_1_p6), .PCin(M_PC), .Jmpin(JmpoutMem), .W_in(W_outmem), .CLK(CLK),
    .MemToRegout(mem_wb_1_memtoregout), .RegWriteout(RegWrite), .haltout(halt), .Dout(mem_wb_1_dout),
    .PCout(WB_PC), .Jmpout(mem_wb_1_jmpout), .W_out(W_out), .IRin(MEM_IR), .IRout(WB_IR));  // open: Ecallin, Jarin, Jarlin, Uretin, Selectin, Ecallout, Jarout, Jarlout, Uretout, Selectout, 同步清零_气泡_高电平有效, 使能端_低电平有效_stall_高电平有效, R1in, R1out, R2in, R2out
  Multiplexer #(.select(1), .width(32), .disabled("Z"), .enable("false")) multiplexer_14 (
    .in0(mem_wb_1_jmpout), .in1(mem_wb_1_dout), .out(RDin), .sel(mem_wb_1_memtoregout));

  // Other names for the same wires on the sheet: IR[31:0] = IF_IR; PC[31:0] = IF_PC; PC1[31:0] = ID_PC;
  //   PC2[31:0] = EX_PC; MEM_PC[31:0] = M_PC; PC3[31:0] = M_PC; PC4[31:0] = WB_PC

  // Notes on the sheet:
  //   中断源
  //   时空图监测，可删除
  //   中断等待指示
  //   数码管输出
  //   指令存储器
  //   contents of rom_1 (hex, n*v repeats v):
  //   413 493 913 993 46413 14e493 296913 39e993 842023 942223 1242423 1342623 a00893 493 913 993 73
  //   指令探针
  //   指令字
  //   Beq
  //   Bne
  //   MemToReg
  //   MemWrite
  //   AluOP
  //   AluSrcB
  //   RegWrite
  //   流水调试日志用
  //   用这个时钟源需要去掉电路中的其他时钟源
  //   为方便自动评测，需要输出流水线各段保存的PC值，注意是PC不是PC+4，另外ID段寄存器写入信息，Mem段内存写入信息也要输出
  //   控制位
  //   暂停节拍，不能为0
  //   数据存储器
  //   戳工具置1进入计数暂停模式，ctrl+k时钟自动运行到对应节拍暂停
  //   ctrl+k关闭时钟连续运行，将控制位置零，进入单步调试模式调试
  //   可计数暂停的时钟源
endmodule

module \气泡流水线  (
  output RegWrite,
  output MemWrite,
  output [31:0] IF_PC,
  output [31:0] ID_PC,
  output [31:0] EX_PC,
  output [31:0] M_PC,
  output [31:0] WB_PC,
  output [31:0] RDin,
  output [31:0] MDin,
  output [31:0] LedData
);

  wire alu_1_equal, AluSrcB, and_2_out, and_3_out, and_4_out, and_5_out, and_6_out, and_7_out, and_8_out,
       and_9_out, BLTU, branch, CLEAR, CLK, clock_1_out, comparator_1_eq, comparator_1_lt, comparator_2_lt,
       comparator_3_eq, d_ff_1_q, Ecall, ecall_t, ex_mem_1_haltout, ex_mem_1_jarlout, ex_mem_1_jarout,
       ex_mem_1_memtoreginout, exregwrite, Go, halt, id_ex_1_beqout, id_ex_1_bneout, if_id_1_pjmpout, IR1,
       IR2, IR3, JALex, JALRex, mem_wb_1_jarlout, mem_wb_1_jarout, mem_wb_1_memtoregout, MemRegWrite,
       MemToReg, MemW, nand_1_out, not_1_out, not_2_out, not_3_out, not_4_out, not_5_out, not_6_out,
       not_7_out, not_8_out, not_9_out, or_1_out, or_4_out, or_5_out, or_7_out, or_8_out, riscv_probe_5_p2,
       RST, S_Type, SB, SBMem, Stall, W1, W2, W3, \单周期硬布线控制器_1_alu_src , \单周期硬布线控制器_1_beq ,
       \单周期硬布线控制器_1_bltu , \单周期硬布线控制器_1_bne , \单周期硬布线控制器_1_ecall , \单周期硬布线控制器_1_jal , \单周期硬布线控制器_1_jalr ,
       \单周期硬布线控制器_1_memtoreg , \单周期硬布线控制器_1_memwrite , \单周期硬布线控制器_1_regwrite , \单周期硬布线控制器_1_sb ;
  wire [1:0] select;
  wire [3:0] AluOP, mips_ram_1_p4, multiplexer_13_out, \单周期硬布线控制器_1_alu_op ;
  wire [4:0] bit_extender_4_out, multiplexer_4_out, multiplexer_6_out, multiplexer_7_out, shifter_3_out,
       W_in, W_out, W_outex, W_outmem;
  wire [11:0] multiplexer_8_out, shifter_1_out;
  wire [12:0] CNT_num;
  wire [15:0] \LoadUse次数 , \总周期数 , \插入气泡数 , \无条件分支数 , \条件分支成功数 ;
  wire [19:0] shifter_2_out;
  wire [31:0] adder_1_out, adder_5_out, alu_1_result, and_1_out, branchdata, EX_IR, ex_mem_1_aluout,
       ex_mem_1_r1out, ex_mem_1_r2out, id_ex_1_imm2out, id_ex_1_imm3out, ID_IR, IF_IR, Imm1, Imm2, Imm3,
       jaldata, jalrin, JmpoutMem, MDinexe, MDinMem, MEM_IR, mem_wb_1_dout, mem_wb_1_jmpout, mips_ram_1_p6,
       multiplexer_1_out, multiplexer_2_out, multiplexer_3_out, multiplexer_9_out, multiplexer_10_out,
       multiplexer_14_out, PC_4, R1, R1Data, R2, regifile_1_r1, regifile_1_r2, shifter_4_out, WB_IR;

  Button \u_总复位  (.out(RST));
  Button _1 (.out(IR1));
  Button _2 (.out(IR2));
  Button _3 (.out(IR3));
  // Probe on \总周期数 
  // Probe on \总周期数 
  Button \u_继续运行  (.out(Go));
  LED #(.active("true")) led_1 (.in(W1));
  LED #(.active("true")) led_2 (.in(W2));
  LED #(.active("true")) led_3 (.in(W3));
  Multiplexer #(.select(1), .width(32), .disabled("Z"), .enable("false")) multiplexer_1 (
    .in0(PC_4), .in1(and_1_out), .out(multiplexer_1_out), .sel(JALRex));
  Hex_Digit_Display hex_digit_display_1 (.value(LedData[31:28]));  // open: dp
  // Probe on IF_PC[19:0]
  // RiscV_Probe riscv_probe_1: pin names not known; wires that end beside it: IF_IR
  assign and_1_out = 32'hfffffffe & adder_1_out;  // AND_Gate and_1, 32 bits wide
  Multiplexer #(.select(1), .width(32), .disabled("Z"), .enable("false")) multiplexer_2 (
    .in0(multiplexer_1_out), .in1(jaldata), .out(multiplexer_2_out), .sel(JALex));
  Multiplexer #(.select(1), .width(32), .disabled("Z"), .enable("false")) multiplexer_3 (
    .in0(multiplexer_2_out), .in1(branchdata), .out(multiplexer_3_out), .sel(branch));
  Hex_Digit_Display hex_digit_display_2 (.value(LedData[23:20]));  // open: dp
  Hex_Digit_Display hex_digit_display_3 (.value(LedData[27:24]));  // open: dp
  // Probe on ID_PC[19:0]
  // RiscV_Probe riscv_probe_2: pin names not known; wires that end beside it: ID_IR
  Adder #(.width(32)) adder_1 (.a(jalrin), .b(R1Data), .out(adder_1_out));  // open: cin, cout
  Register #(.width(32), .trigger("rising"), .Select("low")) PC (
    .D(multiplexer_3_out), .en(not_1_out), .Q(IF_PC), .clk(CLK), .clr(RST));
  not not_1 (not_1_out, or_1_out);
  or or_1 (or_1_out, halt, Stall);
  Hex_Digit_Display hex_digit_display_4 (.value(LedData[19:16]));  // open: dp
  Hex_Digit_Display hex_digit_display_5 (.value(LedData[15:12]));  // open: dp
  Adder #(.width(32)) adder_2 (.a(IF_PC), .b(32'h4), .out(PC_4));  // open: cin, cout
  not not_2 (not_2_out, halt);
  Hex_Digit_Display hex_digit_display_6 (.value(LedData[11:8]));  // open: dp
  Hex_Digit_Display hex_digit_display_7 (.value(LedData[7:4]));  // open: dp
  // Probe on EX_PC[19:0]
  // RiscV_Probe riscv_probe_3: pin names not known; wires that end beside it: EX_IR
  Counter #(.width(16), .max('hffff), .ongoal("wrap"), .trigger("rising"), .behavior("new")) counter_1 (
    .count(not_2_out), .Q(\总周期数 ), .clk(CLK));  // open: load, D, carry, clr, preset, down
  Hex_Digit_Display hex_digit_display_8 (.value(LedData[3:0]));  // open: dp
  ROM #(.addrWidth(10), .dataWidth(32), .Select("high")) rom_1 (.addr(IF_PC[11:2]), .data(IF_IR));
  or or_2 (CLEAR, branch, JALex, JALRex);
  // Probe on \总周期数 
  // Probe on M_PC[19:0]
  // RiscV_Probe riscv_probe_4: pin names not known; wires that end beside it: MEM_IR
  IF_ID if_id_1 (
    .PCin(IF_PC), .IRin(IF_IR), .CLK(CLK), .PCout(ID_PC), .IRout(ID_IR), .\同步清零_气泡_高电平有效 (CLEAR),
    .\使能端_低电平有效_stall_高电平有效 (if_id_1_pjmpout), .Pjmpout(if_id_1_pjmpout));  // open: Pjmpin
  // Probe on \总周期数 
  // Probe on \无条件分支数 
  // Probe on \条件分支成功数 
  // Probe on \插入气泡数 
  // Probe on \LoadUse次数 
  // RiscV_Probe riscv_probe_5: pin names not known; wires that end beside it: ID_IR, riscv_probe_5_p2
  or or_3 (if_id_1_pjmpout, halt, Stall);
  // Probe on IF_PC[11:0]
  // Probe on WB_PC[19:0]
  // RiscV_Probe riscv_probe_6: pin names not known; wires that end beside it: WB_IR
  Multiplexer #(.select(1), .width(5), .disabled("Z"), .enable("false")) multiplexer_4 (
    .in0(ID_IR[24:20]), .in1(5'b00001), .out(multiplexer_4_out), .sel(JALRex));
  Multiplexer #(.select(1), .width(5), .disabled("Z"), .enable("false")) multiplexer_5 (
    .in0(ID_IR[11:7]), .in1(5'b00001), .out(W_in), .sel(JALRex));
  // Probe on EX_PC[11:0]
  // Probe on ID_PC[11:0]
  \单周期硬布线控制器  \u_单周期硬布线控制器_1  (
    .Funct({ID_IR[30], ID_IR[25], ID_IR[14:12]}), .OP(ID_IR[6:2]), .ALU_OP(\单周期硬布线控制器_1_alu_op ),
    .MemToReg(\单周期硬布线控制器_1_memtoreg ), .MemWrite(\单周期硬布线控制器_1_memwrite ), .ALU_SRC(\单周期硬布线控制器_1_alu_src ),
    .RegWrite(\单周期硬布线控制器_1_regwrite ), .ecall(\单周期硬布线控制器_1_ecall ), .in_3(ID_IR[21]),
    .uret(riscv_probe_5_p2), .JAL(\单周期硬布线控制器_1_jal ), .SB(\单周期硬布线控制器_1_sb ), .Jalr(\单周期硬布线控制器_1_jalr ),
    .BLTU(\单周期硬布线控制器_1_bltu ), .Bne(\单周期硬布线控制器_1_bne ), .Beq(\单周期硬布线控制器_1_beq ), .S_type(S_Type));  // open: I, B
  Multiplexer #(.select(1), .width(5), .disabled("Z"), .enable("false")) multiplexer_6 (
    .in0(ID_IR[19:15]), .in1(5'b10001), .out(multiplexer_6_out), .sel(\单周期硬布线控制器_1_ecall ));
  Multiplexer #(.select(1), .width(5), .disabled("Z"), .enable("false")) multiplexer_7 (
    .in0(multiplexer_4_out), .in1(5'b01010), .out(multiplexer_7_out), .sel(\单周期硬布线控制器_1_ecall ));
  // Probe on W_in
  assign Imm1 = {{20{multiplexer_8_out[11]}}, multiplexer_8_out};  // Bit_Extender bit_extender_1
  Multiplexer #(.select(1), .width(12), .disabled("Z"), .enable("false")) multiplexer_8 (
    .in0(ID_IR[31:20]), .in1({ID_IR[31:25], ID_IR[11:7]}), .out(multiplexer_8_out), .sel(S_Type));
  assign Imm2 = {{20{shifter_1_out[11]}}, shifter_1_out};  // Bit_Extender bit_extender_2
  Shifter #(.width(12), .shift("ll")) shifter_1 (
    .in({ID_IR[31], ID_IR[7], ID_IR[30:25], ID_IR[11:8]}), .\dist (4'b0001), .out(shifter_1_out));
  Shifter #(.width(20), .shift("ll")) shifter_2 (
    .in({ID_IR[31], ID_IR[19:12], ID_IR[20], ID_IR[30:21]}), .\dist (5'b00001), .out(shifter_2_out));
  // Probe on M_PC[11:0]
  D_Flip_Flop #(.trigger("high"), .Pre_Clr_Positions("LEGACY"), .NegatePresetClear("false"), .enable("true"), .NewFFLayout("false")) d_ff_1 (.Q(d_ff_1_q));  // open: clk, D, Qn, preset, en, reset
  // Probe on 13'h11a
  // Probe on multiplexer_7_out
  assign Imm3 = {{12{shifter_2_out[19]}}, shifter_2_out};  // Bit_Extender bit_extender_3
  // Probe on WB_PC[11:0]
  Comparator #(.width(13), .mode("twosComplement")) comparator_1 (
    .a(CNT_num), .b(13'h11a), .eq(comparator_1_eq), .lt(comparator_1_lt));  // open: gt
  Clock #(.highDuration(1), .lowDuration(1)) clock_1 (.out(clock_1_out));
  \相关处理逻辑  \u_相关处理逻辑_1  (
    .ExRegWrite(exregwrite), .OP(ID_IR[6:2]), .FUNC({ID_IR[30], ID_IR[25], ID_IR[14:12]}),
    .R1(multiplexer_6_out), .EXREG(EX_IR[11:7]), .R2(multiplexer_7_out), .MEMREG(MEM_IR[11:7]),
    .MemRegWrite(MemRegWrite), .R1MemRe(Stall));  // open: exop, LoadUse, R1EXRE, DH, R2EXRE, R2MemRe
  Regifile regifile_1 (
    .Din(RDin), .Clk(CLK), .R1(regifile_1_r1), .R2(regifile_1_r2), .WE(RegWrite), .W_num(W_out),
    .R1_num(multiplexer_6_out), .R2_num(multiplexer_7_out));
  nand nand_1 (nand_1_out, d_ff_1_q, comparator_1_eq);
  Counter #(.width(13), .max('h1fff), .ongoal("stay"), .trigger("rising"), .behavior("old")) counter_2 (
    .count(comparator_1_lt), .Q(CNT_num), .clk(clock_1_out));  // open: load, D, carry, clr, preset
  ID_EX id_ex_1 (
    .Beqin(\单周期硬布线控制器_1_beq ), .Bnein(\单周期硬布线控制器_1_bne ), .MemToRegin(\单周期硬布线控制器_1_memtoreg ),
    .MemWritein(\单周期硬布线控制器_1_memwrite ), .ALUopin(\单周期硬布线控制器_1_alu_op ), .ALUSRCBin(\单周期硬布线控制器_1_alu_src ),
    .RegWritein(\单周期硬布线控制器_1_regwrite ), .Ecallin(\单周期硬布线控制器_1_ecall ), .Jarin(\单周期硬布线控制器_1_jal ),
    .Jarlin(\单周期硬布线控制器_1_jalr ), .Bltuin(\单周期硬布线控制器_1_bltu ), .R2in(regifile_1_r2), .R1in(regifile_1_r1),
    .PCin(ID_PC), .Imm1in(Imm1), .CLK(CLK), .Beqout(id_ex_1_beqout), .Bneout(id_ex_1_bneout),
    .MemToReginout(MemToReg), .MemWriteout(MemW), .ALUopout(AluOP), .ALUSRCBout(AluSrcB),
    .RegWriteout(exregwrite), .Ecallout(ecall_t), .Jarout(JALex), .Jarlout(JALRex), .Bltuout(BLTU),
    .R2out(MDinexe), .R1out(R1Data), .PCout(EX_PC), .Imm1out(jalrin), .\同步清零_气泡_高电平有效 (or_4_out),
    .Stypein(S_Type), .SBin(\单周期硬布线控制器_1_sb ), .SBout(SB), .W_in(W_in), .W_out(W_outex), .Imm2in(Imm2),
    .Imm2out(id_ex_1_imm2out), .Imm3in(Imm3), .Imm3out(id_ex_1_imm3out), .IRin(ID_IR), .IRout(EX_IR),
    .Stall(halt));  // open: Uretin, Uretout, Stypeout, fwdR1in, fwdR1out, fwdR2in, fwdR2out, pjmpin, pjmpout
  or or_4 (or_4_out, Stall, CLEAR);
  assign CLK = nand_1_out ? clock_1_out : 1'bz;  // Controlled_Buffer controlled_buffer_1
  Pull_Resistor #(.pull(1)) pull_resistor_1 (.node(CLK));
  Multiplexer #(.select(1), .width(32), .disabled("Z"), .enable("false")) multiplexer_9 (
    .in0(MDinexe), .in1(jalrin), .out(multiplexer_9_out), .sel(AluSrcB));
  Adder #(.width(32)) adder_3 (.a(id_ex_1_imm2out), .b(EX_PC), .out(branchdata));  // open: cin, cout
  Comparator #(.width(32), .mode("unsigned")) comparator_2 (
    .a(R1Data), .b(MDinexe), .lt(comparator_2_lt));  // open: gt, eq
  Adder #(.width(32)) adder_4 (.a(id_ex_1_imm3out), .b(EX_PC), .out(jaldata));  // open: cin, cout
  and and_2 (and_2_out, alu_1_equal, id_ex_1_beqout);
  not not_3 (not_3_out, alu_1_equal);
  and and_3 (and_3_out, not_3_out, id_ex_1_bneout);
  ALU alu_1 (
    .X(R1Data), .Y(multiplexer_9_out), .AluOP(AluOP), .Equal(alu_1_equal), .Result(alu_1_result));  // open: Result_2, out_4, out_6
  Multiplexer #(.select(1), .width(32), .disabled("Z"), .enable("false")) multiplexer_10 (
    .in0(alu_1_result), .in1(PC_4), .out(multiplexer_10_out), .sel(or_5_out));
  or or_5 (or_5_out, JALex, JALRex);
  or or_6 (branch, and_2_out, and_3_out, and_4_out);
  and and_4 (and_4_out, BLTU, comparator_2_lt);
  EX_MEM ex_mem_1 (
    .SBin(SB), .RegWritein(exregwrite), .MemToRegin(MemToReg), .MemWritein(MemW), .haltin(ecall_t),
    .Jarin(JALex), .W_lin(W_outex), .Aluin(alu_1_result), .PCin(EX_PC), .Selectin(alu_1_result[1:0]),
    .Jmpin(multiplexer_10_out), .Mdin(MDinexe), .CLK(CLK), .SBout(SBMem), .ReqWriteout(MemRegWrite),
    .MemToReginout(ex_mem_1_memtoreginout), .MemWriteout(MemWrite), .haltout(ex_mem_1_haltout),
    .Jarout(ex_mem_1_jarout), .w_out(W_outmem), .Aluout(ex_mem_1_aluout), .PCout(M_PC), .Selectout(select),
    .Jmpout(JmpoutMem), .MdinoutMem(MDinMem), .\使能端_低电平有效_stall_高电平有效 (halt), .IRin(EX_IR), .IRout(MEM_IR),
    .jarlin(JALRex), .jarlout(ex_mem_1_jarlout), .R1in(R1Data), .R1out(ex_mem_1_r1out), .R2in(MDinexe),
    .R2out(ex_mem_1_r2out));  // open: ALUSRCBin, Ecallin, Uretin, ALUSRCBout, Ecallout, Uretout, 同步清零_气泡_高电平有效
  Counter #(.width(16), .max('hffff), .ongoal("wrap"), .trigger("rising"), .behavior("new")) counter_3 (
    .Q(\插入气泡数 ), .clk(and_5_out));  // open: load, D, count, carry, clr, preset, down
  and and_5 (and_5_out, not_5_out, not_4_out, Stall);
  not not_4 (not_4_out, halt);
  not not_5 (not_5_out, CLK);
  Multiplexer #(.select(1), .width(32), .disabled("Z"), .enable("false")) multiplexer_11 (
    .in0(MDinMem), .in1(shifter_4_out), .out(MDin), .sel(SBMem));
  assign bit_extender_4_out = {{3{select[1]}}, select};  // Bit_Extender bit_extender_4
  Shifter #(.width(5), .shift("ll")) shifter_3 (.in(bit_extender_4_out), .\dist (3'b011), .out(shifter_3_out));
  Comparator #(.width(32), .mode("twosComplement")) comparator_3 (
    .a(R1), .b(32'h22), .eq(comparator_3_eq));  // open: gt, lt
  not not_6 (not_6_out, comparator_3_eq);
  Counter #(.width(16), .max('hffff), .ongoal("wrap"), .trigger("rising"), .behavior("new")) counter_4 (
    .Q(\无条件分支数 ), .clk(and_6_out));  // open: load, D, count, carry, clr, preset, down
  and and_6 (and_6_out, or_7_out, not_7_out);
  or or_7 (or_7_out, JALex, JALRex);
  not not_7 (not_7_out, CLK);
  Shifter #(.width(32), .shift("ll")) shifter_4 (.in(MDinMem), .\dist (shifter_3_out), .out(shifter_4_out));
  and and_7 (and_7_out, Ecall, not_6_out);
  and and_8 (and_8_out, Ecall, comparator_3_eq);
  // MIPS_RAM mips_ram_1: pin names not known; wires that end beside it: ex_mem_1_aluout[11:2], MDin, MemWrite, mips_ram_1_p4, CLK, mips_ram_1_p6
  Multiplexer #(.select(1), .width(4), .disabled("Z"), .enable("false")) multiplexer_12 (
    .in0(4'b1111), .in1(multiplexer_13_out), .out(mips_ram_1_p4), .sel(SBMem));
  Multiplexer #(.select(2), .width(4), .disabled("Z"), .enable("false")) multiplexer_13 (
    .in0(4'b0001), .in1(4'b0010), .in2(4'b0100), .in3(4'b1000), .out(multiplexer_13_out), .sel(select));
  Register #(.width(1), .trigger("rising"), .Select("low")) register_1 (
    .D(and_7_out), .en(not_8_out), .Q(halt), .clk(CLK), .clr(Go));
  not not_8 (not_8_out, halt);
  Counter #(.width(16), .max('hffff), .ongoal("wrap"), .trigger("rising"), .behavior("new")) counter_5 (
    .Q(\条件分支成功数 ), .clk(and_9_out));  // open: load, D, count, carry, clr, preset, down
  and and_9 (and_9_out, branch, not_9_out);
  not not_9 (not_9_out, CLK);
  Register #(.width(32), .trigger("rising"), .Select("low")) PC_2 (
    .D(R2), .en(and_8_out), .Q(LedData), .clk(CLK));  // open: clr
  MEM_WB mem_wb_1 (
    .MemToRegin(ex_mem_1_memtoreginout), .RegWritein(MemRegWrite), .haltin(ex_mem_1_haltout),
    .Jarin(ex_mem_1_jarout), .Jarlin(ex_mem_1_jarlout), .Din(mips_ram_1_p6), .PCin(M_PC), .Jmpin(JmpoutMem),
    .W_in(W_outmem), .CLK(CLK), .MemToRegout(mem_wb_1_memtoregout), .RegWriteout(RegWrite), .haltout(Ecall),
    .Jarout(mem_wb_1_jarout), .Jarlout(mem_wb_1_jarlout), .Dout(mem_wb_1_dout), .PCout(WB_PC),
    .Jmpout(mem_wb_1_jmpout), .W_out(W_out), .\使能端_低电平有效_stall_高电平有效 (halt), .IRin(MEM_IR), .IRout(WB_IR),
    .R1in(ex_mem_1_r1out), .R1out(R1), .R2in(ex_mem_1_r2out), .R2out(R2));  // open: Ecallin, Uretin, Selectin, Ecallout, Uretout, Selectout, 同步清零_气泡_高电平有效
  Multiplexer #(.select(1), .width(32), .disabled("Z"), .enable("false")) multiplexer_14 (
    .in0(mem_wb_1_jmpout), .in1(mem_wb_1_dout), .out(multiplexer_14_out), .sel(mem_wb_1_memtoregout));
  or or_8 (or_8_out, mem_wb_1_jarout, mem_wb_1_jarlout);
  Multiplexer #(.select(1), .width(32), .disabled("Z"), .enable("false")) multiplexer_15 (
    .in0(multiplexer_14_out), .in1(adder_5_out), .out(RDin), .sel(or_8_out));
  Adder #(.width(32)) adder_5 (.a(WB_PC), .b(32'h4), .out(adder_5_out));  // open: cin, cout

  // Other names for the same wires on the sheet: EXREG[4:0] = EX_IR[11:7]; IR[31:0] = IF_IR;
  //   MEMREG[4:0] = MEM_IR[11:7]; PC[31:0] = IF_PC; PC1[31:0] = ID_PC; PC2[31:0] = EX_PC; MEM_PC[31:0] = M_PC;
  //   PC3[31:0] = M_PC; PC4[31:0] = WB_PC

  // Notes on the sheet:
  //   中断源
  //   时空图监测，可删除
  //   中断等待指示
  //   数码管输出
  //   指令存储器
  //   contents of rom_1 (hex, n*v repeats v):
  //   100493 100006f 100493 200913 300993 100006f 100493 200913 300993 100006f 100493 200913 300993
  //   100006f 100493 200913 300993 3b8000ef 100413 100493 1f49493 900533 2200893 73 24d493 48463 fedff06f
  //   900533 2200893 73 100493 249493 900533 2200893 73 48463 fedff06f 100493 1f49493 900533 2200893 73
  //   4034d493 900533 2200893 73 4044d493 900533 2200893 73 4044d493 900533 2200893 73 4044d493 900533
  //   2200893 73 4044d493 900533 2200893 73 4044d493 900533 2200893 73 4044d493 900533 2200893 73 4044d493
  //   900533 2200893 73 100413 1f41993 41f9d993 433 c00913 300b13 140413 f47413 800293 100313 499993
  //   89e9b3 1300533 2200893 73 406282b3 fe0294e3 140413 f00f93 1f47433 1c41413 800293 100313 49d993
  //   89e9b3 1300533 2200893 73 406282b3 fe0294e3 1c45413 406b0b33 b0463 f95ff06f 2b3 fff2c293 829293
  //   ff2e293 500533 2200893 73 fff00413 493 84a023 140413 448493 84a023 140413 448493 84a023 140413
  //   448493 84a023 140413 448493 84a023 140413 448493 84a023 140413 448493 84a023 140413 448493 84a023
  //   140413 448493 84a023 140413 448493 84a023 140413 448493 84a023 140413 448493 84a023 140413 448493
  //   84a023 140413 448493 84a023 140413 448493 84a023 140413 448493 84a023 140413 448493 140413 433
  //   3c00493 42983 4aa03 149a2b3 28663 134a023 1442023 ffc48493 fe9412e3 800533 2200893 73 440413 3c00493
  //   fc9416e3 100293 300313 800493 849493 7648493 900533 2200893 73 800e13 5494b3 6494b3 900533 2200893
  //   73 fffe0e13 fe0e14e3 a00893 73 100293 300313 800493 849493 7648493 1449493 900533 2200893 73 800e13
  //   4054d4b3 4064d4b3 900533 2200893 73 fffe0e13 fe0e14e3 a00893 73 313 2000e13 493 100913 930023 900533
  //   2200893 73 12484b3 130313 fffe0e13 fe0e12e3 800e13 313 32483 900533 2200893 73 430313 fffe0e13
  //   fe0e14e3 a00893 73 ff100493 900533 2200893 73 148493 fe9068e3 900533 2200893 73 a00893 73 a00893 73
  //   413 140413 800533 2200893 73 240413 800533 2200893 73 340413 800533 2200893 73 440413 800533 2200893
  //   73 540413 800533 2200893 73 640413 800533 2200893 73 740413 800533 2200893 73 840413 800533 2200893
  //   2200893 73 8067
  //   指令探针
  //   指令字
  //   控制位
  //   Beq
  //   Bne
  //   MemToReg
  //   MemWrite
  //   AluOP
  //   AluSrcB
  //   RegWrite
  //   流水调试日志用
  //   暂停节拍，不能为0
  //   戳工具置1进入计数暂停模式，ctrl+k时钟自动运行到对应节拍暂停
  //   ctrl+k关闭时钟连续运行，将控制位置零，进入单步调试模式调试
  //   用这个时钟源需要去掉电路中的其他时钟源
  //   可计数暂停的时钟源
  //   为方便自动评测，需要输出流水线各段保存的PC值，注意是PC不是PC+4，另外ID段寄存器写入信息，Mem段内存写入信息也要输出
  //   数据存储器
endmodule
module \重定向流水线  (
  input  IR1,
  input  IR2,
  input  IR3,
  output RegWrite,
  output MemWrite,
  output [31:0] IF_PC,
  output [31:0] ID_PC,
  output [31:0] EX_PC,
  output [31:0] M_PC,
  output [31:0] WB_PC,
  output [31:0] RDin,
  output [31:0] MDin,
  output [31:0] LedData
);

  wire alu_1_equal, AluSrcB, and_2_out, and_3_out, and_4_out, and_5_out, and_6_out, and_7_out, and_9_out,
       and_10_out, and_11_out, and_12_out, and_16_out, and_17_out, BLTU, branch, C1, C2, C3, CLEAR, CLK,
       clock_1_out, comparator_1_eq, comparator_1_lt, comparator_2_lt, comparator_3_eq, comparator_4_eq,
       comparator_5_eq, comparator_6_eq, comparator_7_eq, d_ff_1_q, d_ff_2_q, d_ff_3_q, d_ff_4_q, d_ff_5_q,
       d_ff_6_q, d_ff_7_q, decoder_1_out0, decoder_1_out1, decoder_1_out2, Ecall, ecall_t, ex_mem_1_haltout,
       ex_mem_1_jarlout, ex_mem_1_jarout, ex_mem_1_memtoreginout, exregwrite, Go, halt, id_ex_1_beqout,
       id_ex_1_bneout, IE, if_id_1_pjmpout, INT, IntReady, IR1_t, IR2_t, IR3_t, IRA, IRB, IRC, JALex, JALRex,
       loaduse, mem_wb_1_jarlout, mem_wb_1_jarout, mem_wb_1_memtoregout, MemRegWrite, MemToReg, MemW,
       multiplexer_5_out, nand_1_out, not_1_out, not_2_out, not_4_out, not_5_out, not_6_out, not_7_out,
       not_8_out, not_9_out, not_10_out, not_11_out, not_12_out, not_13_out, or_3_out, or_6_out, or_11_out,
       or_12_out, or_13_out, or_14_out, or_15_out, or_17_out, or_18_out, or_19_out, PC_2_q,
       priority_encoder_1_gs, register_1_q, register_2_q, RST, S_Type, SB, SBMem, Uret, uret_t, W1, W2, W3,
       \单周期硬布线控制器_1_alu_src , \单周期硬布线控制器_1_beq , \单周期硬布线控制器_1_bltu , \单周期硬布线控制器_1_bne , \单周期硬布线控制器_1_ecall ,
       \单周期硬布线控制器_1_jal , \单周期硬布线控制器_1_jalr , \单周期硬布线控制器_1_memtoreg , \单周期硬布线控制器_1_memwrite ,
       \单周期硬布线控制器_1_regwrite , \单周期硬布线控制器_1_sb ;
  wire [1:0] exfwdr1, exfwdr2, multiplexer_14_out, multiplexer_15_out, priority_encoder_1_out, register_5_q,
       select, \相关处理逻辑_1_r1exre , \相关处理逻辑_1_r2exre ;
  wire [3:0] AluOP, mips_ram_1_p4, multiplexer_21_out, \单周期硬布线控制器_1_alu_op ;
  wire [4:0] bit_extender_4_out, multiplexer_8_out, multiplexer_10_out, multiplexer_11_out, shifter_3_out,
       W_in, W_out, W_outex, W_outmem;
  wire [11:0] multiplexer_13_out, shifter_1_out;
  wire [12:0] CNT_num;
  wire [15:0] \LoadUse次数 , \总周期数 , \插入气泡数 , \无条件分支数 , \条件分支成功数 ;
  wire [19:0] shifter_2_out;
  wire [31:0] adder_1_out, adder_5_out, alu_1_result, Aluout, and_1_out, branchdata, EX_IR, ex_mem_1_r1out,
       ex_mem_1_r2out, exoldR1, exoldR2, id_ex_1_imm2out, id_ex_1_imm3out, ID_IR, IF_IR, Imm1, Imm2, Imm3,
       INTPC, jaldata, jalrin, JmpoutMem, MDinexe, MDinMem, MEM_IR, mem_wb_1_dout, mem_wb_1_jmpout, mEPC,
       mips_ram_1_p6, multiplexer_1_out, multiplexer_2_out, multiplexer_3_out, multiplexer_16_out,
       multiplexer_17_out, multiplexer_22_out, NewR1, NextPC, PC_4, PC_q, R1, R2, regifile_1_r1,
       regifile_1_r2, shifter_4_out, WB_IR;

  Button \u_总复位  (.out(RST));
  Button _1 ();  // open: out
  Button _2 ();  // open: out
  Button _3 ();  // open: out
  // Probe on \总周期数 
  // Probe on \总周期数 
  Button \u_继续运行  (.out(Go));
  LED #(.active("true")) led_1 (.in(W1));
  LED #(.active("true")) led_2 (.in(W2));
  LED #(.active("true")) led_3 (.in(W3));
  or or_1 (IR1_t, IR1, IRA);
  Hex_Digit_Display hex_digit_display_1 (.value(LedData[31:28]));  // open: dp
  // Probe on IF_PC[19:0]
  // RiscV_Probe riscv_probe_1: pin names not known; wires that end beside it: IR1_t, IR2_t, IR3_t, IF_IR
  or or_2 (IR2_t, IR2, IRB);
  assign and_1_out = 32'hfffffffe & adder_1_out;  // AND_Gate and_1, 32 bits wide
  Multiplexer #(.select(1), .width(32), .disabled("Z"), .enable("false")) multiplexer_1 (
    .in0(PC_4), .in1(and_1_out), .out(multiplexer_1_out), .sel(JALRex));
  Multiplexer #(.select(1), .width(32), .disabled("Z"), .enable("false")) multiplexer_2 (
    .in0(multiplexer_1_out), .in1(jaldata), .out(multiplexer_2_out), .sel(JALex));
  Multiplexer #(.select(1), .width(32), .disabled("Z"), .enable("false")) multiplexer_3 (
    .in0(multiplexer_2_out), .in1(branchdata), .out(multiplexer_3_out), .sel(branch));
  not not_1 (not_1_out, uret_t);
  Hex_Digit_Display hex_digit_display_2 (.value(LedData[27:24]));  // open: dp
  Hex_Digit_Display hex_digit_display_3 (.value(LedData[23:20]));  // open: dp
  // Probe on ID_PC[19:0]
  // RiscV_Probe riscv_probe_2: pin names not known; wires that end beside it: ID_IR
  Adder #(.width(32)) adder_1 (.a(jalrin), .b(NewR1), .out(adder_1_out));  // open: cin, cout
  Multiplexer #(.select(1), .width(32), .disabled("Z"), .enable("false")) multiplexer_4 (
    .in0(multiplexer_3_out), .in1(mEPC), .out(NextPC), .sel(uret_t));
  Register #(.width(32), .trigger("rising"), .Select("low")) PC (
    .D(NextPC), .en(not_2_out), .Q(PC_q), .clk(CLK), .clr(RST));
  not not_2 (not_2_out, or_3_out);
  or or_3 (or_3_out, halt, loaduse);
  Register #(.width(1), .trigger("rising"), .Select("low")) register_1 (
    .D(1'b1), .Q(register_1_q), .clk(multiplexer_5_out), .clr(register_1_q));  // open: en
  Multiplexer #(.select(1), .width(1), .disabled("Z"), .enable("false")) multiplexer_5 (
    .in0(1'b1), .in1(CLK), .out(multiplexer_5_out), .sel(IntReady));
  Register #(.width(1), .trigger("rising"), .Select("low")) register_2 (
    .D(1'b0), .en(1'b1), .Q(register_2_q), .clk(not_1_out), .preset(INT));  // open: clr, cs
  Hex_Digit_Display hex_digit_display_4 (.value(LedData[15:12]));  // open: dp
  Hex_Digit_Display hex_digit_display_5 (.value(LedData[19:16]));  // open: dp
  or or_4 (IR3_t, IR3, IRC);
  Register #(.width(1), .trigger("rising"), .Select("low")) register_3 (
    .D(1'b1), .Q(IntReady), .clk(INT), .clr(register_1_q));  // open: en
  not not_3 (IE, register_2_q);
  Hex_Digit_Display hex_digit_display_6 (.value(LedData[11:8]));  // open: dp
  Hex_Digit_Display hex_digit_display_7 (.value(LedData[7:4]));  // open: dp
  // Probe on EX_PC[19:0]
  // RiscV_Probe riscv_probe_3: pin names not known; wires that end beside it: EX_IR
  Multiplexer #(.select(1), .width(32), .disabled("Z"), .enable("false")) multiplexer_6 (
    .in0(PC_q), .in1(INTPC), .out(IF_PC), .sel(PC_2_q));
  Register #(.width(1), .trigger("rising"), .Select("low")) PC_2 (
    .D(IntReady), .Q(PC_2_q), .clk(CLK));  // open: en, clr
  Multiplexer #(.select(2), .width(32), .disabled("Z"), .enable("false")) multiplexer_7 (
    .in0(exoldR1), .in1(Aluout), .in2(RDin), .in3(Aluout), .out(NewR1), .sel(exfwdr1));
  Hex_Digit_Display hex_digit_display_8 (.value(LedData[3:0]));  // open: dp
  ROM #(.addrWidth(10), .dataWidth(32), .Select("high")) rom_1 (.addr(IF_PC[11:2]), .data(IF_IR));
  Adder #(.width(32)) adder_2 (.a(IF_PC), .b(32'h4), .out(PC_4));  // open: cin, cout
  or or_5 (CLEAR, branch, JALex, JALRex);
  // Probe on \总周期数 
  // Probe on M_PC[19:0]
  // RiscV_Probe riscv_probe_4: pin names not known; wires that end beside it: MEM_IR
  IF_ID if_id_1 (
    .PCin(IF_PC), .IRin(IF_IR), .CLK(CLK), .PCout(ID_PC), .IRout(ID_IR), .\同步清零_气泡_高电平有效 (or_6_out),
    .\使能端_低电平有效_stall_高电平有效 (if_id_1_pjmpout), .Pjmpout(if_id_1_pjmpout));  // open: Pjmpin
  or or_6 (or_6_out, uret_t, CLEAR);
  Register #(.width(32), .trigger("rising"), .Select("low")) register_4 (
    .D(NextPC), .en(IntReady), .Q(mEPC), .clk(CLK));  // open: clr
  // Probe on \总周期数 
  // Probe on \无条件分支数 
  // Probe on \条件分支成功数 
  // Probe on \插入气泡数 
  // Probe on \LoadUse次数 
  // RiscV_Probe riscv_probe_5: pin names not known; wires that end beside it: ID_IR
  or or_7 (if_id_1_pjmpout, halt, loaduse);
  // Probe on IF_PC[11:0]
  // Probe on WB_PC[19:0]
  // RiscV_Probe riscv_probe_6: pin names not known; wires that end beside it: WB_IR
  Multiplexer #(.select(1), .width(5), .disabled("Z"), .enable("false")) multiplexer_8 (
    .in0(ID_IR[24:20]), .in1(5'b00001), .out(multiplexer_8_out), .sel(JALRex));
  not not_4 (not_4_out, halt);
  Multiplexer #(.select(2), .width(32), .disabled("Z"), .enable("false")) multiplexer_9 (
    .in0(exoldR2), .in1(Aluout), .in2(RDin), .in3(Aluout), .out(MDinexe), .sel(exfwdr2));
  // Probe on ID_PC[11:0]
  // Probe on EX_PC[11:0]
  \单周期硬布线控制器  \u_单周期硬布线控制器_1  (
    .Funct({ID_IR[30], ID_IR[25], ID_IR[14:12]}), .OP(ID_IR[6:2]), .ALU_OP(\单周期硬布线控制器_1_alu_op ),
    .MemToReg(\单周期硬布线控制器_1_memtoreg ), .MemWrite(\单周期硬布线控制器_1_memwrite ), .ALU_SRC(\单周期硬布线控制器_1_alu_src ),
    .RegWrite(\单周期硬布线控制器_1_regwrite ), .ecall(\单周期硬布线控制器_1_ecall ), .in_3(ID_IR[21]), .uret(Uret),
    .JAL(\单周期硬布线控制器_1_jal ), .SB(\单周期硬布线控制器_1_sb ), .Jalr(\单周期硬布线控制器_1_jalr ), .BLTU(\单周期硬布线控制器_1_bltu ),
    .Bne(\单周期硬布线控制器_1_bne ), .Beq(\单周期硬布线控制器_1_beq ), .S_type(S_Type));  // open: I, B
  Multiplexer #(.select(1), .width(5), .disabled("Z"), .enable("false")) multiplexer_10 (
    .in0(ID_IR[19:15]), .in1(5'b10001), .out(multiplexer_10_out), .sel(\单周期硬布线控制器_1_ecall ));
  Multiplexer #(.select(1), .width(5), .disabled("Z"), .enable("false")) multiplexer_11 (
    .in0(multiplexer_8_out), .in1(5'b01010), .out(multiplexer_11_out), .sel(\单周期硬布线控制器_1_ecall ));
  // Probe on W_in
  Multiplexer #(.select(1), .width(5), .disabled("Z"), .enable("false")) multiplexer_12 (
    .in0(ID_IR[11:7]), .in1(5'b00001), .out(W_in), .sel(JALRex));
  Multiplexer #(.select(1), .width(12), .disabled("Z"), .enable("false")) multiplexer_13 (
    .in0(ID_IR[31:20]), .in1({ID_IR[31:25], ID_IR[11:7]}), .out(multiplexer_13_out), .sel(S_Type));
  assign Imm2 = {{20{shifter_1_out[11]}}, shifter_1_out};  // Bit_Extender bit_extender_1
  Shifter #(.width(12), .shift("ll")) shifter_1 (
    .in({ID_IR[31], ID_IR[7], ID_IR[30:25], ID_IR[11:8]}), .\dist (4'b0001), .out(shifter_1_out));
  Shifter #(.width(20), .shift("ll")) shifter_2 (
    .in({ID_IR[31], ID_IR[19:12], ID_IR[20], ID_IR[30:21]}), .\dist (5'b00001), .out(shifter_2_out));
  Counter #(.width(16), .max('hffff), .ongoal("wrap"), .trigger("rising"), .behavior("new")) counter_1 (
    .count(not_4_out), .Q(\总周期数 ), .clk(CLK));  // open: load, D, carry, clr, preset, down
  // Probe on M_PC[11:0]
  D_Flip_Flop #(.trigger("high"), .Pre_Clr_Positions("LEGACY"), .NegatePresetClear("false"), .enable("true"), .NewFFLayout("false")) d_ff_1 (.Q(d_ff_1_q));  // open: clk, D, Qn, preset, en, reset
  // Probe on 13'h8fa
  // Probe on multiplexer_11_out
  assign Imm1 = {{20{multiplexer_13_out[11]}}, multiplexer_13_out};  // Bit_Extender bit_extender_2
  assign Imm3 = {{12{shifter_2_out[19]}}, shifter_2_out};  // Bit_Extender bit_extender_3
  or or_8 (W1, d_ff_5_q, d_ff_2_q);
  or or_9 (W2, d_ff_6_q, d_ff_3_q);
  or or_10 (W3, d_ff_7_q, d_ff_4_q);
  // Probe on WB_PC[11:0]
  Comparator #(.width(13), .mode("twosComplement")) comparator_1 (
    .a(CNT_num), .b(13'h8fa), .eq(comparator_1_eq), .lt(comparator_1_lt));  // open: gt
  Clock #(.highDuration(1), .lowDuration(1)) clock_1 (.out(clock_1_out));
  \相关处理逻辑  \u_相关处理逻辑_1  (
    .exop(EX_IR[6:2]), .ExRegWrite(exregwrite), .OP(ID_IR[6:2]), .FUNC({ID_IR[30], ID_IR[25], ID_IR[14:12]}),
    .R1(multiplexer_10_out), .EXREG(EX_IR[11:7]), .R2(multiplexer_11_out), .MEMREG(MEM_IR[11:7]),
    .MemRegWrite(MemRegWrite), .LoadUse(loaduse), .R1EXRE(\相关处理逻辑_1_r1exre [0]),
    .R1MemRe(\相关处理逻辑_1_r1exre [1]), .R2EXRE(\相关处理逻辑_1_r2exre [0]), .R2MemRe(\相关处理逻辑_1_r2exre [1]));  // open: DH
  Regifile regifile_1 (
    .Din(RDin), .Clk(CLK), .R1(regifile_1_r1), .R2(regifile_1_r2), .WE(RegWrite), .W_num(W_out),
    .R1_num(multiplexer_10_out), .R2_num(multiplexer_11_out));
  D_Flip_Flop #(.trigger("rising"), .Pre_Clr_Positions("LEGACY"), .NegatePresetClear("false"), .enable("true"), .NewFFLayout("true")) d_ff_2 (
    .clk(IR1_t), .D(1'b1), .Q(d_ff_2_q), .reset(d_ff_5_q));  // open: Qn, preset, en
  D_Flip_Flop #(.trigger("rising"), .Pre_Clr_Positions("LEGACY"), .NegatePresetClear("false"), .enable("true"), .NewFFLayout("true")) d_ff_3 (
    .clk(IR2_t), .D(1'b1), .Q(d_ff_3_q), .reset(d_ff_6_q));  // open: Qn, preset, en
  D_Flip_Flop #(.trigger("rising"), .Pre_Clr_Positions("LEGACY"), .NegatePresetClear("false"), .enable("true"), .NewFFLayout("true")) d_ff_4 (
    .clk(IR3_t), .D(1'b1), .Q(d_ff_4_q), .reset(d_ff_7_q));  // open: Qn, preset, en
  nand nand_1 (nand_1_out, d_ff_1_q, comparator_1_eq);
  Counter #(.width(13), .max('h1fff), .ongoal("stay"), .trigger("rising"), .behavior("old")) counter_2 (
    .count(comparator_1_lt), .Q(CNT_num), .clk(clock_1_out));  // open: load, D, carry, clr, preset
  Multiplexer #(.select(1), .width(2), .disabled("Z"), .enable("false")) multiplexer_14 (
    .in0(\相关处理逻辑_1_r1exre ), .in1(2'b00), .out(multiplexer_14_out), .sel(loaduse));
  Multiplexer #(.select(1), .width(2), .disabled("Z"), .enable("false")) multiplexer_15 (
    .in0(\相关处理逻辑_1_r2exre ), .in1(2'b00), .out(multiplexer_15_out), .sel(loaduse));
  or or_11 (or_11_out, loaduse, uret_t, CLEAR);
  or or_12 (or_12_out, d_ff_2_q, d_ff_5_q);
  or or_13 (or_13_out, d_ff_3_q, d_ff_6_q);
  or or_14 (or_14_out, d_ff_4_q, d_ff_7_q);
  assign CLK = nand_1_out ? clock_1_out : 1'bz;  // Controlled_Buffer controlled_buffer_1
  ID_EX id_ex_1 (
    .Beqin(\单周期硬布线控制器_1_beq ), .Bnein(\单周期硬布线控制器_1_bne ), .MemToRegin(\单周期硬布线控制器_1_memtoreg ),
    .MemWritein(\单周期硬布线控制器_1_memwrite ), .ALUopin(\单周期硬布线控制器_1_alu_op ), .ALUSRCBin(\单周期硬布线控制器_1_alu_src ),
    .RegWritein(\单周期硬布线控制器_1_regwrite ), .Ecallin(\单周期硬布线控制器_1_ecall ), .Jarin(\单周期硬布线控制器_1_jal ),
    .Jarlin(\单周期硬布线控制器_1_jalr ), .Uretin(Uret), .Bltuin(\单周期硬布线控制器_1_bltu ), .R2in(regifile_1_r2),
    .R1in(regifile_1_r1), .PCin(ID_PC), .Imm1in(Imm1), .CLK(CLK), .Beqout(id_ex_1_beqout),
    .Bneout(id_ex_1_bneout), .MemToReginout(MemToReg), .MemWriteout(MemW), .ALUopout(AluOP),
    .ALUSRCBout(AluSrcB), .RegWriteout(exregwrite), .Ecallout(ecall_t), .Jarout(JALex), .Jarlout(JALRex),
    .Uretout(uret_t), .Bltuout(BLTU), .R2out(exoldR2), .R1out(exoldR1), .PCout(EX_PC), .Imm1out(jalrin),
    .\同步清零_气泡_高电平有效 (or_11_out), .Stypein(S_Type), .SBin(\单周期硬布线控制器_1_sb ), .SBout(SB), .W_in(W_in),
    .W_out(W_outex), .Imm2in(Imm2), .Imm2out(id_ex_1_imm2out), .Imm3in(Imm3), .Imm3out(id_ex_1_imm3out),
    .IRin(ID_IR), .IRout(EX_IR), .Stall(halt), .fwdR1in(multiplexer_14_out), .fwdR1out(exfwdr1),
    .fwdR2in(multiplexer_15_out), .fwdR2out(exfwdr2));  // open: Stypeout, pjmpin, pjmpout
  and and_2 (and_2_out, or_12_out, ~C1);  // AND_Gate
  and and_3 (and_3_out, or_13_out, ~C2);  // AND_Gate
  and and_4 (and_4_out, or_14_out, ~C3);  // AND_Gate
  Pull_Resistor #(.pull(1)) pull_resistor_1 (.node(CLK));
  Adder #(.width(32)) adder_3 (.a(id_ex_1_imm2out), .b(EX_PC), .out(branchdata));  // open: cin, cout
  D_Flip_Flop #(.trigger("rising"), .Pre_Clr_Positions("LEGACY"), .NegatePresetClear("false"), .enable("true"), .NewFFLayout("true")) d_ff_5 (
    .clk(CLK), .D(and_2_out), .Q(d_ff_5_q));  // open: Qn, preset, en, reset
  D_Flip_Flop #(.trigger("rising"), .Pre_Clr_Positions("LEGACY"), .NegatePresetClear("false"), .enable("true"), .NewFFLayout("true")) d_ff_6 (
    .clk(CLK), .D(and_3_out), .Q(d_ff_6_q));  // open: Qn, preset, en, reset
  D_Flip_Flop #(.trigger("rising"), .Pre_Clr_Positions("LEGACY"), .NegatePresetClear("false"), .enable("true"), .NewFFLayout("true")) d_ff_7 (
    .clk(CLK), .D(and_4_out), .Q(d_ff_7_q));  // open: Qn, preset, en, reset
  Comparator #(.width(32), .mode("unsigned")) comparator_2 (
    .a(NewR1), .b(MDinexe), .lt(comparator_2_lt));  // open: gt, eq
  // Probe on NewR1
  // Probe on multiplexer_16_out
  Multiplexer #(.select(1), .width(32), .disabled("Z"), .enable("false")) multiplexer_16 (
    .in0(MDinexe), .in1(jalrin), .out(multiplexer_16_out), .sel(AluSrcB));
  Adder #(.width(32)) adder_4 (.a(id_ex_1_imm3out), .b(EX_PC), .out(jaldata));  // open: cin, cout
  and and_5 (and_5_out, alu_1_equal, id_ex_1_beqout);
  not not_5 (not_5_out, alu_1_equal);
  and and_6 (and_6_out, not_5_out, id_ex_1_bneout);
  ALU alu_1 (
    .X(NewR1), .Y(multiplexer_16_out), .AluOP(AluOP), .Equal(alu_1_equal), .Result(alu_1_result));  // open: Result_2, out_4, out_6
  Multiplexer #(.select(1), .width(32), .disabled("Z"), .enable("false")) multiplexer_17 (
    .in0(alu_1_result), .in1(PC_4), .out(multiplexer_17_out), .sel(or_15_out));
  or or_15 (or_15_out, JALex, JALRex);
  Priority_Encoder #(.select(2), .disabled("Z")) priority_encoder_1 (
    .in0(d_ff_5_q), .in1(d_ff_6_q), .in2(d_ff_7_q), .in3(1'b0), .out(priority_encoder_1_out),
    .gs(priority_encoder_1_gs), .en_in(1'b1));  // open: en_out
  or or_16 (branch, and_5_out, and_6_out, and_7_out);
  and and_7 (and_7_out, BLTU, comparator_2_lt);
  and and_8 (INT, priority_encoder_1_gs, IE);
  Multiplexer #(.select(2), .width(32), .disabled("Z"), .enable("false")) multiplexer_18 (
    .in0(32'h30ac), .in1(32'h3150), .in2(32'h31f4), .out(INTPC), .sel(priority_encoder_1_out));  // open: in3
  EX_MEM ex_mem_1 (
    .SBin(SB), .RegWritein(exregwrite), .MemToRegin(MemToReg), .MemWritein(MemW), .haltin(ecall_t),
    .Jarin(JALex), .W_lin(W_outex), .Aluin(alu_1_result), .PCin(EX_PC), .Selectin(alu_1_result[1:0]),
    .Jmpin(multiplexer_17_out), .Mdin(MDinexe), .CLK(CLK), .SBout(SBMem), .ReqWriteout(MemRegWrite),
    .MemToReginout(ex_mem_1_memtoreginout), .MemWriteout(MemWrite), .haltout(ex_mem_1_haltout),
    .Jarout(ex_mem_1_jarout), .w_out(W_outmem), .Aluout(Aluout), .PCout(M_PC), .Selectout(select),
    .Jmpout(JmpoutMem), .MdinoutMem(MDinMem), .\使能端_低电平有效_stall_高电平有效 (halt), .IRin(EX_IR), .IRout(MEM_IR),
    .jarlin(JALRex), .jarlout(ex_mem_1_jarlout), .R1in(NewR1), .R1out(ex_mem_1_r1out), .R2in(MDinexe),
    .R2out(ex_mem_1_r2out));  // open: ALUSRCBin, Ecallin, Uretin, ALUSRCBout, Ecallout, Uretout, 同步清零_气泡_高电平有效
  Register #(.width(2), .trigger("rising"), .Select("low")) register_5 (
    .D(priority_encoder_1_out), .en(1'b1), .Q(register_5_q), .clk(INT));  // open: clr
  Counter #(.width(16), .max('hffff), .ongoal("wrap"), .trigger("rising"), .behavior("new")) counter_3 (
    .Q(\插入气泡数 ), .clk(and_9_out));  // open: load, D, count, carry, clr, preset, down
  and and_9 (and_9_out, not_7_out, not_6_out, loaduse);
  not not_6 (not_6_out, halt);
  not not_7 (not_7_out, CLK);
  Multiplexer #(.select(1), .width(32), .disabled("Z"), .enable("false")) multiplexer_19 (
    .in0(MDinMem), .in1(shifter_4_out), .out(MDin), .sel(SBMem));
  assign bit_extender_4_out = {{3{select[1]}}, select};  // Bit_Extender bit_extender_4
  Comparator #(.width(32), .mode("twosComplement")) comparator_3 (
    .a(R1), .b(32'h22), .eq(comparator_3_eq));  // open: gt, lt
  Decoder #(.select(2), .tristate("false"), .disabled("Z"), .enable("false")) decoder_1 (
    .out0(decoder_1_out0), .out1(decoder_1_out1), .out2(decoder_1_out2), .sel(register_5_q));  // open: out3
  Shifter #(.width(5), .shift("ll")) shifter_3 (.in(bit_extender_4_out), .\dist (3'b011), .out(shifter_3_out));
  not not_8 (not_8_out, comparator_3_eq);
  Counter #(.width(16), .max('hffff), .ongoal("wrap"), .trigger("rising"), .behavior("new")) counter_4 (
    .Q(\无条件分支数 ), .clk(and_10_out));  // open: load, D, count, carry, clr, preset, down
  and and_10 (and_10_out, or_17_out, not_9_out);
  not not_9 (not_9_out, CLK);
  or or_17 (or_17_out, JALex, JALRex);
  Shifter #(.width(32), .shift("ll")) shifter_4 (.in(MDinMem), .\dist (shifter_3_out), .out(shifter_4_out));
  and and_11 (and_11_out, Ecall, not_8_out);
  and and_12 (and_12_out, Ecall, comparator_3_eq);
  and and_13 (C1, decoder_1_out0, uret_t);
  and and_14 (C2, decoder_1_out1, uret_t);
  and and_15 (C3, decoder_1_out2, uret_t);
  // MIPS_RAM mips_ram_1: pin names not known; wires that end beside it: Aluout[11:2], MDin, MemWrite, mips_ram_1_p4, CLK, mips_ram_1_p6
  Multiplexer #(.select(1), .width(4), .disabled("Z"), .enable("false")) multiplexer_20 (
    .in0(4'b1111), .in1(multiplexer_21_out), .out(mips_ram_1_p4), .sel(SBMem));
  Multiplexer #(.select(2), .width(4), .disabled("Z"), .enable("false")) multiplexer_21 (
    .in0(4'b0001), .in1(4'b0010), .in2(4'b0100), .in3(4'b1000), .out(multiplexer_21_out), .sel(select));
  Register #(.width(1), .trigger("rising"), .Select("low")) register_6 (
    .D(and_11_out), .en(not_10_out), .Q(halt), .clk(CLK), .clr(Go));
  not not_10 (not_10_out, halt);
  and and_16 (and_16_out, branch, not_11_out);
  Register #(.width(32), .trigger("rising"), .Select("low")) PC_3 (
    .D(R2), .en(and_12_out), .Q(LedData), .clk(CLK));  // open: clr
  Counter #(.width(16), .max('hffff), .ongoal("wrap"), .trigger("rising"), .behavior("new")) counter_5 (
    .Q(\条件分支成功数 ), .clk(and_16_out));  // open: load, D, count, carry, clr, preset, down
  not not_11 (not_11_out, CLK);
  MEM_WB mem_wb_1 (
    .MemToRegin(ex_mem_1_memtoreginout), .RegWritein(MemRegWrite), .haltin(ex_mem_1_haltout),
    .Jarin(ex_mem_1_jarout), .Jarlin(ex_mem_1_jarlout), .Din(mips_ram_1_p6), .PCin(M_PC), .Jmpin(JmpoutMem),
    .W_in(W_outmem), .CLK(CLK), .MemToRegout(mem_wb_1_memtoregout), .RegWriteout(RegWrite), .haltout(Ecall),
    .Jarout(mem_wb_1_jarout), .Jarlout(mem_wb_1_jarlout), .Dout(mem_wb_1_dout), .PCout(WB_PC),
    .Jmpout(mem_wb_1_jmpout), .W_out(W_out), .\使能端_低电平有效_stall_高电平有效 (halt), .IRin(MEM_IR), .IRout(WB_IR),
    .R1in(ex_mem_1_r1out), .R1out(R1), .R2in(ex_mem_1_r2out), .R2out(R2));  // open: Ecallin, Uretin, Selectin, Ecallout, Uretout, Selectout, 同步清零_气泡_高电平有效
  Counter #(.width(16), .max('hffff), .ongoal("wrap"), .trigger("rising"), .behavior("new")) counter_6 (
    .Q(\LoadUse次数 ), .clk(and_17_out));  // open: load, D, count, carry, clr, preset, down
  and and_17 (and_17_out, loaduse, not_13_out, not_12_out);
  not not_12 (not_12_out, CLK);
  not not_13 (not_13_out, halt);
  Multiplexer #(.select(1), .width(32), .disabled("Z"), .enable("false")) multiplexer_22 (
    .in0(mem_wb_1_jmpout), .in1(mem_wb_1_dout), .out(multiplexer_22_out), .sel(mem_wb_1_memtoregout));
  or or_18 (or_18_out, mem_wb_1_jarout, mem_wb_1_jarlout);
  Multiplexer #(.select(1), .width(32), .disabled("Z"), .enable("false")) multiplexer_23 (
    .in0(multiplexer_22_out), .in1(adder_5_out), .out(RDin), .sel(or_18_out));
  Adder #(.width(32)) adder_5 (.a(WB_PC), .b(32'h4), .out(adder_5_out));  // open: cin, cout
  Comparator #(.width(16), .mode("twosComplement")) comparator_4 (
    .a(16'h23b), .b(\总周期数 ), .eq(comparator_4_eq));  // open: gt, lt
  Comparator #(.width(16), .mode("twosComplement")) comparator_5 (
    .a(\总周期数 ), .b(16'h1), .eq(comparator_5_eq));  // open: gt, lt
  Comparator #(.width(16), .mode("twosComplement")) comparator_6 (
    .a(\总周期数 ), .b(16'h4), .eq(comparator_6_eq));  // open: gt, lt
  Comparator #(.width(16), .mode("twosComplement")) comparator_7 (
    .a(\总周期数 ), .b(16'h7), .eq(comparator_7_eq));  // open: gt, lt
  or or_19 (or_19_out, comparator_4_eq, comparator_5_eq);
  assign IRA = or_19_out ? ~CLK : 1'bz;  // Controlled_Inverter controlled_inverter_1
  assign IRB = comparator_6_eq ? ~CLK : 1'bz;  // Controlled_Inverter controlled_inverter_2
  assign IRC = comparator_7_eq ? ~CLK : 1'bz;  // Controlled_Inverter controlled_inverter_3
  Pull_Resistor #(.pull(0)) pull_resistor_2 (.node(IRA));
  Pull_Resistor #(.pull(0)) pull_resistor_3 (.node(IRB));
  Pull_Resistor #(.pull(0)) pull_resistor_4 (.node(IRC));

  // Other names for the same wires on the sheet: exop[4:0] = EX_IR[6:2]; EXREG[4:0] = EX_IR[11:7]; IR[31:0] = IF_IR;
  //   MEMREG[4:0] = MEM_IR[11:7]; NewR2[31:0] = MDinexe; PC[31:0] = IF_PC; PC1[31:0] = ID_PC; PC2[31:0] = EX_PC;
  //   MEM_PC[31:0] = M_PC; PC3[31:0] = M_PC; PC4[31:0] = WB_PC; R1Data[31:0] = NewR1

  // Notes on the sheet:
  //   中断源
  //   时空图监测，可删除
  //   中断等待指示
  //   数码管输出
  //   指令存储器
  //   contents of rom_1 (hex, n*v repeats v):
  //   100493 100006f 100493 200913 300993 100006f 100493 200913 300993 100006f 100493 200913 300993
  //   100006f 100493 200913 300993 3c0000ef 100413 100493 1f49493 900533 2200893 73 24d493 48463 fedff06f
  //   900533 2200893 73 100493 249493 900533 2200893 73 48463 fedff06f 100493 1f49493 900533 2200893 73
  //   4034d493 900533 2200893 73 4044d493 900533 2200893 73 4044d493 900533 2200893 73 4044d493 900533
  //   2200893 73 4044d493 900533 2200893 73 4044d493 900533 2200893 73 4044d493 900533 2200893 73 4044d493
  //   900533 2200893 73 100413 1f41993 41f9d993 433 c00913 300b13 140413 f47413 800293 100313 499993
  //   89e9b3 1300533 2200893 73 406282b3 fe0294e3 140413 f00f93 1f47433 1c41413 800293 100313 49d993
  //   89e9b3 1300533 2200893 73 406282b3 fe0294e3 1c45413 406b0b33 b0463 f95ff06f 2b3 fff2c293 829293
  //   ff2e293 500533 2200893 73 fff00413 493 84a023 140413 448493 84a023 140413 448493 84a023 140413
  //   448493 84a023 140413 448493 84a023 140413 448493 84a023 140413 448493 84a023 140413 448493 84a023
  //   140413 448493 84a023 140413 448493 84a023 140413 448493 84a023 140413 448493 84a023 140413 448493
  //   84a023 140413 448493 84a023 140413 448493 84a023 140413 448493 84a023 140413 448493 140413 433
  //   3c00493 42983 4aa03 149a2b3 28663 134a023 1442023 ffc48493 fe9412e3 800533 2200893 73 440413 3c00493
  //   fc9416e3 3200893 73 100293 300313 800493 849493 7648493 900533 2200893 73 800e13 5494b3 6494b3
  //   900533 2200893 73 fffe0e13 fe0e14e3 a00893 73 100293 300313 800493 849493 7648493 1449493 900533
  //   2200893 73 800e13 4054d4b3 4064d4b3 900533 2200893 73 fffe0e13 fe0e14e3 a00893 73 313 2000e13 493
  //   100913 930023 900533 2200893 73 12484b3 130313 fffe0e13 fe0e12e3 800e13 313 32483 900533 2200893 73
  //   430313 fffe0e13 fe0e14e3 a00893 73 ff100493 900533 2200893 73 148493 fe9068e3 900533 2200893 73
  //   a00893 73 a00893 73 413 140413 800533 2200893 73 240413 800533 2200893 73 340413 800533 2200893 73
  //   440413 800533 2200893 73 540413 800533 2200893 73 640413 800533 2200893 73 740413 800533 2200893 73
  //   840413 800533 2200893 2200893 73 8067
  //   指令探针
  //   指令字
  //   控制位
  //   Beq
  //   Bne
  //   MemToReg
  //   MemWrite
  //   AluOP
  //   AluSrcB
  //   RegWrite
  //   流水调试日志用
  //   暂停节拍，不能为0
  //   戳工具置1进入计数暂停模式，ctrl+k时钟自动运行到对应节拍暂停
  //   ctrl+k关闭时钟连续运行，将控制位置零，进入单步调试模式调试
  //   ctrl+k关闭时钟连续运行，将控制位置零，进入单步调试模式调试
  //   用这个时钟源需要去掉电路中的其他时钟源
  //   可计数暂停的时钟源
  //   为方便自动评测，需要输出流水线各段保存的PC值，注意是PC不是PC+4，另外ID段寄存器写入信息，Mem段内存写入信息也要输出
  //   单级中断测试信号模拟器
endmodule

module \中断按键参考电路  (
  input  \同步清零信号 ,
  output \与中断屏蔽位与 
);

  wire \_1号中断_out , and_1_out, clock_1_out, d_ff_1_q, or_1_out, or_2_out;

  Clock #(.highDuration(1), .lowDuration(1)) clock_1 (.out(clock_1_out));
  Button \_1号中断  (.out(\_1号中断_out ));
  or or_1 (or_1_out, \与中断屏蔽位与 , d_ff_1_q);
  LED #(.active("true")) \_1号中断等待指示灯  (.in(or_1_out));
  D_Flip_Flop #(.trigger("rising"), .Pre_Clr_Positions("LEGACY"), .NegatePresetClear("false"), .enable("true"), .NewFFLayout("false")) d_ff_1 (
    .clk(\_1号中断_out ), .D(1'b1), .Q(d_ff_1_q), .reset(\与中断屏蔽位与 ));  // open: Qn, preset, en
  or or_2 (or_2_out, d_ff_1_q, \与中断屏蔽位与 );
  and and_1 (and_1_out, or_2_out, ~\同步清零信号 );  // AND_Gate
  D_Flip_Flop #(.trigger("rising"), .Pre_Clr_Positions("LEGACY"), .NegatePresetClear("false"), .enable("true"), .NewFFLayout("false")) IR1 (
    .clk(clock_1_out), .D(and_1_out), .Q(\与中断屏蔽位与 ));  // open: Qn, preset, en, reset

  // Notes on the sheet:
  //   中断信号采样参考电路
  //   Reset 
endmodule

module \单周期_单级中断  (
  input  IR1,
  input  IR2,
  input  IR3,
  output RegWrite,
  output MemWrite,
  output [31:0] PC,
  output [31:0] IR,
  output [31:0] RDin,
  output [31:0] MDin,
  output [31:0] LedData
);

  wire alu_1_equal, AluSrcB, and_1_out, and_2_out, and_3_out, and_9_out, and_10_out, and_11_out, and_12_out,
       and_13_out, BLTU, branch, C1, C2, C3, CLK, clock_1_out, comparator_1_lt, comparator_2_eq,
       comparator_2_lt, comparator_3_eq, comparator_4_eq, comparator_5_eq, comparator_6_eq, comparator_7_eq,
       d_ff_1_q, d_ff_2_q, d_ff_3_q, d_ff_4_q, d_ff_5_q, d_ff_6_q, d_ff_7_q, decoder_1_out0, decoder_1_out1,
       decoder_1_out2, ecall, Go, halt, IE, INT, IntReady, IR1_t, IR2_t, IR3_t, IRA, IRB, IRC, JAL, JALR,
       MemToReg, multiplexer_5_out, nand_1_out, not_1_out, not_3_out, not_4_out, not_5_out, not_6_out,
       not_7_out, or_4_out, or_5_out, or_6_out, or_7_out, or_12_out, or_13_out, PC_2_q,
       priority_encoder_1_gs, register_1_q, register_2_q, RST, S_Type, SB, uret, W1, W2, W3,
       \单周期硬布线控制器_1_beq , \单周期硬布线控制器_1_bne ;
  wire [1:0] priority_encoder_1_out, register_4_q, select;
  wire [3:0] AluOP, mips_ram_1_p4, multiplexer_18_out;
  wire [4:0] bit_extender_4_out, multiplexer_8_out, multiplexer_9_out, multiplexer_10_out,
       multiplexer_12_out, shifter_3_out;
  wire [11:0] multiplexer_11_out, shifter_1_out;
  wire [12:0] CNT_num;
  wire [15:0] \总周期数 ;
  wire [19:0] shifter_2_out;
  wire [31:0] adder_1_out, and_4_out, bit_extender_2_out, bit_extender_3_out, branchdata, INTPC, jaldata,
       jalrin, mEPC, mips_ram_1_p6, multiplexer_1_out, multiplexer_2_out, multiplexer_4_out,
       multiplexer_14_out, multiplexer_15_out, multiplexer_16_out, NextPC, PC_4, PC_q, R1Data, shifter_4_out;
  wire [31:2] alu_1_result;

  Button \u_继续运行  (.out(Go));
  Button _1 ();  // open: out
  Button _2 ();  // open: out
  Button _3 ();  // open: out
  LED #(.active("true")) led_1 (.in(W1));
  LED #(.active("true")) led_2 (.in(W2));
  LED #(.active("true")) led_3 (.in(W3));
  or or_1 (W2, d_ff_5_q, d_ff_2_q);
  or or_2 (W3, d_ff_6_q, d_ff_3_q);
  Hex_Digit_Display hex_digit_display_1 (.value(LedData[31:28]));  // open: dp
  D_Flip_Flop #(.trigger("rising"), .Pre_Clr_Positions("LEGACY"), .NegatePresetClear("false"), .enable("true"), .NewFFLayout("true")) d_ff_1 (
    .clk(IR1_t), .D(1'b1), .Q(d_ff_1_q), .reset(d_ff_4_q));  // open: Qn, preset, en
  or or_3 (W1, d_ff_4_q, d_ff_1_q);
  D_Flip_Flop #(.trigger("rising"), .Pre_Clr_Positions("LEGACY"), .NegatePresetClear("false"), .enable("true"), .NewFFLayout("true")) d_ff_2 (
    .clk(IR2_t), .D(1'b1), .Q(d_ff_2_q), .reset(d_ff_5_q));  // open: Qn, preset, en
  D_Flip_Flop #(.trigger("rising"), .Pre_Clr_Positions("LEGACY"), .NegatePresetClear("false"), .enable("true"), .NewFFLayout("true")) d_ff_3 (
    .clk(IR3_t), .D(1'b1), .Q(d_ff_3_q), .reset(d_ff_6_q));  // open: Qn, preset, en
  Hex_Digit_Display hex_digit_display_2 (.value(LedData[23:20]));  // open: dp
  Hex_Digit_Display hex_digit_display_3 (.value(LedData[27:24]));  // open: dp
  or or_4 (or_4_out, d_ff_1_q, d_ff_4_q);
  or or_5 (or_5_out, d_ff_2_q, d_ff_5_q);
  or or_6 (or_6_out, d_ff_3_q, d_ff_6_q);
  Hex_Digit_Display hex_digit_display_4 (.value(LedData[19:16]));  // open: dp
  Hex_Digit_Display hex_digit_display_5 (.value(LedData[15:12]));  // open: dp
  and and_1 (and_1_out, or_5_out, ~C2);  // AND_Gate
  and and_2 (and_2_out, or_6_out, ~C3);  // AND_Gate
  Hex_Digit_Display hex_digit_display_6 (.value(LedData[7:4]));  // open: dp
  Hex_Digit_Display hex_digit_display_7 (.value(LedData[11:8]));  // open: dp
  // Probe on \总周期数 
  and and_3 (and_3_out, or_4_out, ~C1);  // AND_Gate
  Hex_Digit_Display hex_digit_display_8 (.value(LedData[3:0]));  // open: dp
  not not_1 (not_1_out, uret);
  assign and_4_out = 32'hfffffffe & adder_1_out;  // AND_Gate and_4, 32 bits wide
  Multiplexer #(.select(1), .width(32), .disabled("Z"), .enable("false")) multiplexer_1 (
    .in0(PC_4), .in1(and_4_out), .out(multiplexer_1_out), .sel(JALR));
  Multiplexer #(.select(1), .width(32), .disabled("Z"), .enable("false")) multiplexer_2 (
    .in0(multiplexer_1_out), .in1(jaldata), .out(multiplexer_2_out), .sel(JAL));
  D_Flip_Flop #(.trigger("rising"), .Pre_Clr_Positions("LEGACY"), .NegatePresetClear("false"), .enable("true"), .NewFFLayout("true")) d_ff_4 (
    .clk(CLK), .D(and_3_out), .Q(d_ff_4_q));  // open: Qn, preset, en, reset
  D_Flip_Flop #(.trigger("rising"), .Pre_Clr_Positions("LEGACY"), .NegatePresetClear("false"), .enable("true"), .NewFFLayout("true")) d_ff_5 (
    .clk(CLK), .D(and_1_out), .Q(d_ff_5_q));  // open: Qn, preset, en, reset
  D_Flip_Flop #(.trigger("rising"), .Pre_Clr_Positions("LEGACY"), .NegatePresetClear("false"), .enable("true"), .NewFFLayout("true")) d_ff_6 (
    .clk(CLK), .D(and_2_out), .Q(d_ff_6_q));  // open: Qn, preset, en, reset
  Register #(.width(1), .trigger("rising"), .Select("low")) register_1 (
    .D(1'b0), .en(1'b1), .Q(register_1_q), .clk(not_1_out), .preset(INT));  // open: clr, cs
  not not_2 (IE, register_1_q);
  Multiplexer #(.select(1), .width(32), .disabled("Z"), .enable("false")) multiplexer_3 (
    .in0(multiplexer_4_out), .in1(mEPC), .out(NextPC), .sel(uret));
  Register #(.width(32), .trigger("rising"), .Select("low")) u_PC (
    .D(NextPC), .en(or_7_out), .Q(PC_q), .clk(CLK), .clr(RST));
  Multiplexer #(.select(1), .width(32), .disabled("Z"), .enable("false")) multiplexer_4 (
    .in0(multiplexer_2_out), .in1(branchdata), .out(multiplexer_4_out), .sel(branch));
  or or_7 (or_7_out, Go, not_3_out);
  not not_3 (not_3_out, halt);
  Register #(.width(1), .trigger("rising"), .Select("low")) register_2 (
    .D(1'b1), .Q(register_2_q), .clk(multiplexer_5_out), .clr(register_2_q));  // open: en
  Multiplexer #(.select(1), .width(1), .disabled("Z"), .enable("false")) multiplexer_5 (
    .in0(1'b1), .in1(CLK), .out(multiplexer_5_out), .sel(IntReady));
  Priority_Encoder #(.select(2), .disabled("Z")) priority_encoder_1 (
    .in0(d_ff_4_q), .in1(d_ff_5_q), .in2(d_ff_6_q), .in3(1'b0), .out(priority_encoder_1_out),
    .gs(priority_encoder_1_gs), .en_in(1'b1));  // open: en_out
  or or_8 (IR1_t, IR1, IRA);
  Adder #(.width(32)) adder_1 (.a(jalrin), .b(R1Data), .out(adder_1_out));  // open: cin, cout
  Register #(.width(1), .trigger("rising"), .Select("low")) register_3 (
    .D(1'b1), .Q(IntReady), .clk(INT), .clr(register_2_q));  // open: en
  and and_5 (INT, priority_encoder_1_gs, IE);
  or or_9 (IR2_t, IR2, IRB);
  Multiplexer #(.select(1), .width(32), .disabled("Z"), .enable("false")) multiplexer_6 (
    .in0(PC_q), .in1(INTPC), .out(PC), .sel(PC_2_q));
  Register #(.width(1), .trigger("rising"), .Select("low")) PC_2 (
    .D(IntReady), .Q(PC_2_q), .clk(CLK));  // open: en, clr
  Register #(.width(2), .trigger("rising"), .Select("low")) register_4 (
    .D(priority_encoder_1_out), .en(1'b1), .Q(register_4_q), .clk(INT));  // open: clr
  Multiplexer #(.select(2), .width(32), .disabled("Z"), .enable("false")) multiplexer_7 (
    .in0(32'h30ac), .in1(32'h3150), .in2(32'h31f4), .out(INTPC), .sel(priority_encoder_1_out));  // open: in3
  Register #(.width(32), .trigger("rising"), .Select("low")) register_5 (
    .D(NextPC), .en(IntReady), .Q(mEPC), .clk(CLK));  // open: clr
  // RiscV_Probe riscv_probe_1: pin names not known; wires that end beside it: IR
  ROM #(.addrWidth(10), .dataWidth(32), .Select("high")) rom_1 (.addr(PC[11:2]), .data(IR));
  Adder #(.width(32)) adder_2 (.a(PC), .b(32'h4), .out(PC_4));  // open: cin, cout
  Decoder #(.select(2), .tristate("false"), .disabled("Z"), .enable("false")) decoder_1 (
    .out0(decoder_1_out0), .out1(decoder_1_out1), .out2(decoder_1_out2), .sel(register_4_q));  // open: out3
  or or_10 (IR3_t, IR3, IRC);
  \单周期硬布线控制器  \u_单周期硬布线控制器_1  (
    .Funct({IR[30], IR[25], IR[14:12]}), .OP(IR[6:2]), .ALU_OP(AluOP), .MemToReg(MemToReg),
    .MemWrite(MemWrite), .ALU_SRC(AluSrcB), .RegWrite(RegWrite), .ecall(ecall), .in_3(IR[21]), .uret(uret),
    .JAL(JAL), .SB(SB), .Jalr(JALR), .BLTU(BLTU), .Bne(\单周期硬布线控制器_1_bne ), .Beq(\单周期硬布线控制器_1_beq ),
    .S_type(S_Type));  // open: I, B
  Multiplexer #(.select(1), .width(5), .disabled("Z"), .enable("false")) multiplexer_8 (
    .in0(IR[19:15]), .in1(5'b10001), .out(multiplexer_8_out), .sel(ecall));
  Multiplexer #(.select(1), .width(5), .disabled("Z"), .enable("false")) multiplexer_9 (
    .in0(IR[24:20]), .in1(5'b00001), .out(multiplexer_9_out), .sel(JALR));
  Multiplexer #(.select(1), .width(5), .disabled("Z"), .enable("false")) multiplexer_10 (
    .in0(IR[11:7]), .in1(5'b00001), .out(multiplexer_10_out), .sel(JALR));
  Multiplexer #(.select(1), .width(12), .disabled("Z"), .enable("false")) multiplexer_11 (
    .in0(IR[31:20]), .in1({IR[31:25], IR[11:7]}), .out(multiplexer_11_out), .sel(S_Type));
  Shifter #(.width(12), .shift("ll")) shifter_1 (
    .in({IR[31], IR[7], IR[30:25], IR[11:8]}), .\dist (4'b0001), .out(shifter_1_out));
  and and_6 (C1, decoder_1_out0, uret);
  and and_7 (C2, decoder_1_out1, uret);
  and and_8 (C3, decoder_1_out2, uret);
  Multiplexer #(.select(1), .width(5), .disabled("Z"), .enable("false")) multiplexer_12 (
    .in0(multiplexer_9_out), .in1(5'b01010), .out(multiplexer_12_out), .sel(ecall));
  assign jalrin = {{20{multiplexer_11_out[11]}}, multiplexer_11_out};  // Bit_Extender bit_extender_1
  Multiplexer #(.select(1), .width(32), .disabled("Z"), .enable("false")) multiplexer_13 (
    .in0(multiplexer_16_out), .in1(mips_ram_1_p6), .out(RDin), .sel(MemToReg));
  assign bit_extender_2_out = {{20{shifter_1_out[11]}}, shifter_1_out};  // Bit_Extender bit_extender_2
  Shifter #(.width(20), .shift("ll")) shifter_2 (
    .in({IR[31], IR[19:12], IR[20], IR[30:21]}), .\dist (5'b00001), .out(shifter_2_out));
  Adder #(.width(32)) adder_3 (.a(bit_extender_2_out), .b(PC), .out(branchdata));  // open: cin, cout
  assign bit_extender_3_out = {{12{shifter_2_out[19]}}, shifter_2_out};  // Bit_Extender bit_extender_3
  Adder #(.width(32)) adder_4 (.a(bit_extender_3_out), .b(PC), .out(jaldata));  // open: cin, cout
  Regifile regifile_1 (
    .Din(RDin), .Clk(CLK), .R1(R1Data), .R2(MDin), .WE(RegWrite), .W_num(multiplexer_10_out),
    .R1_num(multiplexer_8_out), .R2_num(multiplexer_12_out));
  Multiplexer #(.select(1), .width(32), .disabled("Z"), .enable("false")) multiplexer_14 (
    .in0(MDin), .in1(jalrin), .out(multiplexer_14_out), .sel(AluSrcB));
  not not_4 (not_4_out, halt);
  Counter #(.width(16), .max('hffff), .ongoal("wrap"), .trigger("rising"), .behavior("new")) counter_1 (
    .count(not_4_out), .Q(\总周期数 ), .clk(CLK));  // open: load, D, carry, clr, preset, down
  Comparator #(.width(32), .mode("unsigned")) comparator_1 (
    .a(R1Data), .b(MDin), .lt(comparator_1_lt));  // open: gt, eq
  assign bit_extender_4_out = {{3{select[1]}}, select};  // Bit_Extender bit_extender_4
  Shifter #(.width(5), .shift("ll")) shifter_3 (.in(bit_extender_4_out), .\dist (3'b011), .out(shifter_3_out));
  and and_9 (and_9_out, alu_1_equal, \单周期硬布线控制器_1_beq );
  not not_5 (not_5_out, alu_1_equal);
  and and_10 (and_10_out, not_5_out, \单周期硬布线控制器_1_bne );
  ALU alu_1 (
    .X(R1Data), .Y(multiplexer_14_out), .AluOP(AluOP), .Equal(alu_1_equal), .Result({alu_1_result, select}));  // open: Result_2, out_4, out_6
  Multiplexer #(.select(1), .width(32), .disabled("Z"), .enable("false")) multiplexer_15 (
    .in0(MDin), .in1(shifter_4_out), .out(multiplexer_15_out), .sel(SB));
  Shifter #(.width(32), .shift("ll")) shifter_4 (.in(MDin), .\dist (shifter_3_out), .out(shifter_4_out));
  D_Flip_Flop #(.trigger("high"), .Pre_Clr_Positions("LEGACY"), .NegatePresetClear("false"), .enable("true"), .NewFFLayout("false")) d_ff_7 (.Q(d_ff_7_q));  // open: clk, D, Qn, preset, en, reset
  // Probe on 13'h177
  or or_11 (branch, and_9_out, and_10_out, and_11_out);
  and and_11 (and_11_out, BLTU, comparator_1_lt);
  Multiplexer #(.select(1), .width(32), .disabled("Z"), .enable("false")) multiplexer_16 (
    .in0({alu_1_result, select}), .in1(PC_4), .out(multiplexer_16_out), .sel(or_12_out));
  or or_12 (or_12_out, JAL, JALR);
  Comparator #(.width(13), .mode("twosComplement")) comparator_2 (
    .a(CNT_num), .b(13'h177), .eq(comparator_2_eq), .lt(comparator_2_lt));  // open: gt
  Clock #(.highDuration(1), .lowDuration(1)) clock_1 (.out(clock_1_out));
  // MIPS_RAM mips_ram_1: pin names not known; wires that end beside it: alu_1_result[11:2], multiplexer_15_out, MemWrite, mips_ram_1_p4, CLK, mips_ram_1_p6
  Multiplexer #(.select(1), .width(4), .disabled("Z"), .enable("false")) multiplexer_17 (
    .in0(4'b1111), .in1(multiplexer_18_out), .out(mips_ram_1_p4), .sel(SB));
  Multiplexer #(.select(2), .width(4), .disabled("Z"), .enable("false")) multiplexer_18 (
    .in0(4'b0001), .in1(4'b0010), .in2(4'b0100), .in3(4'b1000), .out(multiplexer_18_out), .sel(select));
  Counter #(.width(13), .max('h1fff), .ongoal("stay"), .trigger("rising"), .behavior("old")) counter_2 (
    .count(comparator_2_lt), .Q(CNT_num), .clk(clock_1_out));  // open: load, D, carry, clr, preset
  Comparator #(.width(32), .mode("twosComplement")) comparator_3 (
    .a(R1Data), .b(32'h22), .eq(comparator_3_eq));  // open: gt, lt
  nand nand_1 (nand_1_out, d_ff_7_q, comparator_2_eq);
  not not_6 (not_6_out, comparator_3_eq);
  assign CLK = nand_1_out ? clock_1_out : 1'bz;  // Controlled_Buffer controlled_buffer_1
  Pull_Resistor #(.pull(1)) pull_resistor_1 (.node(CLK));
  and and_12 (and_12_out, ecall, not_6_out);
  and and_13 (and_13_out, ecall, comparator_3_eq);
  Register #(.width(1), .trigger("rising"), .Select("low")) register_6 (
    .D(and_12_out), .en(not_7_out), .Q(halt), .clk(CLK), .clr(Go));
  not not_7 (not_7_out, halt);
  Comparator #(.width(16), .mode("twosComplement")) comparator_4 (
    .a(16'h23b), .b(\总周期数 ), .eq(comparator_4_eq));  // open: gt, lt
  Comparator #(.width(16), .mode("twosComplement")) comparator_5 (
    .a(\总周期数 ), .b(16'h1), .eq(comparator_5_eq));  // open: gt, lt
  Comparator #(.width(16), .mode("twosComplement")) comparator_6 (
    .a(\总周期数 ), .b(16'h4), .eq(comparator_6_eq));  // open: gt, lt
  Comparator #(.width(16), .mode("twosComplement")) comparator_7 (
    .a(\总周期数 ), .b(16'h7), .eq(comparator_7_eq));  // open: gt, lt
  Register #(.width(32), .trigger("rising"), .Select("low")) PC_3 (
    .D(MDin), .en(and_13_out), .Q(LedData), .clk(CLK));  // open: clr
  or or_13 (or_13_out, comparator_4_eq, comparator_5_eq);
  Pull_Resistor #(.pull(0)) pull_resistor_2 (.node(IRA));
  assign IRA = or_13_out ? ~CLK : 1'bz;  // Controlled_Inverter controlled_inverter_1
  Pull_Resistor #(.pull(0)) pull_resistor_3 (.node(IRB));
  assign IRB = comparator_6_eq ? ~CLK : 1'bz;  // Controlled_Inverter controlled_inverter_2
  Pull_Resistor #(.pull(0)) pull_resistor_4 (.node(IRC));
  assign IRC = comparator_7_eq ? ~CLK : 1'bz;  // Controlled_Inverter controlled_inverter_3

  // Notes on the sheet:
  //   中断源
  //   中断等待指示
  //   总复位信号应将除ROM以外所有存储组件全部清零
  //   数码管输出
  //   数码管输出应该用寄存器锁存，否则显示数据只能一闪而过
  //   指令探针
  //   指令存储器
  //   指令字
  //   contents of rom_1 (hex, n*v repeats v):
  //   7d000113 100413 1f41993 41f9d993 433 c00913 800b13 140413 f47413 800293 100313 499993 89e9b3 1300533
  //   2200893 73 406282b3 fe0294e3 140413 f00f93 1f47433 1c41413 800293 100313 49d993 89e9b3 1300533
  //   2200893 73 406282b3 fe0294e3 1c45413 406b0b33 b0463 f95ff06f 2b3 fff2c293 1029293 fff2e293 500533
  //   2200893 73 f5dff06f 1112023 410113 a12023 410113 812023 410113 1312023 410113 1412023 410113 1512023
  //   410113 1612023 410113 100b13 300a13 100a93 1600433 441413 14469b3 1300533 2200893 73 fe0416e3
  //   415a0a33 fe0a10e3 ffc10113 12b03 ffc10113 12a83 ffc10113 12a03 ffc10113 12983 ffc10113 12403
  //   ffc10113 12503 ffc10113 12883 200073 1112023 410113 a12023 410113 812023 410113 1312023 410113
  //   1412023 410113 1512023 410113 1612023 410113 200b13 300a13 100a93 1600433 441413 14469b3 1300533
  //   2200893 73 fe0416e3 415a0a33 fe0a10e3 ffc10113 12b03 ffc10113 12a83 ffc10113 12a03 ffc10113 12983
  //   ffc10113 12403 ffc10113 12503 ffc10113 12883 200073 1112023 410113 a12023 410113 812023 410113
  //   1312023 410113 1412023 410113 1512023 410113 1612023 410113 300b13 300a13 100a93 1600433 441413
  //   14469b3 1300533 2200893 73 fe0416e3 415a0a33 fe0a10e3 ffc10113 12b03 ffc10113 12a83 ffc10113 12a03
  //   ffc10113 12983 ffc10113 12403 ffc10113 12503 ffc10113 12883 200073
  //   Beq
  //   Bne
  //   AluOP
  //   AluSrcB
  //   RegWrite
  //   MemToReg
  //   MemWrite
  //   为方便自动评测，需要输出PC，IR，寄存器堆写如数据RDin
  //   RAM写使能MemWrite、RAM写入数据MDin等信号
  //   控制位
  //   暂停节拍，不能为0
  //   数据存储器
  //   戳工具置1进入计数暂停模式，ctrl+k时钟自动运行到对应节拍暂停
  //   ctrl+k关闭时钟连续运行，将控制位置零，进入单步调试模式调试
  //   可计数暂停的时钟源
  //   单级中断测试信号模拟器
endmodule

module \单周期_多级中断  (
  input  IR1,
  input  IR2,
  input  IR3,
  output RegWrite,
  output MemWrite,
  output [31:0] PC,
  output [31:0] IR,
  output [31:0] RDin,
  output [31:0] MDin,
  output [31:0] LedData
);

  wire alu_1_equal, AluSrcB, and_1_out, and_2_out, and_3_out, and_9_out, and_10_out, and_11_out, and_12_out,
       and_13_out, BLTU, branch, C1, C2, C3, CLK, clock_1_out, comparator_1_eq, comparator_2_eq,
       comparator_3_eq, comparator_4_eq, comparator_5_eq, comparator_6_eq, comparator_7_lt, comparator_8_eq,
       comparator_9_eq, comparator_9_lt, CSRRCI, CSRRSI, d_ff_1_q, d_ff_2_q, d_ff_3_q, d_ff_4_q, d_ff_5_q,
       d_ff_6_q, d_ff_7_q, decoder_1_out1, decoder_1_out2, decoder_1_out3, decoder_2_out0, decoder_2_out1,
       decoder_2_out2, decoder_3_out1, decoder_3_out2, decoder_3_out3, ecall, Go, halt, IE, INRun, INT,
       Int2PC, IntReady, IR1_t, IR2_t, IR3_t, IRA, IRB, IRC, JAL, JALR, MemToReg, multiplexer_6_out,
       nand_1_out, not_1_out, not_2_out, not_3_out, not_4_out, not_6_out, not_7_out, not_8_out, or_4_out,
       or_5_out, or_6_out, or_7_out, or_8_out, or_9_out, or_10_out, or_14_out, or_15_out, or_17_out,
       register_1_q, register_2_q, register_3_q, register_4_q, register_10_q, RST, S_Type, SB, uret, W1, W2,
       W3, \单周期硬布线控制器_1_beq , \单周期硬布线控制器_1_bne ;
  wire [1:0] counter_1_q, IntNum, multiplexer_8_out, register_9_q, select;
  wire [3:0] AluOP, mips_ram_1_p4, multiplexer_21_out;
  wire [4:0] bit_extender_4_out, multiplexer_11_out, multiplexer_12_out, multiplexer_13_out,
       multiplexer_15_out, shifter_3_out;
  wire [11:0] multiplexer_14_out, shifter_1_out;
  wire [12:0] CNT_num;
  wire [15:0] \总周期数 ;
  wire [19:0] shifter_2_out;
  wire [31:0] adder_1_out, and_4_out, bit_extender_2_out, bit_extender_3_out, branchdata, INTPC, jaldata,
       jalrin, mEPC, mips_ram_1_p6, multiplexer_2_out, multiplexer_3_out, multiplexer_5_out,
       multiplexer_17_out, multiplexer_18_out, multiplexer_19_out, NextPC, PC_4, PC_q, R1Data, register_6_q,
       register_7_q, register_8_q, shifter_4_out;
  wire [31:2] alu_1_result;

  Button \u_继续运行  (.out(Go));
  Button _1 ();  // open: out
  Button _2 ();  // open: out
  Button _3 ();  // open: out
  LED #(.active("true")) led_1 (.in(W1));
  LED #(.active("true")) led_2 (.in(W2));
  LED #(.active("true")) led_3 (.in(W3));
  Decoder #(.select(2), .tristate("false"), .disabled("Z"), .enable("false")) decoder_1 (
    .out1(decoder_1_out1), .out2(decoder_1_out2), .out3(decoder_1_out3), .sel(IntNum));  // open: out0
  or or_1 (W2, d_ff_5_q, d_ff_2_q);
  or or_2 (W3, d_ff_6_q, d_ff_3_q);
  Hex_Digit_Display hex_digit_display_1 (.value(LedData[31:28]));  // open: dp
  Comparator #(.width(16), .mode("twosComplement")) comparator_1 (
    .a(\总周期数 ), .b(16'h7), .eq(comparator_1_eq));  // open: gt, lt
  Comparator #(.width(16), .mode("twosComplement")) comparator_2 (
    .a(\总周期数 ), .b(16'h241), .eq(comparator_2_eq));  // open: gt, lt
  Register #(.width(1), .trigger("rising"), .Select("low")) register_1 (
    .D(1'b1), .en(decoder_1_out1), .Q(register_1_q), .clk(Int2PC), .clr(C1));
  Register #(.width(1), .trigger("rising"), .Select("low")) register_2 (
    .D(1'b1), .en(decoder_1_out2), .Q(register_2_q), .clk(Int2PC), .clr(C2));
  Register #(.width(1), .trigger("rising"), .Select("low")) register_3 (
    .D(1'b1), .en(decoder_1_out3), .Q(register_3_q), .clk(Int2PC), .clr(C3));
  D_Flip_Flop #(.trigger("rising"), .Pre_Clr_Positions("LEGACY"), .NegatePresetClear("false"), .enable("true"), .NewFFLayout("true")) d_ff_1 (
    .clk(IR1_t), .D(1'b1), .Q(d_ff_1_q), .reset(d_ff_4_q));  // open: Qn, preset, en
  or or_3 (W1, d_ff_4_q, d_ff_1_q);
  D_Flip_Flop #(.trigger("rising"), .Pre_Clr_Positions("LEGACY"), .NegatePresetClear("false"), .enable("true"), .NewFFLayout("true")) d_ff_2 (
    .clk(IR2_t), .D(1'b1), .Q(d_ff_2_q), .reset(d_ff_5_q));  // open: Qn, preset, en
  D_Flip_Flop #(.trigger("rising"), .Pre_Clr_Positions("LEGACY"), .NegatePresetClear("false"), .enable("true"), .NewFFLayout("true")) d_ff_3 (
    .clk(IR3_t), .D(1'b1), .Q(d_ff_3_q), .reset(d_ff_6_q));  // open: Qn, preset, en
  Hex_Digit_Display hex_digit_display_2 (.value(LedData[23:20]));  // open: dp
  Hex_Digit_Display hex_digit_display_3 (.value(LedData[27:24]));  // open: dp
  Comparator #(.width(16), .mode("twosComplement")) comparator_3 (
    .a(16'h258), .b(\总周期数 ), .eq(comparator_3_eq));  // open: gt, lt
  or or_4 (or_4_out, comparator_3_eq, comparator_4_eq);
  Comparator #(.width(16), .mode("twosComplement")) comparator_4 (
    .a(\总周期数 ), .b(16'h1), .eq(comparator_4_eq));  // open: gt, lt
  Comparator #(.width(16), .mode("twosComplement")) comparator_5 (
    .a(\总周期数 ), .b(16'h4), .eq(comparator_5_eq));  // open: gt, lt
  or or_5 (or_5_out, comparator_1_eq, comparator_2_eq);
  or or_6 (or_6_out, d_ff_1_q, d_ff_4_q);
  or or_7 (or_7_out, d_ff_2_q, d_ff_5_q);
  or or_8 (or_8_out, d_ff_3_q, d_ff_6_q);
  Hex_Digit_Display hex_digit_display_4 (.value(LedData[19:16]));  // open: dp
  Hex_Digit_Display hex_digit_display_5 (.value(LedData[15:12]));  // open: dp
  Pull_Resistor #(.pull(0)) pull_resistor_1 (.node(IRA));
  assign IRA = or_4_out ? ~CLK : 1'bz;  // Controlled_Inverter controlled_inverter_1
  Pull_Resistor #(.pull(0)) pull_resistor_2 (.node(IRB));
  assign IRB = comparator_5_eq ? ~CLK : 1'bz;  // Controlled_Inverter controlled_inverter_2
  Pull_Resistor #(.pull(0)) pull_resistor_3 (.node(IRC));
  assign IRC = or_5_out ? ~CLK : 1'bz;  // Controlled_Inverter controlled_inverter_3
  Multiplexer #(.select(2), .width(1), .disabled("Z"), .enable("false")) multiplexer_1 (
    .in0(1'b1), .in1(register_1_q), .in2(register_2_q), .in3(register_3_q), .out(INRun), .sel(IntNum));
  and and_1 (and_1_out, or_7_out, ~C2);  // AND_Gate
  and and_2 (and_2_out, or_8_out, ~C3);  // AND_Gate
  Hex_Digit_Display hex_digit_display_6 (.value(LedData[7:4]));  // open: dp
  Hex_Digit_Display hex_digit_display_7 (.value(LedData[11:8]));  // open: dp
  // Probe on \总周期数 
  and and_3 (and_3_out, or_6_out, ~C1);  // AND_Gate
  Hex_Digit_Display hex_digit_display_8 (.value(LedData[3:0]));  // open: dp
  assign and_4_out = 32'hfffffffe & adder_1_out;  // AND_Gate and_4, 32 bits wide
  Multiplexer #(.select(1), .width(32), .disabled("Z"), .enable("false")) multiplexer_2 (
    .in0(PC_4), .in1(and_4_out), .out(multiplexer_2_out), .sel(JALR));
  Multiplexer #(.select(1), .width(32), .disabled("Z"), .enable("false")) multiplexer_3 (
    .in0(multiplexer_2_out), .in1(jaldata), .out(multiplexer_3_out), .sel(JAL));
  D_Flip_Flop #(.trigger("rising"), .Pre_Clr_Positions("LEGACY"), .NegatePresetClear("false"), .enable("true"), .NewFFLayout("true")) d_ff_4 (
    .clk(CLK), .D(and_3_out), .Q(d_ff_4_q));  // open: Qn, preset, en, reset
  D_Flip_Flop #(.trigger("rising"), .Pre_Clr_Positions("LEGACY"), .NegatePresetClear("false"), .enable("true"), .NewFFLayout("true")) d_ff_5 (
    .clk(CLK), .D(and_1_out), .Q(d_ff_5_q));  // open: Qn, preset, en, reset
  D_Flip_Flop #(.trigger("rising"), .Pre_Clr_Positions("LEGACY"), .NegatePresetClear("false"), .enable("true"), .NewFFLayout("true")) d_ff_6 (
    .clk(CLK), .D(and_2_out), .Q(d_ff_6_q));  // open: Qn, preset, en, reset
  or or_9 (or_9_out, IntReady, uret);
  Multiplexer #(.select(1), .width(32), .disabled("Z"), .enable("false")) multiplexer_4 (
    .in0(multiplexer_5_out), .in1(mEPC), .out(NextPC), .sel(uret));
  Register #(.width(32), .trigger("rising"), .Select("low")) u_PC (
    .D(NextPC), .en(or_10_out), .Q(PC_q), .clk(CLK), .clr(RST));
  Multiplexer #(.select(1), .width(32), .disabled("Z"), .enable("false")) multiplexer_5 (
    .in0(multiplexer_3_out), .in1(branchdata), .out(multiplexer_5_out), .sel(branch));
  or or_10 (or_10_out, Go, not_1_out);
  not not_1 (not_1_out, halt);
  Register #(.width(1), .trigger("rising"), .Select("low")) register_4 (
    .D(1'b1), .Q(register_4_q), .clk(multiplexer_6_out), .clr(register_4_q));  // open: en
  Multiplexer #(.select(1), .width(1), .disabled("Z"), .enable("false")) multiplexer_6 (
    .in0(1'b1), .in1(CLK), .out(multiplexer_6_out), .sel(IntReady));
  Priority_Encoder #(.select(2), .disabled("Z")) priority_encoder_1 (
    .in0(1'b1), .in1(d_ff_4_q), .in2(d_ff_5_q), .in3(d_ff_6_q), .out(IntNum), .en_in(1'b1));  // open: gs, en_out
  or or_11 (IR1_t, IR1, IRA);
  Counter #(.width(2), .max('h3), .ongoal("wrap"), .trigger("rising"), .behavior("new")) counter_1 (
    .count(or_9_out), .Q(counter_1_q), .clk(CLK), .down(uret));  // open: load, D, carry, clr, preset
  Decoder #(.select(2), .tristate("false"), .disabled("Z"), .enable("false")) decoder_2 (
    .out0(decoder_2_out0), .out1(decoder_2_out1), .out2(decoder_2_out2), .sel(counter_1_q));  // open: out3
  Adder #(.width(32)) adder_1 (.a(jalrin), .b(R1Data), .out(adder_1_out));  // open: cin, cout
  Register #(.width(1), .trigger("rising"), .Select("low")) register_5 (
    .D(1'b1), .Q(IntReady), .clk(INT), .clr(register_4_q));  // open: en
  or or_12 (IR2_t, IR2, IRB);
  Multiplexer #(.select(1), .width(32), .disabled("Z"), .enable("false")) multiplexer_7 (
    .in0(PC_q), .in1(INTPC), .out(PC), .sel(Int2PC));
  Register #(.width(1), .trigger("rising"), .Select("low")) PC_2 (
    .D(IntReady), .Q(Int2PC), .clk(CLK));  // open: en, clr
  Multiplexer #(.select(1), .width(2), .disabled("Z"), .enable("false")) multiplexer_8 (
    .in0(multiplexer_8_out), .in1(IntNum), .out(multiplexer_8_out), .sel(IE));
  Multiplexer #(.select(2), .width(32), .disabled("Z"), .enable("false")) multiplexer_9 (
    .in1(32'h30ac), .in2(32'h3158), .in3(32'h3204), .out(INTPC), .sel(IntNum));  // open: in0
  Register #(.width(32), .trigger("rising"), .Select("low")) register_6 (
    .D(NextPC), .en(decoder_2_out0), .Q(register_6_q), .clk(CLK));  // open: clr
  Register #(.width(32), .trigger("rising"), .Select("low")) register_7 (
    .D(NextPC), .en(decoder_2_out1), .Q(register_7_q), .clk(CLK));  // open: clr
  Register #(.width(32), .trigger("rising"), .Select("low")) register_8 (
    .D(NextPC), .en(decoder_2_out2), .Q(register_8_q), .clk(CLK));  // open: clr
  // RiscV_Probe riscv_probe_1: pin names not known; wires that end beside it: IR
  ROM #(.addrWidth(10), .dataWidth(32), .Select("high")) rom_1 (.addr(PC[11:2]), .data(IR));
  Adder #(.width(32)) adder_2 (.a(PC), .b(32'h4), .out(PC_4));  // open: cin, cout
  Register #(.width(2), .trigger("rising"), .Select("low")) register_9 (
    .D(multiplexer_8_out), .en(1'b1), .Q(register_9_q), .clk(CLK));  // open: clr
  Decoder #(.select(2), .tristate("false"), .disabled("Z"), .enable("false")) decoder_3 (
    .out1(decoder_3_out1), .out2(decoder_3_out2), .out3(decoder_3_out3), .sel(register_9_q));  // open: out0
  or or_13 (IR3_t, IR3, IRC);
  Multiplexer #(.select(2), .width(32), .disabled("Z"), .enable("false")) multiplexer_10 (
    .in1(register_6_q), .in2(register_7_q), .in3(register_8_q), .out(mEPC), .sel(counter_1_q));  // open: in0
  Comparator #(.width(2), .mode("twosComplement")) comparator_6 (
    .a(multiplexer_8_out), .b(register_9_q), .eq(comparator_6_eq));  // open: gt, lt
  \单周期硬布线控制器  \u_单周期硬布线控制器_1  (
    .Funct({IR[30], IR[25], IR[14:12]}), .OP(IR[6:2]), .ALU_OP(AluOP), .MemToReg(MemToReg),
    .MemWrite(MemWrite), .ALU_SRC(AluSrcB), .RegWrite(RegWrite), .ecall(ecall), .in_3(IR[21]), .uret(uret),
    .JAL(JAL), .SB(SB), .Jalr(JALR), .BLTU(BLTU), .Bne(\单周期硬布线控制器_1_bne ), .Beq(\单周期硬布线控制器_1_beq ),
    .S_type(S_Type), .I(CSRRSI), .B(CSRRCI));
  Multiplexer #(.select(1), .width(5), .disabled("Z"), .enable("false")) multiplexer_11 (
    .in0(IR[19:15]), .in1(5'b10001), .out(multiplexer_11_out), .sel(ecall));
  Multiplexer #(.select(1), .width(5), .disabled("Z"), .enable("false")) multiplexer_12 (
    .in0(IR[24:20]), .in1(5'b00001), .out(multiplexer_12_out), .sel(JALR));
  Multiplexer #(.select(1), .width(5), .disabled("Z"), .enable("false")) multiplexer_13 (
    .in0(IR[11:7]), .in1(5'b00001), .out(multiplexer_13_out), .sel(JALR));
  Multiplexer #(.select(1), .width(12), .disabled("Z"), .enable("false")) multiplexer_14 (
    .in0(IR[31:20]), .in1({IR[31:25], IR[11:7]}), .out(multiplexer_14_out), .sel(S_Type));
  Shifter #(.width(12), .shift("ll")) shifter_1 (
    .in({IR[31], IR[7], IR[30:25], IR[11:8]}), .\dist (4'b0001), .out(shifter_1_out));
  not not_2 (not_2_out, comparator_6_eq);
  and and_5 (C1, decoder_3_out1, uret);
  and and_6 (C2, decoder_3_out2, uret);
  and and_7 (C3, decoder_3_out3, uret);
  Multiplexer #(.select(1), .width(5), .disabled("Z"), .enable("false")) multiplexer_15 (
    .in0(multiplexer_12_out), .in1(5'b01010), .out(multiplexer_15_out), .sel(ecall));
  assign jalrin = {{20{multiplexer_14_out[11]}}, multiplexer_14_out};  // Bit_Extender bit_extender_1
  Multiplexer #(.select(1), .width(32), .disabled("Z"), .enable("false")) multiplexer_16 (
    .in0(multiplexer_19_out), .in1(mips_ram_1_p6), .out(RDin), .sel(MemToReg));
  assign bit_extender_2_out = {{20{shifter_1_out[11]}}, shifter_1_out};  // Bit_Extender bit_extender_2
  Shifter #(.width(20), .shift("ll")) shifter_2 (
    .in({IR[31], IR[19:12], IR[20], IR[30:21]}), .\dist (5'b00001), .out(shifter_2_out));
  and and_8 (INT, not_2_out, ~INRun);  // AND_Gate
  not not_3 (not_3_out, or_14_out);
  or or_14 (or_14_out, CSRRSI, uret);
  Adder #(.width(32)) adder_3 (.a(bit_extender_2_out), .b(PC), .out(branchdata));  // open: cin, cout
  assign bit_extender_3_out = {{12{shifter_2_out[19]}}, shifter_2_out};  // Bit_Extender bit_extender_3
  Adder #(.width(32)) adder_4 (.a(bit_extender_3_out), .b(PC), .out(jaldata));  // open: cin, cout
  or or_15 (or_15_out, Int2PC, CSRRCI);
  Register #(.width(1), .trigger("rising"), .Select("low")) register_10 (
    .D(1'b0), .en(1'b1), .Q(register_10_q), .clk(not_3_out), .preset(or_15_out));  // open: clr, cs
  Regifile regifile_1 (
    .Din(RDin), .Clk(CLK), .R1(R1Data), .R2(MDin), .WE(RegWrite), .W_num(multiplexer_13_out),
    .R1_num(multiplexer_11_out), .R2_num(multiplexer_15_out));
  Multiplexer #(.select(1), .width(32), .disabled("Z"), .enable("false")) multiplexer_17 (
    .in0(MDin), .in1(jalrin), .out(multiplexer_17_out), .sel(AluSrcB));
  not not_4 (not_4_out, halt);
  Counter #(.width(16), .max('hffff), .ongoal("wrap"), .trigger("rising"), .behavior("new")) counter_2 (
    .count(not_4_out), .Q(\总周期数 ), .clk(CLK));  // open: load, D, carry, clr, preset, down
  not not_5 (IE, register_10_q);
  Comparator #(.width(32), .mode("unsigned")) comparator_7 (
    .a(R1Data), .b(MDin), .lt(comparator_7_lt));  // open: gt, eq
  assign bit_extender_4_out = {{3{select[1]}}, select};  // Bit_Extender bit_extender_4
  Shifter #(.width(5), .shift("ll")) shifter_3 (.in(bit_extender_4_out), .\dist (3'b011), .out(shifter_3_out));
  Comparator #(.width(32), .mode("twosComplement")) comparator_8 (
    .a(R1Data), .b(32'h22), .eq(comparator_8_eq));  // open: gt, lt
  and and_9 (and_9_out, alu_1_equal, \单周期硬布线控制器_1_beq );
  not not_6 (not_6_out, alu_1_equal);
  and and_10 (and_10_out, not_6_out, \单周期硬布线控制器_1_bne );
  ALU alu_1 (
    .X(R1Data), .Y(multiplexer_17_out), .AluOP(AluOP), .Equal(alu_1_equal), .Result({alu_1_result, select}));  // open: Result_2, out_4, out_6
  Multiplexer #(.select(1), .width(32), .disabled("Z"), .enable("false")) multiplexer_18 (
    .in0(MDin), .in1(shifter_4_out), .out(multiplexer_18_out), .sel(SB));
  Shifter #(.width(32), .shift("ll")) shifter_4 (.in(MDin), .\dist (shifter_3_out), .out(shifter_4_out));
  and and_11 (and_11_out, ecall, not_7_out);
  not not_7 (not_7_out, comparator_8_eq);
  and and_12 (and_12_out, ecall, comparator_8_eq);
  D_Flip_Flop #(.trigger("high"), .Pre_Clr_Positions("LEGACY"), .NegatePresetClear("false"), .enable("true"), .NewFFLayout("false")) d_ff_7 (.Q(d_ff_7_q));  // open: clk, D, Qn, preset, en, reset
  // Probe on 13'hc
  or or_16 (branch, and_9_out, and_10_out, and_13_out);
  and and_13 (and_13_out, BLTU, comparator_7_lt);
  Multiplexer #(.select(1), .width(32), .disabled("Z"), .enable("false")) multiplexer_19 (
    .in0({alu_1_result, select}), .in1(PC_4), .out(multiplexer_19_out), .sel(or_17_out));
  or or_17 (or_17_out, JAL, JALR);
  not not_8 (not_8_out, halt);
  Comparator #(.width(13), .mode("twosComplement")) comparator_9 (
    .a(CNT_num), .b(13'hc), .eq(comparator_9_eq), .lt(comparator_9_lt));  // open: gt
  Clock #(.highDuration(1), .lowDuration(1)) clock_1 (.out(clock_1_out));
  // MIPS_RAM mips_ram_1: pin names not known; wires that end beside it: alu_1_result[11:2], multiplexer_18_out, MemWrite, mips_ram_1_p4, CLK, mips_ram_1_p6
  Multiplexer #(.select(1), .width(4), .disabled("Z"), .enable("false")) multiplexer_20 (
    .in0(4'b1111), .in1(multiplexer_21_out), .out(mips_ram_1_p4), .sel(SB));
  Multiplexer #(.select(2), .width(4), .disabled("Z"), .enable("false")) multiplexer_21 (
    .in0(4'b0001), .in1(4'b0010), .in2(4'b0100), .in3(4'b1000), .out(multiplexer_21_out), .sel(select));
  Register #(.width(1), .trigger("rising"), .Select("low")) register_11 (
    .D(and_11_out), .en(not_8_out), .Q(halt), .clk(CLK), .clr(Go));
  Register #(.width(32), .trigger("rising"), .Select("low")) PC_3 (
    .D(MDin), .en(and_12_out), .Q(LedData), .clk(CLK));  // open: clr
  Counter #(.width(13), .max('h1fff), .ongoal("stay"), .trigger("rising"), .behavior("old")) counter_3 (
    .count(comparator_9_lt), .Q(CNT_num), .clk(clock_1_out));  // open: load, D, carry, clr, preset
  nand nand_1 (nand_1_out, d_ff_7_q, comparator_9_eq);
  assign CLK = nand_1_out ? clock_1_out : 1'bz;  // Controlled_Buffer controlled_buffer_1
  Pull_Resistor #(.pull(1)) pull_resistor_4 (.node(CLK));

  // Notes on the sheet:
  //   中断源
  //   中断等待指示
  //   总复位信号应将除ROM以外所有存储组件全部清零
  //   多级中断测试信号模拟器
  //   数码管输出
  //   数码管输出应该用寄存器锁存，否则显示数据只能一闪而过
  //   指令探针
  //   指令存储器
  //   指令字
  //   contents of rom_1 (hex, n*v repeats v):
  //   7d000113 100413 1f41993 41f9d993 433 c00913 800b13 140413 f47413 800293 100313 499993 89e9b3 1300533
  //   2200893 73 406282b3 fe0294e3 140413 f00f93 1f47433 1c41413 800293 100313 49d993 89e9b3 1300533
  //   2200893 73 406282b3 fe0294e3 1c45413 406b0b33 b0463 f95ff06f 2b3 fff2c293 1029293 fff2e293 500533
  //   2200893 73 f5dff06f 1112023 410113 a12023 410113 812023 410113 1312023 410113 1412023 410113 1512023
  //   410113 1612023 410113 40e073 100b13 300a13 100a93 1600433 441413 14469b3 1300533 2200893 73 fe0416e3
  //   415a0a33 fe0a10e3 40f073 ffc10113 12b03 ffc10113 12a83 ffc10113 12a03 ffc10113 12983 ffc10113 12403
  //   ffc10113 12503 ffc10113 12883 200073 1112023 410113 a12023 410113 812023 410113 1312023 410113
  //   1412023 410113 1512023 410113 1612023 410113 40e073 200b13 300a13 100a93 1600433 441413 14469b3
  //   1300533 2200893 73 fe0416e3 415a0a33 fe0a10e3 40f073 ffc10113 12b03 ffc10113 12a83 ffc10113 12a03
  //   ffc10113 12983 ffc10113 12403 ffc10113 12503 ffc10113 12883 200073 1112023 410113 a12023 410113
  //   812023 410113 1312023 410113 1412023 410113 1512023 410113 1612023 410113 40e073 300b13 300a13
  //   100a93 1600433 441413 14469b3 1300533 2200893 73 fe0416e3 415a0a33 fe0a10e3 40f073 ffc10113 12b03
  //   ffc10113 12a83 ffc10113 12a03 ffc10113 12983 ffc10113 12403 ffc10113 12503 ffc10113 12883 200073
  //   Beq
  //   Bne
  //   AluOP
  //   AluSrcB
  //   RegWrite
  //   MemToReg
  //   MemWrite
  //   为方便自动评测，需要输出PC，IR，寄存器堆写如数据RDin
  //   RAM写使能MemWrite、RAM写入数据MDin等信号
  //   控制位
  //   暂停节拍，不能为0
  //   数据存储器
  //   戳工具置1进入计数暂停模式，ctrl+k时钟自动运行到对应节拍暂停
  //   ctrl+k关闭时钟连续运行，将控制位置零，进入单步调试模式调试
  //   可计数暂停的时钟源
endmodule

module \封装正确性测试  (
);

  wire IR1, IR2, IR3, MemW, RegW;
  wire [31:0] EX_PC, ID_PC, IF_PC, IR, LED, MDin, MDinr, MEM_PC, PC, RDin, RDinr, WB_PC;

  \单周期RISC_V  \u_单周期risc_v_1  (
    .IR1(IR1), .IR2(IR2), .IR3(IR3), .RegWrite(RegW), .MemWrite(MemW), .PC(PC), .IR(IR), .RDin(RDin),
    .MDin(MDin), .LedData(LED));
  \气泡流水线  \u_气泡流水线_1  (
    .RegWrite(RegW), .MemWrite(MemW), .IF_PC(IF_PC), .ID_PC(ID_PC), .EX_PC(EX_PC), .M_PC(MEM_PC),
    .WB_PC(WB_PC), .RDin(RDinr), .MDin(MDinr), .LedData(LED));
  \单周期_单级中断  \u_单周期_单级中断_1  (
    .IR1(IR1), .IR2(IR2), .IR3(IR3), .RegWrite(RegW), .MemWrite(MemW), .PC(PC), .IR(IR), .RDin(RDin),
    .MDin(MDin), .LedData(LED));
  \理想流水线  \u_理想流水线_1  (
    .RegWrite(RegW), .MemWrite(MemW), .IF_PC(IF_PC), .ID_PC(ID_PC), .EX_PC(EX_PC), .M_PC(MEM_PC),
    .WB_PC(WB_PC), .RDin(RDinr), .MDin(MDinr), .LedData(LED));
  \重定向流水线  \u_重定向流水线_1  (
    .RegWrite(RegW), .MemWrite(MemW), .IF_PC(IF_PC), .ID_PC(ID_PC), .EX_PC(EX_PC), .M_PC(MEM_PC),
    .WB_PC(WB_PC), .RDin(RDinr), .MDin(MDinr), .LedData(LED));  // open: IR1, IR2, IR3
  \单周期_多级中断  \u_单周期_多级中断_1  (
    .IR1(IR1), .IR2(IR2), .IR3(IR3), .RegWrite(RegW), .MemWrite(MemW), .PC(PC), .IR(IR), .RDin(RDin),
    .MDin(MDin), .LedData(LED));

  // Notes on the sheet:
  //   单周期封装测试
  //   气泡流水封装测试
  //   单周期+单级中断封装测试
  //   请检查上面封装有无位宽不匹配，引脚标签是否和连接的标签相对应，否则无法在educoder平台上正确测试
  //   理想流水封装测试
  //   重定向流水封装测试
  //   单周期+多级中断封装测试
endmodule

module IF_ID (
  input  [31:0] PCin,
  input  [31:0] IRin,
  input  Pjmpin,
  input  \同步清零_气泡_高电平有效 ,
  input  \使能端_低电平有效_stall_高电平有效 ,
  input  CLK,
  output [31:0] PCout,
  output [31:0] IRout,
  output Pjmpout
);

  wire multiplexer_3_out, pull_resistor_2_node;
  wire [31:0] multiplexer_1_out, multiplexer_2_out;

  Multiplexer #(.select(1), .width(32), .disabled("Z"), .enable("false")) multiplexer_1 (
    .in0(PCin), .in1({32{1'b0}}), .out(multiplexer_1_out), .sel(\同步清零_气泡_高电平有效 ));
  Multiplexer #(.select(1), .width(32), .disabled("Z"), .enable("false")) multiplexer_2 (
    .in0(IRin), .in1({32{1'b0}}), .out(multiplexer_2_out), .sel(\同步清零_气泡_高电平有效 ));
  Multiplexer #(.select(1), .width(1), .disabled("Z"), .enable("false")) multiplexer_3 (
    .in0(Pjmpin), .in1(1'b0), .out(multiplexer_3_out), .sel(\同步清零_气泡_高电平有效 ));
  Pull_Resistor #(.pull(0)) pull_resistor_1 (.node(\同步清零_气泡_高电平有效 ));
  Pull_Resistor #(.pull(0)) pull_resistor_2 (.node(pull_resistor_2_node));
  not not_1 (pull_resistor_2_node, \使能端_低电平有效_stall_高电平有效 );
  Register #(.width(32), .trigger("rising"), .Select("low")) register_1 (
    .D(multiplexer_1_out), .en(pull_resistor_2_node), .Q(PCout), .clk(CLK));  // open: clr
  Register #(.width(32), .trigger("rising"), .Select("low")) register_2 (
    .D(multiplexer_2_out), .en(pull_resistor_2_node), .Q(IRout), .clk(CLK));  // open: clr
  Register #(.width(1), .trigger("rising"), .Select("low")) register_3 (
    .D(multiplexer_3_out), .en(pull_resistor_2_node), .Q(Pjmpout), .clk(CLK));  // open: clr
endmodule

module ID_EX (
  input  SBin,
  input  Stypein,
  input  Beqin,
  input  Bnein,
  input  MemToRegin,
  input  MemWritein,
  input  [3:0] ALUopin,
  input  ALUSRCBin,
  input  RegWritein,
  input  Ecallin,
  input  Jarin,
  input  Jarlin,
  input  Uretin,
  input  Bltuin,
  input  [4:0] W_in,
  input  [31:0] R2in,
  input  [31:0] R1in,
  input  [31:0] PCin,
  input  [31:0] Imm1in,
  input  [31:0] Imm2in,
  input  [31:0] Imm3in,
  input  [31:0] IRin,
  input  [1:0] fwdR1in,
  input  [1:0] fwdR2in,
  input  pjmpin,
  input  CLK,
  input  Stall,
  input  \同步清零_气泡_高电平有效 ,
  output SBout,
  output Stypeout,
  output Beqout,
  output Bneout,
  output MemToReginout,
  output MemWriteout,
  output [3:0] ALUopout,
  output ALUSRCBout,
  output RegWriteout,
  output Ecallout,
  output Jarout,
  output Jarlout,
  output Uretout,
  output Bltuout,
  output [4:0] W_out,
  output [31:0] R2out,
  output [31:0] R1out,
  output [31:0] PCout,
  output [31:0] Imm1out,
  output [31:0] Imm2out,
  output [31:0] Imm3out,
  output [31:0] IRout,
  output [1:0] fwdR1out,
  output [1:0] fwdR2out,
  output pjmpout
);

  wire and_1_out, multiplexer_1_out, multiplexer_2_out, multiplexer_3_out, multiplexer_4_out,
       multiplexer_5_out, multiplexer_6_out, multiplexer_8_out, multiplexer_9_out, multiplexer_10_out,
       multiplexer_11_out, multiplexer_12_out, multiplexer_13_out, multiplexer_14_out, multiplexer_25_out,
       or_1_out;
  wire [1:0] multiplexer_23_out, multiplexer_24_out;
  wire [3:0] multiplexer_7_out;
  wire [4:0] multiplexer_15_out;
  wire [31:0] multiplexer_16_out, multiplexer_17_out, multiplexer_18_out, multiplexer_19_out,
       multiplexer_20_out, multiplexer_21_out, multiplexer_22_out;

  Multiplexer #(.select(1), .width(1), .disabled("Z"), .enable("false")) multiplexer_1 (
    .in0(SBin), .in1(1'b0), .out(multiplexer_1_out), .sel(\同步清零_气泡_高电平有效 ));
  Multiplexer #(.select(1), .width(1), .disabled("Z"), .enable("false")) multiplexer_2 (
    .in0(Stypein), .in1(1'b0), .out(multiplexer_2_out), .sel(\同步清零_气泡_高电平有效 ));
  Multiplexer #(.select(1), .width(1), .disabled("Z"), .enable("false")) multiplexer_3 (
    .in0(Beqin), .in1(1'b0), .out(multiplexer_3_out), .sel(\同步清零_气泡_高电平有效 ));
  Multiplexer #(.select(1), .width(1), .disabled("Z"), .enable("false")) multiplexer_4 (
    .in0(Bnein), .in1(1'b0), .out(multiplexer_4_out), .sel(\同步清零_气泡_高电平有效 ));
  Multiplexer #(.select(1), .width(1), .disabled("Z"), .enable("false")) multiplexer_5 (
    .in0(MemToRegin), .in1(1'b0), .out(multiplexer_5_out), .sel(\同步清零_气泡_高电平有效 ));
  Multiplexer #(.select(1), .width(1), .disabled("Z"), .enable("false")) multiplexer_6 (
    .in0(MemWritein), .in1(1'b0), .out(multiplexer_6_out), .sel(\同步清零_气泡_高电平有效 ));
  Multiplexer #(.select(1), .width(4), .disabled("Z"), .enable("false")) multiplexer_7 (
    .in0(ALUopin), .in1(4'b0000), .out(multiplexer_7_out), .sel(\同步清零_气泡_高电平有效 ));
  Multiplexer #(.select(1), .width(1), .disabled("Z"), .enable("false")) multiplexer_8 (
    .in0(ALUSRCBin), .in1(1'b0), .out(multiplexer_8_out), .sel(\同步清零_气泡_高电平有效 ));
  Multiplexer #(.select(1), .width(1), .disabled("Z"), .enable("false")) multiplexer_9 (
    .in0(RegWritein), .in1(1'b0), .out(multiplexer_9_out), .sel(\同步清零_气泡_高电平有效 ));
  Multiplexer #(.select(1), .width(1), .disabled("Z"), .enable("false")) multiplexer_10 (
    .in0(Ecallin), .in1(1'b0), .out(multiplexer_10_out), .sel(\同步清零_气泡_高电平有效 ));
  Multiplexer #(.select(1), .width(1), .disabled("Z"), .enable("false")) multiplexer_11 (
    .in0(Jarin), .in1(1'b0), .out(multiplexer_11_out), .sel(\同步清零_气泡_高电平有效 ));
  Multiplexer #(.select(1), .width(1), .disabled("Z"), .enable("false")) multiplexer_12 (
    .in0(Jarlin), .in1(1'b0), .out(multiplexer_12_out), .sel(\同步清零_气泡_高电平有效 ));
  Multiplexer #(.select(1), .width(1), .disabled("Z"), .enable("false")) multiplexer_13 (
    .in0(Uretin), .in1(1'b0), .out(multiplexer_13_out), .sel(\同步清零_气泡_高电平有效 ));
  Multiplexer #(.select(1), .width(1), .disabled("Z"), .enable("false")) multiplexer_14 (
    .in0(Bltuin), .in1(1'b0), .out(multiplexer_14_out), .sel(\同步清零_气泡_高电平有效 ));
  Multiplexer #(.select(1), .width(5), .disabled("Z"), .enable("false")) multiplexer_15 (
    .in0(W_in), .in1({5{1'b0}}), .out(multiplexer_15_out), .sel(\同步清零_气泡_高电平有效 ));
  Multiplexer #(.select(1), .width(32), .disabled("Z"), .enable("false")) multiplexer_16 (
    .in0(R2in), .in1({32{1'b0}}), .out(multiplexer_16_out), .sel(\同步清零_气泡_高电平有效 ));
  Multiplexer #(.select(1), .width(32), .disabled("Z"), .enable("false")) multiplexer_17 (
    .in0(R1in), .in1({32{1'b0}}), .out(multiplexer_17_out), .sel(\同步清零_气泡_高电平有效 ));
  Multiplexer #(.select(1), .width(32), .disabled("Z"), .enable("false")) multiplexer_18 (
    .in0(PCin), .in1({32{1'b0}}), .out(multiplexer_18_out), .sel(\同步清零_气泡_高电平有效 ));
  Multiplexer #(.select(1), .width(32), .disabled("Z"), .enable("false")) multiplexer_19 (
    .in0(Imm1in), .in1({32{1'b0}}), .out(multiplexer_19_out), .sel(\同步清零_气泡_高电平有效 ));
  Multiplexer #(.select(1), .width(32), .disabled("Z"), .enable("false")) multiplexer_20 (
    .in0(Imm2in), .in1({32{1'b0}}), .out(multiplexer_20_out), .sel(\同步清零_气泡_高电平有效 ));
  Multiplexer #(.select(1), .width(32), .disabled("Z"), .enable("false")) multiplexer_21 (
    .in0(Imm3in), .in1({32{1'b0}}), .out(multiplexer_21_out), .sel(\同步清零_气泡_高电平有效 ));
  Multiplexer #(.select(1), .width(32), .disabled("Z"), .enable("false")) multiplexer_22 (
    .in0(IRin), .in1({32{1'b0}}), .out(multiplexer_22_out), .sel(\同步清零_气泡_高电平有效 ));
  Multiplexer #(.select(1), .width(2), .disabled("Z"), .enable("false")) multiplexer_23 (
    .in0(fwdR1in), .in1(2'b00), .out(multiplexer_23_out), .sel(\同步清零_气泡_高电平有效 ));
  Multiplexer #(.select(1), .width(2), .disabled("Z"), .enable("false")) multiplexer_24 (
    .in0(fwdR2in), .in1(2'b00), .out(multiplexer_24_out), .sel(\同步清零_气泡_高电平有效 ));
  Multiplexer #(.select(1), .width(1), .disabled("Z"), .enable("false")) multiplexer_25 (
    .in0(pjmpin), .in1(1'b0), .out(multiplexer_25_out), .sel(\同步清零_气泡_高电平有效 ));
  or or_1 (or_1_out, and_1_out, \同步清零_气泡_高电平有效 );
  and and_1 (and_1_out, ~\同步清零_气泡_高电平有效 , ~Stall);  // AND_Gate
  Register #(.width(1), .trigger("rising"), .Select("low")) register_1 (
    .D(multiplexer_1_out), .en(or_1_out), .Q(SBout), .clk(CLK));  // open: clr
  Register #(.width(1), .trigger("rising"), .Select("low")) register_2 (
    .D(multiplexer_2_out), .en(or_1_out), .Q(Stypeout), .clk(CLK));  // open: clr
  Register #(.width(1), .trigger("rising"), .Select("low")) register_3 (
    .D(multiplexer_3_out), .en(or_1_out), .Q(Beqout), .clk(CLK));  // open: clr
  Register #(.width(1), .trigger("rising"), .Select("low")) register_4 (
    .D(multiplexer_4_out), .en(or_1_out), .Q(Bneout), .clk(CLK));  // open: clr
  Register #(.width(1), .trigger("rising"), .Select("low")) register_5 (
    .D(multiplexer_5_out), .en(or_1_out), .Q(MemToReginout), .clk(CLK));  // open: clr
  Register #(.width(1), .trigger("rising"), .Select("low")) register_6 (
    .D(multiplexer_6_out), .en(or_1_out), .Q(MemWriteout), .clk(CLK));  // open: clr
  Register #(.width(4), .trigger("rising"), .Select("low")) register_7 (
    .D(multiplexer_7_out), .en(or_1_out), .Q(ALUopout), .clk(CLK));  // open: clr
  Register #(.width(1), .trigger("rising"), .Select("low")) register_8 (
    .D(multiplexer_8_out), .en(or_1_out), .Q(ALUSRCBout), .clk(CLK));  // open: clr
  Register #(.width(1), .trigger("rising"), .Select("low")) register_9 (
    .D(multiplexer_9_out), .en(or_1_out), .Q(RegWriteout), .clk(CLK));  // open: clr
  Register #(.width(1), .trigger("rising"), .Select("low")) register_10 (
    .D(multiplexer_10_out), .en(or_1_out), .Q(Ecallout), .clk(CLK));  // open: clr
  Register #(.width(1), .trigger("rising"), .Select("low")) register_11 (
    .D(multiplexer_11_out), .en(or_1_out), .Q(Jarout), .clk(CLK));  // open: clr
  Register #(.width(1), .trigger("rising"), .Select("low")) register_12 (
    .D(multiplexer_12_out), .en(or_1_out), .Q(Jarlout), .clk(CLK));  // open: clr
  Register #(.width(1), .trigger("rising"), .Select("low")) register_13 (
    .D(multiplexer_13_out), .en(or_1_out), .Q(Uretout), .clk(CLK));  // open: clr
  Register #(.width(1), .trigger("rising"), .Select("low")) register_14 (
    .D(multiplexer_14_out), .en(or_1_out), .Q(Bltuout), .clk(CLK));  // open: clr
  Register #(.width(5), .trigger("rising"), .Select("low")) register_15 (
    .D(multiplexer_15_out), .en(or_1_out), .Q(W_out), .clk(CLK));  // open: clr
  Register #(.width(32), .trigger("rising"), .Select("low")) register_16 (
    .D(multiplexer_16_out), .en(or_1_out), .Q(R2out), .clk(CLK));  // open: clr
  Register #(.width(32), .trigger("rising"), .Select("low")) register_17 (
    .D(multiplexer_17_out), .en(or_1_out), .Q(R1out), .clk(CLK));  // open: clr
  Register #(.width(32), .trigger("rising"), .Select("low")) register_18 (
    .D(multiplexer_18_out), .en(or_1_out), .Q(PCout), .clk(CLK));  // open: clr
  Register #(.width(32), .trigger("rising"), .Select("low")) register_19 (
    .D(multiplexer_19_out), .en(or_1_out), .Q(Imm1out), .clk(CLK));  // open: clr
  Register #(.width(32), .trigger("rising"), .Select("low")) register_20 (
    .D(multiplexer_20_out), .en(or_1_out), .Q(Imm2out), .clk(CLK));  // open: clr
  Register #(.width(32), .trigger("rising"), .Select("low")) register_21 (
    .D(multiplexer_21_out), .en(or_1_out), .Q(Imm3out), .clk(CLK));  // open: clr
  Register #(.width(32), .trigger("rising"), .Select("low")) register_22 (
    .D(multiplexer_22_out), .en(or_1_out), .Q(IRout), .clk(CLK));  // open: clr
  Register #(.width(2), .trigger("rising"), .Select("low")) register_23 (
    .D(multiplexer_23_out), .en(or_1_out), .Q(fwdR1out), .clk(CLK));  // open: clr
  Register #(.width(2), .trigger("rising"), .Select("low")) register_24 (
    .D(multiplexer_24_out), .en(or_1_out), .Q(fwdR2out), .clk(CLK));  // open: clr
  Register #(.width(1), .trigger("rising"), .Select("low")) register_25 (
    .D(multiplexer_25_out), .en(or_1_out), .Q(pjmpout), .clk(CLK));  // open: clr
endmodule

module EX_MEM (
  input  SBin,
  input  RegWritein,
  input  MemToRegin,
  input  MemWritein,
  input  ALUSRCBin,
  input  haltin,
  input  Ecallin,
  input  Jarin,
  input  [4:0] W_lin,
  input  Uretin,
  input  jarlin,
  input  [31:0] Aluin,
  input  [31:0] PCin,
  input  [1:0] Selectin,
  input  [31:0] Jmpin,
  input  [31:0] Mdin,
  input  [31:0] IRin,
  input  [31:0] R1in,
  input  [31:0] R2in,
  input  \同步清零_气泡_高电平有效 ,
  input  CLK,
  input  \使能端_低电平有效_stall_高电平有效 ,
  output SBout,
  output ReqWriteout,
  output MemToReginout,
  output MemWriteout,
  output ALUSRCBout,
  output haltout,
  output Ecallout,
  output Jarout,
  output [4:0] w_out,
  output Uretout,
  output jarlout,
  output [31:0] Aluout,
  output [31:0] PCout,
  output [1:0] Selectout,
  output [31:0] Jmpout,
  output [31:0] MdinoutMem,
  output [31:0] IRout,
  output [31:0] R1out,
  output [31:0] R2out
);

  wire multiplexer_1_out, multiplexer_2_out, multiplexer_3_out, multiplexer_4_out, multiplexer_5_out,
       multiplexer_6_out, multiplexer_7_out, multiplexer_8_out, multiplexer_10_out, multiplexer_11_out,
       pull_resistor_2_node;
  wire [1:0] multiplexer_14_out;
  wire [4:0] multiplexer_9_out;
  wire [31:0] multiplexer_12_out, multiplexer_13_out, multiplexer_15_out, multiplexer_16_out,
       multiplexer_17_out, multiplexer_18_out, multiplexer_19_out;

  Multiplexer #(.select(1), .width(1), .disabled("Z"), .enable("false")) multiplexer_1 (
    .in0(SBin), .in1(1'b0), .out(multiplexer_1_out), .sel(\同步清零_气泡_高电平有效 ));
  Multiplexer #(.select(1), .width(1), .disabled("Z"), .enable("false")) multiplexer_2 (
    .in0(RegWritein), .in1(1'b0), .out(multiplexer_2_out), .sel(\同步清零_气泡_高电平有效 ));
  Multiplexer #(.select(1), .width(1), .disabled("Z"), .enable("false")) multiplexer_3 (
    .in0(MemToRegin), .in1(1'b0), .out(multiplexer_3_out), .sel(\同步清零_气泡_高电平有效 ));
  Multiplexer #(.select(1), .width(1), .disabled("Z"), .enable("false")) multiplexer_4 (
    .in0(MemWritein), .in1(1'b0), .out(multiplexer_4_out), .sel(\同步清零_气泡_高电平有效 ));
  Multiplexer #(.select(1), .width(1), .disabled("Z"), .enable("false")) multiplexer_5 (
    .in0(ALUSRCBin), .in1(1'b0), .out(multiplexer_5_out), .sel(\同步清零_气泡_高电平有效 ));
  Multiplexer #(.select(1), .width(1), .disabled("Z"), .enable("false")) multiplexer_6 (
    .in0(haltin), .in1(1'b0), .out(multiplexer_6_out), .sel(\同步清零_气泡_高电平有效 ));
  Multiplexer #(.select(1), .width(1), .disabled("Z"), .enable("false")) multiplexer_7 (
    .in0(Ecallin), .in1(1'b0), .out(multiplexer_7_out), .sel(\同步清零_气泡_高电平有效 ));
  Multiplexer #(.select(1), .width(1), .disabled("Z"), .enable("false")) multiplexer_8 (
    .in0(Jarin), .in1(1'b0), .out(multiplexer_8_out), .sel(\同步清零_气泡_高电平有效 ));
  Multiplexer #(.select(1), .width(5), .disabled("Z"), .enable("false")) multiplexer_9 (
    .in0(W_lin), .in1({5{1'b0}}), .out(multiplexer_9_out), .sel(\同步清零_气泡_高电平有效 ));
  Multiplexer #(.select(1), .width(1), .disabled("Z"), .enable("false")) multiplexer_10 (
    .in0(Uretin), .in1(1'b0), .out(multiplexer_10_out), .sel(\同步清零_气泡_高电平有效 ));
  Multiplexer #(.select(1), .width(1), .disabled("Z"), .enable("false")) multiplexer_11 (
    .in0(jarlin), .in1(1'b0), .out(multiplexer_11_out), .sel(\同步清零_气泡_高电平有效 ));
  Multiplexer #(.select(1), .width(32), .disabled("Z"), .enable("false")) multiplexer_12 (
    .in0(Aluin), .in1({32{1'b0}}), .out(multiplexer_12_out), .sel(\同步清零_气泡_高电平有效 ));
  Multiplexer #(.select(1), .width(32), .disabled("Z"), .enable("false")) multiplexer_13 (
    .in0(PCin), .in1({32{1'b0}}), .out(multiplexer_13_out), .sel(\同步清零_气泡_高电平有效 ));
  Multiplexer #(.select(1), .width(2), .disabled("Z"), .enable("false")) multiplexer_14 (
    .in0(Selectin), .in1(2'b00), .out(multiplexer_14_out), .sel(\同步清零_气泡_高电平有效 ));
  Multiplexer #(.select(1), .width(32), .disabled("Z"), .enable("false")) multiplexer_15 (
    .in0(Jmpin), .in1({32{1'b0}}), .out(multiplexer_15_out), .sel(\同步清零_气泡_高电平有效 ));
  Multiplexer #(.select(1), .width(32), .disabled("Z"), .enable("false")) multiplexer_16 (
    .in0(Mdin), .in1({32{1'b0}}), .out(multiplexer_16_out), .sel(\同步清零_气泡_高电平有效 ));
  Multiplexer #(.select(1), .width(32), .disabled("Z"), .enable("false")) multiplexer_17 (
    .in0(IRin), .in1({32{1'b0}}), .out(multiplexer_17_out), .sel(\同步清零_气泡_高电平有效 ));
  Multiplexer #(.select(1), .width(32), .disabled("Z"), .enable("false")) multiplexer_18 (
    .in0(R1in), .in1({32{1'b0}}), .out(multiplexer_18_out), .sel(\同步清零_气泡_高电平有效 ));
  Multiplexer #(.select(1), .width(32), .disabled("Z"), .enable("false")) multiplexer_19 (
    .in0(R2in), .in1({32{1'b0}}), .out(multiplexer_19_out), .sel(\同步清零_气泡_高电平有效 ));
  Pull_Resistor #(.pull(0)) pull_resistor_1 (.node(\同步清零_气泡_高电平有效 ));
  Register #(.width(1), .trigger("rising"), .Select("low")) register_1 (
    .D(multiplexer_1_out), .en(pull_resistor_2_node), .Q(SBout), .clk(CLK));  // open: clr
  Register #(.width(1), .trigger("rising"), .Select("low")) register_2 (
    .D(multiplexer_2_out), .en(pull_resistor_2_node), .Q(ReqWriteout), .clk(CLK));  // open: clr
  Register #(.width(1), .trigger("rising"), .Select("low")) register_3 (
    .D(multiplexer_3_out), .en(pull_resistor_2_node), .Q(MemToReginout), .clk(CLK));  // open: clr
  Register #(.width(1), .trigger("rising"), .Select("low")) register_4 (
    .D(multiplexer_4_out), .en(pull_resistor_2_node), .Q(MemWriteout), .clk(CLK));  // open: clr
  Register #(.width(1), .trigger("rising"), .Select("low")) register_5 (
    .D(multiplexer_5_out), .en(pull_resistor_2_node), .Q(ALUSRCBout));  // open: clk, clr
  Register #(.width(1), .trigger("rising"), .Select("low")) register_6 (
    .D(multiplexer_6_out), .en(pull_resistor_2_node), .Q(haltout), .clk(CLK));  // open: clr
  Register #(.width(1), .trigger("rising"), .Select("low")) register_7 (
    .D(multiplexer_7_out), .en(pull_resistor_2_node), .Q(Ecallout), .clk(CLK));  // open: clr
  Register #(.width(1), .trigger("rising"), .Select("low")) register_8 (
    .D(multiplexer_8_out), .en(pull_resistor_2_node), .Q(Jarout), .clk(CLK));  // open: clr
  Register #(.width(5), .trigger("rising"), .Select("low")) register_9 (
    .D(multiplexer_9_out), .en(pull_resistor_2_node), .Q(w_out), .clk(CLK));  // open: clr
  Register #(.width(1), .trigger("rising"), .Select("low")) register_10 (
    .D(multiplexer_10_out), .en(pull_resistor_2_node), .Q(Uretout), .clk(CLK));  // open: clr
  Register #(.width(1), .trigger("rising"), .Select("low")) register_11 (
    .D(multiplexer_11_out), .en(pull_resistor_2_node), .Q(jarlout), .clk(CLK));  // open: clr
  Register #(.width(32), .trigger("rising"), .Select("low")) register_12 (
    .D(multiplexer_12_out), .en(pull_resistor_2_node), .Q(Aluout), .clk(CLK));  // open: clr
  Register #(.width(32), .trigger("rising"), .Select("low")) register_13 (
    .D(multiplexer_13_out), .en(pull_resistor_2_node), .Q(PCout), .clk(CLK));  // open: clr
  Register #(.width(2), .trigger("rising"), .Select("low")) register_14 (
    .D(multiplexer_14_out), .en(pull_resistor_2_node), .Q(Selectout), .clk(CLK));  // open: clr
  Register #(.width(32), .trigger("rising"), .Select("low")) register_15 (
    .D(multiplexer_15_out), .en(pull_resistor_2_node), .Q(Jmpout), .clk(CLK));  // open: clr
  Register #(.width(32), .trigger("rising"), .Select("low")) register_16 (
    .D(multiplexer_16_out), .en(pull_resistor_2_node), .Q(MdinoutMem), .clk(CLK));  // open: clr
  Register #(.width(32), .trigger("rising"), .Select("low")) register_17 (
    .D(multiplexer_17_out), .en(pull_resistor_2_node), .Q(IRout), .clk(CLK));  // open: clr
  Register #(.width(32), .trigger("rising"), .Select("low")) register_18 (
    .D(multiplexer_18_out), .en(pull_resistor_2_node), .Q(R1out), .clk(CLK));  // open: clr
  Register #(.width(32), .trigger("rising"), .Select("low")) register_19 (
    .D(multiplexer_19_out), .en(pull_resistor_2_node), .Q(R2out), .clk(CLK));  // open: clr
  Pull_Resistor #(.pull(0)) pull_resistor_2 (.node(pull_resistor_2_node));
  not not_1 (pull_resistor_2_node, \使能端_低电平有效_stall_高电平有效 );
endmodule

module MEM_WB (
  input  MemToRegin,
  input  RegWritein,
  input  haltin,
  input  Ecallin,
  input  Jarin,
  input  Jarlin,
  input  Uretin,
  input  [31:0] Din,
  input  [31:0] PCin,
  input  [1:0] Selectin,
  input  [31:0] Jmpin,
  input  [4:0] W_in,
  input  [31:0] IRin,
  input  [31:0] R1in,
  input  [31:0] R2in,
  input  \同步清零_气泡_高电平有效 ,
  input  CLK,
  input  \使能端_低电平有效_stall_高电平有效 ,
  output MemToRegout,
  output RegWriteout,
  output haltout,
  output Ecallout,
  output Jarout,
  output Jarlout,
  output Uretout,
  output [31:0] Dout,
  output [31:0] PCout,
  output [1:0] Selectout,
  output [31:0] Jmpout,
  output [4:0] W_out,
  output [31:0] IRout,
  output [31:0] R1out,
  output [31:0] R2out
);

  wire multiplexer_1_out, multiplexer_2_out, multiplexer_3_out, multiplexer_4_out, multiplexer_5_out,
       multiplexer_6_out, multiplexer_7_out, pull_resistor_2_node;
  wire [1:0] multiplexer_10_out;
  wire [4:0] multiplexer_12_out;
  wire [31:0] multiplexer_8_out, multiplexer_9_out, multiplexer_11_out, multiplexer_13_out,
       multiplexer_14_out, multiplexer_15_out;

  Multiplexer #(.select(1), .width(1), .disabled("Z"), .enable("false")) multiplexer_1 (
    .in0(MemToRegin), .in1(1'b0), .out(multiplexer_1_out), .sel(\同步清零_气泡_高电平有效 ));
  Multiplexer #(.select(1), .width(1), .disabled("Z"), .enable("false")) multiplexer_2 (
    .in0(RegWritein), .in1(1'b0), .out(multiplexer_2_out), .sel(\同步清零_气泡_高电平有效 ));
  Multiplexer #(.select(1), .width(1), .disabled("Z"), .enable("false")) multiplexer_3 (
    .in0(haltin), .in1(1'b0), .out(multiplexer_3_out), .sel(\同步清零_气泡_高电平有效 ));
  Multiplexer #(.select(1), .width(1), .disabled("Z"), .enable("false")) multiplexer_4 (
    .in0(Ecallin), .in1(1'b0), .out(multiplexer_4_out), .sel(\同步清零_气泡_高电平有效 ));
  Multiplexer #(.select(1), .width(1), .disabled("Z"), .enable("false")) multiplexer_5 (
    .in0(Jarin), .in1(1'b0), .out(multiplexer_5_out), .sel(\同步清零_气泡_高电平有效 ));
  Multiplexer #(.select(1), .width(1), .disabled("Z"), .enable("false")) multiplexer_6 (
    .in0(Jarlin), .in1(1'b0), .out(multiplexer_6_out), .sel(\同步清零_气泡_高电平有效 ));
  Multiplexer #(.select(1), .width(1), .disabled("Z"), .enable("false")) multiplexer_7 (
    .in0(Uretin), .in1(1'b0), .out(multiplexer_7_out), .sel(\同步清零_气泡_高电平有效 ));
  Multiplexer #(.select(1), .width(32), .disabled("Z"), .enable("false")) multiplexer_8 (
    .in0(Din), .in1({32{1'b0}}), .out(multiplexer_8_out), .sel(\同步清零_气泡_高电平有效 ));
  Multiplexer #(.select(1), .width(32), .disabled("Z"), .enable("false")) multiplexer_9 (
    .in0(PCin), .in1({32{1'b0}}), .out(multiplexer_9_out), .sel(\同步清零_气泡_高电平有效 ));
  Multiplexer #(.select(1), .width(2), .disabled("Z"), .enable("false")) multiplexer_10 (
    .in0(Selectin), .in1(2'b00), .out(multiplexer_10_out), .sel(\同步清零_气泡_高电平有效 ));
  Multiplexer #(.select(1), .width(32), .disabled("Z"), .enable("false")) multiplexer_11 (
    .in0(Jmpin), .in1({32{1'b0}}), .out(multiplexer_11_out), .sel(\同步清零_气泡_高电平有效 ));
  Multiplexer #(.select(1), .width(5), .disabled("Z"), .enable("false")) multiplexer_12 (
    .in0(W_in), .in1({5{1'b0}}), .out(multiplexer_12_out), .sel(\同步清零_气泡_高电平有效 ));
  Multiplexer #(.select(1), .width(32), .disabled("Z"), .enable("false")) multiplexer_13 (
    .in0(IRin), .in1({32{1'b0}}), .out(multiplexer_13_out), .sel(\同步清零_气泡_高电平有效 ));
  Multiplexer #(.select(1), .width(32), .disabled("Z"), .enable("false")) multiplexer_14 (
    .in0(R1in), .in1({32{1'b0}}), .out(multiplexer_14_out), .sel(\同步清零_气泡_高电平有效 ));
  Multiplexer #(.select(1), .width(32), .disabled("Z"), .enable("false")) multiplexer_15 (
    .in0(R2in), .in1({32{1'b0}}), .out(multiplexer_15_out), .sel(\同步清零_气泡_高电平有效 ));
  Pull_Resistor #(.pull(0)) pull_resistor_1 (.node(\同步清零_气泡_高电平有效 ));
  Register #(.width(1), .trigger("rising"), .Select("low")) register_1 (
    .D(multiplexer_1_out), .en(pull_resistor_2_node), .Q(MemToRegout), .clk(CLK));  // open: clr
  Register #(.width(1), .trigger("rising"), .Select("low")) register_2 (
    .D(multiplexer_2_out), .en(pull_resistor_2_node), .Q(RegWriteout), .clk(CLK));  // open: clr
  Register #(.width(1), .trigger("rising"), .Select("low")) register_3 (
    .D(multiplexer_3_out), .en(pull_resistor_2_node), .Q(haltout), .clk(CLK));  // open: clr
  Register #(.width(1), .trigger("rising"), .Select("low")) register_4 (
    .D(multiplexer_4_out), .en(pull_resistor_2_node), .Q(Ecallout), .clk(CLK));  // open: clr
  Register #(.width(1), .trigger("rising"), .Select("low")) register_5 (
    .D(multiplexer_5_out), .en(pull_resistor_2_node), .Q(Jarout), .clk(CLK));  // open: clr
  Register #(.width(1), .trigger("rising"), .Select("low")) register_6 (
    .D(multiplexer_6_out), .en(pull_resistor_2_node), .Q(Jarlout), .clk(CLK));  // open: clr
  Register #(.width(1), .trigger("rising"), .Select("low")) register_7 (
    .D(multiplexer_7_out), .en(pull_resistor_2_node), .Q(Uretout), .clk(CLK));  // open: clr
  Register #(.width(32), .trigger("rising"), .Select("low")) register_8 (
    .D(multiplexer_8_out), .en(pull_resistor_2_node), .Q(Dout), .clk(CLK));  // open: clr
  Register #(.width(32), .trigger("rising"), .Select("low")) register_9 (
    .D(multiplexer_9_out), .en(pull_resistor_2_node), .Q(PCout), .clk(CLK));  // open: clr
  Register #(.width(2), .trigger("rising"), .Select("low")) register_10 (
    .D(multiplexer_10_out), .en(pull_resistor_2_node), .Q(Selectout), .clk(CLK));  // open: clr
  Register #(.width(32), .trigger("rising"), .Select("low")) register_11 (
    .D(multiplexer_11_out), .en(pull_resistor_2_node), .Q(Jmpout), .clk(CLK));  // open: clr
  Register #(.width(5), .trigger("rising"), .Select("low")) register_12 (
    .D(multiplexer_12_out), .en(pull_resistor_2_node), .Q(W_out), .clk(CLK));  // open: clr
  Register #(.width(32), .trigger("rising"), .Select("low")) register_13 (
    .D(multiplexer_13_out), .en(pull_resistor_2_node), .Q(IRout), .clk(CLK));  // open: clr
  Register #(.width(32), .trigger("rising"), .Select("low")) register_14 (
    .D(multiplexer_14_out), .en(pull_resistor_2_node), .Q(R1out), .clk(CLK));  // open: clr
  Register #(.width(32), .trigger("rising"), .Select("low")) register_15 (
    .D(multiplexer_15_out), .en(pull_resistor_2_node), .Q(R2out), .clk(CLK));  // open: clr
  Pull_Resistor #(.pull(0)) pull_resistor_2 (.node(pull_resistor_2_node));
  not not_1 (pull_resistor_2_node, \使能端_低电平有效_stall_高电平有效 );
endmodule

module \相关处理逻辑  (
  input  [4:0] exop,
  input  ExRegWrite,
  input  [4:0] OP,
  input  [4:0] FUNC,
  input  [4:0] R1,
  input  [4:0] EXREG,
  input  [4:0] R2,
  input  [4:0] MEMREG,
  input  MemRegWrite,
  output LoadUse,
  output R1EXRE,
  output DH,
  output R1MemRe,
  output R2EXRE,
  output R2MemRe
);

  wire comparator_1_eq, comparator_2_eq, comparator_3_eq, comparator_4_eq, comparator_5_eq, comparator_6_eq,
       comparator_7_eq, comparator_8_eq, comparator_9_eq, \for相关处理逻辑_1_r1 , \for相关处理逻辑_1_r2 , not_1_out,
       not_2_out, not_3_out, not_4_out, or_1_out;

  \for相关处理逻辑  \for相关处理逻辑_1  (
    .OP2(OP[0]), .OP3(OP[1]), .OP4(OP[2]), .OP5(OP[3]), .OP6(OP[4]), .F12(FUNC[0]), .F13(FUNC[1]),
    .F14(FUNC[2]), .F25(FUNC[3]), .F30(FUNC[4]), .R1(\for相关处理逻辑_1_r1 ), .R2(\for相关处理逻辑_1_r2 ));
  Comparator #(.width(5), .mode("unsigned")) comparator_1 (
    .a(R1), .b({5{1'b0}}), .eq(comparator_1_eq));  // open: gt, lt
  Comparator #(.width(5), .mode("unsigned")) comparator_2 (.a(R1), .b(EXREG), .eq(comparator_2_eq));  // open: gt, lt
  Comparator #(.width(5), .mode("unsigned")) comparator_3 (.a(R2), .b(EXREG), .eq(comparator_3_eq));  // open: gt, lt
  Comparator #(.width(5), .mode("unsigned")) comparator_4 (.a(R1), .b(MEMREG), .eq(comparator_4_eq));  // open: gt, lt
  Comparator #(.width(5), .mode("unsigned")) comparator_5 (.a(R2), .b(MEMREG), .eq(comparator_5_eq));  // open: gt, lt
  not not_1 (not_1_out, comparator_6_eq);
  Comparator #(.width(5), .mode("unsigned")) comparator_6 (
    .a(R1), .b({5{1'b0}}), .eq(comparator_6_eq));  // open: gt, lt
  not not_2 (not_2_out, comparator_7_eq);
  Comparator #(.width(5), .mode("unsigned")) comparator_7 (
    .a(R2), .b({5{1'b0}}), .eq(comparator_7_eq));  // open: gt, lt
  not not_3 (not_3_out, comparator_8_eq);
  Comparator #(.width(5), .mode("unsigned")) comparator_8 (
    .a(R2), .b({5{1'b0}}), .eq(comparator_8_eq));  // open: gt, lt
  not not_4 (not_4_out, comparator_1_eq);
  Comparator #(.width(5), .mode("unsigned")) comparator_9 (
    .a(exop), .b({5{1'b0}}), .eq(comparator_9_eq));  // open: gt, lt
  and and_1 (R1EXRE, not_4_out, \for相关处理逻辑_1_r1 , ExRegWrite, comparator_2_eq);
  and and_2 (R1MemRe, not_1_out, \for相关处理逻辑_1_r1 , MemRegWrite, comparator_4_eq);
  and and_3 (R2EXRE, not_2_out, comparator_3_eq, \for相关处理逻辑_1_r2 , ExRegWrite);
  and and_4 (R2MemRe, MemRegWrite, comparator_5_eq, \for相关处理逻辑_1_r2 , not_3_out);
  or or_1 (or_1_out, R2EXRE, R1EXRE);
  or or_2 (DH, R1EXRE, R1MemRe, R2EXRE, R2MemRe);
  and and_5 (LoadUse, comparator_9_eq, or_1_out);
endmodule
module \流水线_分支预测  (
  output RegWrite,
  output MemWrite,
  output [31:0] IF_PC,
  output [31:0] ID_PC,
  output [31:0] EX_PC,
  output [31:0] M_PC,
  output [31:0] WB_PC,
  output [31:0] RDin,
  output [31:0] MDin,
  output [31:0] LedData
);

  wire alu_1_equal, AluSrcB, and_2_out, and_3_out, and_4_out, and_5_out, and_6_out, and_7_out, and_8_out,
       and_9_out, and_10_out, and_11_out, B, BLTU, branch, CLEAR, CLK, clock_1_out, comparator_1_eq,
       comparator_1_lt, comparator_2_lt, comparator_3_eq, d_ff_1_q, Ecall, ecall_t, EX_B, EX_BDo,
       ex_mem_1_haltout, ex_mem_1_jarlout, ex_mem_1_jarout, ex_mem_1_memtoreginout, EX_Pjmp, EXPerr,
       exregwrite, Go, halt, I, id_ex_1_beqout, id_ex_1_bneout, ID_Pjmp, IR1, IR2, IR3, JALex, jalid, JALRex,
       loaduse, mem_wb_1_jarlout, mem_wb_1_jarout, mem_wb_1_memtoregout, MemRegWrite, MemToReg, MemW,
       nand_1_out, not_1_out, not_2_out, not_3_out, not_4_out, not_5_out, not_6_out, not_7_out, not_8_out,
       not_9_out, not_10_out, not_11_out, not_12_out, or_2_out, or_3_out, or_5_out, or_8_out, or_9_out, Pjmp,
       riscv_probe_5_p2, RST, S_Type, SB, SBMem, Uret, uret_t, W1, W2, W3, \单周期硬布线控制器_1_alu_src ,
       \单周期硬布线控制器_1_beq , \单周期硬布线控制器_1_bltu , \单周期硬布线控制器_1_bne , \单周期硬布线控制器_1_ecall , \单周期硬布线控制器_1_jalr ,
       \单周期硬布线控制器_1_memtoreg , \单周期硬布线控制器_1_memwrite , \单周期硬布线控制器_1_regwrite , \单周期硬布线控制器_1_sb ;
  wire [1:0] exfwdr1, exfwdr2, multiplexer_13_out, multiplexer_14_out, select, \相关处理逻辑_1_r1exre ,
       \相关处理逻辑_1_r2exre ;
  wire [3:0] AluOP, mips_ram_1_p4, multiplexer_19_out, \单周期硬布线控制器_1_alu_op ;
  wire [4:0] bit_extender_5_out, multiplexer_9_out, multiplexer_10_out, shifter_3_out, W_out, W_outex,
       W_outmem;
  wire [11:0] multiplexer_11_out, shifter_1_out;
  wire [12:0] CNT_num;
  wire [15:0] \LoadUse次数 , \总周期数 , \插入气泡数 , \无条件分支数 , \条件分支成功数 ;
  wire [31:0] adder_1_out, adder_6_out, alu_1_result, Aluout, and_1_out, bit_extender_2_out,
       bit_extender_3_out, branchdata, btb_1_jmpaddr, EX_IR, ex_mem_1_r1out, ex_mem_1_r2out, EX_PC_4,
       EXBData, exoldR1, exoldR2, id_ex_1_imm2out, id_ex_1_imm3out, ID_IR, IF_IR, Imm1, Imm2, Imm3, jaldata,
       jalrin, JmpoutMem, MDinexe, MDinMem, MEM_IR, mem_wb_1_dout, mem_wb_1_jmpout, mips_ram_1_p6,
       multiplexer_2_out, multiplexer_3_out, multiplexer_4_out, multiplexer_5_out, multiplexer_6_out,
       multiplexer_12_out, multiplexer_15_out, multiplexer_16_out, multiplexer_20_out, NewR1, PC_4, R1, R2,
       regifile_1_r1, regifile_1_r2, shifter_4_out, WB_IR;

  Button \u_总复位  (.out(RST));
  Button _1 ();  // open: out
  Button _2 ();  // open: out
  Button _3 ();  // open: out
  // Probe on \总周期数 
  // Probe on \总周期数 
  Button \u_继续运行  (.out(Go));
  LED #(.active("true")) led_1 (.in(W1));
  LED #(.active("true")) led_2 (.in(W2));
  LED #(.active("true")) led_3 (.in(W3));
  Hex_Digit_Display hex_digit_display_1 (.value(LedData[31:28]));  // open: dp
  // Probe on IF_PC[19:0]
  // RiscV_Probe riscv_probe_1: pin names not known; wires that end beside it: IR1, IR2, IR3, IF_IR
  Multiplexer #(.select(1), .width(32), .disabled("Z"), .enable("false")) multiplexer_1 (
    .in0(jaldata), .in1(and_1_out), .out(EXBData), .sel(JALRex));
  assign and_1_out = 32'hfffffffe & adder_1_out;  // AND_Gate and_1, 32 bits wide
  Multiplexer #(.select(1), .width(32), .disabled("Z"), .enable("false")) multiplexer_2 (
    .in0(EX_PC_4), .in1(and_1_out), .out(multiplexer_2_out), .sel(JALRex));
  Multiplexer #(.select(1), .width(32), .disabled("Z"), .enable("false")) multiplexer_3 (
    .in0(multiplexer_2_out), .in1(jaldata), .out(multiplexer_3_out), .sel(JALex));
  Multiplexer #(.select(1), .width(32), .disabled("Z"), .enable("false")) multiplexer_4 (
    .in0(multiplexer_3_out), .in1(branchdata), .out(multiplexer_4_out), .sel(branch));
  Hex_Digit_Display hex_digit_display_2 (.value(LedData[27:24]));  // open: dp
  Hex_Digit_Display hex_digit_display_3 (.value(LedData[23:20]));  // open: dp
  // Probe on ID_PC[19:0]
  // RiscV_Probe riscv_probe_2: pin names not known; wires that end beside it: ID_IR
  Adder #(.width(32)) adder_1 (.a(jalrin), .b(NewR1), .out(adder_1_out));  // open: cin, cout
  Multiplexer #(.select(1), .width(32), .disabled("Z"), .enable("false")) multiplexer_5 (
    .in0(multiplexer_6_out), .in1(multiplexer_4_out), .out(multiplexer_5_out), .sel(EXPerr));
  Register #(.width(32), .trigger("rising"), .Select("low")) PC (
    .D(multiplexer_5_out), .en(and_2_out), .Q(IF_PC), .clk(CLK), .clr(RST));
  and and_2 (and_2_out, not_1_out, not_2_out);
  not not_1 (not_1_out, halt);
  not not_2 (not_2_out, loaduse);
  Hex_Digit_Display hex_digit_display_4 (.value(LedData[19:16]));  // open: dp
  Hex_Digit_Display hex_digit_display_5 (.value(LedData[15:12]));  // open: dp
  BTB btb_1 (
    .EXbranchdata(EXBData), .PC(IF_PC), .CLK(CLK), .EXPC(EX_PC), .EXBranchDo(EX_BDo), .EXBranch(EX_B),
    .jmpAddr(btb_1_jmpaddr), .JMP(Pjmp));
  Hex_Digit_Display hex_digit_display_6 (.value(LedData[11:8]));  // open: dp
  Hex_Digit_Display hex_digit_display_7 (.value(LedData[7:4]));  // open: dp
  // Probe on EX_PC[19:0]
  // RiscV_Probe riscv_probe_3: pin names not known; wires that end beside it: EX_IR
  Multiplexer #(.select(1), .width(32), .disabled("Z"), .enable("false")) multiplexer_6 (
    .in0(PC_4), .in1(btb_1_jmpaddr), .out(multiplexer_6_out), .sel(Pjmp));
  Multiplexer #(.select(2), .width(32), .disabled("Z"), .enable("false")) multiplexer_7 (
    .in0(exoldR1), .in1(Aluout), .in2(RDin), .in3(Aluout), .out(NewR1), .sel(exfwdr1));
  Hex_Digit_Display hex_digit_display_8 (.value(LedData[3:0]));  // open: dp
  ROM #(.addrWidth(10), .dataWidth(32), .Select("high")) rom_1 (.addr(IF_PC[11:2]), .data(IF_IR));
  Adder #(.width(32)) adder_2 (.a(IF_PC), .b(32'h4), .out(PC_4));  // open: cin, cout
  or or_1 (CLEAR, EXPerr, JALex, JALRex);
  // Probe on \总周期数 
  // Probe on M_PC[19:0]
  // RiscV_Probe riscv_probe_4: pin names not known; wires that end beside it: MEM_IR
  IF_ID if_id_1 (
    .PCin(IF_PC), .IRin(IF_IR), .CLK(CLK), .PCout(ID_PC), .IRout(ID_IR), .\同步清零_气泡_高电平有效 (EXPerr),
    .\使能端_低电平有效_stall_高电平有效 (or_2_out), .Pjmpin(Pjmp), .Pjmpout(ID_Pjmp));
  // Probe on \总周期数 
  // Probe on \无条件分支数 
  // Probe on \条件分支成功数 
  // Probe on \插入气泡数 
  // Probe on \LoadUse次数 
  // RiscV_Probe riscv_probe_5: pin names not known; wires that end beside it: jalid, riscv_probe_5_p2, riscv_probe_5_p2, ID_IR, ID_IR[24:20]
  or or_2 (or_2_out, halt, loaduse);
  // Probe on IF_PC[11:0]
  // Probe on WB_PC[19:0]
  // RiscV_Probe riscv_probe_6: pin names not known; wires that end beside it: WB_IR
  not not_3 (not_3_out, halt);
  Multiplexer #(.select(2), .width(32), .disabled("Z"), .enable("false")) multiplexer_8 (
    .in0(exoldR2), .in1(Aluout), .in2(RDin), .in3(Aluout), .out(MDinexe), .sel(exfwdr2));
  // Probe on EX_PC[11:0]
  // Probe on ID_PC[11:0]
  \单周期硬布线控制器  \u_单周期硬布线控制器_1  (
    .Funct({ID_IR[30], ID_IR[25], ID_IR[14:12]}), .OP(ID_IR[6:2]), .ALU_OP(\单周期硬布线控制器_1_alu_op ),
    .MemToReg(\单周期硬布线控制器_1_memtoreg ), .MemWrite(\单周期硬布线控制器_1_memwrite ), .ALU_SRC(\单周期硬布线控制器_1_alu_src ),
    .RegWrite(\单周期硬布线控制器_1_regwrite ), .ecall(\单周期硬布线控制器_1_ecall ), .in_3(ID_IR[21]), .uret(Uret),
    .JAL(jalid), .SB(\单周期硬布线控制器_1_sb ), .Jalr(\单周期硬布线控制器_1_jalr ), .BLTU(\单周期硬布线控制器_1_bltu ),
    .Bne(\单周期硬布线控制器_1_bne ), .Beq(\单周期硬布线控制器_1_beq ), .S_type(S_Type), .I(I), .B(B));
  Multiplexer #(.select(1), .width(5), .disabled("Z"), .enable("false")) multiplexer_9 (
    .in0(ID_IR[19:15]), .in1(5'b10001), .out(multiplexer_9_out), .sel(\单周期硬布线控制器_1_ecall ));
  Multiplexer #(.select(1), .width(5), .disabled("Z"), .enable("false")) multiplexer_10 (
    .in0(ID_IR[24:20]), .in1(5'b01010), .out(multiplexer_10_out), .sel(\单周期硬布线控制器_1_ecall ));
  // Probe on ID_IR[11:7]
  Multiplexer #(.select(1), .width(12), .disabled("Z"), .enable("false")) multiplexer_11 (
    .in0(ID_IR[31:20]), .in1({ID_IR[31:25], ID_IR[11:7]}), .out(multiplexer_11_out), .sel(S_Type));
  assign Imm2 = {{20{shifter_1_out[11]}}, shifter_1_out};  // Bit_Extender bit_extender_1
  Shifter #(.width(12), .shift("ll")) shifter_1 (
    .in({ID_IR[31], ID_IR[7], ID_IR[30:25], ID_IR[11:8]}), .\dist (4'b0001), .out(shifter_1_out));
  assign bit_extender_2_out = {{20{ID_IR[31]}}, {ID_IR[31], ID_IR[7], ID_IR[30:25], ID_IR[11:8]}};  // Bit_Extender bit_extender_2
  assign bit_extender_3_out = {{12{ID_IR[31]}}, {ID_IR[31], ID_IR[19:12], ID_IR[20], ID_IR[30:21]}};  // Bit_Extender bit_extender_3
  Counter #(.width(16), .max('hffff), .ongoal("wrap"), .trigger("rising"), .behavior("new")) counter_1 (
    .count(not_3_out), .Q(\总周期数 ), .clk(CLK));  // open: load, D, carry, clr, preset, down
  // Probe on M_PC[11:0]
  D_Flip_Flop #(.trigger("high"), .Pre_Clr_Positions("LEGACY"), .NegatePresetClear("false"), .enable("true"), .NewFFLayout("false")) d_ff_1 (.Q(d_ff_1_q));  // open: clk, D, Qn, preset, en, reset
  // Probe on 13'h156
  // Probe on multiplexer_10_out
  assign Imm1 = {{20{multiplexer_11_out[11]}}, multiplexer_11_out};  // Bit_Extender bit_extender_4
  Multiplexer #(.select(4), .width(32), .disabled("Z"), .enable("false")) multiplexer_12 (
    .in1(Imm1), .in2(Imm1), .in4(bit_extender_2_out), .in8(bit_extender_3_out), .out(multiplexer_12_out),
    .sel({jalid, B, S_Type, I}));  // open: in0, in3, in5, in6, in7, in9, in10, in11, in12, in13, in14, in15
  // Probe on WB_PC[11:0]
  Comparator #(.width(13), .mode("twosComplement")) comparator_1 (
    .a(CNT_num), .b(13'h156), .eq(comparator_1_eq), .lt(comparator_1_lt));  // open: gt
  Clock #(.highDuration(1), .lowDuration(1)) clock_1 (.out(clock_1_out));
  \相关处理逻辑  \u_相关处理逻辑_1  (
    .exop(EX_IR[6:2]), .ExRegWrite(exregwrite), .OP(ID_IR[6:2]), .FUNC({ID_IR[30], ID_IR[25], ID_IR[14:12]}),
    .R1(multiplexer_9_out), .EXREG(EX_IR[11:7]), .R2(multiplexer_10_out), .MEMREG(MEM_IR[11:7]),
    .MemRegWrite(MemRegWrite), .LoadUse(loaduse), .R1EXRE(\相关处理逻辑_1_r1exre [0]),
    .R1MemRe(\相关处理逻辑_1_r1exre [1]), .R2EXRE(\相关处理逻辑_1_r2exre [0]), .R2MemRe(\相关处理逻辑_1_r2exre [1]));  // open: DH
  Regifile regifile_1 (
    .Din(RDin), .Clk(CLK), .R1(regifile_1_r1), .R2(regifile_1_r2), .WE(RegWrite), .W_num(W_out),
    .R1_num(multiplexer_9_out), .R2_num(multiplexer_10_out));
  Shifter #(.width(32), .shift("ll")) shifter_2 (.in(multiplexer_12_out), .\dist (5'b00001), .out(Imm3));
  nand nand_1 (nand_1_out, d_ff_1_q, comparator_1_eq);
  Counter #(.width(13), .max('h1fff), .ongoal("stay"), .trigger("rising"), .behavior("old")) counter_2 (
    .count(comparator_1_lt), .Q(CNT_num), .clk(clock_1_out));  // open: load, D, carry, clr, preset
  Multiplexer #(.select(1), .width(2), .disabled("Z"), .enable("false")) multiplexer_13 (
    .in0(\相关处理逻辑_1_r1exre ), .in1(2'b00), .out(multiplexer_13_out), .sel(loaduse));
  Multiplexer #(.select(1), .width(2), .disabled("Z"), .enable("false")) multiplexer_14 (
    .in0(\相关处理逻辑_1_r2exre ), .in1(2'b00), .out(multiplexer_14_out), .sel(loaduse));
  or or_3 (or_3_out, loaduse, uret_t, EXPerr);
  assign CLK = nand_1_out ? clock_1_out : 1'bz;  // Controlled_Buffer controlled_buffer_1
  ID_EX id_ex_1 (
    .Beqin(\单周期硬布线控制器_1_beq ), .Bnein(\单周期硬布线控制器_1_bne ), .MemToRegin(\单周期硬布线控制器_1_memtoreg ),
    .MemWritein(\单周期硬布线控制器_1_memwrite ), .ALUopin(\单周期硬布线控制器_1_alu_op ), .ALUSRCBin(\单周期硬布线控制器_1_alu_src ),
    .RegWritein(\单周期硬布线控制器_1_regwrite ), .Ecallin(\单周期硬布线控制器_1_ecall ), .Jarin(jalid),
    .Jarlin(\单周期硬布线控制器_1_jalr ), .Uretin(Uret), .Bltuin(\单周期硬布线控制器_1_bltu ), .R2in(regifile_1_r2),
    .R1in(regifile_1_r1), .PCin(ID_PC), .Imm1in(Imm1), .CLK(CLK), .Beqout(id_ex_1_beqout),
    .Bneout(id_ex_1_bneout), .MemToReginout(MemToReg), .MemWriteout(MemW), .ALUopout(AluOP),
    .ALUSRCBout(AluSrcB), .RegWriteout(exregwrite), .Ecallout(ecall_t), .Jarout(JALex), .Jarlout(JALRex),
    .Uretout(uret_t), .Bltuout(BLTU), .R2out(exoldR2), .R1out(exoldR1), .PCout(EX_PC), .Imm1out(jalrin),
    .\同步清零_气泡_高电平有效 (or_3_out), .Stypein(S_Type), .SBin(\单周期硬布线控制器_1_sb ), .SBout(SB), .W_in(ID_IR[11:7]),
    .W_out(W_outex), .Imm2in(Imm2), .Imm2out(id_ex_1_imm2out), .Imm3in(Imm3), .Imm3out(id_ex_1_imm3out),
    .IRin(ID_IR), .IRout(EX_IR), .Stall(halt), .fwdR1in(multiplexer_13_out), .fwdR1out(exfwdr1),
    .fwdR2in(multiplexer_14_out), .fwdR2out(exfwdr2), .pjmpin(ID_Pjmp), .pjmpout(EX_Pjmp));  // open: Stypeout
  Pull_Resistor #(.pull(1)) pull_resistor_1 (.node(CLK));
  Adder #(.width(32)) adder_3 (.a(id_ex_1_imm2out), .b(EX_PC), .out(branchdata));  // open: cin, cout
  or or_4 (EX_B, id_ex_1_beqout, id_ex_1_bneout, JALex, BLTU, JALRex, EX_Pjmp);
  Comparator #(.width(32), .mode("unsigned")) comparator_2 (
    .a(NewR1), .b(MDinexe), .lt(comparator_2_lt));  // open: gt, eq
  // Probe on NewR1
  // Probe on multiplexer_15_out
  Multiplexer #(.select(1), .width(32), .disabled("Z"), .enable("false")) multiplexer_15 (
    .in0(MDinexe), .in1(jalrin), .out(multiplexer_15_out), .sel(AluSrcB));
  Adder #(.width(32)) adder_4 (.a(id_ex_1_imm3out), .b(EX_PC), .out(jaldata));  // open: cin, cout
  and and_3 (and_3_out, alu_1_equal, id_ex_1_beqout);
  not not_4 (not_4_out, alu_1_equal);
  and and_4 (and_4_out, not_4_out, id_ex_1_bneout);
  ALU alu_1 (
    .X(NewR1), .Y(multiplexer_15_out), .AluOP(AluOP), .Equal(alu_1_equal), .Result(alu_1_result));  // open: Result_2, out_4, out_6
  Multiplexer #(.select(1), .width(32), .disabled("Z"), .enable("false")) multiplexer_16 (
    .in0(alu_1_result), .in1(PC_4), .out(multiplexer_16_out), .sel(or_5_out));
  or or_5 (or_5_out, JALex, JALRex);
  or or_6 (EX_BDo, branch, JALRex, JALex);
  or or_7 (branch, and_3_out, and_4_out, and_5_out);
  and and_5 (and_5_out, BLTU, comparator_2_lt);
  Adder #(.width(32)) adder_5 (.a(EX_PC), .b(32'h4), .out(EX_PC_4));  // open: cin, cout
  EX_MEM ex_mem_1 (
    .SBin(SB), .RegWritein(exregwrite), .MemToRegin(MemToReg), .MemWritein(MemW), .haltin(ecall_t),
    .Jarin(JALex), .W_lin(W_outex), .Aluin(alu_1_result), .PCin(EX_PC), .Selectin(alu_1_result[1:0]),
    .Jmpin(multiplexer_16_out), .Mdin(MDinexe), .CLK(CLK), .SBout(SBMem), .ReqWriteout(MemRegWrite),
    .MemToReginout(ex_mem_1_memtoreginout), .MemWriteout(MemWrite), .haltout(ex_mem_1_haltout),
    .Jarout(ex_mem_1_jarout), .w_out(W_outmem), .Aluout(Aluout), .PCout(M_PC), .Selectout(select),
    .Jmpout(JmpoutMem), .MdinoutMem(MDinMem), .\使能端_低电平有效_stall_高电平有效 (halt), .IRin(EX_IR), .IRout(MEM_IR),
    .jarlin(JALRex), .jarlout(ex_mem_1_jarlout), .R1in(NewR1), .R1out(ex_mem_1_r1out), .R2in(MDinexe),
    .R2out(ex_mem_1_r2out));  // open: ALUSRCBin, Ecallin, Uretin, ALUSRCBout, Ecallout, Uretout, 同步清零_气泡_高电平有效
  Counter #(.width(16), .max('hffff), .ongoal("wrap"), .trigger("rising"), .behavior("new")) counter_3 (
    .Q(\插入气泡数 ), .clk(and_6_out));  // open: load, D, count, carry, clr, preset, down
  and and_6 (and_6_out, not_5_out, not_6_out, loaduse);
  not not_5 (not_5_out, CLK);
  not not_6 (not_6_out, halt);
  Multiplexer #(.select(1), .width(32), .disabled("Z"), .enable("false")) multiplexer_17 (
    .in0(MDinMem), .in1(shifter_4_out), .out(MDin), .sel(SBMem));
  assign bit_extender_5_out = {{3{select[1]}}, select};  // Bit_Extender bit_extender_5
  Comparator #(.width(32), .mode("twosComplement")) comparator_3 (
    .a(R1), .b(32'h22), .eq(comparator_3_eq));  // open: gt, lt
  xor xor_1 (EXPerr, EX_Pjmp, EX_BDo);
  Shifter #(.width(5), .shift("ll")) shifter_3 (.in(bit_extender_5_out), .\dist (3'b011), .out(shifter_3_out));
  not not_7 (not_7_out, comparator_3_eq);
  Counter #(.width(16), .max('hffff), .ongoal("wrap"), .trigger("rising"), .behavior("new")) counter_4 (
    .Q(\无条件分支数 ), .clk(and_7_out));  // open: load, D, count, carry, clr, preset, down
  and and_7 (and_7_out, or_8_out, not_8_out);
  not not_8 (not_8_out, CLK);
  or or_8 (or_8_out, JALex, JALRex);
  Shifter #(.width(32), .shift("ll")) shifter_4 (.in(MDinMem), .\dist (shifter_3_out), .out(shifter_4_out));
  and and_8 (and_8_out, Ecall, not_7_out);
  and and_9 (and_9_out, Ecall, comparator_3_eq);
  // MIPS_RAM mips_ram_1: pin names not known; wires that end beside it: Aluout[11:2], MDin, MemWrite, mips_ram_1_p4, CLK, mips_ram_1_p6
  Multiplexer #(.select(1), .width(4), .disabled("Z"), .enable("false")) multiplexer_18 (
    .in0(4'b1111), .in1(multiplexer_19_out), .out(mips_ram_1_p4), .sel(SBMem));
  Multiplexer #(.select(2), .width(4), .disabled("Z"), .enable("false")) multiplexer_19 (
    .in0(4'b0001), .in1(4'b0010), .in2(4'b0100), .in3(4'b1000), .out(multiplexer_19_out), .sel(select));
  Register #(.width(1), .trigger("rising"), .Select("low")) register_1 (
    .D(and_8_out), .en(not_9_out), .Q(halt), .clk(CLK), .clr(Go));
  not not_9 (not_9_out, halt);
  // Probe on R2
  and and_10 (and_10_out, branch, not_10_out);
  Register #(.width(32), .trigger("rising"), .Select("low")) PC_2 (
    .D(R2), .en(and_9_out), .Q(LedData), .clk(CLK));  // open: clr
  Counter #(.width(16), .max('hffff), .ongoal("wrap"), .trigger("rising"), .behavior("new")) counter_5 (
    .Q(\条件分支成功数 ), .clk(and_10_out));  // open: load, D, count, carry, clr, preset, down
  not not_10 (not_10_out, CLK);
  MEM_WB mem_wb_1 (
    .MemToRegin(ex_mem_1_memtoreginout), .RegWritein(MemRegWrite), .haltin(ex_mem_1_haltout),
    .Jarin(ex_mem_1_jarout), .Jarlin(ex_mem_1_jarlout), .Din(mips_ram_1_p6), .PCin(M_PC), .Jmpin(JmpoutMem),
    .W_in(W_outmem), .CLK(CLK), .MemToRegout(mem_wb_1_memtoregout), .RegWriteout(RegWrite), .haltout(Ecall),
    .Jarout(mem_wb_1_jarout), .Jarlout(mem_wb_1_jarlout), .Dout(mem_wb_1_dout), .PCout(WB_PC),
    .Jmpout(mem_wb_1_jmpout), .W_out(W_out), .\使能端_低电平有效_stall_高电平有效 (halt), .IRin(MEM_IR), .IRout(WB_IR),
    .R1in(ex_mem_1_r1out), .R1out(R1), .R2in(ex_mem_1_r2out), .R2out(R2));  // open: Ecallin, Uretin, Selectin, Ecallout, Uretout, Selectout, 同步清零_气泡_高电平有效
  Counter #(.width(16), .max('hffff), .ongoal("wrap"), .trigger("rising"), .behavior("new")) counter_6 (
    .Q(\LoadUse次数 ), .clk(and_11_out));  // open: load, D, count, carry, clr, preset, down
  and and_11 (and_11_out, loaduse, not_11_out, not_12_out);
  not not_11 (not_11_out, halt);
  not not_12 (not_12_out, CLK);
  Multiplexer #(.select(1), .width(32), .disabled("Z"), .enable("false")) multiplexer_20 (
    .in0(mem_wb_1_jmpout), .in1(mem_wb_1_dout), .out(multiplexer_20_out), .sel(mem_wb_1_memtoregout));
  or or_9 (or_9_out, mem_wb_1_jarout, mem_wb_1_jarlout);
  Multiplexer #(.select(1), .width(32), .disabled("Z"), .enable("false")) multiplexer_21 (
    .in0(multiplexer_20_out), .in1(adder_6_out), .out(RDin), .sel(or_9_out));
  Adder #(.width(32)) adder_6 (.a(WB_PC), .b(32'h4), .out(adder_6_out));  // open: cin, cout

  // Other names for the same wires on the sheet: W_in[4:0] = ID_IR[11:7]; exop[4:0] = EX_IR[6:2];
  //   EXREG[4:0] = EX_IR[11:7]; IR[31:0] = IF_IR; MEMREG[4:0] = MEM_IR[11:7]; NewR2[31:0] = MDinexe; PC[31:0] = IF_PC;
  //   PC1[31:0] = ID_PC; PC2[31:0] = EX_PC; MEM_PC[31:0] = M_PC; PC3[31:0] = M_PC; PC4[31:0] = WB_PC;
  //   R1Data[31:0] = NewR1

  // Notes on the sheet:
  //   中断源
  //   时空图监测，可删除
  //   中断等待指示
  //   数码管输出
  //   指令存储器
  //   contents of rom_1 (hex, n*v repeats v):
  //   100493 100006f 100493 200913 300993 100006f 100493 200913 300993 100006f 100493 200913 300993
  //   100006f 100493 200913 300993 3c0000ef 100413 100493 1f49493 900533 2200893 73 24d493 48463 fedff06f
  //   900533 2200893 73 100493 249493 900533 2200893 73 48463 fedff06f 100493 1f49493 900533 2200893 73
  //   4034d493 900533 2200893 73 4044d493 900533 2200893 73 4044d493 900533 2200893 73 4044d493 900533
  //   2200893 73 4044d493 900533 2200893 73 4044d493 900533 2200893 73 4044d493 900533 2200893 73 4044d493
  //   900533 2200893 73 100413 1f41993 41f9d993 433 c00913 300b13 140413 f47413 800293 100313 499993
  //   89e9b3 1300533 2200893 73 406282b3 fe0294e3 140413 f00f93 1f47433 1c41413 800293 100313 49d993
  //   89e9b3 1300533 2200893 73 406282b3 fe0294e3 1c45413 406b0b33 b0463 f95ff06f 2b3 fff2c293 829293
  //   ff2e293 500533 2200893 73 fff00413 493 84a023 140413 448493 84a023 140413 448493 84a023 140413
  //   448493 84a023 140413 448493 84a023 140413 448493 84a023 140413 448493 84a023 140413 448493 84a023
  //   140413 448493 84a023 140413 448493 84a023 140413 448493 84a023 140413 448493 84a023 140413 448493
  //   84a023 140413 448493 84a023 140413 448493 84a023 140413 448493 84a023 140413 448493 140413 433
  //   3c00493 42983 4aa03 149a2b3 28663 134a023 1442023 ffc48493 fe9412e3 800533 2200893 73 440413 3c00493
  //   fc9416e3 3200893 73 100293 300313 800493 849493 7648493 900533 2200893 73 800e13 5494b3 6494b3
  //   900533 2200893 73 fffe0e13 fe0e14e3 a00893 73 100293 300313 800493 849493 7648493 1449493 900533
  //   2200893 73 800e13 4054d4b3 4064d4b3 900533 2200893 73 fffe0e13 fe0e14e3 a00893 73 313 2000e13 493
  //   100913 930023 900533 2200893 73 12484b3 130313 fffe0e13 fe0e12e3 800e13 313 32483 900533 2200893 73
  //   430313 fffe0e13 fe0e14e3 a00893 73 ff100493 900533 2200893 73 148493 fe9068e3 900533 2200893 73
  //   a00893 73 a00893 73 413 140413 800533 2200893 73 240413 800533 2200893 73 340413 800533 2200893 73
  //   440413 800533 2200893 73 540413 800533 2200893 73 640413 800533 2200893 73 740413 800533 2200893 73
  //   840413 800533 2200893 2200893 73 8067
  //   指令探针
  //   指令字
  //   控制位
  //   Beq
  //   Bne
  //   MemToReg
  //   MemWrite
  //   AluOP
  //   AluSrcB
  //   RegWrite
  //   流水调试日志用
  //   暂停节拍，不能为0
  //   戳工具置1进入计数暂停模式，ctrl+k时钟自动运行到对应节拍暂停
  //   ctrl+k关闭时钟连续运行，将控制位置零，进入单步调试模式调试
  //   ctrl+k关闭时钟连续运行，将控制位置零，进入单步调试模式调试
  //   用这个时钟源需要去掉电路中的其他时钟源
  //   可计数暂停的时钟源
  //   为方便自动评测，需要输出流水线各段保存的PC值，注意是PC不是PC+4，另外ID段寄存器写入信息，Mem段内存写入信息也要输出
endmodule

module \for相关处理逻辑  (
  input  OP2,
  input  OP3,
  input  OP4,
  input  OP5,
  input  OP6,
  input  F12,
  input  F13,
  input  F14,
  input  F25,
  input  F30,
  output R1,
  output R2
);

  wire and_1_out, and_2_out, and_3_out, and_4_out, and_5_out, and_6_out, and_7_out, and_8_out, and_9_out,
       and_10_out, and_11_out, and_12_out, and_13_out, and_14_out, and_15_out, and_16_out, and_17_out,
       and_18_out, and_19_out, and_20_out, and_21_out, and_22_out, not_1_out, not_2_out, not_3_out,
       not_4_out, not_5_out, not_6_out, not_7_out, not_8_out, not_9_out, not_10_out, not_11_out, not_12_out,
       not_13_out, not_14_out, not_15_out, not_16_out, not_17_out, not_18_out, not_19_out, not_20_out,
       not_21_out, not_22_out, not_23_out, not_24_out, not_25_out, not_26_out, not_27_out, not_28_out,
       not_29_out, not_30_out, not_31_out, not_32_out, not_33_out, not_34_out, not_35_out, not_36_out,
       not_37_out, not_38_out, not_39_out, not_40_out, not_41_out, not_42_out, not_43_out, not_44_out,
       not_45_out, not_46_out, not_47_out, not_48_out, not_49_out, not_50_out, not_51_out, not_52_out,
       not_53_out, not_54_out, not_55_out, not_56_out, not_57_out, not_58_out, not_59_out, not_60_out,
       not_61_out, not_62_out, not_63_out, not_64_out, not_65_out, not_66_out, not_67_out, not_68_out,
       not_69_out, not_70_out, not_71_out, not_72_out, not_73_out, not_74_out, not_75_out, not_76_out,
       not_77_out, not_78_out, not_79_out, not_80_out, not_81_out, not_82_out, not_83_out, not_84_out,
       not_85_out, not_86_out, not_87_out, not_88_out, not_89_out, not_90_out, not_91_out, not_92_out,
       not_93_out, not_94_out, not_95_out, not_96_out, not_97_out, not_98_out, not_99_out, not_100_out,
       not_101_out, not_102_out, not_103_out, not_104_out, not_105_out, not_106_out, not_107_out,
       not_108_out, not_109_out, not_110_out, not_111_out, not_112_out, not_113_out, not_114_out,
       not_115_out, not_116_out, not_117_out, not_118_out, not_119_out;

  not not_1 (not_1_out, OP2);
  not not_2 (not_2_out, OP3);
  not not_3 (not_3_out, OP5);
  not not_4 (not_4_out, OP6);
  not not_5 (not_5_out, F12);
  not not_6 (not_6_out, F14);
  not not_7 (not_7_out, OP2);
  not not_8 (not_8_out, OP3);
  not not_9 (not_9_out, OP4);
  not not_10 (not_10_out, OP6);
  not not_11 (not_11_out, F12);
  not not_12 (not_12_out, F14);
  not not_13 (not_13_out, OP2);
  not not_14 (not_14_out, OP3);
  not not_15 (not_15_out, OP4);
  not not_16 (not_16_out, F13);
  not not_17 (not_17_out, F14);
  not not_18 (not_18_out, OP3);
  not not_19 (not_19_out, OP4);
  not not_20 (not_20_out, F12);
  not not_21 (not_21_out, F13);
  not not_22 (not_22_out, F14);
  not not_23 (not_23_out, OP2);
  not not_24 (not_24_out, OP3);
  not not_25 (not_25_out, OP4);
  not not_26 (not_26_out, F12);
  not not_27 (not_27_out, OP2);
  not not_28 (not_28_out, OP3);
  not not_29 (not_29_out, OP5);
  not not_30 (not_30_out, OP6);
  not not_31 (not_31_out, F12);
  not not_32 (not_32_out, OP2);
  not not_33 (not_33_out, OP3);
  not not_34 (not_34_out, OP6);
  not not_35 (not_35_out, F12);
  not not_36 (not_36_out, F13);
  not not_37 (not_37_out, F14);
  not not_38 (not_38_out, F25);
  not not_39 (not_39_out, OP2);
  not not_40 (not_40_out, OP3);
  not not_41 (not_41_out, OP6);
  not not_42 (not_42_out, F13);
  not not_43 (not_43_out, F14);
  not not_44 (not_44_out, F25);
  not not_45 (not_45_out, F30);
  not not_46 (not_46_out, OP2);
  not not_47 (not_47_out, OP3);
  not not_48 (not_48_out, OP5);
  not not_49 (not_49_out, OP6);
  not not_50 (not_50_out, OP2);
  not not_51 (not_51_out, OP3);
  not not_52 (not_52_out, OP6);
  not not_53 (not_53_out, F13);
  not not_54 (not_54_out, F25);
  not not_55 (not_55_out, OP2);
  not not_56 (not_56_out, OP3);
  not not_57 (not_57_out, F12);
  not not_58 (not_58_out, F13);
  not not_59 (not_59_out, F14);
  not not_60 (not_60_out, F25);
  not not_61 (not_61_out, F30);
  not not_62 (not_62_out, OP2);
  not not_63 (not_63_out, OP3);
  not not_64 (not_64_out, OP6);
  not not_65 (not_65_out, F25);
  not not_66 (not_66_out, F30);
  not not_67 (not_67_out, F12);
  not not_68 (not_68_out, OP4);
  not not_69 (not_69_out, OP3);
  not not_70 (not_70_out, OP2);
  not not_71 (not_71_out, OP2);
  not not_72 (not_72_out, OP3);
  not not_73 (not_73_out, OP4);
  not not_74 (not_74_out, OP6);
  not not_75 (not_75_out, F12);
  not not_76 (not_76_out, F14);
  not not_77 (not_77_out, OP2);
  not not_78 (not_78_out, OP3);
  not not_79 (not_79_out, OP6);
  not not_80 (not_80_out, F12);
  not not_81 (not_81_out, F13);
  not not_82 (not_82_out, F14);
  not not_83 (not_83_out, F25);
  not not_84 (not_84_out, OP2);
  not not_85 (not_85_out, OP3);
  not not_86 (not_86_out, F12);
  not not_87 (not_87_out, F13);
  not not_88 (not_88_out, F14);
  not not_89 (not_89_out, F25);
  not not_90 (not_90_out, F30);
  not not_91 (not_91_out, OP2);
  not not_92 (not_92_out, OP3);
  not not_93 (not_93_out, OP4);
  not not_94 (not_94_out, F13);
  not not_95 (not_95_out, F14);
  not not_96 (not_96_out, OP2);
  not not_97 (not_97_out, OP3);
  not not_98 (not_98_out, OP4);
  not not_99 (not_99_out, F12);
  not not_100 (not_100_out, OP2);
  not not_101 (not_101_out, OP3);
  not not_102 (not_102_out, OP6);
  not not_103 (not_103_out, F14);
  not not_104 (not_104_out, F25);
  not not_105 (not_105_out, F30);
  not not_106 (not_106_out, OP2);
  not not_107 (not_107_out, OP3);
  not not_108 (not_108_out, OP6);
  not not_109 (not_109_out, F25);
  not not_110 (not_110_out, F30);
  not not_111 (not_111_out, OP2);
  not not_112 (not_112_out, OP3);
  not not_113 (not_113_out, OP6);
  not not_114 (not_114_out, F13);
  not not_115 (not_115_out, F25);
  not not_116 (not_116_out, F12);
  not not_117 (not_117_out, OP4);
  not not_118 (not_118_out, OP3);
  not not_119 (not_119_out, OP2);
  and and_1 (and_1_out, not_1_out, not_2_out, not_3_out, not_4_out, not_5_out, not_6_out);
  and and_2 (and_2_out, not_7_out, not_8_out, not_9_out, not_10_out, not_11_out, F13, not_12_out);
  and and_3 (and_3_out, not_13_out, not_14_out, not_15_out, OP5, OP6, not_16_out, not_17_out);
  and and_4 (and_4_out, not_18_out, not_19_out, OP5, OP6, not_20_out, not_21_out, not_22_out);
  and and_5 (and_5_out, not_23_out, not_24_out, not_25_out, OP5, OP6, not_26_out, F13, F14);
  and and_6 (and_6_out, not_27_out, not_28_out, OP4, not_29_out, not_30_out, not_31_out);
  and and_7 (and_7_out, not_32_out, not_33_out, OP4, not_34_out, not_35_out, not_36_out, not_37_out, not_38_out);
  and and_8 (and_8_out, not_39_out, not_40_out, OP4, not_41_out, not_42_out, not_43_out, not_44_out, not_45_out);
  and and_9 (and_9_out, not_46_out, not_47_out, OP4, not_48_out, not_49_out, F13, F14);
  and and_10 (and_10_out, not_50_out, not_51_out, OP4, not_52_out, F12, not_53_out, F14, not_54_out);
  and and_11 (and_11_out, not_55_out, not_56_out, OP4, OP5, not_57_out, not_58_out, not_59_out, not_60_out, not_61_out);
  and and_12 (and_12_out, not_62_out, not_63_out, OP4, OP5, not_64_out, F13, not_65_out, not_66_out);
  and and_13 (and_13_out, F14, F13, not_67_out, OP6, OP5, not_68_out, not_69_out, not_70_out);
  and and_14 (and_14_out, not_71_out, not_72_out, not_73_out, OP5, not_74_out, not_75_out, not_76_out);
  and and_15 (and_15_out, not_77_out, not_78_out, OP5, not_79_out, not_80_out, not_81_out, not_82_out, not_83_out);
  and and_16 (and_16_out, not_84_out, not_85_out, OP5, not_86_out, not_87_out, not_88_out, not_89_out, not_90_out);
  and and_17 (and_17_out, not_91_out, not_92_out, not_93_out, OP5, OP6, not_94_out, not_95_out);
  and and_18 (and_18_out, not_96_out, not_97_out, not_98_out, OP5, OP6, not_99_out, F13, F14);
  and and_19 (and_19_out, not_100_out, not_101_out, OP4, OP5, not_102_out, not_103_out, not_104_out, not_105_out);
  and and_20 (and_20_out, not_106_out, not_107_out, OP4, OP5, not_108_out, F13, not_109_out, not_110_out);
  and and_21 (and_21_out, not_111_out, not_112_out, OP4, OP5, not_113_out, F12, not_114_out, F14, not_115_out);
  and and_22 (and_22_out, F14, F13, not_116_out, OP6, OP5, not_117_out, not_118_out, not_119_out);
  or or_1 (R1, and_1_out, and_2_out, and_3_out, and_4_out, and_5_out, and_6_out, and_7_out, and_8_out, and_9_out, and_10_out, and_11_out, and_12_out, and_13_out);
  or or_2 (R2, and_14_out, and_15_out, and_16_out, and_17_out, and_18_out, and_19_out, and_20_out, and_21_out, and_22_out);
endmodule

module \比较MAX  (
  input  [15:0] X,
  input  [15:0] Y,
  input  [2:0] X_num,
  input  [2:0] Y_num,
  output [15:0] MAX,
  output [2:0] MAX_num
);

  wire comparator_1_eq, comparator_1_gt, or_1_out;

  Comparator #(.width(16), .mode("twosComplement")) comparator_1 (
    .a(X), .b(Y), .gt(comparator_1_gt), .eq(comparator_1_eq));  // open: lt
  or or_1 (or_1_out, comparator_1_gt, comparator_1_eq);
  Multiplexer #(.select(1), .width(16), .disabled("Z"), .enable("true")) multiplexer_1 (
    .in0(Y), .in1(X), .out(MAX), .sel(or_1_out), .en(1'b1));
  Multiplexer #(.select(1), .width(3), .disabled("Z"), .enable("false")) multiplexer_2 (
    .in0(Y_num), .in1(X_num), .out(MAX_num), .sel(or_1_out));
endmodule

module BTB (
  input  [31:0] EXbranchdata,
  input  [31:0] PC,
  input  CLK,
  input  [31:0] EXPC,
  input  EXBranchDo,
  input  EXBranch,
  output [31:0] jmpAddr,
  output JMP
);

  wire and_9_out, and_10_out, and_19_out, and_20_out, and_21_out, and_22_out, and_23_out, and_24_out,
       and_25_out, and_26_out, comparator_1_eq, comparator_2_eq, comparator_3_eq, comparator_4_eq,
       comparator_5_eq, comparator_6_eq, comparator_7_eq, comparator_8_eq, comparator_9_eq, comparator_10_eq,
       comparator_11_eq, comparator_12_eq, comparator_13_eq, comparator_14_eq, comparator_15_eq,
       comparator_16_eq, d_ff_1_q, d_ff_2_q, d_ff_3_q, d_ff_4_q, d_ff_5_q, d_ff_6_q, d_ff_7_q, d_ff_8_q, L1,
       L2, L3, L4, L5, L6, L7, L8, MissEX, not_1_out, not_2_out, not_3_out, not_4_out, not_5_out, not_6_out,
       not_7_out, not_8_out, or_1_out, or_2_out, or_3_out, or_4_out, or_5_out, or_6_out, or_7_out, or_8_out,
       S1, S2, S3, S4, S5, S6, S7, S8, v1, v2, v3, v4, v5, v6, v7, v8, W1, W2, W3, W4, W5, W6, W7, W8;
  wire [0:0] controlled_buffer_9_out, controlled_buffer_10_out, controlled_buffer_11_out,
       controlled_buffer_12_out, controlled_buffer_13_out, controlled_buffer_14_out,
       controlled_buffer_15_out, controlled_buffer_16_out;
  wire [1:0] help_1_nextl, help_2_nextl, help_3_nextl, help_4_nextl, help_5_nextl, help_6_nextl,
       help_7_nextl, help_8_nextl, P1, P2, P3, P4, P5, P6, P7, P8;
  wire [2:0] multiplexer_1_out, priority_encoder_1_out, \比较max_1_max_num , \比较max_2_max_num ,
       \比较max_3_max_num , \比较max_4_max_num , \比较max_5_max_num , \比较max_6_max_num , \比较max_7_max_num ;
  wire [15:0] cnt1, cnt2, cnt3, cnt4, cnt5, cnt6, cnt7, cnt8, \比较max_1_max , \比较max_2_max , \比较max_3_max ,
       \比较max_4_max , \比较max_5_max , \比较max_6_max ;
  wire [31:0] B1, B2, B3, B4, B5, B6, B7, B8, register_17_q, register_18_q, register_19_q, register_20_q,
       register_21_q, register_22_q, register_23_q, register_24_q;

  Register #(.width(1), .trigger("rising"), .Select("low")) register_1 (
    .D(1'b1), .en(W4), .Q(v4), .clk(CLK));  // open: clr
  Register #(.width(1), .trigger("rising"), .Select("low")) register_2 (
    .D(1'b1), .en(W5), .Q(v5), .clk(CLK));  // open: clr
  Register #(.width(1), .trigger("rising"), .Select("low")) register_3 (
    .D(1'b1), .en(W6), .Q(v6), .clk(CLK));  // open: clr
  Register #(.width(1), .trigger("rising"), .Select("low")) register_4 (
    .D(1'b1), .en(W7), .Q(v7), .clk(CLK));  // open: clr
  Register #(.width(1), .trigger("rising"), .Select("low")) register_5 (
    .D(1'b1), .en(W8), .Q(v8), .clk(CLK));  // open: clr
  Register #(.width(1), .trigger("rising"), .Select("low")) register_6 (
    .D(1'b1), .en(W1), .Q(v1), .clk(CLK));  // open: clr
  Register #(.width(1), .trigger("rising"), .Select("low")) register_7 (
    .D(1'b1), .en(W2), .Q(v2), .clk(CLK));  // open: clr
  Register #(.width(1), .trigger("rising"), .Select("low")) register_8 (
    .D(1'b1), .en(W3), .Q(v3), .clk(CLK));  // open: clr
  Register #(.width(32), .trigger("rising"), .Select("low")) register_9 (
    .D(EXPC), .en(W7), .Q(B7), .clk(CLK));  // open: clr
  Register #(.width(32), .trigger("rising"), .Select("low")) register_10 (
    .D(EXPC), .en(W8), .Q(B8), .clk(CLK));  // open: clr
  Register #(.width(32), .trigger("rising"), .Select("low")) register_11 (
    .D(EXPC), .en(W2), .Q(B2), .clk(CLK));  // open: clr
  Register #(.width(32), .trigger("rising"), .Select("low")) register_12 (
    .D(EXPC), .en(W3), .Q(B3), .clk(CLK));  // open: clr
  Register #(.width(32), .trigger("rising"), .Select("low")) register_13 (
    .D(EXPC), .en(W4), .Q(B4), .clk(CLK));  // open: clr
  Register #(.width(32), .trigger("rising"), .Select("low")) register_14 (
    .D(EXPC), .en(W5), .Q(B5), .clk(CLK));  // open: clr
  Register #(.width(32), .trigger("rising"), .Select("low")) register_15 (
    .D(EXPC), .en(W6), .Q(B6), .clk(CLK));  // open: clr
  Register #(.width(32), .trigger("rising"), .Select("low")) register_16 (
    .D(EXPC), .en(W1), .Q(B1), .clk(CLK));  // open: clr
  or or_1 (or_1_out, W2, L2);
  or or_2 (or_2_out, W3, L3);
  or or_3 (or_3_out, W4, L4);
  or or_4 (or_4_out, W5, L5);
  D_Flip_Flop #(.trigger("rising"), .Pre_Clr_Positions("LEGACY"), .NegatePresetClear("false"), .enable("true"), .NewFFLayout("false")) d_ff_1 (
    .clk(CLK), .D(or_5_out), .Q(d_ff_1_q));  // open: Qn, preset, en, reset
  or or_5 (or_5_out, W6, L6);
  Counter #(.width(16), .max('hffff), .ongoal("wrap"), .trigger("rising"), .behavior("new")) counter_1 (
    .Q(cnt7), .clk(CLK), .clr(d_ff_2_q), .down(W7));  // open: load, D, count, carry, preset
  D_Flip_Flop #(.trigger("rising"), .Pre_Clr_Positions("LEGACY"), .NegatePresetClear("false"), .enable("true"), .NewFFLayout("false")) d_ff_2 (
    .clk(CLK), .D(or_6_out), .Q(d_ff_2_q));  // open: Qn, preset, en, reset
  or or_6 (or_6_out, W7, L7);
  Counter #(.width(16), .max('hffff), .ongoal("wrap"), .trigger("rising"), .behavior("new")) counter_2 (
    .Q(cnt8), .clk(CLK), .clr(d_ff_3_q), .down(W8));  // open: load, D, count, carry, preset
  D_Flip_Flop #(.trigger("rising"), .Pre_Clr_Positions("LEGACY"), .NegatePresetClear("false"), .enable("true"), .NewFFLayout("false")) d_ff_3 (
    .clk(CLK), .D(or_7_out), .Q(d_ff_3_q));  // open: Qn, preset, en, reset
  or or_7 (or_7_out, W8, L8);
  D_Flip_Flop #(.trigger("rising"), .Pre_Clr_Positions("LEGACY"), .NegatePresetClear("false"), .enable("true"), .NewFFLayout("false")) d_ff_4 (
    .clk(CLK), .D(or_8_out), .Q(d_ff_4_q));  // open: Qn, preset, en, reset
  or or_8 (or_8_out, W1, L1);
  Counter #(.width(16), .max('hffff), .ongoal("wrap"), .trigger("rising"), .behavior("new")) counter_3 (
    .Q(cnt2), .clk(CLK), .clr(d_ff_5_q), .down(W2));  // open: load, D, count, carry, preset
  D_Flip_Flop #(.trigger("rising"), .Pre_Clr_Positions("LEGACY"), .NegatePresetClear("false"), .enable("true"), .NewFFLayout("false")) d_ff_5 (
    .clk(CLK), .D(or_1_out), .Q(d_ff_5_q));  // open: Qn, preset, en, reset
  Counter #(.width(16), .max('hffff), .ongoal("wrap"), .trigger("rising"), .behavior("new")) counter_4 (
    .Q(cnt3), .clk(CLK), .clr(d_ff_6_q), .down(W3));  // open: load, D, count, carry, preset
  D_Flip_Flop #(.trigger("rising"), .Pre_Clr_Positions("LEGACY"), .NegatePresetClear("false"), .enable("true"), .NewFFLayout("false")) d_ff_6 (
    .clk(CLK), .D(or_2_out), .Q(d_ff_6_q));  // open: Qn, preset, en, reset
  Counter #(.width(16), .max('hffff), .ongoal("wrap"), .trigger("rising"), .behavior("new")) counter_5 (
    .Q(cnt4), .clk(CLK), .clr(d_ff_7_q), .down(W4));  // open: load, D, count, carry, preset
  D_Flip_Flop #(.trigger("rising"), .Pre_Clr_Positions("LEGACY"), .NegatePresetClear("false"), .enable("true"), .NewFFLayout("false")) d_ff_7 (
    .clk(CLK), .D(or_3_out), .Q(d_ff_7_q));  // open: Qn, preset, en, reset
  Counter #(.width(16), .max('hffff), .ongoal("wrap"), .trigger("rising"), .behavior("new")) counter_6 (
    .Q(cnt5), .clk(CLK), .clr(d_ff_8_q), .down(W5));  // open: load, D, count, carry, preset
  D_Flip_Flop #(.trigger("rising"), .Pre_Clr_Positions("LEGACY"), .NegatePresetClear("false"), .enable("true"), .NewFFLayout("false")) d_ff_8 (
    .clk(CLK), .D(or_4_out), .Q(d_ff_8_q));  // open: Qn, preset, en, reset
  Counter #(.width(16), .max('hffff), .ongoal("wrap"), .trigger("rising"), .behavior("new")) counter_7 (
    .Q(cnt6), .clk(CLK), .clr(d_ff_1_q), .down(W6));  // open: load, D, count, carry, preset
  Counter #(.width(16), .max('hffff), .ongoal("wrap"), .trigger("rising"), .behavior("new")) counter_8 (
    .Q(cnt1), .clk(CLK), .clr(d_ff_4_q), .down(W1));  // open: load, D, count, carry, preset
  Register #(.width(32), .trigger("rising"), .Select("low")) register_17 (
    .D(EXbranchdata), .en(W5), .Q(register_17_q), .clk(CLK));  // open: clr
  Register #(.width(32), .trigger("rising"), .Select("low")) register_18 (
    .D(EXbranchdata), .en(W6), .Q(register_18_q), .clk(CLK));  // open: clr
  Register #(.width(32), .trigger("rising"), .Select("low")) register_19 (
    .D(EXbranchdata), .en(W7), .Q(register_19_q), .clk(CLK));  // open: clr
  Register #(.width(32), .trigger("rising"), .Select("low")) register_20 (
    .D(EXbranchdata), .en(W8), .Q(register_20_q), .clk(CLK));  // open: clr
  assign jmpAddr = L8 ? register_20_q : 32'bz;  // Controlled_Buffer controlled_buffer_1
  Register #(.width(32), .trigger("rising"), .Select("low")) register_21 (
    .D(EXbranchdata), .en(W1), .Q(register_21_q), .clk(CLK));  // open: clr
  assign jmpAddr = L2 ? register_22_q : 32'bz;  // Controlled_Buffer controlled_buffer_2
  Register #(.width(32), .trigger("rising"), .Select("low")) register_22 (
    .D(EXbranchdata), .en(W2), .Q(register_22_q), .clk(CLK));  // open: clr
  assign jmpAddr = L3 ? register_23_q : 32'bz;  // Controlled_Buffer controlled_buffer_3
  Register #(.width(32), .trigger("rising"), .Select("low")) register_23 (
    .D(EXbranchdata), .en(W3), .Q(register_23_q), .clk(CLK));  // open: clr
  assign jmpAddr = L4 ? register_24_q : 32'bz;  // Controlled_Buffer controlled_buffer_4
  Register #(.width(32), .trigger("rising"), .Select("low")) register_24 (
    .D(EXbranchdata), .en(W4), .Q(register_24_q), .clk(CLK));  // open: clr
  assign jmpAddr = L5 ? register_17_q : 32'bz;  // Controlled_Buffer controlled_buffer_5
  assign jmpAddr = L6 ? register_18_q : 32'bz;  // Controlled_Buffer controlled_buffer_6
  assign jmpAddr = L7 ? register_19_q : 32'bz;  // Controlled_Buffer controlled_buffer_7
  assign jmpAddr = L1 ? register_21_q : 32'bz;  // Controlled_Buffer controlled_buffer_8
  \比较MAX  \u_比较max_1  (
    .X(cnt1), .Y(cnt2), .X_num(3'b000), .Y_num(3'b001), .MAX(\比较max_1_max ), .MAX_num(\比较max_1_max_num ));
  \比较MAX  \u_比较max_2  (
    .X(cnt3), .Y(cnt4), .X_num(3'b010), .Y_num(3'b011), .MAX(\比较max_2_max ), .MAX_num(\比较max_2_max_num ));
  \比较MAX  \u_比较max_3  (
    .X(cnt5), .Y(cnt6), .X_num(3'b100), .Y_num(3'b101), .MAX(\比较max_3_max ), .MAX_num(\比较max_3_max_num ));
  \比较MAX  \u_比较max_4  (
    .X(cnt7), .Y(cnt8), .X_num(3'b110), .Y_num(3'b111), .MAX(\比较max_4_max ), .MAX_num(\比较max_4_max_num ));
  Comparator #(.width(32), .mode("twosComplement")) comparator_1 (
    .a(B1), .b(PC), .eq(comparator_1_eq));  // open: gt, lt
  Comparator #(.width(32), .mode("twosComplement")) comparator_2 (
    .a(B2), .b(PC), .eq(comparator_2_eq));  // open: gt, lt
  Comparator #(.width(32), .mode("twosComplement")) comparator_3 (
    .a(B3), .b(PC), .eq(comparator_3_eq));  // open: gt, lt
  Comparator #(.width(32), .mode("twosComplement")) comparator_4 (
    .a(B4), .b(PC), .eq(comparator_4_eq));  // open: gt, lt
  Comparator #(.width(32), .mode("twosComplement")) comparator_5 (
    .a(B5), .b(PC), .eq(comparator_5_eq));  // open: gt, lt
  Comparator #(.width(32), .mode("twosComplement")) comparator_6 (
    .a(B6), .b(PC), .eq(comparator_6_eq));  // open: gt, lt
  Comparator #(.width(32), .mode("twosComplement")) comparator_7 (
    .a(B7), .b(PC), .eq(comparator_7_eq));  // open: gt, lt
  Comparator #(.width(32), .mode("twosComplement")) comparator_8 (
    .a(B8), .b(PC), .eq(comparator_8_eq));  // open: gt, lt
  and and_1 (L1, comparator_1_eq, v1);
  and and_2 (L2, comparator_2_eq, v2);
  and and_3 (L3, comparator_3_eq, v3);
  and and_4 (L4, comparator_4_eq, v4);
  and and_5 (L5, comparator_5_eq, v5);
  and and_6 (L6, comparator_6_eq, v6);
  and and_7 (L7, comparator_7_eq, v7);
  and and_8 (L8, comparator_8_eq, v8);
  \比较MAX  \u_比较max_5  (
    .X(\比较max_1_max ), .Y(\比较max_2_max ), .X_num(\比较max_1_max_num ), .Y_num(\比较max_2_max_num ),
    .MAX(\比较max_5_max ), .MAX_num(\比较max_5_max_num ));
  \比较MAX  \u_比较max_6  (
    .X(\比较max_3_max ), .Y(\比较max_4_max ), .X_num(\比较max_3_max_num ), .Y_num(\比较max_4_max_num ),
    .MAX(\比较max_6_max ), .MAX_num(\比较max_6_max_num ));
  and and_9 (and_9_out, v1, v2, v3, v4, v5, v6, v7, v8);
  \比较MAX  \u_比较max_7  (
    .X(\比较max_5_max ), .Y(\比较max_6_max ), .X_num(\比较max_5_max_num ), .Y_num(\比较max_6_max_num ),
    .MAX_num(\比较max_7_max_num ));  // open: MAX
  not not_1 (not_1_out, v1);
  not not_2 (not_2_out, v2);
  not not_3 (not_3_out, v3);
  not not_4 (not_4_out, v4);
  not not_5 (not_5_out, v5);
  not not_6 (not_6_out, v6);
  not not_7 (not_7_out, v7);
  not not_8 (not_8_out, v8);
  Priority_Encoder #(.select(3), .disabled("Z")) priority_encoder_1 (
    .in0(not_1_out), .in1(not_2_out), .in2(not_3_out), .in3(not_4_out), .in4(not_5_out), .in5(not_6_out),
    .in6(not_7_out), .in7(not_8_out), .out(priority_encoder_1_out), .en_out(and_9_out));  // open: gs, en_in
  Multiplexer #(.select(1), .width(3), .disabled("Z"), .enable("false")) multiplexer_1 (
    .in0(priority_encoder_1_out), .in1(\比较max_7_max_num ), .out(multiplexer_1_out), .sel(and_9_out));
  and and_10 (and_10_out, MissEX, EXBranch);
  Comparator #(.width(32), .mode("twosComplement")) comparator_9 (
    .a(B1), .b(EXPC), .eq(comparator_9_eq));  // open: gt, lt
  Comparator #(.width(32), .mode("twosComplement")) comparator_10 (
    .a(B2), .b(EXPC), .eq(comparator_10_eq));  // open: gt, lt
  Comparator #(.width(32), .mode("twosComplement")) comparator_11 (
    .a(B3), .b(EXPC), .eq(comparator_11_eq));  // open: gt, lt
  Comparator #(.width(32), .mode("twosComplement")) comparator_12 (
    .a(B4), .b(EXPC), .eq(comparator_12_eq));  // open: gt, lt
  Comparator #(.width(32), .mode("twosComplement")) comparator_13 (
    .a(B5), .b(EXPC), .eq(comparator_13_eq));  // open: gt, lt
  Comparator #(.width(32), .mode("twosComplement")) comparator_14 (
    .a(B6), .b(EXPC), .eq(comparator_14_eq));  // open: gt, lt
  Comparator #(.width(32), .mode("twosComplement")) comparator_15 (
    .a(B7), .b(EXPC), .eq(comparator_15_eq));  // open: gt, lt
  Comparator #(.width(32), .mode("twosComplement")) comparator_16 (
    .a(B8), .b(EXPC), .eq(comparator_16_eq));  // open: gt, lt
  Demultiplexer #(.select(3), .width(1), .tristate("false"), .disabled("Z"), .enable("false")) demultiplexer_1 (
    .out0(W1), .out1(W2), .out2(W3), .out3(W4), .out4(W5), .out5(W6), .out6(W7), .out7(W8), .in(and_10_out),
    .sel(multiplexer_1_out));
  and and_11 (S1, comparator_9_eq, v1);
  and and_12 (S2, comparator_10_eq, v2);
  and and_13 (S3, comparator_11_eq, v3);
  and and_14 (S4, comparator_12_eq, v4);
  and and_15 (S5, comparator_13_eq, v5);
  and and_16 (S6, comparator_14_eq, v6);
  and and_17 (S7, comparator_15_eq, v7);
  and and_18 (S8, comparator_16_eq, v8);
  assign {JMP, controlled_buffer_9_out[0]} = L1 ? P1 : 2'bz;  // Controlled_Buffer controlled_buffer_9
  assign {JMP, controlled_buffer_10_out[0]} = L2 ? P2 : 2'bz;  // Controlled_Buffer controlled_buffer_10
  assign {JMP, controlled_buffer_11_out[0]} = L3 ? P3 : 2'bz;  // Controlled_Buffer controlled_buffer_11
  assign {JMP, controlled_buffer_12_out[0]} = L4 ? P4 : 2'bz;  // Controlled_Buffer controlled_buffer_12
  assign {JMP, controlled_buffer_13_out[0]} = L5 ? P5 : 2'bz;  // Controlled_Buffer controlled_buffer_13
  assign {JMP, controlled_buffer_14_out[0]} = L6 ? P6 : 2'bz;  // Controlled_Buffer controlled_buffer_14
  assign {JMP, controlled_buffer_15_out[0]} = L7 ? P7 : 2'bz;  // Controlled_Buffer controlled_buffer_15
  assign {JMP, controlled_buffer_16_out[0]} = L8 ? P8 : 2'bz;  // Controlled_Buffer controlled_buffer_16
  Pull_Resistor #(.pull(0)) pull_resistor_1 (.node(JMP));
  nor nor_1 (MissEX, S1, S2, S3, S4, S5, S6, S7, S8);
  and and_19 (and_19_out, EXBranch, S1);
  and and_20 (and_20_out, EXBranch, S2);
  and and_21 (and_21_out, S3, EXBranch);
  and and_22 (and_22_out, S4, EXBranch);
  and and_23 (and_23_out, S5, EXBranch);
  and and_24 (and_24_out, S6, EXBranch);
  and and_25 (and_25_out, S7, EXBranch);
  and and_26 (and_26_out, S8, EXBranch);
  help help_1 (.H(P1[1]), .L(P1[0]), .JMP(EXBranchDo), .NextH(help_1_nextl[1]), .NextL(help_1_nextl[0]));
  help help_2 (.H(P2[1]), .L(P2[0]), .JMP(EXBranchDo), .NextH(help_2_nextl[1]), .NextL(help_2_nextl[0]));
  help help_3 (.H(P3[1]), .L(P3[0]), .JMP(EXBranchDo), .NextH(help_3_nextl[1]), .NextL(help_3_nextl[0]));
  help help_4 (.H(P4[1]), .L(P4[0]), .JMP(EXBranchDo), .NextH(help_4_nextl[1]), .NextL(help_4_nextl[0]));
  help help_5 (.H(P5[1]), .L(P5[0]), .JMP(EXBranchDo), .NextH(help_5_nextl[1]), .NextL(help_5_nextl[0]));
  help help_6 (.H(P6[1]), .L(P6[0]), .JMP(EXBranchDo), .NextH(help_6_nextl[1]), .NextL(help_6_nextl[0]));
  help help_7 (.H(P7[1]), .L(P7[0]), .JMP(EXBranchDo), .NextH(help_7_nextl[1]), .NextL(help_7_nextl[0]));
  help help_8 (.H(P8[1]), .L(P8[0]), .JMP(EXBranchDo), .NextH(help_8_nextl[1]), .NextL(help_8_nextl[0]));
  Register #(.width(2), .trigger("rising"), .Select("low")) register_25 (
    .D(help_1_nextl), .en(and_19_out), .Q(P1), .clk(CLK));  // open: clr
  Register #(.width(2), .trigger("rising"), .Select("low")) register_26 (
    .D(help_2_nextl), .en(and_20_out), .Q(P2), .clk(CLK));  // open: clr
  Register #(.width(2), .trigger("rising"), .Select("low")) register_27 (
    .D(help_3_nextl), .en(and_21_out), .Q(P3), .clk(CLK));  // open: clr
  Register #(.width(2), .trigger("rising"), .Select("low")) register_28 (
    .D(help_4_nextl), .en(and_22_out), .Q(P4), .clk(CLK));  // open: clr
  Register #(.width(2), .trigger("rising"), .Select("low")) register_29 (
    .D(help_5_nextl), .en(and_23_out), .Q(P5), .clk(CLK));  // open: clr
  Register #(.width(2), .trigger("rising"), .Select("low")) register_30 (
    .D(help_6_nextl), .en(and_24_out), .Q(P6), .clk(CLK));  // open: clr
  Register #(.width(2), .trigger("rising"), .Select("low")) register_31 (
    .D(help_7_nextl), .en(and_25_out), .Q(P7), .clk(CLK));  // open: clr
  Register #(.width(2), .trigger("rising"), .Select("low")) register_32 (
    .D(help_8_nextl), .en(and_26_out), .Q(P8), .clk(CLK));  // open: clr

  // Other names for the same wires on the sheet: EXbranchPC[31:0] = EXPC
endmodule

module help (
  input  H,
  input  L,
  input  JMP,
  output NextH,
  output NextL
);

  wire and_1_out, and_2_out, and_3_out, and_4_out;

  and and_1 (and_1_out, L, JMP);
  and and_2 (and_2_out, H, ~L);  // AND_Gate
  and and_3 (and_3_out, ~H, ~L, JMP);  // AND_Gate
  and and_4 (and_4_out, H, ~L, ~JMP);  // AND_Gate
  or or_1 (NextH, and_1_out, and_2_out);
  or or_2 (NextL, and_3_out, and_4_out);
endmodule

module \动态分支预测控制器  (
  input  [4:0] OP,
  input  [4:0] Funct,
  input  in_3,
  output [3:0] ALU_OP,
  output uret,
  output MemToReg,
  output ecall,
  output MemWrite,
  output ALU_SRC,
  output RegWrite,
  output SB,
  output BLTU,
  output S_type,
  output Beq,
  output Bne,
  output Jalr,
  output JAL,
  output I,
  output B
);

  wire \控制信号自动生成_1_ecall ;

  \运算控制器自动生成  \u_运算控制器自动生成_1  (
    .OP2(OP[0]), .OP3(OP[1]), .OP4(OP[2]), .OP5(OP[3]), .OP6(OP[4]), .F12(Funct[0]), .F13(Funct[1]),
    .F14(Funct[2]), .F25(Funct[3]), .F30(Funct[4]), .S0(ALU_OP[0]), .S1(ALU_OP[1]), .S2(ALU_OP[2]),
    .S3(ALU_OP[3]));
  \控制信号自动生成  \u_控制信号自动生成_1  (
    .OP2(OP[0]), .OP3(OP[1]), .MemToReg(MemToReg), .OP4(OP[2]), .OP5(OP[3]), .OP6(OP[4]), .F12(Funct[0]),
    .MemWrite(MemWrite), .F13(Funct[1]), .F14(Funct[2]), .F25(Funct[3]), .F30(Funct[4]), .ALU_SRC(ALU_SRC),
    .RegWrite(RegWrite), .SB(SB), .BLTU(BLTU), .ecall(\控制信号自动生成_1_ecall ), .S_Type(S_type), .CSRRCI(I),
    .CSRRSI(B), .BEQ(Beq), .BNE(Bne), .JALR(Jalr), .JAL(JAL));
  and and_1 (uret, in_3, \控制信号自动生成_1_ecall );
  and and_2 (ecall, ~in_3, \控制信号自动生成_1_ecall );  // AND_Gate

  // Other names for the same wires on the sheet: IR21 = in_3; OP_CODE[4:0] = OP

  // Notes on the sheet:
  //   运算器控制器，根据指令生成运算器功能选择信号
endmodule

module \动态分支预测控制信号自动生成  (
  input  OP2,
  input  OP3,
  input  OP4,
  input  OP5,
  input  OP6,
  input  F12,
  input  F13,
  input  F14,
  input  F25,
  input  F30,
  output MemToReg,
  output MemWrite,
  output ALU_SRC,
  output RegWrite,
  output SB,
  output BLTU,
  output ecall,
  output S_Type,
  output CSRRCI,
  output CSRRSI,
  output BEQ,
  output BNE,
  output JALR,
  output JAL
);

  wire and_3_out, and_4_out, and_5_out, and_6_out, and_7_out, and_8_out, and_9_out, and_10_out, and_11_out,
       and_12_out, and_13_out, and_14_out, and_15_out, and_16_out, and_17_out, and_18_out, and_19_out,
       and_24_out, and_25_out, and_26_out, and_27_out, and_28_out, and_29_out, and_30_out, and_31_out,
       and_32_out, not_1_out, not_2_out, not_3_out, not_4_out, not_5_out, not_6_out, not_7_out, not_8_out,
       not_9_out, not_10_out, not_11_out, not_12_out, not_13_out, not_14_out, not_15_out, not_16_out,
       not_17_out, not_18_out, not_19_out, not_20_out, not_21_out, not_22_out, not_23_out, not_24_out,
       not_25_out, not_26_out, not_27_out, not_28_out, not_29_out, not_30_out, not_31_out, not_32_out,
       not_33_out, not_34_out, not_35_out, not_36_out, not_37_out, not_38_out, not_39_out, not_40_out,
       not_41_out, not_42_out, not_43_out, not_44_out, not_45_out, not_46_out, not_47_out, not_48_out,
       not_49_out, not_50_out, not_51_out, not_52_out, not_53_out, not_54_out, not_55_out, not_56_out,
       not_57_out, not_58_out, not_59_out, not_60_out, not_61_out, not_62_out, not_63_out, not_64_out,
       not_65_out, not_66_out, not_67_out, not_68_out, not_69_out, not_70_out, not_71_out, not_72_out,
       not_73_out, not_74_out, not_75_out, not_76_out, not_77_out, not_78_out, not_79_out, not_80_out,
       not_81_out, not_82_out, not_83_out, not_84_out, not_85_out, not_86_out, not_87_out, not_88_out,
       not_89_out, not_90_out, not_91_out, not_92_out, not_93_out, not_94_out, not_95_out, not_96_out,
       not_97_out, not_98_out, not_99_out, not_100_out, not_101_out, not_102_out, not_103_out, not_104_out,
       not_105_out, not_106_out, not_107_out, not_108_out, not_109_out, not_110_out, not_111_out,
       not_112_out, not_113_out, not_114_out, not_115_out, not_116_out, not_117_out, not_118_out,
       not_119_out, not_120_out, not_121_out, not_122_out, not_123_out, not_124_out, not_125_out,
       not_126_out, not_127_out, not_128_out, not_129_out, not_130_out, not_131_out, not_132_out,
       not_133_out, not_134_out, not_135_out, not_136_out, not_137_out, not_138_out, not_139_out,
       not_140_out, not_141_out, not_142_out, not_143_out, not_144_out, not_145_out, not_146_out,
       not_147_out, not_148_out, not_149_out, not_150_out, not_151_out, not_152_out, not_153_out,
       not_154_out, not_155_out, not_156_out, not_157_out, not_158_out, not_159_out, not_160_out,
       not_161_out, not_162_out, not_163_out, not_164_out, not_165_out, not_166_out, not_167_out,
       not_168_out, not_169_out, not_170_out, not_171_out, not_172_out, not_173_out, not_174_out,
       not_175_out, not_176_out, not_177_out, not_178_out, not_179_out, not_180_out, not_181_out,
       not_182_out, not_183_out, not_184_out, not_185_out, not_186_out;

  not not_1 (not_1_out, OP2);
  not not_2 (not_2_out, OP3);
  not not_3 (not_3_out, OP4);
  not not_4 (not_4_out, OP5);
  not not_5 (not_5_out, OP6);
  not not_6 (not_6_out, F12);
  not not_7 (not_7_out, F14);
  not not_8 (not_8_out, OP2);
  not not_9 (not_9_out, OP3);
  not not_10 (not_10_out, OP4);
  not not_11 (not_11_out, OP6);
  not not_12 (not_12_out, F12);
  not not_13 (not_13_out, F14);
  not not_14 (not_14_out, OP2);
  not not_15 (not_15_out, OP3);
  not not_16 (not_16_out, OP5);
  not not_17 (not_17_out, OP6);
  not not_18 (not_18_out, F12);
  not not_19 (not_19_out, F14);
  not not_20 (not_20_out, OP2);
  not not_21 (not_21_out, OP3);
  not not_22 (not_22_out, OP4);
  not not_23 (not_23_out, OP6);
  not not_24 (not_24_out, F12);
  not not_25 (not_25_out, F14);
  not not_26 (not_26_out, OP2);
  not not_27 (not_27_out, OP3);
  not not_28 (not_28_out, OP5);
  not not_29 (not_29_out, OP6);
  not not_30 (not_30_out, F12);
  not not_31 (not_31_out, OP2);
  not not_32 (not_32_out, OP3);
  not not_33 (not_33_out, OP5);
  not not_34 (not_34_out, OP6);
  not not_35 (not_35_out, F13);
  not not_36 (not_36_out, F25);
  not not_37 (not_37_out, F30);
  not not_38 (not_38_out, OP2);
  not not_39 (not_39_out, OP3);
  not not_40 (not_40_out, OP5);
  not not_41 (not_41_out, OP6);
  not not_42 (not_42_out, F25);
  not not_43 (not_43_out, OP2);
  not not_44 (not_44_out, OP3);
  not not_45 (not_45_out, OP5);
  not not_46 (not_46_out, OP6);
  not not_47 (not_47_out, OP3);
  not not_48 (not_48_out, OP4);
  not not_49 (not_49_out, F12);
  not not_50 (not_50_out, F13);
  not not_51 (not_51_out, F14);
  not not_52 (not_52_out, OP2);
  not not_53 (not_53_out, OP3);
  not not_54 (not_54_out, OP5);
  not not_55 (not_55_out, OP6);
  not not_56 (not_56_out, F12);
  not not_57 (not_57_out, F14);
  not not_58 (not_58_out, OP2);
  not not_59 (not_59_out, OP3);
  not not_60 (not_60_out, OP5);
  not not_61 (not_61_out, OP6);
  not not_62 (not_62_out, F12);
  not not_63 (not_63_out, OP2);
  not not_64 (not_64_out, OP3);
  not not_65 (not_65_out, OP6);
  not not_66 (not_66_out, F12);
  not not_67 (not_67_out, F13);
  not not_68 (not_68_out, F14);
  not not_69 (not_69_out, F25);
  not not_70 (not_70_out, OP2);
  not not_71 (not_71_out, OP3);
  not not_72 (not_72_out, OP6);
  not not_73 (not_73_out, F13);
  not not_74 (not_74_out, F14);
  not not_75 (not_75_out, F25);
  not not_76 (not_76_out, F30);
  not not_77 (not_77_out, OP2);
  not not_78 (not_78_out, OP3);
  not not_79 (not_79_out, OP5);
  not not_80 (not_80_out, OP6);
  not not_81 (not_81_out, F25);
  not not_82 (not_82_out, OP2);
  not not_83 (not_83_out, OP3);
  not not_84 (not_84_out, OP5);
  not not_85 (not_85_out, OP6);
  not not_86 (not_86_out, OP2);
  not not_87 (not_87_out, OP3);
  not not_88 (not_88_out, OP6);
  not not_89 (not_89_out, F13);
  not not_90 (not_90_out, F25);
  not not_91 (not_91_out, OP2);
  not not_92 (not_92_out, OP3);
  not not_93 (not_93_out, OP6);
  not not_94 (not_94_out, F25);
  not not_95 (not_95_out, F30);
  not not_96 (not_96_out, OP4);
  not not_97 (not_97_out, F12);
  not not_98 (not_98_out, F13);
  not not_99 (not_99_out, F14);
  not not_100 (not_100_out, OP4);
  not not_101 (not_101_out, OP2);
  not not_102 (not_102_out, OP3);
  not not_103 (not_103_out, OP4);
  not not_104 (not_104_out, OP6);
  not not_105 (not_105_out, F12);
  not not_106 (not_106_out, F13);
  not not_107 (not_107_out, F14);
  not not_108 (not_108_out, OP2);
  not not_109 (not_109_out, OP3);
  not not_110 (not_110_out, OP4);
  not not_111 (not_111_out, F12);
  not not_112 (not_112_out, OP2);
  not not_113 (not_113_out, OP3);
  not not_114 (not_114_out, F12);
  not not_115 (not_115_out, F13);
  not not_116 (not_116_out, F14);
  not not_117 (not_117_out, F25);
  not not_118 (not_118_out, F30);
  not not_119 (not_119_out, OP2);
  not not_120 (not_120_out, OP3);
  not not_121 (not_121_out, OP4);
  not not_122 (not_122_out, OP6);
  not not_123 (not_123_out, F12);
  not not_124 (not_124_out, F14);
  not not_125 (not_125_out, OP2);
  not not_126 (not_126_out, OP3);
  not not_127 (not_127_out, OP5);
  not not_128 (not_128_out, OP6);
  not not_129 (not_129_out, F12);
  not not_130 (not_130_out, F14);
  not not_131 (not_131_out, OP2);
  not not_132 (not_132_out, OP3);
  not not_133 (not_133_out, OP5);
  not not_134 (not_134_out, OP6);
  not not_135 (not_135_out, F12);
  not not_136 (not_136_out, OP2);
  not not_137 (not_137_out, OP3);
  not not_138 (not_138_out, OP5);
  not not_139 (not_139_out, OP6);
  not not_140 (not_140_out, F13);
  not not_141 (not_141_out, F25);
  not not_142 (not_142_out, F30);
  not not_143 (not_143_out, OP2);
  not not_144 (not_144_out, OP3);
  not not_145 (not_145_out, OP5);
  not not_146 (not_146_out, OP6);
  not not_147 (not_147_out, F25);
  not not_148 (not_148_out, OP2);
  not not_149 (not_149_out, OP3);
  not not_150 (not_150_out, OP5);
  not not_151 (not_151_out, OP6);
  not not_152 (not_152_out, OP3);
  not not_153 (not_153_out, OP4);
  not not_154 (not_154_out, F12);
  not not_155 (not_155_out, F13);
  not not_156 (not_156_out, F14);
  not not_157 (not_157_out, OP2);
  not not_158 (not_158_out, OP3);
  not not_159 (not_159_out, OP4);
  not not_160 (not_160_out, F13);
  not not_161 (not_161_out, F14);
  not not_162 (not_162_out, OP2);
  not not_163 (not_163_out, OP3);
  not not_164 (not_164_out, OP4);
  not not_165 (not_165_out, F12);
  not not_166 (not_166_out, F12);
  not not_167 (not_167_out, OP4);
  not not_168 (not_168_out, OP3);
  not not_169 (not_169_out, OP2);
  not not_170 (not_170_out, OP2);
  not not_171 (not_171_out, OP3);
  not not_172 (not_172_out, OP4);
  not not_173 (not_173_out, F12);
  not not_174 (not_174_out, F13);
  not not_175 (not_175_out, F14);
  not not_176 (not_176_out, OP2);
  not not_177 (not_177_out, OP3);
  not not_178 (not_178_out, OP4);
  not not_179 (not_179_out, F13);
  not not_180 (not_180_out, F14);
  not not_181 (not_181_out, OP3);
  not not_182 (not_182_out, OP4);
  not not_183 (not_183_out, F12);
  not not_184 (not_184_out, F13);
  not not_185 (not_185_out, F14);
  not not_186 (not_186_out, OP4);
  and and_1 (MemToReg, not_1_out, not_2_out, not_3_out, not_4_out, not_5_out, not_6_out, F13, not_7_out);
  and and_2 (MemWrite, not_8_out, not_9_out, not_10_out, OP5, not_11_out, not_12_out, not_13_out);
  and and_3 (and_3_out, not_14_out, not_15_out, not_16_out, not_17_out, not_18_out, F13, not_19_out);
  and and_4 (and_4_out, not_20_out, not_21_out, not_22_out, OP5, not_23_out, not_24_out, not_25_out);
  and and_5 (and_5_out, not_26_out, not_27_out, OP4, not_28_out, not_29_out, not_30_out);
  and and_6 (and_6_out, not_31_out, not_32_out, OP4, not_33_out, not_34_out, not_35_out, not_36_out, not_37_out);
  and and_7 (and_7_out, not_38_out, not_39_out, OP4, not_40_out, not_41_out, F14, not_42_out);
  and and_8 (and_8_out, not_43_out, not_44_out, OP4, not_45_out, not_46_out, F13, F14);
  and and_9 (and_9_out, OP2, not_47_out, not_48_out, OP5, OP6, not_49_out, not_50_out, not_51_out);
  and and_10 (and_10_out, not_52_out, not_53_out, not_54_out, not_55_out, not_56_out, F13, not_57_out);
  and and_11 (and_11_out, not_58_out, not_59_out, OP4, not_60_out, not_61_out, not_62_out);
  and and_12 (and_12_out, not_63_out, not_64_out, OP4, not_65_out, not_66_out, not_67_out, not_68_out, not_69_out);
  and and_13 (and_13_out, not_70_out, not_71_out, OP4, not_72_out, not_73_out, not_74_out, not_75_out, not_76_out);
  and and_14 (and_14_out, not_77_out, not_78_out, OP4, not_79_out, not_80_out, F14, not_81_out);
  and and_15 (and_15_out, not_82_out, not_83_out, OP4, not_84_out, not_85_out, F13, F14);
  and and_16 (and_16_out, not_86_out, not_87_out, OP4, not_88_out, F12, not_89_out, F14, not_90_out, F30);
  and and_17 (and_17_out, not_91_out, not_92_out, OP4, OP5, not_93_out, F13, not_94_out, not_95_out);
  and and_18 (and_18_out, OP2, not_96_out, OP5, OP6, not_97_out, not_98_out, not_99_out);
  and and_19 (and_19_out, OP2, OP3, not_100_out, OP5, OP6);
  and and_20 (SB, not_101_out, not_102_out, not_103_out, OP5, not_104_out, not_105_out, not_106_out, not_107_out);
  and and_21 (BLTU, not_108_out, not_109_out, not_110_out, OP5, OP6, not_111_out, F13, F14);
  and and_22 (ecall, not_112_out, not_113_out, OP4, OP5, OP6, not_114_out, not_115_out, not_116_out, not_117_out, not_118_out);
  and and_23 (S_Type, not_119_out, not_120_out, not_121_out, OP5, not_122_out, not_123_out, not_124_out);
  and and_24 (and_24_out, not_125_out, not_126_out, not_127_out, not_128_out, not_129_out, F13, not_130_out);
  and and_25 (and_25_out, not_131_out, not_132_out, OP4, not_133_out, not_134_out, not_135_out);
  and and_26 (and_26_out, not_136_out, not_137_out, OP4, not_138_out, not_139_out, not_140_out, not_141_out, not_142_out);
  and and_27 (and_27_out, not_143_out, not_144_out, OP4, not_145_out, not_146_out, F14, not_147_out);
  and and_28 (and_28_out, not_148_out, not_149_out, OP4, not_150_out, not_151_out, F13, F14);
  and and_29 (and_29_out, OP2, not_152_out, not_153_out, OP5, OP6, not_154_out, not_155_out, not_156_out);
  and and_30 (and_30_out, not_157_out, not_158_out, not_159_out, OP5, OP6, not_160_out, not_161_out);
  and and_31 (and_31_out, not_162_out, not_163_out, not_164_out, OP5, OP6, not_165_out, F13, F14);
  and and_32 (and_32_out, F14, F13, not_166_out, OP6, OP5, not_167_out, not_168_out, not_169_out);
  and and_33 (BEQ, not_170_out, not_171_out, not_172_out, OP5, OP6, not_173_out, not_174_out, not_175_out);
  and and_34 (BNE, not_176_out, not_177_out, not_178_out, OP5, OP6, F12, not_179_out, not_180_out);
  and and_35 (JALR, OP2, not_181_out, not_182_out, OP5, OP6, not_183_out, not_184_out, not_185_out);
  and and_36 (JAL, OP2, OP3, not_186_out, OP5, OP6);
  or or_1 (ALU_SRC, and_3_out, and_4_out, and_5_out, and_6_out, and_7_out, and_8_out, and_9_out);
  or or_2 (CSRRCI, and_24_out, and_25_out, and_26_out, and_27_out, and_28_out, and_29_out);
  or or_3 (CSRRSI, and_30_out, and_31_out, and_32_out);
  or or_4 (RegWrite, and_10_out, and_11_out, and_12_out, and_13_out, and_14_out, and_15_out, and_16_out, and_17_out, and_18_out, and_19_out);
endmodule
